// Logisim project 实验3-CSXJ1902-U201913821-朱旭鹏.circ as structural Verilog: 6 circuits, main circuit 四位乘法器
module \四位乘法器  (
  input  [3:0] in_1,
  input  [3:0] in_2,
  output [7:0] out_3
);

  wire [7:0] adder_1_out, adder_2_out, adder_3_out, adder_4_out, multiplexer_1_out, multiplexer_2_out,
       multiplexer_3_out, shifter_1_out, shifter_2_out, shifter_3_out, shifter_4_out;

  Adder #(.width(8)) adder_1 (.a({8{1'b0}}), .b({4'b0000, in_2}), .out(adder_1_out));  // open: cin, cout
  Multiplexer #(.select(1), .width(8), .disabled("Z"), .enable("false")) multiplexer_1 (
    .in0({8{1'b0}}), .in1(adder_1_out), .out(multiplexer_1_out), .sel(in_1[0]));
  Shifter #(.width(8), .shift("ll")) shifter_1 (.in({4'b0000, in_2}), .\dist (3'b001), .out(shifter_1_out));
  Adder #(.width(8)) adder_2 (.a(multiplexer_1_out), .b(shifter_1_out), .out(adder_2_out));  // open: cin, cout
  Multiplexer #(.select(1), .width(8), .disabled("Z"), .enable("false")) multiplexer_2 (
    .in0(multiplexer_1_out), .in1(adder_2_out), .out(multiplexer_2_out), .sel(in_1[1]));
  Shifter #(.width(8), .shift("ll")) shifter_2 (.in(shifter_1_out), .\dist (3'b001), .out(shifter_2_out));
  Adder #(.width(8)) adder_3 (.a(multiplexer_2_out), .b(shifter_2_out), .out(adder_3_out));  // open: cin, cout
  Multiplexer #(.select(1), .width(8), .disabled("Z"), .enable("false")) multiplexer_3 (
    .in0(multiplexer_2_out), .in1(adder_3_out), .out(multiplexer_3_out), .sel(in_1[2]));
  Shifter #(.width(8), .shift("ll")) shifter_3 (.in(shifter_2_out), .\dist (3'b001), .out(shifter_3_out));
  Multiplexer #(.select(1), .width(8), .disabled("Z"), .enable("false")) multiplexer_4 (
    .in0(multiplexer_3_out), .in1(adder_4_out), .out(out_3), .sel(in_1[3]));
  Adder #(.width(8)) adder_4 (.a(multiplexer_3_out), .b(shifter_3_out), .out(adder_4_out));  // open: cin, cout
  Shifter #(.width(8), .shift("ll")) shifter_4 (.in(shifter_3_out), .\dist (3'b001), .out(shifter_4_out));
endmodule

module \四位乘法器测试电路  (
  input  [3:0] in_1,
  input  [3:0] in_2,
  output [7:0] out_3
);

  \四位乘法器  \u_四位乘法器_1  (.in_1(in_1), .out_3(out_3), .in_2(in_2));
endmodule

module \_32X4乘法器  (
  input  [3:0] in_1,
  input  [31:0] in_2,
  output [31:0] out_3
);

  wire [31:0] adder_1_out, adder_2_out, adder_3_out, adder_4_out, multiplexer_1_out, multiplexer_2_out,
       multiplexer_3_out, shifter_1_out, shifter_2_out, shifter_3_out, shifter_4_out;

  Adder #(.width(32)) adder_1 (.a({32{1'b0}}), .b(in_2), .out(adder_1_out));  // open: cin, cout
  Multiplexer #(.select(1), .width(32), .disabled("Z"), .enable("false")) multiplexer_1 (
    .in0({32{1'b0}}), .in1(adder_1_out), .out(multiplexer_1_out), .sel(in_1[0]));
  Shifter #(.width(32), .shift("ll")) shifter_1 (.in(in_2), .\dist (5'b00001), .out(shifter_1_out));
  Adder #(.width(32)) adder_2 (.a(multiplexer_1_out), .b(shifter_1_out), .out(adder_2_out));  // open: cin, cout
  Multiplexer #(.select(1), .width(32), .disabled("Z"), .enable("false")) multiplexer_2 (
    .in0(multiplexer_1_out), .in1(adder_2_out), .out(multiplexer_2_out), .sel(in_1[1]));
  Shifter #(.width(32), .shift("ll")) shifter_2 (.in(shifter_1_out), .\dist (5'b00001), .out(shifter_2_out));
  Adder #(.width(32)) adder_3 (.a(multiplexer_2_out), .b(shifter_2_out), .out(adder_3_out));  // open: cin, cout
  Multiplexer #(.select(1), .width(32), .disabled("Z"), .enable("false")) multiplexer_3 (
    .in0(multiplexer_2_out), .in1(adder_3_out), .out(multiplexer_3_out), .sel(in_1[2]));
  Shifter #(.width(32), .shift("ll")) shifter_3 (.in(shifter_2_out), .\dist (5'b00001), .out(shifter_3_out));
  Multiplexer #(.select(1), .width(32), .disabled("Z"), .enable("false")) multiplexer_4 (
    .in0(multiplexer_3_out), .in1(adder_4_out), .out(out_3), .sel(in_1[3]));
  Adder #(.width(32)) adder_4 (.a(multiplexer_3_out), .b(shifter_3_out), .out(adder_4_out));  // open: cin, cout
  Shifter #(.width(32), .shift("ll")) shifter_4 (.in(shifter_3_out), .\dist (5'b00001), .out(shifter_4_out));
endmodule

module \_32X4乘法器测试电路  (
  input  [3:0] in_1,
  input  [31:0] in_2,
  output [31:0] out_3
);

  \_32X4乘法器  \u_32x4乘法器_1  (.in_1(in_1), .in_2(in_2), .out_3(out_3));
endmodule

module \_32X32乘法器  (
  input  [31:0] B,
  input  [31:0] A,
  output [31:0] out_3
);

  wire [31:0] adder_1_out, adder_2_out, adder_3_out, adder_4_out, adder_5_out, adder_6_out,
       \n32x4乘法器_1_out_3 , \n32x4乘法器_2_out_3 , \n32x4乘法器_3_out_3 , \n32x4乘法器_4_out_3 , \n32x4乘法器_5_out_3 ,
       \n32x4乘法器_6_out_3 , \n32x4乘法器_7_out_3 , \n32x4乘法器_8_out_3 , shifter_1_out, shifter_2_out,
       shifter_3_out, shifter_4_out, shifter_5_out, shifter_6_out, shifter_7_out, shifter_8_out;

  \_32X4乘法器  \u_32x4乘法器_1  (.in_1(A[3:0]), .in_2(B), .out_3(\n32x4乘法器_1_out_3 ));
  \_32X4乘法器  \u_32x4乘法器_2  (.in_1(A[7:4]), .in_2(B), .out_3(\n32x4乘法器_2_out_3 ));
  \_32X4乘法器  \u_32x4乘法器_3  (.in_1(A[11:8]), .in_2(B), .out_3(\n32x4乘法器_3_out_3 ));
  \_32X4乘法器  \u_32x4乘法器_4  (.in_1(A[15:12]), .in_2(B), .out_3(\n32x4乘法器_4_out_3 ));
  \_32X4乘法器  \u_32x4乘法器_5  (.in_1(A[19:16]), .in_2(B), .out_3(\n32x4乘法器_5_out_3 ));
  \_32X4乘法器  \u_32x4乘法器_6  (.in_1(A[23:20]), .in_2(B), .out_3(\n32x4乘法器_6_out_3 ));
  \_32X4乘法器  \u_32x4乘法器_7  (.in_1(A[27:24]), .in_2(B), .out_3(\n32x4乘法器_7_out_3 ));
  \_32X4乘法器  \u_32x4乘法器_8  (.in_1(A[31:28]), .in_2(B), .out_3(\n32x4乘法器_8_out_3 ));
  Shifter #(.width(32), .shift("ll")) shifter_1 (.in(\n32x4乘法器_1_out_3 ), .\dist ({5{1'b0}}), .out(shifter_1_out));
  Shifter #(.width(32), .shift("ll")) shifter_2 (.in(\n32x4乘法器_2_out_3 ), .\dist (5'b00100), .out(shifter_2_out));
  Shifter #(.width(32), .shift("ll")) shifter_3 (.in(\n32x4乘法器_3_out_3 ), .\dist (5'b01000), .out(shifter_3_out));
  Shifter #(.width(32), .shift("ll")) shifter_4 (.in(\n32x4乘法器_4_out_3 ), .\dist (5'b01100), .out(shifter_4_out));
  Shifter #(.width(32), .shift("ll")) shifter_5 (.in(\n32x4乘法器_5_out_3 ), .\dist (5'b10000), .out(shifter_5_out));
  Shifter #(.width(32), .shift("ll")) shifter_6 (.in(\n32x4乘法器_6_out_3 ), .\dist (5'b10100), .out(shifter_6_out));
  Shifter #(.width(32), .shift("ll")) shifter_7 (.in(\n32x4乘法器_7_out_3 ), .\dist (5'b11000), .out(shifter_7_out));
  Shifter #(.width(32), .shift("ll")) shifter_8 (.in(\n32x4乘法器_8_out_3 ), .\dist (5'b11100), .out(shifter_8_out));
  Adder #(.width(32)) adder_1 (.a(shifter_1_out), .b(shifter_2_out), .out(adder_1_out));  // open: cin, cout
  Adder #(.width(32)) adder_2 (.a(shifter_3_out), .b(shifter_4_out), .out(adder_2_out));  // open: cin, cout
  Adder #(.width(32)) adder_3 (.a(shifter_5_out), .b(shifter_6_out), .out(adder_3_out));  // open: cin, cout
  Adder #(.width(32)) adder_4 (.a(shifter_7_out), .b(shifter_8_out), .out(adder_4_out));  // open: cin, cout
  Adder #(.width(32)) adder_5 (.a(adder_1_out), .b(adder_2_out), .out(adder_5_out));  // open: cin, cout
  Adder #(.width(32)) adder_6 (.a(adder_3_out), .b(adder_4_out), .out(adder_6_out));  // open: cin, cout
  Adder #(.width(32)) adder_7 (.a(adder_5_out), .b(adder_6_out), .out(out_3));  // open: cin, cout
endmodule

module \_32X32乘法器测试电路  (
  input  [31:0] in_1,
  input  [31:0] in_2,
  output [31:0] out_3
);

  \_32X32乘法器  \u_32x32乘法器_1  (.A(in_1), .out_3(out_3), .B(in_2));
endmodule
