// Logisim project 实验2-CSXJ1902-U201913821-朱旭鹏.circ as structural Verilog: 9 circuits, main circuit 四位二进制可逆计数器
// 可逆计数器
module \四位二进制可逆计数器  (
  input  CPD,
  input  CPU,
  input  CLR,
  input  in_4,
  input  in_5,
  input  in_6,
  input  in_7,
  input  in_8,
  output Q3,
  output Q2,
  output Q1,
  output Q0
);

  wire and_1_out, and_2_out, and_3_out, and_4_out, and_5_out, and_6_out, and_7_out, and_8_out, and_9_out,
       and_10_out, and_11_out, and_12_out, and_13_out, and_14_out, and_15_out, and_16_out, and_17_out, D0_qn,
       D1_qn, D2_qn, D3_qn, not_1_out, not_2_out, not_3_out, not_4_out, not_5_out, or_1_out, or_2_out,
       or_3_out, or_4_out, or_5_out, or_6_out, or_7_out, xor_1_out;

  and and_1 (and_1_out, CPU, in_4);
  and and_2 (and_2_out, CPD, in_4);
  and and_3 (and_3_out, in_4, CLR);
  and and_4 (and_4_out, and_2_out, D2_qn, D1_qn, D0_qn);
  and and_5 (and_5_out, and_1_out, Q2, Q1, Q0);
  and and_6 (and_6_out, and_2_out, D1_qn, D0_qn);
  and and_7 (and_7_out, and_1_out, Q1, Q0);
  and and_8 (and_8_out, and_2_out, D0_qn);
  and and_9 (and_9_out, and_1_out, Q0);
  or or_1 (or_1_out, and_4_out, and_5_out);
  or or_2 (or_2_out, and_6_out, and_7_out);
  or or_3 (or_3_out, and_8_out, and_9_out);
  xor xor_1 (xor_1_out, and_2_out, and_1_out);
  not not_1 (not_1_out, in_4);
  D_Flip_Flop #(.trigger("falling"), .Pre_Clr_Positions("LEGACY"), .NegatePresetClear("false"), .enable("true"), .NewFFLayout("false")) D3 (
    .clk(or_1_out), .D(D3_qn), .Q(Q3), .Qn(D3_qn), .preset(and_13_out), .reset(or_4_out));  // open: en
  D_Flip_Flop #(.trigger("falling"), .Pre_Clr_Positions("LEGACY"), .NegatePresetClear("false"), .enable("true"), .NewFFLayout("false")) D2 (
    .clk(or_2_out), .D(D2_qn), .Q(Q2), .Qn(D2_qn), .preset(and_12_out), .reset(or_5_out));  // open: en
  D_Flip_Flop #(.trigger("falling"), .Pre_Clr_Positions("LEGACY"), .NegatePresetClear("false"), .enable("true"), .NewFFLayout("false")) D1 (
    .clk(or_3_out), .D(D1_qn), .Q(Q1), .Qn(D1_qn), .preset(and_11_out), .reset(or_6_out));  // open: en
  D_Flip_Flop #(.trigger("falling"), .Pre_Clr_Positions("LEGACY"), .NegatePresetClear("false"), .enable("true"), .NewFFLayout("false")) D0 (
    .clk(xor_1_out), .D(D0_qn), .Q(Q0), .Qn(D0_qn), .preset(and_10_out), .reset(or_7_out));  // open: en
  or or_4 (or_4_out, and_3_out, and_17_out);
  or or_5 (or_5_out, and_3_out, and_16_out);
  or or_6 (or_6_out, and_3_out, and_15_out);
  or or_7 (or_7_out, and_3_out, and_14_out);
  and and_10 (and_10_out, not_1_out, in_5);
  and and_11 (and_11_out, not_1_out, in_6);
  and and_12 (and_12_out, not_1_out, in_8);
  and and_13 (and_13_out, not_1_out, in_7);
  and and_14 (and_14_out, not_1_out, not_2_out);
  and and_15 (and_15_out, not_1_out, not_3_out);
  not not_2 (not_2_out, in_5);
  and and_16 (and_16_out, not_1_out, not_4_out);
  not not_3 (not_3_out, in_6);
  not not_4 (not_4_out, in_8);
  and and_17 (and_17_out, not_1_out, not_5_out);
  not not_5 (not_5_out, in_7);

  // Notes on the sheet:
  //   四位二进制可逆计数器
endmodule

module \四位二进制可逆计数器测试电路  (
  input  DT,
  input  S3,
  input  S2,
  input  S1,
  input  S0,
  input  CPD,
  input  CPU,
  input  CLR,
  output S3_2,
  output S2_2,
  output S1_2,
  output S0_2
);

  \四位二进制可逆计数器  \u_四位二进制可逆计数器_1  (
    .Q3(S3_2), .Q2(S2_2), .Q1(S1_2), .Q0(S0_2), .CPD(CPD), .CPU(CPU), .CLR(CLR), .in_4(DT), .in_5(S0),
    .in_8(S2), .in_6(S1), .in_7(S3));
endmodule

// 二进制&8421
module \二进制转8421码电路  (
  input  A0,
  input  A1,
  input  A2,
  input  A3,
  output S1,
  output S2,
  output S4,
  output S8,
  output S10,
  output S20,
  output S40,
  output S80
);

  wire and_1_out, or_1_out;

  or or_1 (or_1_out, A1, A2);
  and and_1 (and_1_out, or_1_out, A3);
  // 先行进位的四位二进制并行加法器 先行进位的四位二进制并行加法器_1: pin names not known; wires that end beside it: A0, A1, A2, A3, 1'b0, and_1_out, and_1_out, 1'b0, 1'b0, S1, S2, S4, S8, S10

  assign S20 = 1'b0;
  assign S40 = 1'b0;
  assign S80 = 1'b0;

  // Notes on the sheet:
  //   A0
  //   A1
  //   A2
  //   A3
  //   B0
  //   B1
  //   B2
  //   B3
  //   C0
  //   S0
  //   S1
  //   S2
  //   S3
  //   C4
endmodule

module \二进制转8421码测试电路  (
  input  A0,
  input  A1,
  input  A2,
  input  A3,
  output out_5,
  output out_6,
  output out_7,
  output out_8,
  output out_9,
  output out_10,
  output out_11,
  output out_12
);

  \二进制转8421码电路  \u_二进制转8421码电路_1  (
    .A0(A0), .A1(A1), .A2(A2), .A3(A3), .S1(out_12), .S2(out_11), .S4(out_10), .S8(out_9), .S10(out_8),
    .S20(out_7), .S40(out_6), .S80(out_5));
endmodule

module \显示电路  (
  input  A3,
  input  A2,
  input  A1,
  input  A0,
  output out_5,
  output out_6,
  output out_7,
  output out_8,
  output out_9,
  output out_10,
  output out_11
);

  wire A1_A0_out, A1_nA0_out, A2_A0_out, A2_A1_out, A2_nA0_out, A2_nA1_A0_out, A2_nA1_out, A3_nA1_out,
       nA1_nA0_out, nA2_A1_out, nA2_nA0_out, not_1_out, not_2_out, not_3_out, not_4_out;

  not not_1 (not_1_out, A3);
  not not_2 (not_2_out, A2);
  not not_3 (not_3_out, A1);
  not not_4 (not_4_out, A0);
  xnor A2_A0 (A2_A0_out, A2, A0);
  xnor A1_A0 (A1_A0_out, A1, A0);
  and nA2_nA0 (nA2_nA0_out, not_2_out, not_4_out);
  and A1_nA0 (A1_nA0_out, A1, not_4_out);
  and nA2_A1 (nA2_A1_out, not_2_out, A1);
  and A2_nA1_A0 (A2_nA1_A0_out, A2, not_3_out, A0);
  and nA1_nA0 (nA1_nA0_out, not_3_out, not_4_out);
  and A2_nA0 (A2_nA0_out, A2, not_4_out);
  and A2_nA1 (A2_nA1_out, A2, not_3_out);
  and A3_nA1 (A3_nA1_out, A3, not_3_out);
  xor A2_A1 (A2_A1_out, A2, A1);
  or a (out_5, A2_A0_out, A3, A1);
  or b (out_6, A1_A0_out, not_2_out);
  nand c (out_7, A1, not_1_out, not_2_out, not_4_out);
  or d (out_8, nA2_nA0_out, A1_nA0_out, A3, nA2_A1_out, A2_nA1_A0_out);
  or e (out_9, nA2_nA0_out, A1_nA0_out);
  or f (out_10, nA1_nA0_out, A2_nA0_out, A2_nA1_out, A3_nA1_out);
  or g (out_11, A1_nA0_out, A2_A1_out, A3);

  // Notes on the sheet:
  //   七段译码器
endmodule

module \显示电路测试电路  (
  input  in_1,
  input  in_2,
  input  in_3,
  input  in_4
);

  wire \二进制转8421码电路_1_s1 , \二进制转8421码电路_1_s2 , \二进制转8421码电路_1_s4 , \二进制转8421码电路_1_s8 , \二进制转8421码电路_1_s10 ,
       \二进制转8421码电路_1_s20 , \二进制转8421码电路_1_s40 , \二进制转8421码电路_1_s80 , \显示电路_1_out_5 , \显示电路_1_out_6 ,
       \显示电路_1_out_7 , \显示电路_1_out_8 , \显示电路_1_out_9 , \显示电路_1_out_10 , \显示电路_1_out_11 , \显示电路_2_out_5 ,
       \显示电路_2_out_6 , \显示电路_2_out_7 , \显示电路_2_out_8 , \显示电路_2_out_9 , \显示电路_2_out_10 , \显示电路_2_out_11 ;

  _7_Segment_Display #(.active("true")) u_7_segment_display_1 (
    .g(\显示电路_1_out_11 ), .f(\显示电路_1_out_10 ), .a(\显示电路_1_out_5 ), .b(\显示电路_1_out_6 ), .e(\显示电路_1_out_9 ),
    .d(\显示电路_1_out_8 ), .c(\显示电路_1_out_7 ));  // open: dp
  \显示电路  \u_显示电路_1  (
    .A3(\二进制转8421码电路_1_s80 ), .A2(\二进制转8421码电路_1_s40 ), .A1(\二进制转8421码电路_1_s20 ), .A0(\二进制转8421码电路_1_s10 ),
    .out_5(\显示电路_1_out_5 ), .out_6(\显示电路_1_out_6 ), .out_7(\显示电路_1_out_7 ), .out_8(\显示电路_1_out_8 ),
    .out_9(\显示电路_1_out_9 ), .out_10(\显示电路_1_out_10 ), .out_11(\显示电路_1_out_11 ));
  \二进制转8421码电路  \u_二进制转8421码电路_1  (
    .A0(in_1), .A1(in_2), .A2(in_3), .A3(in_4), .S1(\二进制转8421码电路_1_s1 ), .S2(\二进制转8421码电路_1_s2 ),
    .S4(\二进制转8421码电路_1_s4 ), .S8(\二进制转8421码电路_1_s8 ), .S10(\二进制转8421码电路_1_s10 ), .S20(\二进制转8421码电路_1_s20 ),
    .S40(\二进制转8421码电路_1_s40 ), .S80(\二进制转8421码电路_1_s80 ));
  _7_Segment_Display #(.active("true")) u_7_segment_display_2 (
    .g(\显示电路_2_out_11 ), .f(\显示电路_2_out_10 ), .a(\显示电路_2_out_5 ), .b(\显示电路_2_out_6 ), .e(\显示电路_2_out_9 ),
    .d(\显示电路_2_out_8 ), .c(\显示电路_2_out_7 ));  // open: dp
  \显示电路  \u_显示电路_2  (
    .A3(\二进制转8421码电路_1_s8 ), .A2(\二进制转8421码电路_1_s4 ), .A1(\二进制转8421码电路_1_s2 ), .A0(\二进制转8421码电路_1_s1 ),
    .out_5(\显示电路_2_out_5 ), .out_6(\显示电路_2_out_6 ), .out_7(\显示电路_2_out_7 ), .out_8(\显示电路_2_out_8 ),
    .out_9(\显示电路_2_out_9 ), .out_10(\显示电路_2_out_10 ), .out_11(\显示电路_2_out_11 ));
endmodule

module \报警电路  (
  input  DT,
  input  S3,
  input  S2,
  input  S1,
  input  S0,
  output out_6,
  output out_7,
  output out_8,
  output out_9
);

  wire and_1_out, and_2_out, and_3_out, CLR_out, D_out, not_1_out, U_out, \无人信号_out , \满人信号_out ;

  \四位二进制可逆计数器  \u_四位二进制可逆计数器_1  (
    .Q3(out_6), .Q2(out_7), .Q1(out_8), .Q0(out_9), .CPD(and_3_out), .CPU(and_1_out), .CLR(CLR_out),
    .in_4(DT), .in_5(S0), .in_8(S2), .in_6(S1), .in_7(S3));
  or \u_无人信号  (\无人信号_out , out_6, out_7, out_8, out_9);
  and \u_满人信号  (\满人信号_out , out_9, out_8, out_7, out_6);
  not not_1 (not_1_out, \满人信号_out );
  and and_1 (and_1_out, not_1_out, U_out);
  LED #(.active("true")) led_1 (.in(and_2_out));
  and and_2 (and_2_out, \满人信号_out , U_out);
  Button U (.out(U_out));
  Button CLR (.out(CLR_out));
  and and_3 (and_3_out, \无人信号_out , D_out);
  Button D (.out(D_out));
endmodule

module \小型实验室门禁系统  (
  input  U,
  input  CLR,
  input  D,
  output out_4,
  output out_5,
  output out_6,
  output out_7,
  output out_8,
  output out_9,
  output out_10,
  output out_11,
  output out_12,
  output out_13,
  output out_14,
  output out_15,
  output out_16,
  output out_17,
  output out_18
);

  wire and_1_out, and_3_out, not_1_out, \二进制转8421码电路_1_s1 , \二进制转8421码电路_1_s2 , \二进制转8421码电路_1_s4 ,
       \二进制转8421码电路_1_s8 , \二进制转8421码电路_1_s10 , \二进制转8421码电路_1_s20 , \二进制转8421码电路_1_s40 ,
       \二进制转8421码电路_1_s80 , \四位二进制可逆计数器_1_q0 , \四位二进制可逆计数器_1_q1 , \四位二进制可逆计数器_1_q2 , \四位二进制可逆计数器_1_q3 ,
       \无人信号_out , \满人信号_out ;

  \二进制转8421码电路  \u_二进制转8421码电路_1  (
    .A0(\四位二进制可逆计数器_1_q0 ), .A1(\四位二进制可逆计数器_1_q1 ), .A2(\四位二进制可逆计数器_1_q2 ), .A3(\四位二进制可逆计数器_1_q3 ),
    .S1(\二进制转8421码电路_1_s1 ), .S2(\二进制转8421码电路_1_s2 ), .S4(\二进制转8421码电路_1_s4 ), .S8(\二进制转8421码电路_1_s8 ),
    .S10(\二进制转8421码电路_1_s10 ), .S20(\二进制转8421码电路_1_s20 ), .S40(\二进制转8421码电路_1_s40 ), .S80(\二进制转8421码电路_1_s80 ));
  \显示电路  \u_显示电路_1  (
    .A3(\二进制转8421码电路_1_s80 ), .A2(\二进制转8421码电路_1_s40 ), .A1(\二进制转8421码电路_1_s20 ), .A0(\二进制转8421码电路_1_s10 ),
    .out_5(out_4), .out_6(out_5), .out_7(out_6), .out_8(out_7), .out_9(out_8), .out_10(out_9), .out_11(out_10));
  \四位二进制可逆计数器  \u_四位二进制可逆计数器_1  (
    .Q3(\四位二进制可逆计数器_1_q3 ), .Q2(\四位二进制可逆计数器_1_q2 ), .Q1(\四位二进制可逆计数器_1_q1 ), .Q0(\四位二进制可逆计数器_1_q0 ),
    .CPD(and_3_out), .CPU(and_1_out), .CLR(CLR), .in_4(1'b1), .in_5(1'b0), .in_8(1'b0), .in_6(1'b0),
    .in_7(1'b0));
  \显示电路  \u_显示电路_2  (
    .A3(\二进制转8421码电路_1_s8 ), .A2(\二进制转8421码电路_1_s4 ), .A1(\二进制转8421码电路_1_s2 ), .A0(\二进制转8421码电路_1_s1 ),
    .out_5(out_11), .out_6(out_12), .out_7(out_13), .out_8(out_14), .out_9(out_15), .out_10(out_16),
    .out_11(out_17));
  or \u_无人信号  (\无人信号_out , \四位二进制可逆计数器_1_q3 , \四位二进制可逆计数器_1_q2 , \四位二进制可逆计数器_1_q1 , \四位二进制可逆计数器_1_q0 );
  and \u_满人信号  (\满人信号_out , \四位二进制可逆计数器_1_q0 , \四位二进制可逆计数器_1_q1 , \四位二进制可逆计数器_1_q2 , \四位二进制可逆计数器_1_q3 );
  not not_1 (not_1_out, \满人信号_out );
  and and_1 (and_1_out, not_1_out, U);
  and and_2 (out_18, \满人信号_out , U);
  and and_3 (and_3_out, \无人信号_out , D);
endmodule

module \小型门禁系统测试电路  (
);

  wire CLR_out, D_out, U_out, \小型实验室门禁系统_1_out_4 , \小型实验室门禁系统_1_out_5 , \小型实验室门禁系统_1_out_6 ,
       \小型实验室门禁系统_1_out_7 , \小型实验室门禁系统_1_out_8 , \小型实验室门禁系统_1_out_9 , \小型实验室门禁系统_1_out_10 ,
       \小型实验室门禁系统_1_out_11 , \小型实验室门禁系统_1_out_12 , \小型实验室门禁系统_1_out_13 , \小型实验室门禁系统_1_out_14 ,
       \小型实验室门禁系统_1_out_15 , \小型实验室门禁系统_1_out_16 , \小型实验室门禁系统_1_out_17 , \小型实验室门禁系统_1_out_18 ;

  Button D (.out(D_out));
  Button CLR (.out(CLR_out));
  Button U (.out(U_out));
  _7_Segment_Display #(.active("true")) u_7_segment_display_1 (
    .g(\小型实验室门禁系统_1_out_10 ), .f(\小型实验室门禁系统_1_out_9 ), .a(\小型实验室门禁系统_1_out_4 ), .b(\小型实验室门禁系统_1_out_5 ),
    .e(\小型实验室门禁系统_1_out_8 ), .d(\小型实验室门禁系统_1_out_7 ), .c(\小型实验室门禁系统_1_out_6 ));  // open: dp
  _7_Segment_Display #(.active("true")) u_7_segment_display_2 (
    .g(\小型实验室门禁系统_1_out_17 ), .f(\小型实验室门禁系统_1_out_16 ), .a(\小型实验室门禁系统_1_out_11 ), .b(\小型实验室门禁系统_1_out_12 ),
    .e(\小型实验室门禁系统_1_out_15 ), .d(\小型实验室门禁系统_1_out_14 ), .c(\小型实验室门禁系统_1_out_13 ));  // open: dp
  \小型实验室门禁系统  \u_小型实验室门禁系统_1  (
    .U(U_out), .CLR(CLR_out), .D(D_out), .out_18(\小型实验室门禁系统_1_out_18 ), .out_9(\小型实验室门禁系统_1_out_9 ),
    .out_4(\小型实验室门禁系统_1_out_4 ), .out_10(\小型实验室门禁系统_1_out_10 ), .out_5(\小型实验室门禁系统_1_out_5 ),
    .out_8(\小型实验室门禁系统_1_out_8 ), .out_7(\小型实验室门禁系统_1_out_7 ), .out_6(\小型实验室门禁系统_1_out_6 ),
    .out_11(\小型实验室门禁系统_1_out_11 ), .out_12(\小型实验室门禁系统_1_out_12 ), .out_13(\小型实验室门禁系统_1_out_13 ),
    .out_14(\小型实验室门禁系统_1_out_14 ), .out_15(\小型实验室门禁系统_1_out_15 ), .out_16(\小型实验室门禁系统_1_out_16 ),
    .out_17(\小型实验室门禁系统_1_out_17 ));
  LED #(.active("true")) led_1 (.in(\小型实验室门禁系统_1_out_18 ));
endmodule
