// Logisim project 实验5-CS1901-U201913821-朱旭鹏.circ as structural Verilog
module \四位二进制可逆计数器  (
  input  CPD,
  input  CPU,
  input  CLR,
  input  in_4,
  input  in_5,
  input  in_6,
  input  in_7,
  input  in_8,
  output Q3,
  output Q2,
  output Q1,
  output Q0
);

  wire and_1_out, and_2_out, and_3_out, and_4_out, and_5_out, and_6_out, and_7_out, and_8_out, and_9_out,
       and_10_out, and_11_out, and_12_out, and_13_out, and_14_out, and_15_out, and_16_out, and_17_out, D0_qn,
       D1_qn, D2_qn, D3_qn, not_1_out, not_2_out, not_3_out, not_4_out, not_5_out, or_1_out, or_2_out,
       or_3_out, or_4_out, or_5_out, or_6_out, or_7_out, xor_1_out;

  and and_1 (and_1_out, CPD, in_4);
  and and_2 (and_2_out, CPU, in_4);
  and and_3 (and_3_out, in_4, CLR);
  and and_4 (and_4_out, and_1_out, D2_qn, D1_qn, D0_qn);
  and and_5 (and_5_out, and_2_out, Q2, Q1, Q0);
  and and_6 (and_6_out, and_1_out, D1_qn, D0_qn);
  and and_7 (and_7_out, and_2_out, Q1, Q0);
  and and_8 (and_8_out, and_1_out, D0_qn);
  and and_9 (and_9_out, and_2_out, Q0);
  or or_1 (or_1_out, and_4_out, and_5_out);
  or or_2 (or_2_out, and_6_out, and_7_out);
  or or_3 (or_3_out, and_8_out, and_9_out);
  xor xor_1 (xor_1_out, and_1_out, and_2_out);
  not not_1 (not_1_out, in_4);
  D_Flip_Flop #(.trigger("falling"), .Pre_Clr_Positions("LEGACY"), .NegatePresetClear("false"), .enable("true"), .NewFFLayout("false")) D3 (
    .clk(or_1_out), .D(D3_qn), .Q(Q3), .Qn(D3_qn), .preset(and_13_out), .reset(or_4_out));  // open: en
  D_Flip_Flop #(.trigger("falling"), .Pre_Clr_Positions("LEGACY"), .NegatePresetClear("false"), .enable("true"), .NewFFLayout("false")) D2 (
    .clk(or_2_out), .D(D2_qn), .Q(Q2), .Qn(D2_qn), .preset(and_12_out), .reset(or_5_out));  // open: en
  D_Flip_Flop #(.trigger("falling"), .Pre_Clr_Positions("LEGACY"), .NegatePresetClear("false"), .enable("true"), .NewFFLayout("false")) D1 (
    .clk(or_3_out), .D(D1_qn), .Q(Q1), .Qn(D1_qn), .preset(and_11_out), .reset(or_6_out));  // open: en
  D_Flip_Flop #(.trigger("falling"), .Pre_Clr_Positions("LEGACY"), .NegatePresetClear("false"), .enable("true"), .NewFFLayout("false")) D0 (
    .clk(xor_1_out), .D(D0_qn), .Q(Q0), .Qn(D0_qn), .preset(and_10_out), .reset(or_7_out));  // open: en
  or or_4 (or_4_out, and_3_out, and_17_out);
  or or_5 (or_5_out, and_3_out, and_16_out);
  or or_6 (or_6_out, and_3_out, and_15_out);
  or or_7 (or_7_out, and_3_out, and_14_out);
  and and_10 (and_10_out, not_1_out, in_5);
  and and_11 (and_11_out, not_1_out, in_6);
  and and_12 (and_12_out, not_1_out, in_8);
  and and_13 (and_13_out, not_1_out, in_7);
  and and_14 (and_14_out, not_1_out, not_2_out);
  and and_15 (and_15_out, not_1_out, not_3_out);
  not not_2 (not_2_out, in_5);
  and and_16 (and_16_out, not_1_out, not_4_out);
  not not_3 (not_3_out, in_6);
  not not_4 (not_4_out, in_8);
  and and_17 (and_17_out, not_1_out, not_5_out);
  not not_5 (not_5_out, in_7);

  // Notes on the sheet:
  //   四位二进制可逆计数器
endmodule

module \六十进制计数器  (
  input  CPU,
  input  CLR,
  input  CPD,
  input  Adj,
  output QD1,
  output QC1,
  output QB1,
  output QA1,
  output QD0,
  output QC0,
  output QB0,
  output QA0,
  output GCC
);

  wire A_out, and_1_out, B_out, C_out, D_out, E_out, H_out, I_out, J_out, or_1_out;
  wire [3:0] \四位二进制可逆计数器_1_q0 , \四位二进制可逆计数器_2_q0 ;
  wire [5:0] adder_1_out, multiplier_1_out;
  wire [5:4] divider_1_out, divider_1_rem;

  or I (I_out, CLR, B_out);
  nand E (E_out, C_out, H_out);
  and J (J_out, E_out, CPD, H_out);
  and and_1 (and_1_out, CPU, A_out);
  and B (B_out, \四位二进制可逆计数器_1_q0 [0], \四位二进制可逆计数器_1_q0 [1], \四位二进制可逆计数器_2_q0 [3], \四位二进制可逆计数器_2_q0 [2]);
  or or_1 (or_1_out, B_out, CLR);
  nor C (C_out, \四位二进制可逆计数器_1_q0 [0], \四位二进制可逆计数器_1_q0 [1], \四位二进制可逆计数器_1_q0 [2], \四位二进制可逆计数器_1_q0 [3]);
  nor H (H_out, \四位二进制可逆计数器_2_q0 [3], \四位二进制可逆计数器_2_q0 [2], \四位二进制可逆计数器_2_q0 [1], \四位二进制可逆计数器_2_q0 [0]);
  and A (A_out, \四位二进制可逆计数器_2_q0 [3], \四位二进制可逆计数器_2_q0 [2], \四位二进制可逆计数器_2_q0 [1], \四位二进制可逆计数器_2_q0 [0]);
  and D (D_out, CPD, E_out, Adj);
  nand G (GCC, ~Adj, B_out);  // NAND_Gate
  \四位二进制可逆计数器  \u_四位二进制可逆计数器_1  (
    .Q3(\四位二进制可逆计数器_1_q0 [3]), .Q2(\四位二进制可逆计数器_1_q0 [2]), .Q1(\四位二进制可逆计数器_1_q0 [1]),
    .Q0(\四位二进制可逆计数器_1_q0 [0]), .CPD(J_out), .CPU(and_1_out), .CLR(I_out), .in_4(1'b1), .in_5(1'b0),
    .in_6(1'b0), .in_8(1'b0), .in_7(1'b0));
  \四位二进制可逆计数器  \u_四位二进制可逆计数器_2  (
    .Q3(\四位二进制可逆计数器_2_q0 [3]), .Q2(\四位二进制可逆计数器_2_q0 [2]), .Q1(\四位二进制可逆计数器_2_q0 [1]),
    .Q0(\四位二进制可逆计数器_2_q0 [0]), .CPD(D_out), .CPU(CPU), .CLR(or_1_out), .in_4(1'b1), .in_5(1'b0), .in_6(1'b0),
    .in_8(1'b0), .in_7(1'b0));
  Multiplier #(.width(6)) multiplier_1 (
    .a({2'b00, \四位二进制可逆计数器_1_q0 }), .b(6'b010000), .out(multiplier_1_out));  // open: cin, cout
  Adder #(.width(6)) adder_1 (
    .a(multiplier_1_out), .b({2'b00, \四位二进制可逆计数器_2_q0 }), .out(adder_1_out));  // open: cin, cout
  Divider #(.width(6)) divider_1 (
    .a(adder_1_out), .b(6'b001010), .out({divider_1_out, QD1, QC1, QB1, QA1}),
    .rem({divider_1_rem, QD0, QC0, QB0, QA0}));  // open: upper
endmodule

module \六十进制计数器测试电路  (
  input  in_1,
  input  in_2,
  output out_3
);

  wire button_1_out, button_2_out;
  wire [3:0] \六十进制计数器_1_qa0 , \六十进制计数器_1_qa1 ;

  Button button_1 (.out(button_1_out));
  Button button_2 (.out(button_2_out));
  Hex_Digit_Display hex_digit_display_1 (.value(\六十进制计数器_1_qa1 ));  // open: dp
  Hex_Digit_Display hex_digit_display_2 (.value(\六十进制计数器_1_qa0 ));  // open: dp
  \六十进制计数器  \u_六十进制计数器_1  (
    .CPU(button_1_out), .CLR(in_2), .CPD(button_2_out), .Adj(in_1), .GCC(out_3), .QD1(\六十进制计数器_1_qa1 [3]),
    .QC1(\六十进制计数器_1_qa1 [2]), .QB1(\六十进制计数器_1_qa1 [1]), .QA1(\六十进制计数器_1_qa1 [0]), .QD0(\六十进制计数器_1_qa0 [3]),
    .QC0(\六十进制计数器_1_qa0 [2]), .QB0(\六十进制计数器_1_qa0 [1]), .QA0(\六十进制计数器_1_qa0 [0]));
endmodule

module \十二进制计数器或二十四进制的计数器电路  (
  input  in_1,
  input  in_2,
  input  in_3,
  input  in_4,
  input  in_5,
  output out_6,
  output out_7,
  output out_8,
  output out_9,
  output out_10,
  output out_11,
  output out_12,
  output out_13,
  output out_14,
  output out_15
);

  wire and_1_out, and_2_out, and_3_out, and_4_out, comparator_2_gt, multiplexer_2_out, not_1_out, or_1_out;
  wire [3:0] multiplexer_3_out, subtractor_2_out, \六十进制计数器_1_qa0 , \六十进制计数器_1_qa1 ;
  wire [7:0] subtractor_1_out;

  \六十进制计数器  \u_六十进制计数器_1  (
    .CPU(in_2), .CLR(or_1_out), .CPD(in_4), .Adj(in_3), .QD1(\六十进制计数器_1_qa1 [3]), .QC1(\六十进制计数器_1_qa1 [2]),
    .QB1(\六十进制计数器_1_qa1 [1]), .QA1(\六十进制计数器_1_qa1 [0]), .QD0(\六十进制计数器_1_qa0 [3]), .QC0(\六十进制计数器_1_qa0 [2]),
    .QB0(\六十进制计数器_1_qa0 [1]), .QA0(\六十进制计数器_1_qa0 [0]));  // open: GCC
  and and_1 (and_1_out, \六十进制计数器_1_qa1 [0], \六十进制计数器_1_qa0 [1]);
  and and_2 (and_2_out, \六十进制计数器_1_qa1 [1], \六十进制计数器_1_qa0 [2]);
  or or_1 (or_1_out, multiplexer_2_out, in_5);
  Multiplexer #(.select(1), .width(1), .disabled("Z"), .enable("false")) multiplexer_1 (
    .in0(and_1_out), .in1(and_2_out), .out(out_6), .sel(1'b1));
  Multiplexer #(.select(1), .width(1), .disabled("Z"), .enable("false")) multiplexer_2 (
    .in0(and_1_out), .in1(and_2_out), .out(multiplexer_2_out), .sel(1'b1));
  not not_1 (not_1_out, in_1);
  Comparator #(.width(8), .mode("twosComplement")) comparator_1 (
    .a({\六十进制计数器_1_qa1 , \六十进制计数器_1_qa0 }), .b(8'h12), .gt(out_11));  // open: eq, lt
  and and_3 (and_3_out, out_11, not_1_out);
  Subtractor #(.width(8)) subtractor_1 (
    .a({\六十进制计数器_1_qa1 , \六十进制计数器_1_qa0 }), .b(8'h12), .out(subtractor_1_out));  // open: bin, bout
  Multiplexer #(.select(1), .width(8), .disabled("Z"), .enable("false")) multiplexer_3 (
    .in0({\六十进制计数器_1_qa1 , \六十进制计数器_1_qa0 }), .in1(subtractor_1_out),
    .out({out_12, out_13, out_14, out_15, multiplexer_3_out}), .sel(and_3_out));
  // Probe on {out_12, out_13, out_14, out_15, multiplexer_3_out}
  // Probe on multiplexer_3_out
  Comparator #(.width(4), .mode("unsigned")) comparator_2 (
    .a(multiplexer_3_out), .b(4'b1100), .gt(comparator_2_gt));  // open: eq, lt
  Subtractor #(.width(4)) subtractor_2 (.a(multiplexer_3_out), .b(4'b0110), .out(subtractor_2_out));  // open: bin, bout
  Multiplexer #(.select(1), .width(4), .disabled("Z"), .enable("false")) multiplexer_4 (
    .in0(multiplexer_3_out), .in1(subtractor_2_out), .out({out_7, out_8, out_9, out_10}), .sel(and_4_out));
  and and_4 (and_4_out, comparator_2_gt, not_1_out);
endmodule

module \十二进制计数器或二十四进制的计数器测试电路  (
  input  in_1,
  input  in_2,
  input  in_3,
  output out_4
);

  wire button_1_out, button_2_out;
  wire [3:0] \十二进制计数器或二十四进制的计数器电路_1_out_10 , \十二进制计数器或二十四进制的计数器电路_1_out_15 ;

  Button button_1 (.out(button_1_out));
  Button button_2 (.out(button_2_out));
  Hex_Digit_Display hex_digit_display_1 (.value(\十二进制计数器或二十四进制的计数器电路_1_out_15 ));  // open: dp
  Hex_Digit_Display hex_digit_display_2 (.value(\十二进制计数器或二十四进制的计数器电路_1_out_10 ));  // open: dp
  \十二进制计数器或二十四进制的计数器电路  \u_十二进制计数器或二十四进制的计数器电路_1  (
    .in_2(button_1_out), .in_3(in_1), .in_4(button_2_out), .out_6(out_4), .in_5(in_3), .in_1(in_2),
    .out_7(\十二进制计数器或二十四进制的计数器电路_1_out_10 [3]), .out_8(\十二进制计数器或二十四进制的计数器电路_1_out_10 [2]),
    .out_9(\十二进制计数器或二十四进制的计数器电路_1_out_10 [1]), .out_10(\十二进制计数器或二十四进制的计数器电路_1_out_10 [0]),
    .out_12(\十二进制计数器或二十四进制的计数器电路_1_out_15 [3]), .out_13(\十二进制计数器或二十四进制的计数器电路_1_out_15 [2]),
    .out_14(\十二进制计数器或二十四进制的计数器电路_1_out_15 [1]), .out_15(\十二进制计数器或二十四进制的计数器电路_1_out_15 [0]));  // open: out_11
endmodule

module \上下午文字显示的电路  (
  input  in_1,
  input  in_2,
  output [6:0] _2,
  output [6:0] _3,
  output [6:0] _4,
  output [6:0] _1,
  output [6:0] _5
);

  wire [6:0] multiplexer_1_out, multiplexer_2_out;

  Multiplexer #(.select(1), .width(7), .disabled("Z"), .enable("false")) multiplexer_1 (
    .in0(7'b0001001), .in1(7'b1001000), .out(multiplexer_1_out), .sel(in_1));
  Multiplexer #(.select(1), .width(7), .disabled("Z"), .enable("false")) multiplexer_2 (
    .in0(7'b0000001), .in1(7'b1000000), .out(multiplexer_2_out), .sel(in_1));
  Multiplexer #(.select(1), .width(7), .disabled("Z"), .enable("false")) multiplexer_3 (
    .in0({7{1'b0}}), .in1(multiplexer_1_out), .out(_3), .sel(in_2));
  Multiplexer #(.select(1), .width(7), .disabled("Z"), .enable("false")) multiplexer_4 (
    .in0({7{1'b0}}), .in1({7{1'b1}}), .out(_2), .sel(in_2));
  Multiplexer #(.select(1), .width(7), .disabled("Z"), .enable("false")) multiplexer_5 (
    .in0({7{1'b0}}), .in1(multiplexer_2_out), .out(_1), .sel(in_2));

  assign _4 = _3;
  assign _5 = _1;
endmodule

module \上下午文字显示测试电路  (
  input  in_1,
  input  in_2
);

  wire [6:0] \上下午文字显示的电路_1__1 , \上下午文字显示的电路_1__2 , \上下午文字显示的电路_1__3 , \上下午文字显示的电路_1__4 , \上下午文字显示的电路_1__5 ;

  DotMatrix #(.inputtype("column"), .matrixcols(5), .matrixrows(7), .persist(0), .dotshape("square")) dotmatrix_1 (
    .col0(\上下午文字显示的电路_1__1 ), .col1(\上下午文字显示的电路_1__2 ), .col2(\上下午文字显示的电路_1__3 ), .col3(\上下午文字显示的电路_1__4 ),
    .col4(\上下午文字显示的电路_1__5 ));
  \上下午文字显示的电路  \u_上下午文字显示的电路_1  (
    ._1(\上下午文字显示的电路_1__1 ), ._2(\上下午文字显示的电路_1__2 ), ._3(\上下午文字显示的电路_1__3 ), ._4(\上下午文字显示的电路_1__4 ),
    ._5(\上下午文字显示的电路_1__5 ), .in_1(in_1), .in_2(in_2));
endmodule

module \电子钟整点报时电路  (
  input  [3:0] Min2,
  input  [3:0] Min1,
  input  [3:0] Sel2,
  output out_4
);

  wire comparator_1_eq, comparator_2_eq, comparator_3_eq;

  Comparator #(.width(4), .mode("twosComplement")) comparator_1 (
    .a(4'b0101), .b(Min2), .eq(comparator_1_eq));  // open: gt, lt
  Comparator #(.width(4), .mode("twosComplement")) comparator_2 (
    .a(4'b1001), .b(Min1), .eq(comparator_2_eq));  // open: gt, lt
  and and_1 (out_4, comparator_1_eq, comparator_2_eq, comparator_3_eq);
  Comparator #(.width(4), .mode("twosComplement")) comparator_3 (
    .a(4'b0101), .b(Sel2), .eq(comparator_3_eq));  // open: gt, lt
endmodule

module \电子钟整点报时电路测试电路  (
  input  [3:0] in_1,
  input  [3:0] in_2,
  input  [3:0] in_3,
  output out_4
);

  \电子钟整点报时电路  \u_电子钟整点报时电路_1  (.Min2(in_1), .Min1(in_2), .Sel2(in_3), .out_4(out_4));
endmodule

module \秒脉冲产生电路  (
  input  in_1,
  output out_2
);

  Counter #(.width(2), .max('h3), .ongoal("wrap"), .trigger("rising"), .behavior("new")) counter_1 (
    .D(2'b01), .carry(out_2), .clk(in_1), .down(1'b1));  // open: load, count, Q, clr, preset
endmodule

module \多功能数字钟  (
  input  in_1,
  input  Cpd,
  input  Cpu,
  input  Clr,
  input  Sel,
  input  CP,
  input  Adj1,
  input  Adj0,
  output [3:0] Hour1,
  output [3:0] Hour2,
  output [3:0] Min1,
  output [6:0] _2,
  output [6:0] _3,
  output [6:0] _4,
  output [6:0] _5,
  output [3:0] Min2,
  output [3:0] Sec1,
  output [3:0] Sec2,
  output [6:0] _1,
  output out_20,
  output out_21
);

  wire and_1_out, and_2_out, and_3_out, comparator_1_eq, multiplexer_3_out, multiplexer_9_out, not_1_out,
       or_1_out, or_2_out, \六十进制计数器_1_gcc , \六十进制计数器_2_gcc , \十二进制计数器或二十四进制的计数器电路_1_out_11 ,
       \电子钟整点报时电路_1_out_4 , \秒脉冲产生电路_1_out_2 , \闹钟_1_out_11 , \闹钟_1_out_16 ;
  wire [1:0] multiplexer_1_out, multiplexer_2_out;
  wire [3:0] n00_12_1_out_4, n00_12_1_out_5, n00_12_2_out_4, n00_12_2_out_5, \六十进制计数器_1_qa0 ,
       \六十进制计数器_1_qa1 , \六十进制计数器_2_qa0 , \六十进制计数器_2_qa1 , \十二进制计数器或二十四进制的计数器电路_1_out_10 ,
       \十二进制计数器或二十四进制的计数器电路_1_out_15 , \闹钟_1_out_12 , \闹钟_1_out_13 , \闹钟_1_out_14 , \闹钟_1_out_15 ;

  // Probe on n00_12_1_out_4
  or or_1 (or_1_out, and_1_out, ~\六十进制计数器_1_gcc );  // OR_Gate
  and and_1 (and_1_out, Cpu, multiplexer_2_out[0]);
  Multiplexer #(.select(1), .width(2), .disabled("Z"), .enable("false")) multiplexer_1 (
    .in0(2'b01), .in1(2'b10), .out(multiplexer_1_out), .sel(Adj1));
  not not_1 (not_1_out, Sel);
  and and_2 (and_2_out, Adj0, ~in_1);  // AND_Gate
  _00__12 u_00_12_1 (
    .out_4(n00_12_1_out_4), .out_5(n00_12_1_out_5), .in_2(\十二进制计数器或二十四进制的计数器电路_1_out_15 ),
    .in_3(\十二进制计数器或二十四进制的计数器电路_1_out_10 ), .in_1(Sel));
  Multiplexer #(.select(1), .width(2), .disabled("Z"), .enable("false")) multiplexer_2 (
    .in0(2'b00), .in1(multiplexer_1_out), .out(multiplexer_2_out), .sel(and_2_out));
  \十二进制计数器或二十四进制的计数器电路  \u_十二进制计数器或二十四进制的计数器电路_1  (
    .in_2(or_1_out), .in_3(multiplexer_2_out[0]), .in_4(Cpd), .in_5(Clr), .in_1(Sel),
    .out_11(\十二进制计数器或二十四进制的计数器电路_1_out_11 ), .out_7(\十二进制计数器或二十四进制的计数器电路_1_out_10 [3]),
    .out_8(\十二进制计数器或二十四进制的计数器电路_1_out_10 [2]), .out_9(\十二进制计数器或二十四进制的计数器电路_1_out_10 [1]),
    .out_10(\十二进制计数器或二十四进制的计数器电路_1_out_10 [0]), .out_12(\十二进制计数器或二十四进制的计数器电路_1_out_15 [3]),
    .out_13(\十二进制计数器或二十四进制的计数器电路_1_out_15 [2]), .out_14(\十二进制计数器或二十四进制的计数器电路_1_out_15 [1]),
    .out_15(\十二进制计数器或二十四进制的计数器电路_1_out_15 [0]));  // open: out_6
  \上下午文字显示的电路  \u_上下午文字显示的电路_1  (
    ._1(_1), ._2(_2), ._3(_3), ._4(_4), ._5(_5), .in_1(multiplexer_9_out), .in_2(not_1_out));
  and and_3 (and_3_out, Cpu, multiplexer_2_out[1]);
  or or_2 (or_2_out, and_3_out, ~\六十进制计数器_2_gcc );  // OR_Gate
  // Probe on \六十进制计数器_1_qa1 
  Multiplexer #(.select(1), .width(1), .disabled("Z"), .enable("false")) multiplexer_3 (
    .in0(CP), .in1(1'b0), .out(multiplexer_3_out), .sel(and_2_out));
  // Probe on \六十进制计数器_1_qa0 
  \六十进制计数器  \u_六十进制计数器_1  (
    .CPU(or_2_out), .CLR(Clr), .CPD(Cpd), .Adj(multiplexer_2_out[1]), .GCC(\六十进制计数器_1_gcc ),
    .QD1(\六十进制计数器_1_qa1 [3]), .QC1(\六十进制计数器_1_qa1 [2]), .QB1(\六十进制计数器_1_qa1 [1]), .QA1(\六十进制计数器_1_qa1 [0]),
    .QD0(\六十进制计数器_1_qa0 [3]), .QC0(\六十进制计数器_1_qa0 [2]), .QB0(\六十进制计数器_1_qa0 [1]), .QA0(\六十进制计数器_1_qa0 [0]));
  \秒脉冲产生电路  \u_秒脉冲产生电路_1  (.in_1(multiplexer_3_out), .out_2(\秒脉冲产生电路_1_out_2 ));
  \电子钟整点报时电路  \u_电子钟整点报时电路_1  (
    .Min2(\六十进制计数器_1_qa1 ), .Min1(\六十进制计数器_1_qa0 ), .Sel2(\六十进制计数器_2_qa1 ), .out_4(\电子钟整点报时电路_1_out_4 ));
  // Probe on \六十进制计数器_2_qa1 
  and and_4 (out_20, \电子钟整点报时电路_1_out_4 , \秒脉冲产生电路_1_out_2 );
  \六十进制计数器  \u_六十进制计数器_2  (
    .CPU(\秒脉冲产生电路_1_out_2 ), .CLR(Clr), .CPD(1'b0), .Adj(1'b0), .GCC(\六十进制计数器_2_gcc ),
    .QD1(\六十进制计数器_2_qa1 [3]), .QC1(\六十进制计数器_2_qa1 [2]), .QB1(\六十进制计数器_2_qa1 [1]), .QA1(\六十进制计数器_2_qa1 [0]),
    .QD0(\六十进制计数器_2_qa0 [3]), .QC0(\六十进制计数器_2_qa0 [2]), .QB0(\六十进制计数器_2_qa0 [1]), .QA0(\六十进制计数器_2_qa0 [0]));
  \闹钟  \u_闹钟_1  (
    .InputSec2(\六十进制计数器_2_qa1 ), .Input_Hour_2(\十二进制计数器或二十四进制的计数器电路_1_out_10 ),
    .Input_Min_1(\六十进制计数器_1_qa1 ), .Input_Min_2(\六十进制计数器_1_qa0 ),
    .Input_Hour_1(\十二进制计数器或二十四进制的计数器电路_1_out_15 ), .out_11(\闹钟_1_out_11 ), .alarm_set(in_1), .Cpu(Cpu),
    .Adj(Adj0), .in_9(Sel), .Cpd(Cpd), .out_13(\闹钟_1_out_13 ), .out_14(\闹钟_1_out_14 ),
    .out_15(\闹钟_1_out_15 ), .out_12(\闹钟_1_out_12 ), .out_16(\闹钟_1_out_16 ));
  Multiplexer #(.select(1), .width(4), .disabled("Z"), .enable("false")) multiplexer_4 (
    .in0(n00_12_1_out_5), .in1(n00_12_2_out_5), .out(Hour1), .sel(in_1));
  and and_5 (out_21, \闹钟_1_out_11 , comparator_1_eq, \秒脉冲产生电路_1_out_2 );
  Multiplexer #(.select(1), .width(4), .disabled("Z"), .enable("false")) multiplexer_5 (
    .in0(n00_12_1_out_4), .in1(n00_12_2_out_4), .out(Hour2), .sel(in_1));
  Multiplexer #(.select(1), .width(4), .disabled("Z"), .enable("false")) multiplexer_6 (
    .in0(\六十进制计数器_1_qa1 ), .in1(\闹钟_1_out_15 ), .out(Min1), .sel(in_1));
  _00__12 u_00_12_2 (
    .out_4(n00_12_2_out_4), .out_5(n00_12_2_out_5), .in_2(\闹钟_1_out_13 ), .in_3(\闹钟_1_out_14 ), .in_1(Sel));
  Multiplexer #(.select(1), .width(4), .disabled("Z"), .enable("false")) multiplexer_7 (
    .in0(\六十进制计数器_1_qa0 ), .in1(\闹钟_1_out_12 ), .out(Min2), .sel(in_1));
  Multiplexer #(.select(1), .width(4), .disabled("Z"), .enable("false")) multiplexer_8 (
    .in0(\六十进制计数器_2_qa1 ), .in1(4'b0000), .out(Sec1), .sel(in_1));
  Multiplexer #(.select(1), .width(1), .disabled("Z"), .enable("false")) multiplexer_9 (
    .in0(\十二进制计数器或二十四进制的计数器电路_1_out_11 ), .in1(\闹钟_1_out_16 ), .out(multiplexer_9_out), .sel(in_1));
  Comparator #(.width(1), .mode("twosComplement")) comparator_1 (
    .a(\十二进制计数器或二十四进制的计数器电路_1_out_11 ), .b(\闹钟_1_out_16 ), .eq(comparator_1_eq));  // open: gt, lt
  Multiplexer #(.select(1), .width(4), .disabled("Z"), .enable("false")) multiplexer_10 (
    .in0(\六十进制计数器_2_qa0 ), .in1(4'b0000), .out(Sec2), .sel(in_1));
endmodule

module \闹钟  (
  input  [3:0] InputSec2,
  input  [3:0] Input_Hour_2,
  input  [3:0] Input_Min_1,
  input  [3:0] Input_Min_2,
  input  [3:0] Input_Hour_1,
  input  alarm_set,
  input  Cpu,
  input  Adj,
  input  in_9,
  input  Cpd,
  output out_11,
  output [3:0] out_12,
  output [3:0] out_13,
  output [3:0] out_14,
  output [3:0] out_15,
  output out_16
);

  wire and_1_out, and_2_out, and_3_out, and_4_out, comparator_1_eq, comparator_2_eq, comparator_3_eq,
       comparator_4_eq, comparator_5_eq;

  Comparator #(.width(4), .mode("twosComplement")) comparator_1 (
    .a(out_13), .b(Input_Hour_1), .eq(comparator_1_eq));  // open: gt, lt
  and and_1 (and_1_out, Cpu, ~Adj, alarm_set);  // AND_Gate
  and and_2 (and_2_out, alarm_set, ~Adj, Cpd);  // AND_Gate
  Comparator #(.width(4), .mode("twosComplement")) comparator_2 (
    .a(out_14), .b(Input_Hour_2), .eq(comparator_2_eq));  // open: gt, lt
  Comparator #(.width(4), .mode("twosComplement")) comparator_3 (
    .a(out_15), .b(Input_Min_1), .eq(comparator_3_eq));  // open: gt, lt
  \十二进制计数器或二十四进制的计数器电路  \u_十二进制计数器或二十四进制的计数器电路_1  (
    .in_2(and_1_out), .in_3(1'b1), .in_4(and_2_out), .in_1(in_9), .out_11(out_16), .out_7(out_14[3]),
    .out_8(out_14[2]), .out_9(out_14[1]), .out_10(out_14[0]), .out_12(out_13[3]), .out_13(out_13[2]),
    .out_14(out_13[1]), .out_15(out_13[0]));  // open: out_6, in_5
  and and_3 (and_3_out, alarm_set, Cpu, Adj);
  and and_4 (and_4_out, Adj, Cpd, alarm_set);
  Comparator #(.width(4), .mode("twosComplement")) comparator_4 (
    .a(InputSec2), .b(4'b0000), .eq(comparator_4_eq));  // open: gt, lt
  Comparator #(.width(4), .mode("twosComplement")) comparator_5 (
    .a(out_12), .b(Input_Min_2), .eq(comparator_5_eq));  // open: gt, lt
  \六十进制计数器  \u_六十进制计数器_1  (
    .CPU(and_3_out), .CPD(and_4_out), .Adj(1'b1), .QD1(out_15[3]), .QC1(out_15[2]), .QB1(out_15[1]),
    .QA1(out_15[0]), .QD0(out_12[3]), .QC0(out_12[2]), .QB0(out_12[1]), .QA0(out_12[0]));  // open: CLR, GCC
  and and_5 (out_11, comparator_4_eq, 1'b1, comparator_1_eq, comparator_3_eq, comparator_5_eq, comparator_2_eq);
endmodule

module temp (
  input  in_1,
  input  in_2,
  input  in_3,
  input  in_4,
  input  in_5
);

  wire button_1_out, button_2_out, clock_1_out, \多功能数字钟_1_out_20 , \多功能数字钟_1_out_21 ;
  wire [3:0] \多功能数字钟_1_hour1 , \多功能数字钟_1_hour2 , \多功能数字钟_1_min1 , \多功能数字钟_1_min2 , \多功能数字钟_1_sec1 ,
       \多功能数字钟_1_sec2 ;
  wire [6:0] \多功能数字钟_1__1 , \多功能数字钟_1__2 , \多功能数字钟_1__3 , \多功能数字钟_1__4 , \多功能数字钟_1__5 ;

  DotMatrix #(.inputtype("column"), .matrixcols(5), .matrixrows(7), .persist(0), .dotshape("square")) dotmatrix_1 (
    .col0(\多功能数字钟_1__1 ), .col1(\多功能数字钟_1__2 ), .col2(\多功能数字钟_1__3 ), .col3(\多功能数字钟_1__4 ),
    .col4(\多功能数字钟_1__5 ));
  Button button_1 (.out(button_1_out));
  Clock #(.highDuration(1), .lowDuration(1)) clock_1 (.out(clock_1_out));
  \多功能数字钟  \u_多功能数字钟_1  (
    .Cpd(button_2_out), .Cpu(button_1_out), .Clr(in_4), .Sel(in_3), .Adj1(in_1), .out_20(\多功能数字钟_1_out_20 ),
    .Hour1(\多功能数字钟_1_hour1 ), .Hour2(\多功能数字钟_1_hour2 ), ._1(\多功能数字钟_1__1 ), ._2(\多功能数字钟_1__2 ),
    ._3(\多功能数字钟_1__3 ), ._4(\多功能数字钟_1__4 ), .Min1(\多功能数字钟_1_min1 ), .Min2(\多功能数字钟_1_min2 ),
    ._5(\多功能数字钟_1__5 ), .Sec1(\多功能数字钟_1_sec1 ), .Sec2(\多功能数字钟_1_sec2 ), .CP(clock_1_out), .in_1(in_5),
    .out_21(\多功能数字钟_1_out_21 ), .Adj0(in_2));
  Button button_2 (.out(button_2_out));
  Hex_Digit_Display hex_digit_display_1 (.value(\多功能数字钟_1_hour1 ));  // open: dp
  Hex_Digit_Display hex_digit_display_2 (.value(\多功能数字钟_1_hour2 ));  // open: dp
  Hex_Digit_Display hex_digit_display_3 (.value(\多功能数字钟_1_min1 ));  // open: dp
  Hex_Digit_Display hex_digit_display_4 (.value(\多功能数字钟_1_min2 ));  // open: dp
  Hex_Digit_Display hex_digit_display_5 (.value(\多功能数字钟_1_sec1 ));  // open: dp
  Hex_Digit_Display hex_digit_display_6 (.value(\多功能数字钟_1_sec2 ));  // open: dp
  LED #(.active("true")) led_1 (.in(\多功能数字钟_1_out_21 ));
  LED #(.active("true")) led_2 (.in(\多功能数字钟_1_out_20 ));
endmodule

module _00__12 (
  input  in_1,
  input  [3:0] in_2,
  input  [3:0] in_3,
  output [3:0] out_4,
  output [3:0] out_5
);

  wire and_1_out, comparator_1_eq, comparator_2_eq, not_1_out;

  not not_1 (not_1_out, in_1);
  Comparator #(.width(4), .mode("twosComplement")) comparator_1 (
    .a(in_2), .b(4'b0000), .eq(comparator_1_eq));  // open: gt, lt
  Comparator #(.width(4), .mode("twosComplement")) comparator_2 (
    .a(in_3), .b(4'b0000), .eq(comparator_2_eq));  // open: gt, lt
  and and_1 (and_1_out, comparator_1_eq, not_1_out, comparator_2_eq);
  Multiplexer #(.select(1), .width(4), .disabled("Z"), .enable("false")) multiplexer_1 (
    .in0(in_3), .in1(4'b0010), .out(out_4), .sel(and_1_out));
  Multiplexer #(.select(1), .width(4), .disabled("Z"), .enable("false")) multiplexer_2 (
    .in0(in_2), .in1(4'b0001), .out(out_5), .sel(and_1_out));
endmodule
