// Logisim project 实验4-CS1901-U201913821-朱旭鹏.circ as structural Verilog: 5 circuits, main circuit 四位除法器
module \四位除法器  (
  input  [3:0] n2,
  input  [3:0] d,
  output [3:0] out_3,
  output [3:0] out_4
);

  wire comparator_1_gt, comparator_2_gt, comparator_3_gt, comparator_4_gt;
  wire [3:0] multiplexer_1_out, multiplexer_2_out, multiplexer_3_out, multiplexer_4_out, multiplexer_5_out,
       multiplexer_6_out, or_1_out, or_2_out, or_3_out, or_4_out, shifter_1_out, shifter_2_out,
       shifter_3_out, shifter_4_out, subtractor_1_out, subtractor_2_out, subtractor_3_out, subtractor_4_out;
  wire [7:4] shifter_1_out_2, shifter_2_out_2, shifter_3_out_2, shifter_4_out_2;

  assign or_1_out = 4'b0001 | shifter_1_out;  // OR_Gate or_1, 4 bits wide
  Shifter #(.width(8), .shift("ll")) shifter_1 (
    .in({4'b0000, n2}), .\dist (3'b001), .out({shifter_1_out_2, shifter_1_out}));
  Multiplexer #(.select(1), .width(4), .disabled("Z"), .enable("false")) multiplexer_1 (
    .in0(or_1_out), .in1(shifter_1_out), .out(multiplexer_1_out), .sel(comparator_1_gt));
  Comparator #(.width(4), .mode("twosComplement")) comparator_1 (
    .a(d), .b(shifter_1_out_2), .gt(comparator_1_gt));  // open: eq, lt
  Subtractor #(.width(4)) subtractor_1 (.a(shifter_1_out_2), .b(d), .out(subtractor_1_out));  // open: bin, bout
  Multiplexer #(.select(1), .width(4), .disabled("Z"), .enable("false")) multiplexer_2 (
    .in0(subtractor_1_out), .in1(shifter_1_out_2), .out(multiplexer_2_out), .sel(comparator_1_gt));
  // Probe on d
  assign or_2_out = 4'b0001 | shifter_2_out;  // OR_Gate or_2, 4 bits wide
  Shifter #(.width(8), .shift("ll")) shifter_2 (
    .in({multiplexer_2_out, multiplexer_1_out}), .\dist (3'b001), .out({shifter_2_out_2, shifter_2_out}));
  Multiplexer #(.select(1), .width(4), .disabled("Z"), .enable("false")) multiplexer_3 (
    .in0(or_2_out), .in1(shifter_2_out), .out(multiplexer_3_out), .sel(comparator_2_gt));
  Comparator #(.width(4), .mode("twosComplement")) comparator_2 (
    .a(d), .b(shifter_2_out_2), .gt(comparator_2_gt));  // open: eq, lt
  Subtractor #(.width(4)) subtractor_2 (.a(shifter_2_out_2), .b(d), .out(subtractor_2_out));  // open: bin, bout
  Multiplexer #(.select(1), .width(4), .disabled("Z"), .enable("false")) multiplexer_4 (
    .in0(subtractor_2_out), .in1(shifter_2_out_2), .out(multiplexer_4_out), .sel(comparator_2_gt));
  assign or_3_out = 4'b0001 | shifter_3_out;  // OR_Gate or_3, 4 bits wide
  Shifter #(.width(8), .shift("ll")) shifter_3 (
    .in({multiplexer_4_out, multiplexer_3_out}), .\dist (3'b001), .out({shifter_3_out_2, shifter_3_out}));
  Multiplexer #(.select(1), .width(4), .disabled("Z"), .enable("false")) multiplexer_5 (
    .in0(or_3_out), .in1(shifter_3_out), .out(multiplexer_5_out), .sel(comparator_3_gt));
  Comparator #(.width(4), .mode("twosComplement")) comparator_3 (
    .a(d), .b(shifter_3_out_2), .gt(comparator_3_gt));  // open: eq, lt
  Subtractor #(.width(4)) subtractor_3 (.a(shifter_3_out_2), .b(d), .out(subtractor_3_out));  // open: bin, bout
  Multiplexer #(.select(1), .width(4), .disabled("Z"), .enable("false")) multiplexer_6 (
    .in0(subtractor_3_out), .in1(shifter_3_out_2), .out(multiplexer_6_out), .sel(comparator_3_gt));
  assign or_4_out = 4'b0001 | shifter_4_out;  // OR_Gate or_4, 4 bits wide
  Shifter #(.width(8), .shift("ll")) shifter_4 (
    .in({multiplexer_6_out, multiplexer_5_out}), .\dist (3'b001), .out({shifter_4_out_2, shifter_4_out}));
  Multiplexer #(.select(1), .width(4), .disabled("Z"), .enable("false")) multiplexer_7 (
    .in0(or_4_out), .in1(shifter_4_out), .out(out_3), .sel(comparator_4_gt));
  Comparator #(.width(4), .mode("twosComplement")) comparator_4 (
    .a(d), .b(shifter_4_out_2), .gt(comparator_4_gt));  // open: eq, lt
  Subtractor #(.width(4)) subtractor_4 (.a(shifter_4_out_2), .b(d), .out(subtractor_4_out));  // open: bin, bout
  Multiplexer #(.select(1), .width(4), .disabled("Z"), .enable("false")) multiplexer_8 (
    .in0(subtractor_4_out), .in1(shifter_4_out_2), .out(out_4), .sel(comparator_4_gt));
endmodule

module \四位除法器测试电路  (
  input  [3:0] in_1,
  input  [3:0] in_2,
  output [3:0] out_3,
  output [3:0] out_4
);

  \四位除法器  \u_四位除法器_1  (.n2(in_1), .d(in_2), .out_3(out_3), .out_4(out_4));
endmodule

module \_32位除法器测试电路  (
  input  [31:0] n,
  input  [31:0] d,
  output [31:0] quot,
  output [31:0] out_4
);

  \_32位除法器  \u_32位除法器_1  (.in_1(n), .in_2(d), .rem(out_4), .quot(quot));
endmodule

module \_32位除法器  (
  input  [31:0] in_1,
  input  [31:0] in_2,
  output [31:0] rem,
  output [31:0] quot
);

  wire [31:0] \n32位除法器1_1_next_quot , \n32位除法器1_1_next_rem , \n32位除法器1_2_next_quot , \n32位除法器1_2_next_rem ,
       \n32位除法器1_3_next_quot , \n32位除法器1_3_next_rem , \n32位除法器1_4_next_quot , \n32位除法器1_4_next_rem ,
       \n32位除法器1_5_next_quot , \n32位除法器1_5_next_rem , \n32位除法器1_6_next_quot , \n32位除法器1_6_next_rem ,
       \n32位除法器1_7_next_quot , \n32位除法器1_7_next_rem , \n32位除法器1_8_next_quot , \n32位除法器1_8_next_rem ,
       \n32位除法器1_9_next_quot , \n32位除法器1_9_next_rem , \n32位除法器1_10_next_quot , \n32位除法器1_10_next_rem ,
       \n32位除法器1_11_next_quot , \n32位除法器1_11_next_rem , \n32位除法器1_12_next_quot , \n32位除法器1_12_next_rem ,
       \n32位除法器1_13_next_quot , \n32位除法器1_13_next_rem , \n32位除法器1_14_next_quot , \n32位除法器1_14_next_rem ,
       \n32位除法器1_15_next_quot , \n32位除法器1_15_next_rem , \n32位除法器1_16_next_quot , \n32位除法器1_16_next_rem ,
       \n32位除法器1_17_next_quot , \n32位除法器1_17_next_rem , \n32位除法器1_18_next_quot , \n32位除法器1_18_next_rem ,
       \n32位除法器1_19_next_quot , \n32位除法器1_19_next_rem , \n32位除法器1_20_next_quot , \n32位除法器1_20_next_rem ,
       \n32位除法器1_21_next_quot , \n32位除法器1_21_next_rem , \n32位除法器1_22_next_quot , \n32位除法器1_22_next_rem ,
       \n32位除法器1_23_next_quot , \n32位除法器1_23_next_rem , \n32位除法器1_24_next_quot , \n32位除法器1_24_next_rem ,
       \n32位除法器1_25_next_quot , \n32位除法器1_25_next_rem , \n32位除法器1_26_next_quot , \n32位除法器1_26_next_rem ,
       \n32位除法器1_27_next_quot , \n32位除法器1_27_next_rem , \n32位除法器1_28_next_quot , \n32位除法器1_28_next_rem ,
       \n32位除法器1_29_next_quot , \n32位除法器1_29_next_rem , \n32位除法器1_30_next_quot , \n32位除法器1_30_next_rem ,
       \n32位除法器1_31_next_quot , \n32位除法器1_31_next_rem ;

  \_32位除法器1  \u_32位除法器1_1  (
    .d(in_1), .cur_rem({32{1'b0}}), .cur_quot(in_2), .next_rem(\n32位除法器1_1_next_rem ),
    .next_quot(\n32位除法器1_1_next_quot ));
  \_32位除法器1  \u_32位除法器1_2  (
    .d(in_1), .cur_rem(\n32位除法器1_31_next_rem ), .cur_quot(\n32位除法器1_31_next_quot ),
    .next_rem(\n32位除法器1_2_next_rem ), .next_quot(\n32位除法器1_2_next_quot ));
  \_32位除法器1  \u_32位除法器1_3  (
    .d(in_1), .cur_rem(\n32位除法器1_1_next_rem ), .cur_quot(\n32位除法器1_1_next_quot ),
    .next_rem(\n32位除法器1_3_next_rem ), .next_quot(\n32位除法器1_3_next_quot ));
  \_32位除法器1  \u_32位除法器1_4  (
    .d(in_1), .cur_rem(\n32位除法器1_2_next_rem ), .cur_quot(\n32位除法器1_2_next_quot ),
    .next_rem(\n32位除法器1_4_next_rem ), .next_quot(\n32位除法器1_4_next_quot ));
  // Probe on \n32位除法器1_4_next_rem 
  \_32位除法器1  \u_32位除法器1_5  (
    .d(in_1), .cur_rem(\n32位除法器1_3_next_rem ), .cur_quot(\n32位除法器1_3_next_quot ),
    .next_rem(\n32位除法器1_5_next_rem ), .next_quot(\n32位除法器1_5_next_quot ));
  \_32位除法器1  \u_32位除法器1_6  (
    .d(in_1), .cur_rem(\n32位除法器1_4_next_rem ), .cur_quot(\n32位除法器1_4_next_quot ),
    .next_rem(\n32位除法器1_6_next_rem ), .next_quot(\n32位除法器1_6_next_quot ));
  \_32位除法器1  \u_32位除法器1_7  (
    .d(in_1), .cur_rem(\n32位除法器1_5_next_rem ), .cur_quot(\n32位除法器1_5_next_quot ),
    .next_rem(\n32位除法器1_7_next_rem ), .next_quot(\n32位除法器1_7_next_quot ));
  \_32位除法器1  \u_32位除法器1_8  (
    .d(in_1), .cur_rem(\n32位除法器1_6_next_rem ), .cur_quot(\n32位除法器1_6_next_quot ),
    .next_rem(\n32位除法器1_8_next_rem ), .next_quot(\n32位除法器1_8_next_quot ));
  \_32位除法器1  \u_32位除法器1_9  (
    .d(in_1), .cur_rem(\n32位除法器1_7_next_rem ), .cur_quot(\n32位除法器1_7_next_quot ),
    .next_rem(\n32位除法器1_9_next_rem ), .next_quot(\n32位除法器1_9_next_quot ));
  \_32位除法器1  \u_32位除法器1_10  (
    .d(in_1), .cur_rem(\n32位除法器1_8_next_rem ), .cur_quot(\n32位除法器1_8_next_quot ),
    .next_rem(\n32位除法器1_10_next_rem ), .next_quot(\n32位除法器1_10_next_quot ));
  \_32位除法器1  \u_32位除法器1_11  (
    .d(in_1), .cur_rem(\n32位除法器1_9_next_rem ), .cur_quot(\n32位除法器1_9_next_quot ),
    .next_rem(\n32位除法器1_11_next_rem ), .next_quot(\n32位除法器1_11_next_quot ));
  \_32位除法器1  \u_32位除法器1_12  (
    .d(in_1), .cur_rem(\n32位除法器1_10_next_rem ), .cur_quot(\n32位除法器1_10_next_quot ),
    .next_rem(\n32位除法器1_12_next_rem ), .next_quot(\n32位除法器1_12_next_quot ));
  \_32位除法器1  \u_32位除法器1_13  (
    .d(in_1), .cur_rem(\n32位除法器1_11_next_rem ), .cur_quot(\n32位除法器1_11_next_quot ),
    .next_rem(\n32位除法器1_13_next_rem ), .next_quot(\n32位除法器1_13_next_quot ));
  \_32位除法器1  \u_32位除法器1_14  (
    .d(in_1), .cur_rem(\n32位除法器1_12_next_rem ), .cur_quot(\n32位除法器1_12_next_quot ),
    .next_rem(\n32位除法器1_14_next_rem ), .next_quot(\n32位除法器1_14_next_quot ));
  \_32位除法器1  \u_32位除法器1_15  (
    .d(in_1), .cur_rem(\n32位除法器1_13_next_rem ), .cur_quot(\n32位除法器1_13_next_quot ),
    .next_rem(\n32位除法器1_15_next_rem ), .next_quot(\n32位除法器1_15_next_quot ));
  \_32位除法器1  \u_32位除法器1_16  (
    .d(in_1), .cur_rem(\n32位除法器1_14_next_rem ), .cur_quot(\n32位除法器1_14_next_quot ),
    .next_rem(\n32位除法器1_16_next_rem ), .next_quot(\n32位除法器1_16_next_quot ));
  \_32位除法器1  \u_32位除法器1_17  (
    .d(in_1), .cur_rem(\n32位除法器1_15_next_rem ), .cur_quot(\n32位除法器1_15_next_quot ),
    .next_rem(\n32位除法器1_17_next_rem ), .next_quot(\n32位除法器1_17_next_quot ));
  \_32位除法器1  \u_32位除法器1_18  (
    .d(in_1), .cur_rem(\n32位除法器1_16_next_rem ), .cur_quot(\n32位除法器1_16_next_quot ),
    .next_rem(\n32位除法器1_18_next_rem ), .next_quot(\n32位除法器1_18_next_quot ));
  \_32位除法器1  \u_32位除法器1_19  (
    .d(in_1), .cur_rem(\n32位除法器1_17_next_rem ), .cur_quot(\n32位除法器1_17_next_quot ),
    .next_rem(\n32位除法器1_19_next_rem ), .next_quot(\n32位除法器1_19_next_quot ));
  \_32位除法器1  \u_32位除法器1_20  (
    .d(in_1), .cur_rem(\n32位除法器1_18_next_rem ), .cur_quot(\n32位除法器1_18_next_quot ),
    .next_rem(\n32位除法器1_20_next_rem ), .next_quot(\n32位除法器1_20_next_quot ));
  \_32位除法器1  \u_32位除法器1_21  (
    .d(in_1), .cur_rem(\n32位除法器1_19_next_rem ), .cur_quot(\n32位除法器1_19_next_quot ),
    .next_rem(\n32位除法器1_21_next_rem ), .next_quot(\n32位除法器1_21_next_quot ));
  \_32位除法器1  \u_32位除法器1_22  (
    .d(in_1), .cur_rem(\n32位除法器1_20_next_rem ), .cur_quot(\n32位除法器1_20_next_quot ),
    .next_rem(\n32位除法器1_22_next_rem ), .next_quot(\n32位除法器1_22_next_quot ));
  \_32位除法器1  \u_32位除法器1_23  (
    .d(in_1), .cur_rem(\n32位除法器1_21_next_rem ), .cur_quot(\n32位除法器1_21_next_quot ),
    .next_rem(\n32位除法器1_23_next_rem ), .next_quot(\n32位除法器1_23_next_quot ));
  \_32位除法器1  \u_32位除法器1_24  (
    .d(in_1), .cur_rem(\n32位除法器1_22_next_rem ), .cur_quot(\n32位除法器1_22_next_quot ),
    .next_rem(\n32位除法器1_24_next_rem ), .next_quot(\n32位除法器1_24_next_quot ));
  \_32位除法器1  \u_32位除法器1_25  (
    .d(in_1), .cur_rem(\n32位除法器1_23_next_rem ), .cur_quot(\n32位除法器1_23_next_quot ),
    .next_rem(\n32位除法器1_25_next_rem ), .next_quot(\n32位除法器1_25_next_quot ));
  \_32位除法器1  \u_32位除法器1_26  (
    .d(in_1), .cur_rem(\n32位除法器1_24_next_rem ), .cur_quot(\n32位除法器1_24_next_quot ),
    .next_rem(\n32位除法器1_26_next_rem ), .next_quot(\n32位除法器1_26_next_quot ));
  \_32位除法器1  \u_32位除法器1_27  (
    .d(in_1), .cur_rem(\n32位除法器1_25_next_rem ), .cur_quot(\n32位除法器1_25_next_quot ),
    .next_rem(\n32位除法器1_27_next_rem ), .next_quot(\n32位除法器1_27_next_quot ));
  \_32位除法器1  \u_32位除法器1_28  (
    .d(in_1), .cur_rem(\n32位除法器1_26_next_rem ), .cur_quot(\n32位除法器1_26_next_quot ),
    .next_rem(\n32位除法器1_28_next_rem ), .next_quot(\n32位除法器1_28_next_quot ));
  \_32位除法器1  \u_32位除法器1_29  (
    .d(in_1), .cur_rem(\n32位除法器1_27_next_rem ), .cur_quot(\n32位除法器1_27_next_quot ),
    .next_rem(\n32位除法器1_29_next_rem ), .next_quot(\n32位除法器1_29_next_quot ));
  \_32位除法器1  \u_32位除法器1_30  (
    .d(in_1), .cur_rem(\n32位除法器1_28_next_rem ), .cur_quot(\n32位除法器1_28_next_quot ),
    .next_rem(\n32位除法器1_30_next_rem ), .next_quot(\n32位除法器1_30_next_quot ));
  \_32位除法器1  \u_32位除法器1_31  (
    .d(in_1), .cur_rem(\n32位除法器1_29_next_rem ), .cur_quot(\n32位除法器1_29_next_quot ),
    .next_rem(\n32位除法器1_31_next_rem ), .next_quot(\n32位除法器1_31_next_quot ));
  \_32位除法器1  \u_32位除法器1_32  (
    .d(in_1), .cur_rem(\n32位除法器1_30_next_rem ), .cur_quot(\n32位除法器1_30_next_quot ), .next_rem(rem),
    .next_quot(quot));
endmodule

module \_32位除法器1  (
  input  [31:0] d,
  input  [31:0] cur_rem,
  input  [31:0] cur_quot,
  output [31:0] next_rem,
  output [31:0] next_quot
);

  wire comparator_1_gt;
  wire [31:0] or_1_out, or_2_out, shifter_1_out, shifter_2_out, shifter_3_out, subtractor_1_out;

  Shifter #(.width(32), .shift("ll")) shifter_1 (.in(cur_rem), .\dist (5'b00001), .out(shifter_1_out));
  assign or_1_out = shifter_1_out | shifter_2_out;  // OR_Gate or_1, 32 bits wide
  Shifter #(.width(32), .shift("lr")) shifter_2 (.in(cur_quot), .\dist ({5{1'b1}}), .out(shifter_2_out));
  Shifter #(.width(32), .shift("ll")) shifter_3 (.in(cur_quot), .\dist (5'b00001), .out(shifter_3_out));
  Multiplexer #(.select(1), .width(32), .disabled("Z"), .enable("false")) multiplexer_1 (
    .in0(or_2_out), .in1(shifter_3_out), .out(next_quot), .sel(comparator_1_gt));
  Subtractor #(.width(32)) subtractor_1 (.a(or_1_out), .b(d), .out(subtractor_1_out));  // open: bin, bout
  Comparator #(.width(32), .mode("twosComplement")) comparator_1 (
    .a(d), .b(or_1_out), .gt(comparator_1_gt));  // open: eq, lt
  assign or_2_out = 32'h1 | shifter_3_out;  // OR_Gate or_2, 32 bits wide
  Multiplexer #(.select(1), .width(32), .disabled("Z"), .enable("false")) multiplexer_2 (
    .in0(subtractor_1_out), .in1(or_1_out), .out(next_rem), .sel(comparator_1_gt));
endmodule
