// Logisim project cpu24.circ as structural Verilog: 27 circuits, main circuit ◇单周期MIPS
module \单周期MIPS  (
  input  in_1,
  input  in_2
);

  wire and_1_out, and_2_out, and_3_out, BLTZ, CLK, comparator_1_eq, halt, LB, Led, MemToReg, MemWrite,
       mips_alu_1_equal, not_1_out, or_1_out, or_2_out, RegWrite, SignedExt, SLLV, \单周期硬布线控制器_1_alu_src ,
       \单周期硬布线控制器_1_beq , \单周期硬布线控制器_1_bne , \单周期硬布线控制器_1_jal , \单周期硬布线控制器_1_jmp , \单周期硬布线控制器_1_jr ,
       \单周期硬布线控制器_1_regdst , \单周期硬布线控制器_1_syscall ;
  wire [3:0] \单周期硬布线控制器_1_alu_op ;
  wire [4:0] multiplexer_4_out, multiplexer_5_out, multiplexer_6_out, multiplexer_7_out, multiplexer_8_out;
  wire [7:0] multiplexer_12_out;
  wire [31:0] adder_2_out, Addr, bit_extender_1_out, bit_extender_2_out, bit_extender_3_out, IR, LedData,
       MDin, multiplexer_1_out, multiplexer_2_out, multiplexer_3_out, multiplexer_9_out, multiplexer_10_out,
       multiplexer_11_out, multiplexer_13_out, multiplexer_15_out, PC, PC_4, R1, ram_1_data, RDin,
       shifter_1_out;

  Clock #(.highDuration(1), .lowDuration(1)) clock_1 (.out(CLK));
  Multiplexer #(.select(1), .width(32), .disabled("Z"), .enable("false")) multiplexer_1 (
    .in0(PC_4), .in1(adder_2_out), .out(multiplexer_1_out), .sel(or_2_out));
  Multiplexer #(.select(1), .width(32), .disabled("Z"), .enable("false")) multiplexer_2 (
    .in0(multiplexer_1_out), .in1({PC[31:28], IR[25:0], 2'b00}), .out(multiplexer_2_out),
    .sel(\单周期硬布线控制器_1_jmp ));
  // Probe on multiplexer_3_out
  Multiplexer #(.select(1), .width(32), .disabled("Z"), .enable("false")) multiplexer_3 (
    .in0(multiplexer_2_out), .in1(R1), .out(multiplexer_3_out), .sel(\单周期硬布线控制器_1_jr ));
  or or_1 (or_1_out, not_1_out, in_1);
  not not_1 (not_1_out, halt);
  Register #(.width(32), .trigger("rising"), .Select("low")) u_PC (
    .D(multiplexer_3_out), .en(or_1_out), .Q(PC), .clk(CLK), .clr(in_2));
  Adder #(.width(32)) adder_1 (.a(PC), .b(32'h4), .out(PC_4));  // open: cin, cout
  ROM #(.addrWidth(10), .dataWidth(32), .Select("high")) rom_1 (.addr(PC[11:2]), .data(IR));
  \单周期硬布线控制器  \u_单周期硬布线控制器_1  (
    .Func(IR[5:0]), .OP(IR[31:26]), .ALU_OP(\单周期硬布线控制器_1_alu_op ), .MemToReg(MemToReg), .MemWrite(MemWrite),
    .ALU_SRC(\单周期硬布线控制器_1_alu_src ), .SysCALL(\单周期硬布线控制器_1_syscall ), .SignedExt(SignedExt),
    .RegDst(\单周期硬布线控制器_1_regdst ), .JR(\单周期硬布线控制器_1_jr ), .JMP(\单周期硬布线控制器_1_jmp ), .Beq(\单周期硬布线控制器_1_beq ),
    .JAL(\单周期硬布线控制器_1_jal ), .Bne(\单周期硬布线控制器_1_bne ), .SLLV(SLLV), .LB(LB), .BLTZ(BLTZ), .RegWrite(RegWrite));  // open: out_20, out_21, ERET, Func_2, MFC0, MTC0
  Multiplexer #(.select(1), .width(5), .disabled("Z"), .enable("false")) multiplexer_4 (
    .in0(IR[25:21]), .in1(5'b00010), .out(multiplexer_4_out), .sel(\单周期硬布线控制器_1_syscall ));
  Multiplexer #(.select(1), .width(5), .disabled("Z"), .enable("false")) multiplexer_5 (
    .in0(IR[20:16]), .in1(5'b00100), .out(multiplexer_5_out), .sel(\单周期硬布线控制器_1_syscall ));
  Multiplexer #(.select(1), .width(5), .disabled("Z"), .enable("false")) multiplexer_6 (
    .in0(IR[20:16]), .in1(IR[15:11]), .out(multiplexer_6_out), .sel(\单周期硬布线控制器_1_regdst ));
  Multiplexer #(.select(1), .width(5), .disabled("Z"), .enable("false")) multiplexer_7 (
    .in0(IR[10:6]), .in1(R1[4:0]), .out(multiplexer_7_out), .sel(SLLV));
  assign bit_extender_1_out = {{16{1'b0}}, IR[15:0]};  // Bit_Extender bit_extender_1
  assign bit_extender_2_out = {{16{IR[15]}}, IR[15:0]};  // Bit_Extender bit_extender_2
  Multiplexer #(.select(1), .width(5), .disabled("Z"), .enable("false")) multiplexer_8 (
    .in0(multiplexer_6_out), .in1({5{1'b1}}), .out(multiplexer_8_out), .sel(\单周期硬布线控制器_1_jal ));
  Multiplexer #(.select(1), .width(32), .disabled("Z"), .enable("false")) multiplexer_9 (
    .in0(bit_extender_1_out), .in1(bit_extender_2_out), .out(multiplexer_9_out), .sel(SignedExt));
  Shifter #(.width(32), .shift("ll")) shifter_1 (.in(bit_extender_2_out), .\dist (5'b00010), .out(shifter_1_out));
  MIPS_Regifile mips_regifile_1 (
    .Din(RDin), .Clk(CLK), .R1(R1), .R2(MDin), .WE(RegWrite), .WAdr(multiplexer_8_out),
    .R1Adr(multiplexer_4_out), .R2Adr(multiplexer_5_out));
  Multiplexer #(.select(1), .width(32), .disabled("Z"), .enable("false")) multiplexer_10 (
    .in0(MDin), .in1(multiplexer_9_out), .out(multiplexer_10_out), .sel(\单周期硬布线控制器_1_alu_src ));
  MIPS_ALU mips_alu_1 (
    .X(R1), .Y(multiplexer_11_out), .AluOP(\单周期硬布线控制器_1_alu_op ), .Equal(mips_alu_1_equal), .Result(Addr),
    .shamt(multiplexer_7_out));  // open: Result_2
  Multiplexer #(.select(1), .width(32), .disabled("Z"), .enable("false")) multiplexer_11 (
    .in0(multiplexer_10_out), .in1({32{1'b0}}), .out(multiplexer_11_out), .sel(BLTZ));
  Adder #(.width(32)) adder_2 (.a(shifter_1_out), .b(PC_4), .out(adder_2_out));  // open: cin, cout
  and and_1 (and_1_out, Addr[0], BLTZ);
  and and_2 (and_2_out, \单周期硬布线控制器_1_beq , mips_alu_1_equal);
  and and_3 (and_3_out, \单周期硬布线控制器_1_bne , ~mips_alu_1_equal);  // AND_Gate
  or or_2 (or_2_out, and_2_out, and_1_out, and_3_out);
  Comparator #(.width(32), .mode("twosComplement")) comparator_1 (
    .a(R1), .b(32'h22), .eq(comparator_1_eq));  // open: gt, lt
  Register #(.width(32), .trigger("rising"), .Select("low")) register_1 (
    .D(MDin), .en(Led), .Q(LedData), .clk(CLK));  // open: clr
  and and_4 (Led, \单周期硬布线控制器_1_syscall , comparator_1_eq);
  and and_5 (halt, \单周期硬布线控制器_1_syscall , ~comparator_1_eq);  // AND_Gate
  RAM #(.addrWidth(10), .dataWidth(32), .bus("separate"), .Select("high")) ram_1 (
    .addr(Addr[11:2]), .din(MDin), .data(ram_1_data), .str(MemWrite), .clk(CLK), .clr(in_2));  // open: sel, ld
  Multiplexer #(.select(2), .width(8), .disabled("Z"), .enable("false")) multiplexer_12 (
    .in0(ram_1_data[7:0]), .in1(ram_1_data[15:8]), .in2(ram_1_data[23:16]), .in3(ram_1_data[31:24]),
    .out(multiplexer_12_out), .sel(Addr[1:0]));
  Multiplexer #(.select(1), .width(32), .disabled("Z"), .enable("false")) multiplexer_13 (
    .in0(Addr), .in1(multiplexer_15_out), .out(multiplexer_13_out), .sel(MemToReg));
  assign bit_extender_3_out = {{24{multiplexer_12_out[7]}}, multiplexer_12_out};  // Bit_Extender bit_extender_3
  Multiplexer #(.select(1), .width(32), .disabled("Z"), .enable("false")) multiplexer_14 (
    .in0(multiplexer_13_out), .in1(PC_4), .out(RDin), .sel(\单周期硬布线控制器_1_jal ));
  Multiplexer #(.select(1), .width(32), .disabled("Z"), .enable("false")) multiplexer_15 (
    .in0(ram_1_data), .in1(bit_extender_3_out), .out(multiplexer_15_out), .sel(LB));

  // Other names for the same wires on the sheet: Go = in_1; RST = in_2

  // Notes on the sheet:
  //   总复位信号应将除ROM以外所有存储组件全部清零
  //   指令存储器
  //   指令字
  //   contents of rom_1 (hex, n*v repeats v):
  //   2011fff1 112020 20020022 c 22310001 620fffb 2002000a c 20090000 200b0010 34118483 20120404 118c00
  //   129400 36318281 22520404 ad310000 2328820 21290004 216bffff 1560fffb 200b0020 20090000 81310000
  //   112020 20020022 c 21290001 216bffff 1560fff9 2002000a c 20080001 20090003 20110876 112020 20020022 c
  //   200b0008 1118804 1318804 112020 20020022 c 216bffff 1560fff9 2002000a c 2008ffff 20117777 112020
  //   20020022 c 200b0010 3a31ffff 112020 20020022 c 216bffff 1560fffa 2002000a c
  //   JMP
  //   JR
  //   OP
  //   Func
  //   rs
  //   rt
  //   rd
  //   shamt
  //   imm16
  //   imm26
  //   Beq
  //   Bne
  //   MemToReg
  //   MemWrite
  //   AluOP
  //   AluSrcB
  //   RegWrite
  //   JAL
  //   RegDst
  //   Syscall
endmodule

// 单周期硬布线控制器
module \单周期硬布线控制器  (
  input  [5:0] OP,
  input  [5:0] Func,
  input  [4:0] Func_2,
  output [3:0] ALU_OP,
  output RegWrite,
  output MemToReg,
  output MemWrite,
  output ALU_SRC,
  output SysCALL,
  output SignedExt,
  output RegDst,
  output Beq,
  output Bne,
  output JR,
  output JMP,
  output JAL,
  output SLLV,
  output LB,
  output BLTZ,
  output out_20,
  output out_21,
  output ERET,
  output MFC0,
  output MTC0
);

  wire comparator_1_eq, comparator_2_eq, comparator_3_eq, comparator_4_eq, or_1_out, undriven;

  Comparator #(.width(6), .mode("twosComplement")) comparator_1 (
    .a(OP), .b(6'b010000), .eq(comparator_1_eq));  // open: gt, lt
  Comparator #(.width(6), .mode("twosComplement")) comparator_2 (
    .a(Func), .b(6'b011000), .eq(comparator_2_eq));  // open: gt, lt
  Comparator #(.width(5), .mode("twosComplement")) comparator_3 (
    .a(Func_2), .b({5{1'b0}}), .eq(comparator_3_eq));  // open: gt, lt
  Comparator #(.width(5), .mode("twosComplement")) comparator_4 (
    .a(Func_2), .b(5'b00100), .eq(comparator_4_eq));  // open: gt, lt
  \运算控制器自动生成  \u_运算控制器自动生成_1  (
    .OP0(OP[0]), .OP1(OP[1]), .OP2(OP[2]), .OP3(OP[3]), .OP4(OP[4]), .OP5(OP[5]), .F0(Func[0]), .F1(Func[1]),
    .F2(Func[2]), .F3(Func[3]), .F4(Func[4]), .F5(Func[5]), .S0(ALU_OP[0]), .S1(ALU_OP[1]), .S2(ALU_OP[2]),
    .S3(ALU_OP[3]));
  \控制信号自动生成  \u_控制信号自动生成_1  (
    .OP0(OP[0]), .OP1(OP[1]), .OP2(OP[2]), .OP3(OP[3]), .OP4(OP[4]), .OP5(OP[5]), .F0(Func[0]), .F1(Func[1]),
    .F2(Func[2]), .F3(Func[3]), .F4(Func[4]), .F5(Func[5]), .MemToReg(MemToReg), .MemWrite(MemWrite),
    .ALU_SRC(ALU_SRC), .RegWrite(RegWrite), .SysCALL(SysCALL), .SignedExt(SignedExt), .RegDst(RegDst),
    .BEQ(Beq), .BNE(Bne), .JR(JR), .JUMP(JMP), .JAL(JAL), .SLLV(SLLV), .LB(LB), .BLTZ(BLTZ));
  \寄存器使用情况电路  \u_寄存器使用情况电路_1  (
    .OP0(OP[0]), .OP1(OP[1]), .OP2(OP[2]), .OP3(OP[3]), .OP4(OP[4]), .OP5(OP[5]), .F0(Func[0]), .F1(Func[1]),
    .F2(Func[2]), .F3(Func[3]), .F4(Func[4]), .F5(Func[5]), .R1_USED(out_20), .R2_USED(out_21));
  and and_1 (ERET, comparator_1_eq, comparator_2_eq);
  and and_2 (MFC0, comparator_3_eq, comparator_1_eq);
  and and_3 (MTC0, comparator_4_eq, comparator_1_eq);
  or or_1 (or_1_out, MFC0, undriven);

  // Other names for the same wires on the sheet: MF_MC[4:0] = Func_2; OP_CODE[5:0] = OP

  // Notes on the sheet:
  //   运算器控制器，根据指令生成运算器功能选择信号
  //   控制信号生成，产生数据通路需要的其他控制信号
endmodule

// 运算器控制器
module \运算控制器自动生成  (
  input  OP0,
  input  OP1,
  input  OP2,
  input  OP3,
  input  OP4,
  input  OP5,
  input  F0,
  input  F1,
  input  F2,
  input  F3,
  input  F4,
  input  F5,
  output S0,
  output S1,
  output S2,
  output S3
);

  wire and_1_out, and_2_out, and_3_out, and_4_out, and_5_out, and_6_out, and_7_out, and_8_out, and_9_out,
       and_10_out, and_11_out, and_12_out, and_13_out, and_14_out, and_15_out, and_16_out, and_17_out,
       and_18_out, and_19_out, and_20_out, and_21_out, and_22_out, and_23_out, and_24_out, and_25_out,
       and_26_out, and_27_out, and_28_out, and_29_out, and_30_out, and_31_out, and_32_out, and_33_out,
       not_1_out, not_2_out, not_3_out, not_4_out, not_5_out, not_6_out, not_7_out, not_8_out, not_9_out,
       not_10_out, not_11_out, not_12_out, not_13_out, not_14_out, not_15_out, not_16_out, not_17_out,
       not_18_out, not_19_out, not_20_out, not_21_out, not_22_out, not_23_out, not_24_out, not_25_out,
       not_26_out, not_27_out, not_28_out, not_29_out, not_30_out, not_31_out, not_32_out, not_33_out,
       not_34_out, not_35_out, not_36_out, not_37_out, not_38_out, not_39_out, not_40_out, not_41_out,
       not_42_out, not_43_out, not_44_out, not_45_out, not_46_out, not_47_out, not_48_out, not_49_out,
       not_50_out, not_51_out, not_52_out, not_53_out, not_54_out, not_55_out, not_56_out, not_57_out,
       not_58_out, not_59_out, not_60_out, not_61_out, not_62_out, not_63_out, not_64_out, not_65_out,
       not_66_out, not_67_out, not_68_out, not_69_out, not_70_out, not_71_out, not_72_out, not_73_out,
       not_74_out, not_75_out, not_76_out, not_77_out, not_78_out, not_79_out, not_80_out, not_81_out,
       not_82_out, not_83_out, not_84_out, not_85_out, not_86_out, not_87_out, not_88_out, not_89_out,
       not_90_out, not_91_out, not_92_out, not_93_out, not_94_out, not_95_out, not_96_out, not_97_out,
       not_98_out, not_99_out, not_100_out, not_101_out, not_102_out, not_103_out, not_104_out, not_105_out,
       not_106_out, not_107_out, not_108_out, not_109_out, not_110_out, not_111_out, not_112_out,
       not_113_out, not_114_out, not_115_out, not_116_out, not_117_out, not_118_out, not_119_out,
       not_120_out, not_121_out, not_122_out, not_123_out, not_124_out, not_125_out, not_126_out,
       not_127_out, not_128_out, not_129_out, not_130_out, not_131_out, not_132_out, not_133_out,
       not_134_out, not_135_out, not_136_out, not_137_out, not_138_out, not_139_out, not_140_out,
       not_141_out, not_142_out, not_143_out, not_144_out, not_145_out, not_146_out, not_147_out,
       not_148_out, not_149_out, not_150_out, not_151_out, not_152_out, not_153_out, not_154_out,
       not_155_out, not_156_out, not_157_out, not_158_out, not_159_out, not_160_out, not_161_out,
       not_162_out, not_163_out, not_164_out, not_165_out, not_166_out, not_167_out, not_168_out,
       not_169_out, not_170_out, not_171_out, not_172_out, not_173_out, not_174_out, not_175_out,
       not_176_out, not_177_out, not_178_out, not_179_out, not_180_out, not_181_out, not_182_out,
       not_183_out, not_184_out, not_185_out, not_186_out, not_187_out, not_188_out, not_189_out;

  not not_1 (not_1_out, OP1);
  not not_2 (not_2_out, OP2);
  not not_3 (not_3_out, OP4);
  not not_4 (not_4_out, OP5);
  not not_5 (not_5_out, F1);
  not not_6 (not_6_out, F2);
  not not_7 (not_7_out, F3);
  not not_8 (not_8_out, F4);
  not not_9 (not_9_out, OP1);
  not not_10 (not_10_out, OP2);
  not not_11 (not_11_out, OP4);
  not not_12 (not_12_out, OP5);
  not not_13 (not_13_out, F0);
  not not_14 (not_14_out, F1);
  not not_15 (not_15_out, F4);
  not not_16 (not_16_out, OP1);
  not not_17 (not_17_out, OP2);
  not not_18 (not_18_out, OP4);
  not not_19 (not_19_out, OP5);
  not not_20 (not_20_out, F0);
  not not_21 (not_21_out, F3);
  not not_22 (not_22_out, F4);
  not not_23 (not_23_out, OP1);
  not not_24 (not_24_out, OP2);
  not not_25 (not_25_out, OP4);
  not not_26 (not_26_out, OP5);
  not not_27 (not_27_out, F0);
  not not_28 (not_28_out, F2);
  not not_29 (not_29_out, F4);
  not not_30 (not_30_out, OP1);
  not not_31 (not_31_out, OP2);
  not not_32 (not_32_out, OP4);
  not not_33 (not_33_out, OP5);
  not not_34 (not_34_out, F2);
  not not_35 (not_35_out, F3);
  not not_36 (not_36_out, F4);
  not not_37 (not_37_out, F5);
  not not_38 (not_38_out, OP0);
  not not_39 (not_39_out, OP1);
  not not_40 (not_40_out, OP2);
  not not_41 (not_41_out, OP3);
  not not_42 (not_42_out, OP4);
  not not_43 (not_43_out, OP0);
  not not_44 (not_44_out, OP4);
  not not_45 (not_45_out, OP5);
  not not_46 (not_46_out, OP4);
  not not_47 (not_47_out, OP5);
  not not_48 (not_48_out, OP1);
  not not_49 (not_49_out, OP2);
  not not_50 (not_50_out, OP4);
  not not_51 (not_51_out, OP5);
  not not_52 (not_52_out, OP2);
  not not_53 (not_53_out, OP4);
  not not_54 (not_54_out, OP1);
  not not_55 (not_55_out, OP2);
  not not_56 (not_56_out, OP3);
  not not_57 (not_57_out, OP4);
  not not_58 (not_58_out, OP5);
  not not_59 (not_59_out, F0);
  not not_60 (not_60_out, F1);
  not not_61 (not_61_out, F3);
  not not_62 (not_62_out, F4);
  not not_63 (not_63_out, OP1);
  not not_64 (not_64_out, OP2);
  not not_65 (not_65_out, OP3);
  not not_66 (not_66_out, OP4);
  not not_67 (not_67_out, OP5);
  not not_68 (not_68_out, F0);
  not not_69 (not_69_out, F2);
  not not_70 (not_70_out, F3);
  not not_71 (not_71_out, F4);
  not not_72 (not_72_out, OP1);
  not not_73 (not_73_out, OP2);
  not not_74 (not_74_out, OP3);
  not not_75 (not_75_out, OP4);
  not not_76 (not_76_out, OP5);
  not not_77 (not_77_out, F0);
  not not_78 (not_78_out, F2);
  not not_79 (not_79_out, F4);
  not not_80 (not_80_out, OP1);
  not not_81 (not_81_out, OP2);
  not not_82 (not_82_out, OP3);
  not not_83 (not_83_out, OP4);
  not not_84 (not_84_out, OP5);
  not not_85 (not_85_out, F3);
  not not_86 (not_86_out, F4);
  not not_87 (not_87_out, OP0);
  not not_88 (not_88_out, OP1);
  not not_89 (not_89_out, OP4);
  not not_90 (not_90_out, OP5);
  not not_91 (not_91_out, OP0);
  not not_92 (not_92_out, OP2);
  not not_93 (not_93_out, OP4);
  not not_94 (not_94_out, OP5);
  not not_95 (not_95_out, OP1);
  not not_96 (not_96_out, OP2);
  not not_97 (not_97_out, OP3);
  not not_98 (not_98_out, OP4);
  not not_99 (not_99_out, OP5);
  not not_100 (not_100_out, OP0);
  not not_101 (not_101_out, OP1);
  not not_102 (not_102_out, OP2);
  not not_103 (not_103_out, OP3);
  not not_104 (not_104_out, OP4);
  not not_105 (not_105_out, F0);
  not not_106 (not_106_out, F1);
  not not_107 (not_107_out, F3);
  not not_108 (not_108_out, F4);
  not not_109 (not_109_out, OP0);
  not not_110 (not_110_out, OP1);
  not not_111 (not_111_out, OP2);
  not not_112 (not_112_out, OP3);
  not not_113 (not_113_out, OP4);
  not not_114 (not_114_out, F0);
  not not_115 (not_115_out, F2);
  not not_116 (not_116_out, F3);
  not not_117 (not_117_out, F4);
  not not_118 (not_118_out, OP0);
  not not_119 (not_119_out, OP1);
  not not_120 (not_120_out, OP2);
  not not_121 (not_121_out, OP3);
  not not_122 (not_122_out, OP4);
  not not_123 (not_123_out, F1);
  not not_124 (not_124_out, F2);
  not not_125 (not_125_out, F3);
  not not_126 (not_126_out, F4);
  not not_127 (not_127_out, OP0);
  not not_128 (not_128_out, OP1);
  not not_129 (not_129_out, OP2);
  not not_130 (not_130_out, OP3);
  not not_131 (not_131_out, OP4);
  not not_132 (not_132_out, F2);
  not not_133 (not_133_out, F4);
  not not_134 (not_134_out, OP0);
  not not_135 (not_135_out, OP1);
  not not_136 (not_136_out, OP2);
  not not_137 (not_137_out, OP3);
  not not_138 (not_138_out, OP4);
  not not_139 (not_139_out, OP0);
  not not_140 (not_140_out, OP1);
  not not_141 (not_141_out, OP4);
  not not_142 (not_142_out, OP5);
  not not_143 (not_143_out, OP1);
  not not_144 (not_144_out, OP2);
  not not_145 (not_145_out, OP4);
  not not_146 (not_146_out, OP5);
  not not_147 (not_147_out, OP2);
  not not_148 (not_148_out, OP4);
  not not_149 (not_149_out, OP4);
  not not_150 (not_150_out, OP5);
  not not_151 (not_151_out, OP1);
  not not_152 (not_152_out, OP2);
  not not_153 (not_153_out, OP3);
  not not_154 (not_154_out, OP4);
  not not_155 (not_155_out, OP5);
  not not_156 (not_156_out, F0);
  not not_157 (not_157_out, F1);
  not not_158 (not_158_out, F4);
  not not_159 (not_159_out, OP1);
  not not_160 (not_160_out, OP2);
  not not_161 (not_161_out, OP3);
  not not_162 (not_162_out, OP4);
  not not_163 (not_163_out, OP5);
  not not_164 (not_164_out, F2);
  not not_165 (not_165_out, F4);
  not not_166 (not_166_out, OP1);
  not not_167 (not_167_out, OP2);
  not not_168 (not_168_out, OP3);
  not not_169 (not_169_out, OP4);
  not not_170 (not_170_out, OP5);
  not not_171 (not_171_out, F3);
  not not_172 (not_172_out, F4);
  not not_173 (not_173_out, OP1);
  not not_174 (not_174_out, OP2);
  not not_175 (not_175_out, OP3);
  not not_176 (not_176_out, OP4);
  not not_177 (not_177_out, OP5);
  not not_178 (not_178_out, F3);
  not not_179 (not_179_out, F4);
  not not_180 (not_180_out, OP0);
  not not_181 (not_181_out, OP4);
  not not_182 (not_182_out, OP5);
  not not_183 (not_183_out, OP1);
  not not_184 (not_184_out, OP2);
  not not_185 (not_185_out, OP3);
  not not_186 (not_186_out, OP4);
  not not_187 (not_187_out, OP5);
  not not_188 (not_188_out, OP4);
  not not_189 (not_189_out, OP5);
  and and_1 (and_1_out, not_1_out, not_2_out, not_3_out, not_4_out, not_5_out, not_6_out, not_7_out, not_8_out, F5);
  and and_2 (and_2_out, not_9_out, not_10_out, not_11_out, not_12_out, not_13_out, not_14_out, F2, not_15_out, F5);
  and and_3 (and_3_out, not_16_out, not_17_out, not_18_out, not_19_out, not_20_out, F2, not_21_out, not_22_out, F5);
  and and_4 (and_4_out, not_23_out, not_24_out, not_25_out, not_26_out, not_27_out, F1, not_28_out, F3, not_29_out, F5);
  and and_5 (and_5_out, not_30_out, not_31_out, not_32_out, not_33_out, F0, F1, not_34_out, not_35_out, not_36_out, not_37_out);
  and and_6 (and_6_out, not_38_out, not_39_out, not_40_out, not_41_out, not_42_out, OP5);
  and and_7 (and_7_out, not_43_out, OP3, not_44_out, not_45_out);
  and and_8 (and_8_out, OP1, OP2, OP3, not_46_out, not_47_out);
  and and_9 (and_9_out, OP0, not_48_out, not_49_out, not_50_out, not_51_out);
  and and_10 (and_10_out, OP0, OP1, not_52_out, not_53_out, OP5);
  and and_11 (and_11_out, not_54_out, not_55_out, not_56_out, not_57_out, not_58_out, not_59_out, not_60_out, F2, not_61_out, not_62_out, F5);
  and and_12 (and_12_out, not_63_out, not_64_out, not_65_out, not_66_out, not_67_out, not_68_out, F1, not_69_out, not_70_out, not_71_out);
  and and_13 (and_13_out, not_72_out, not_73_out, not_74_out, not_75_out, not_76_out, not_77_out, F1, not_78_out, not_79_out, F5);
  and and_14 (and_14_out, not_80_out, not_81_out, not_82_out, not_83_out, not_84_out, F0, F1, F2, not_85_out, not_86_out, F5);
  and and_15 (and_15_out, not_87_out, not_88_out, OP2, OP3, not_89_out, not_90_out);
  and and_16 (and_16_out, not_91_out, OP1, not_92_out, OP3, not_93_out, not_94_out);
  and and_17 (and_17_out, OP0, not_95_out, not_96_out, not_97_out, not_98_out, not_99_out);
  and and_18 (and_18_out, not_100_out, not_101_out, not_102_out, not_103_out, not_104_out, not_105_out, not_106_out, not_107_out, not_108_out, F5);
  and and_19 (and_19_out, not_109_out, not_110_out, not_111_out, not_112_out, not_113_out, not_114_out, not_115_out, not_116_out, not_117_out, F5);
  and and_20 (and_20_out, not_118_out, not_119_out, not_120_out, not_121_out, not_122_out, not_123_out, not_124_out, not_125_out, not_126_out, F5);
  and and_21 (and_21_out, not_127_out, not_128_out, not_129_out, not_130_out, not_131_out, F0, F1, not_132_out, F3, not_133_out, F5);
  and and_22 (and_22_out, not_134_out, not_135_out, not_136_out, not_137_out, not_138_out, OP5);
  and and_23 (and_23_out, not_139_out, not_140_out, OP3, not_141_out, not_142_out);
  and and_24 (and_24_out, not_143_out, not_144_out, OP3, not_145_out, not_146_out);
  and and_25 (and_25_out, OP0, OP1, not_147_out, not_148_out, OP5);
  and and_26 (and_26_out, OP0, OP1, OP2, OP3, not_149_out, not_150_out);
  and and_27 (and_27_out, not_151_out, not_152_out, not_153_out, not_154_out, not_155_out, not_156_out, not_157_out, F2, F3, not_158_out, F5);
  and and_28 (and_28_out, not_159_out, not_160_out, not_161_out, not_162_out, not_163_out, F1, not_164_out, F3, not_165_out, F5);
  and and_29 (and_29_out, not_166_out, not_167_out, not_168_out, not_169_out, not_170_out, F1, F2, not_171_out, not_172_out, F5);
  and and_30 (and_30_out, not_173_out, not_174_out, not_175_out, not_176_out, not_177_out, F0, F2, not_178_out, not_179_out, F5);
  and and_31 (and_31_out, not_180_out, OP1, OP3, not_181_out, not_182_out);
  and and_32 (and_32_out, OP0, not_183_out, not_184_out, not_185_out, not_186_out, not_187_out);
  and and_33 (and_33_out, OP0, OP2, OP3, not_188_out, not_189_out);
  or or_1 (S0, and_1_out, and_2_out, and_3_out, and_4_out, and_5_out, and_6_out, and_7_out, and_8_out, and_9_out, and_10_out);
  or or_2 (S1, and_11_out, and_12_out, and_13_out, and_14_out, and_15_out, and_16_out, and_17_out);
  or or_3 (S2, and_18_out, and_19_out, and_20_out, and_21_out, and_22_out, and_23_out, and_24_out, and_25_out, and_26_out);
  or or_4 (S3, and_27_out, and_28_out, and_29_out, and_30_out, and_31_out, and_32_out, and_33_out);
endmodule

// 控制信号生成
module \控制信号自动生成  (
  input  OP0,
  input  OP1,
  input  OP2,
  input  OP3,
  input  OP4,
  input  OP5,
  input  F0,
  input  F1,
  input  F2,
  input  F3,
  input  F4,
  input  F5,
  output MemToReg,
  output MemWrite,
  output ALU_SRC,
  output RegWrite,
  output SysCALL,
  output SignedExt,
  output RegDst,
  output BEQ,
  output BNE,
  output JR,
  output JUMP,
  output JAL,
  output SLLV,
  output LB,
  output BLTZ
);

  wire and_1_out, and_2_out, and_4_out, and_5_out, and_6_out, and_7_out, and_8_out, and_9_out, and_10_out,
       and_11_out, and_12_out, and_13_out, and_14_out, and_15_out, and_16_out, and_17_out, and_18_out,
       and_19_out, and_21_out, and_22_out, and_23_out, and_24_out, and_25_out, and_26_out, and_27_out,
       and_28_out, and_29_out, and_30_out, and_31_out, and_32_out, and_33_out, and_34_out, and_35_out,
       and_36_out, and_37_out, and_41_out, and_42_out, not_1_out, not_2_out, not_3_out, not_4_out, not_5_out,
       not_6_out, not_7_out, not_8_out, not_9_out, not_10_out, not_11_out, not_12_out, not_13_out,
       not_14_out, not_15_out, not_16_out, not_17_out, not_18_out, not_19_out, not_20_out, not_21_out,
       not_22_out, not_23_out, not_24_out, not_25_out, not_26_out, not_27_out, not_28_out, not_29_out,
       not_30_out, not_31_out, not_32_out, not_33_out, not_34_out, not_35_out, not_36_out, not_37_out,
       not_38_out, not_39_out, not_40_out, not_41_out, not_42_out, not_43_out, not_44_out, not_45_out,
       not_46_out, not_47_out, not_48_out, not_49_out, not_50_out, not_51_out, not_52_out, not_53_out,
       not_54_out, not_55_out, not_56_out, not_57_out, not_58_out, not_59_out, not_60_out, not_61_out,
       not_62_out, not_63_out, not_64_out, not_65_out, not_66_out, not_67_out, not_68_out, not_69_out,
       not_70_out, not_71_out, not_72_out, not_73_out, not_74_out, not_75_out, not_76_out, not_77_out,
       not_78_out, not_79_out, not_80_out, not_81_out, not_82_out, not_83_out, not_84_out, not_85_out,
       not_86_out, not_87_out, not_88_out, not_89_out, not_90_out, not_91_out, not_92_out, not_93_out,
       not_94_out, not_95_out, not_96_out, not_97_out, not_98_out, not_99_out, not_100_out, not_101_out,
       not_102_out, not_103_out, not_104_out, not_105_out, not_106_out, not_107_out, not_108_out,
       not_109_out, not_110_out, not_111_out, not_112_out, not_113_out, not_114_out, not_115_out,
       not_116_out, not_117_out, not_118_out, not_119_out, not_120_out, not_121_out, not_122_out,
       not_123_out, not_124_out, not_125_out, not_126_out, not_127_out, not_128_out, not_129_out,
       not_130_out, not_131_out, not_132_out, not_133_out, not_134_out, not_135_out, not_136_out,
       not_137_out, not_138_out, not_139_out, not_140_out, not_141_out, not_142_out, not_143_out,
       not_144_out, not_145_out, not_146_out, not_147_out, not_148_out, not_149_out, not_150_out,
       not_151_out, not_152_out, not_153_out, not_154_out, not_155_out, not_156_out, not_157_out,
       not_158_out, not_159_out, not_160_out, not_161_out, not_162_out, not_163_out, not_164_out,
       not_165_out, not_166_out, not_167_out, not_168_out, not_169_out, not_170_out, not_171_out,
       not_172_out, not_173_out, not_174_out, not_175_out, not_176_out, not_177_out, not_178_out,
       not_179_out, not_180_out, not_181_out, not_182_out, not_183_out, not_184_out, not_185_out,
       not_186_out, not_187_out, not_188_out, not_189_out, not_190_out, not_191_out, not_192_out,
       not_193_out, not_194_out, not_195_out, not_196_out, not_197_out, not_198_out, not_199_out,
       not_200_out, not_201_out, not_202_out, not_203_out, not_204_out, not_205_out, not_206_out,
       not_207_out, not_208_out, not_209_out, not_210_out, not_211_out, not_212_out, not_213_out,
       not_214_out, not_215_out, not_216_out, not_217_out, not_218_out, not_219_out, not_220_out,
       not_221_out, not_222_out, not_223_out, not_224_out, not_225_out, not_226_out, not_227_out,
       not_228_out, not_229_out, not_230_out, not_231_out, not_232_out, not_233_out, not_234_out,
       not_235_out, not_236_out, not_237_out, not_238_out, not_239_out, not_240_out, not_241_out,
       not_242_out, not_243_out, not_244_out, not_245_out, not_246_out, not_247_out, not_248_out,
       not_249_out, not_250_out, not_251_out, not_252_out, not_253_out, not_254_out, not_255_out,
       not_256_out, not_257_out, not_258_out, not_259_out, not_260_out, not_261_out, not_262_out,
       not_263_out, not_264_out, not_265_out, not_266_out, not_267_out, not_268_out, not_269_out,
       not_270_out, not_271_out, not_272_out, not_273_out, not_274_out, not_275_out, not_276_out,
       not_277_out, not_278_out, not_279_out, not_280_out, not_281_out, not_282_out, not_283_out,
       not_284_out, not_285_out, not_286_out, not_287_out, not_288_out, not_289_out, not_290_out,
       not_291_out, not_292_out, not_293_out, not_294_out, not_295_out, not_296_out, not_297_out,
       not_298_out, not_299_out, not_300_out;

  not not_1 (not_1_out, OP1);
  not not_2 (not_2_out, OP2);
  not not_3 (not_3_out, OP3);
  not not_4 (not_4_out, OP4);
  not not_5 (not_5_out, F0);
  not not_6 (not_6_out, F1);
  not not_7 (not_7_out, F2);
  not not_8 (not_8_out, F3);
  not not_9 (not_9_out, F4);
  not not_10 (not_10_out, F5);
  not not_11 (not_11_out, OP2);
  not not_12 (not_12_out, OP3);
  not not_13 (not_13_out, OP4);
  not not_14 (not_14_out, OP2);
  not not_15 (not_15_out, OP4);
  not not_16 (not_16_out, OP0);
  not not_17 (not_17_out, OP1);
  not not_18 (not_18_out, OP2);
  not not_19 (not_19_out, OP3);
  not not_20 (not_20_out, OP4);
  not not_21 (not_21_out, OP0);
  not not_22 (not_22_out, OP4);
  not not_23 (not_23_out, OP5);
  not not_24 (not_24_out, OP1);
  not not_25 (not_25_out, OP4);
  not not_26 (not_26_out, OP5);
  not not_27 (not_27_out, OP4);
  not not_28 (not_28_out, OP5);
  not not_29 (not_29_out, OP2);
  not not_30 (not_30_out, OP4);
  not not_31 (not_31_out, OP0);
  not not_32 (not_32_out, OP1);
  not not_33 (not_33_out, OP2);
  not not_34 (not_34_out, OP3);
  not not_35 (not_35_out, OP4);
  not not_36 (not_36_out, F0);
  not not_37 (not_37_out, F1);
  not not_38 (not_38_out, F3);
  not not_39 (not_39_out, F4);
  not not_40 (not_40_out, OP0);
  not not_41 (not_41_out, OP1);
  not not_42 (not_42_out, OP2);
  not not_43 (not_43_out, OP3);
  not not_44 (not_44_out, OP4);
  not not_45 (not_45_out, F0);
  not not_46 (not_46_out, F2);
  not not_47 (not_47_out, F3);
  not not_48 (not_48_out, F4);
  not not_49 (not_49_out, OP0);
  not not_50 (not_50_out, OP1);
  not not_51 (not_51_out, OP2);
  not not_52 (not_52_out, OP3);
  not not_53 (not_53_out, OP4);
  not not_54 (not_54_out, F1);
  not not_55 (not_55_out, F3);
  not not_56 (not_56_out, F4);
  not not_57 (not_57_out, OP0);
  not not_58 (not_58_out, OP1);
  not not_59 (not_59_out, OP2);
  not not_60 (not_60_out, OP3);
  not not_61 (not_61_out, OP4);
  not not_62 (not_62_out, F2);
  not not_63 (not_63_out, F3);
  not not_64 (not_64_out, F4);
  not not_65 (not_65_out, F5);
  not not_66 (not_66_out, OP0);
  not not_67 (not_67_out, OP1);
  not not_68 (not_68_out, OP2);
  not not_69 (not_69_out, OP3);
  not not_70 (not_70_out, OP4);
  not not_71 (not_71_out, F2);
  not not_72 (not_72_out, F4);
  not not_73 (not_73_out, OP0);
  not not_74 (not_74_out, OP1);
  not not_75 (not_75_out, OP2);
  not not_76 (not_76_out, OP3);
  not not_77 (not_77_out, OP4);
  not not_78 (not_78_out, F3);
  not not_79 (not_79_out, F4);
  not not_80 (not_80_out, OP0);
  not not_81 (not_81_out, OP1);
  not not_82 (not_82_out, OP2);
  not not_83 (not_83_out, OP3);
  not not_84 (not_84_out, OP4);
  not not_85 (not_85_out, OP0);
  not not_86 (not_86_out, OP4);
  not not_87 (not_87_out, OP5);
  not not_88 (not_88_out, OP1);
  not not_89 (not_89_out, OP4);
  not not_90 (not_90_out, OP5);
  not not_91 (not_91_out, OP4);
  not not_92 (not_92_out, OP5);
  not not_93 (not_93_out, OP2);
  not not_94 (not_94_out, OP3);
  not not_95 (not_95_out, OP4);
  not not_96 (not_96_out, OP0);
  not not_97 (not_97_out, OP1);
  not not_98 (not_98_out, OP2);
  not not_99 (not_99_out, OP3);
  not not_100 (not_100_out, OP4);
  not not_101 (not_101_out, OP5);
  not not_102 (not_102_out, F0);
  not not_103 (not_103_out, F1);
  not not_104 (not_104_out, F4);
  not not_105 (not_105_out, F5);
  not not_106 (not_106_out, OP1);
  not not_107 (not_107_out, OP2);
  not not_108 (not_108_out, OP4);
  not not_109 (not_109_out, OP5);
  not not_110 (not_110_out, F0);
  not not_111 (not_111_out, F1);
  not not_112 (not_112_out, F3);
  not not_113 (not_113_out, F4);
  not not_114 (not_114_out, F5);
  not not_115 (not_115_out, OP0);
  not not_116 (not_116_out, OP1);
  not not_117 (not_117_out, OP2);
  not not_118 (not_118_out, OP3);
  not not_119 (not_119_out, OP4);
  not not_120 (not_120_out, OP0);
  not not_121 (not_121_out, OP2);
  not not_122 (not_122_out, OP4);
  not not_123 (not_123_out, OP5);
  not not_124 (not_124_out, OP1);
  not not_125 (not_125_out, OP3);
  not not_126 (not_126_out, OP4);
  not not_127 (not_127_out, OP5);
  not not_128 (not_128_out, OP1);
  not not_129 (not_129_out, OP2);
  not not_130 (not_130_out, OP4);
  not not_131 (not_131_out, OP5);
  not not_132 (not_132_out, OP2);
  not not_133 (not_133_out, OP4);
  not not_134 (not_134_out, OP5);
  not not_135 (not_135_out, OP4);
  not not_136 (not_136_out, OP3);
  not not_137 (not_137_out, OP2);
  not not_138 (not_138_out, OP1);
  not not_139 (not_139_out, OP0);
  not not_140 (not_140_out, F5);
  not not_141 (not_141_out, F4);
  not not_142 (not_142_out, F3);
  not not_143 (not_143_out, F2);
  not not_144 (not_144_out, F1);
  not not_145 (not_145_out, F0);
  not not_146 (not_146_out, OP5);
  not not_147 (not_147_out, OP4);
  not not_148 (not_148_out, OP3);
  not not_149 (not_149_out, OP2);
  not not_150 (not_150_out, OP1);
  not not_151 (not_151_out, OP0);
  not not_152 (not_152_out, F5);
  not not_153 (not_153_out, F4);
  not not_154 (not_154_out, F3);
  not not_155 (not_155_out, F2);
  not not_156 (not_156_out, OP5);
  not not_157 (not_157_out, OP4);
  not not_158 (not_158_out, OP3);
  not not_159 (not_159_out, OP2);
  not not_160 (not_160_out, OP1);
  not not_161 (not_161_out, OP0);
  not not_162 (not_162_out, F5);
  not not_163 (not_163_out, F4);
  not not_164 (not_164_out, F3);
  not not_165 (not_165_out, F2);
  not not_166 (not_166_out, F0);
  not not_167 (not_167_out, OP5);
  not not_168 (not_168_out, OP4);
  not not_169 (not_169_out, OP3);
  not not_170 (not_170_out, OP2);
  not not_171 (not_171_out, OP1);
  not not_172 (not_172_out, OP0);
  not not_173 (not_173_out, F4);
  not not_174 (not_174_out, F3);
  not not_175 (not_175_out, F2);
  not not_176 (not_176_out, F1);
  not not_177 (not_177_out, F0);
  not not_178 (not_178_out, OP5);
  not not_179 (not_179_out, OP4);
  not not_180 (not_180_out, OP3);
  not not_181 (not_181_out, OP2);
  not not_182 (not_182_out, OP1);
  not not_183 (not_183_out, OP0);
  not not_184 (not_184_out, F4);
  not not_185 (not_185_out, F3);
  not not_186 (not_186_out, F2);
  not not_187 (not_187_out, F1);
  not not_188 (not_188_out, OP5);
  not not_189 (not_189_out, OP4);
  not not_190 (not_190_out, OP3);
  not not_191 (not_191_out, OP2);
  not not_192 (not_192_out, OP1);
  not not_193 (not_193_out, OP0);
  not not_194 (not_194_out, F4);
  not not_195 (not_195_out, F3);
  not not_196 (not_196_out, F2);
  not not_197 (not_197_out, F0);
  not not_198 (not_198_out, OP5);
  not not_199 (not_199_out, OP4);
  not not_200 (not_200_out, OP3);
  not not_201 (not_201_out, OP2);
  not not_202 (not_202_out, OP1);
  not not_203 (not_203_out, OP0);
  not not_204 (not_204_out, F4);
  not not_205 (not_205_out, F3);
  not not_206 (not_206_out, F1);
  not not_207 (not_207_out, F0);
  not not_208 (not_208_out, OP5);
  not not_209 (not_209_out, OP4);
  not not_210 (not_210_out, OP3);
  not not_211 (not_211_out, OP2);
  not not_212 (not_212_out, OP1);
  not not_213 (not_213_out, OP0);
  not not_214 (not_214_out, F4);
  not not_215 (not_215_out, F3);
  not not_216 (not_216_out, F1);
  not not_217 (not_217_out, OP5);
  not not_218 (not_218_out, OP4);
  not not_219 (not_219_out, OP3);
  not not_220 (not_220_out, OP2);
  not not_221 (not_221_out, OP1);
  not not_222 (not_222_out, OP0);
  not not_223 (not_223_out, F4);
  not not_224 (not_224_out, F3);
  not not_225 (not_225_out, OP5);
  not not_226 (not_226_out, OP4);
  not not_227 (not_227_out, OP3);
  not not_228 (not_228_out, OP2);
  not not_229 (not_229_out, OP1);
  not not_230 (not_230_out, OP0);
  not not_231 (not_231_out, F4);
  not not_232 (not_232_out, F2);
  not not_233 (not_233_out, F0);
  not not_234 (not_234_out, OP5);
  not not_235 (not_235_out, OP4);
  not not_236 (not_236_out, OP3);
  not not_237 (not_237_out, OP2);
  not not_238 (not_238_out, OP1);
  not not_239 (not_239_out, OP0);
  not not_240 (not_240_out, F4);
  not not_241 (not_241_out, F2);
  not not_242 (not_242_out, OP0);
  not not_243 (not_243_out, OP1);
  not not_244 (not_244_out, OP3);
  not not_245 (not_245_out, OP4);
  not not_246 (not_246_out, OP5);
  not not_247 (not_247_out, OP1);
  not not_248 (not_248_out, OP3);
  not not_249 (not_249_out, OP4);
  not not_250 (not_250_out, OP5);
  not not_251 (not_251_out, OP0);
  not not_252 (not_252_out, OP1);
  not not_253 (not_253_out, OP2);
  not not_254 (not_254_out, OP3);
  not not_255 (not_255_out, OP4);
  not not_256 (not_256_out, OP5);
  not not_257 (not_257_out, F0);
  not not_258 (not_258_out, F1);
  not not_259 (not_259_out, F2);
  not not_260 (not_260_out, F4);
  not not_261 (not_261_out, F5);
  not not_262 (not_262_out, OP0);
  not not_263 (not_263_out, OP2);
  not not_264 (not_264_out, OP3);
  not not_265 (not_265_out, OP4);
  not not_266 (not_266_out, OP5);
  not not_267 (not_267_out, F0);
  not not_268 (not_268_out, F1);
  not not_269 (not_269_out, F2);
  not not_270 (not_270_out, F4);
  not not_271 (not_271_out, F5);
  not not_272 (not_272_out, OP2);
  not not_273 (not_273_out, OP3);
  not not_274 (not_274_out, OP4);
  not not_275 (not_275_out, OP5);
  not not_276 (not_276_out, OP2);
  not not_277 (not_277_out, OP3);
  not not_278 (not_278_out, OP4);
  not not_279 (not_279_out, OP5);
  not not_280 (not_280_out, OP0);
  not not_281 (not_281_out, OP1);
  not not_282 (not_282_out, OP2);
  not not_283 (not_283_out, OP3);
  not not_284 (not_284_out, OP4);
  not not_285 (not_285_out, OP5);
  not not_286 (not_286_out, F0);
  not not_287 (not_287_out, F1);
  not not_288 (not_288_out, F3);
  not not_289 (not_289_out, F4);
  not not_290 (not_290_out, F5);
  not not_291 (not_291_out, OP0);
  not not_292 (not_292_out, OP1);
  not not_293 (not_293_out, OP2);
  not not_294 (not_294_out, OP3);
  not not_295 (not_295_out, OP4);
  not not_296 (not_296_out, OP1);
  not not_297 (not_297_out, OP2);
  not not_298 (not_298_out, OP3);
  not not_299 (not_299_out, OP4);
  not not_300 (not_300_out, OP5);
  and and_1 (and_1_out, not_1_out, not_2_out, not_3_out, not_4_out, OP5, not_5_out, not_6_out, not_7_out, not_8_out, not_9_out, not_10_out);
  and and_2 (and_2_out, OP0, not_11_out, not_12_out, not_13_out, OP5);
  and and_3 (MemWrite, OP0, OP1, not_14_out, OP3, not_15_out, OP5);
  and and_4 (and_4_out, not_16_out, not_17_out, not_18_out, not_19_out, not_20_out, OP5);
  and and_5 (and_5_out, not_21_out, OP3, not_22_out, not_23_out);
  and and_6 (and_6_out, not_24_out, OP3, not_25_out, not_26_out);
  and and_7 (and_7_out, OP2, OP3, not_27_out, not_28_out);
  and and_8 (and_8_out, OP0, OP1, not_29_out, not_30_out, OP5);
  and and_9 (and_9_out, not_31_out, not_32_out, not_33_out, not_34_out, not_35_out, not_36_out, not_37_out, not_38_out, not_39_out);
  and and_10 (and_10_out, not_40_out, not_41_out, not_42_out, not_43_out, not_44_out, not_45_out, not_46_out, not_47_out, not_48_out);
  and and_11 (and_11_out, not_49_out, not_50_out, not_51_out, not_52_out, not_53_out, not_54_out, not_55_out, not_56_out, F5);
  and and_12 (and_12_out, not_57_out, not_58_out, not_59_out, not_60_out, not_61_out, F1, not_62_out, not_63_out, not_64_out, not_65_out);
  and and_13 (and_13_out, not_66_out, not_67_out, not_68_out, not_69_out, not_70_out, F1, not_71_out, F3, not_72_out, F5);
  and and_14 (and_14_out, not_73_out, not_74_out, not_75_out, not_76_out, not_77_out, F0, F2, not_78_out, not_79_out, F5);
  and and_15 (and_15_out, not_80_out, not_81_out, not_82_out, not_83_out, not_84_out, OP5);
  and and_16 (and_16_out, not_85_out, OP3, not_86_out, not_87_out);
  and and_17 (and_17_out, not_88_out, OP3, not_89_out, not_90_out);
  and and_18 (and_18_out, OP2, OP3, not_91_out, not_92_out);
  and and_19 (and_19_out, OP0, OP1, not_93_out, not_94_out, not_95_out);
  and and_20 (SysCALL, not_96_out, not_97_out, not_98_out, not_99_out, not_100_out, not_101_out, not_102_out, not_103_out, F2, F3, not_104_out, not_105_out);
  and and_21 (and_21_out, not_106_out, not_107_out, not_108_out, not_109_out, not_110_out, not_111_out, F2, not_112_out, not_113_out, not_114_out);
  and and_22 (and_22_out, not_115_out, not_116_out, not_117_out, not_118_out, not_119_out, OP5);
  and and_23 (and_23_out, not_120_out, not_121_out, OP3, not_122_out, not_123_out);
  and and_24 (and_24_out, not_124_out, OP2, not_125_out, not_126_out, not_127_out);
  and and_25 (and_25_out, OP0, not_128_out, not_129_out, not_130_out, not_131_out);
  and and_26 (and_26_out, OP0, OP1, not_132_out, not_133_out, OP5);
  and and_27 (and_27_out, not_134_out, not_135_out, not_136_out, not_137_out, not_138_out, not_139_out, not_140_out, not_141_out, not_142_out, not_143_out, not_144_out, not_145_out);
  and and_28 (and_28_out, not_146_out, not_147_out, not_148_out, not_149_out, not_150_out, not_151_out, not_152_out, not_153_out, not_154_out, not_155_out, F1, F0);
  and and_29 (and_29_out, not_156_out, not_157_out, not_158_out, not_159_out, not_160_out, not_161_out, not_162_out, not_163_out, not_164_out, not_165_out, F1, not_166_out);
  and and_30 (and_30_out, not_167_out, not_168_out, not_169_out, not_170_out, not_171_out, not_172_out, F5, not_173_out, not_174_out, not_175_out, not_176_out, not_177_out);
  and and_31 (and_31_out, not_178_out, not_179_out, not_180_out, not_181_out, not_182_out, not_183_out, F5, not_184_out, not_185_out, not_186_out, not_187_out, F0);
  and and_32 (and_32_out, not_188_out, not_189_out, not_190_out, not_191_out, not_192_out, not_193_out, F5, not_194_out, not_195_out, not_196_out, F1, not_197_out);
  and and_33 (and_33_out, not_198_out, not_199_out, not_200_out, not_201_out, not_202_out, not_203_out, F5, not_204_out, not_205_out, F2, not_206_out, not_207_out);
  and and_34 (and_34_out, not_208_out, not_209_out, not_210_out, not_211_out, not_212_out, not_213_out, F5, not_214_out, not_215_out, F2, not_216_out, F0);
  and and_35 (and_35_out, not_217_out, not_218_out, not_219_out, not_220_out, not_221_out, not_222_out, F5, not_223_out, not_224_out, F2, F1, F0);
  and and_36 (and_36_out, not_225_out, not_226_out, not_227_out, not_228_out, not_229_out, not_230_out, F5, not_231_out, F3, not_232_out, F1, not_233_out);
  and and_37 (and_37_out, not_234_out, not_235_out, not_236_out, not_237_out, not_238_out, not_239_out, F5, not_240_out, F3, not_241_out, F1, F0);
  and and_38 (BEQ, not_242_out, not_243_out, OP2, not_244_out, not_245_out, not_246_out);
  and and_39 (BNE, OP0, not_247_out, OP2, not_248_out, not_249_out, not_250_out);
  and and_40 (JR, not_251_out, not_252_out, not_253_out, not_254_out, not_255_out, not_256_out, not_257_out, not_258_out, not_259_out, F3, not_260_out, not_261_out);
  and and_41 (and_41_out, not_262_out, not_263_out, not_264_out, not_265_out, not_266_out, not_267_out, not_268_out, not_269_out, F3, not_270_out, not_271_out);
  and and_42 (and_42_out, OP1, not_272_out, not_273_out, not_274_out, not_275_out);
  and and_43 (JAL, OP0, OP1, not_276_out, not_277_out, not_278_out, not_279_out);
  and and_44 (SLLV, not_280_out, not_281_out, not_282_out, not_283_out, not_284_out, not_285_out, not_286_out, not_287_out, F2, not_288_out, not_289_out, not_290_out);
  and and_45 (LB, not_291_out, not_292_out, not_293_out, not_294_out, not_295_out, OP5);
  and and_46 (BLTZ, OP0, not_296_out, not_297_out, not_298_out, not_299_out, not_300_out);
  or or_1 (MemToReg, and_1_out, and_2_out);
  or or_2 (ALU_SRC, and_4_out, and_5_out, and_6_out, and_7_out, and_8_out);
  or or_3 (RegWrite, and_9_out, and_10_out, and_11_out, and_12_out, and_13_out, and_14_out, and_15_out, and_16_out, and_17_out, and_18_out, and_19_out);
  or or_4 (SignedExt, and_21_out, and_22_out, and_23_out, and_24_out, and_25_out, and_26_out);
  or or_5 (RegDst, and_27_out, and_28_out, and_29_out, and_30_out, and_31_out, and_32_out, and_33_out, and_34_out, and_35_out, and_36_out, and_37_out);
  or or_6 (JUMP, and_41_out, and_42_out);
endmodule

// ALU
module MIPS_ALU (
  input  [4:0] shamt,
  input  [31:0] X,
  input  [31:0] Y,
  input  [3:0] AluOP,
  output Equal,
  output [31:0] Result,
  output [31:0] Result_2
);

  wire [0:0] comparator_1_lt, comparator_2_lt;
  wire [31:0] adder_1_out, AND_out, divider_1_out, divider_1_rem, multiplier_1_cout, multiplier_1_out,
       NOR_out, OR_out, shifter_1_out, shifter_2_out, shifter_3_out, subtractor_1_out, XOR_out;

  assign AND_out = X & Y;  // AND_Gate AND, 32 bits wide
  assign OR_out = X | Y;  // OR_Gate OR, 32 bits wide
  Shifter #(.width(32), .shift("ll")) shifter_1 (.in(Y), .\dist (shamt), .out(shifter_1_out));
  Shifter #(.width(32), .shift("ar")) shifter_2 (.in(Y), .\dist (shamt), .out(shifter_2_out));
  Shifter #(.width(32), .shift("lr")) shifter_3 (.in(Y), .\dist (shamt), .out(shifter_3_out));
  Multiplier #(.width(32)) multiplier_1 (.a(X), .b(Y), .out(multiplier_1_out), .cout(multiplier_1_cout));  // open: cin
  Divider #(.width(32)) divider_1 (.a(X), .b(Y), .out(divider_1_out), .rem(divider_1_rem));  // open: upper
  Adder #(.width(32)) adder_1 (.a(X), .b(Y), .out(adder_1_out));  // open: cin, cout
  Subtractor #(.width(32)) subtractor_1 (.a(X), .b(Y), .out(subtractor_1_out));  // open: bin, bout
  assign XOR_out = X ^ Y;  // XOR_Gate XOR, 32 bits wide
  assign NOR_out = ~(X | Y);  // NOR_Gate NOR, 32 bits wide
  Comparator #(.width(32), .mode("twosComplement")) comparator_1 (
    .a(X), .b(Y), .eq(Equal), .lt(comparator_1_lt[0]));  // open: gt
  Comparator #(.width(32), .mode("unsigned")) comparator_2 (.a(X), .b(Y), .lt(comparator_2_lt[0]));  // open: gt, eq
  Multiplexer #(.select(4), .width(32), .disabled("Z"), .enable("false")) multiplexer_1 (
    .in0(shifter_1_out), .in1(shifter_2_out), .in2(shifter_3_out), .in3(multiplier_1_out),
    .in4(divider_1_out), .in5(adder_1_out), .in6(subtractor_1_out), .in7(AND_out), .in8(OR_out),
    .in9(XOR_out), .in10(NOR_out), .in11({{31{1'b0}}, comparator_1_lt[0]}),
    .in12({{31{1'b0}}, comparator_2_lt[0]}), .in13({32{1'b0}}), .in14({32{1'b0}}), .in15({32{1'b0}}),
    .out(Result), .sel(AluOP));
  Multiplexer #(.select(4), .width(32), .disabled("Z"), .enable("false")) multiplexer_2 (
    .in0({32{1'b0}}), .in1({32{1'b0}}), .in2({32{1'b0}}), .in3(multiplier_1_cout), .in4(divider_1_rem),
    .in5({32{1'b0}}), .in6({32{1'b0}}), .in7({32{1'b0}}), .in8({32{1'b0}}), .in9({32{1'b0}}),
    .in10({32{1'b0}}), .in11({32{1'b0}}), .in12({32{1'b0}}), .in13({32{1'b0}}), .in14({32{1'b0}}),
    .in15({32{1'b0}}), .out(Result_2), .sel(AluOP));

  // Other names for the same wires on the sheet: Result2[31:0] = Result_2; S[3:0] = AluOP

  // Notes on the sheet:
  //   不要改变此引脚区域内容，也不要改变ALU封装形式
  //   输入引脚
  //   输出引脚
endmodule

module MIPS_Regifile (
  input  [31:0] Din,
  input  Clk,
  input  WE,
  input  [4:0] WAdr,
  input  [4:0] R1Adr,
  input  [4:0] R2Adr,
  output [31:0] R1,
  output [31:0] R2
);

  // RegisterFile registerfile_1: pin names not known; wires that end beside it: Din, Clk, WE, WAdr, R1Adr, R2Adr, R1, R2
endmodule

module \理想流水线  (
  output RegWrite,
  output MemWrite,
  output [31:0] IF_PC,
  output [31:0] ID_PC,
  output [31:0] EX_PC,
  output [31:0] M_PC,
  output [31:0] WB_PC,
  output [31:0] RDin,
  output [31:0] MDin,
  output [31:0] LedData
);

  wire BLTZ, CLK, clock_1_out, clock_2_out, comparator_1_eq, comparator_2_eq, comparator_2_lt, d_ff_1_q,
       Enable, ex_mem_1_out_21, ex_mem_1_out_23, ex_mem_1_out_24, ex_mem_1_out_25, ex_mem_1_out_26,
       ex_mem_1_out_28, Go, halt, id_ex_1_out_34, id_ex_1_out_35, id_ex_1_out_37, id_ex_1_out_38,
       id_ex_1_out_39, id_ex_1_out_40, id_ex_1_out_41, id_ex_1_out_43, IR1, IR2, IR3, LB, lb_t, Led,
       mem_wb_1_out_21, mips_probe_4_p1, nand_1_out, not_1_out, RegDst, RST, SignedExt, SLLV, Syscall, W1,
       W2, W3, \单周期硬布线控制器_1_alu_src , \单周期硬布线控制器_1_memtoreg , \单周期硬布线控制器_1_memwrite , \单周期硬布线控制器_1_regdst ,
       \单周期硬布线控制器_1_regwrite ;
  wire [3:0] id_ex_1_out_36, \单周期硬布线控制器_1_alu_op ;
  wire [4:0] id_ex_1_out_42_2, multiplexer_1_out, multiplexer_2_out, multiplexer_3_out;
  wire [7:0] multiplexer_8_out;
  wire [12:0] CNT_num;
  wire [15:0] \LoadUse次数 , \总周期数 , \插入气泡数 , \无条件分支数 , \条件分支成功数 ;
  wire [31:0] adder_1_out, bit_extender_1_out, bit_extender_2_out, bit_extender_3_out, EX_IR,
       ex_mem_1_out_20, id_ex_1_out_32, id_ex_1_out_33, id_ex_1_out_42, ID_IR, IF_IR, MEM_IR,
       mem_wb_1_out_17, mem_wb_1_out_18, mips_alu_1_result, mips_regifile_1_r2, multiplexer_5_out,
       multiplexer_6_out, multiplexer_7_out, R1, ram_1_data, WB_IR;

  Button \u_总复位  (.out(RST));
  Button _1 (.out(IR1));
  Button _2 (.out(IR2));
  Button _3 (.out(IR3));
  // Probe on \总周期数 
  // Probe on \总周期数 
  Button \u_继续运行  (.out(Go));
  LED #(.active("true")) led_1 (.in(W1));
  LED #(.active("true")) led_2 (.in(W2));
  LED #(.active("true")) led_3 (.in(W3));
  not not_1 (not_1_out, halt);
  Register #(.width(32), .trigger("rising"), .Select("low")) PC (
    .D(adder_1_out), .en(Enable), .Q(IF_PC), .clk(CLK), .clr(RST));
  Hex_Digit_Display hex_digit_display_1 (.value(LedData[31:28]));  // open: dp
  // Probe on IF_PC[19:0]
  // Mips_Probe mips_probe_1: pin names not known; wires that end beside it: IF_IR
  Counter #(.width(16), .max('hffff), .ongoal("wrap"), .trigger("rising"), .behavior("old")) counter_1 (
    .count(not_1_out), .Q(\总周期数 ), .clk(CLK), .clr(RST));  // open: load, D, carry, preset
  Adder #(.width(32)) adder_1 (.a(IF_PC), .b(32'h4), .out(adder_1_out));  // open: cin, cout
  Hex_Digit_Display hex_digit_display_2 (.value(LedData[23:20]));  // open: dp
  Hex_Digit_Display hex_digit_display_3 (.value(LedData[27:24]));  // open: dp
  // Probe on ID_PC[19:0]
  // Mips_Probe mips_probe_2: pin names not known; wires that end beside it: ID_IR
  Hex_Digit_Display hex_digit_display_4 (.value(LedData[15:12]));  // open: dp
  Hex_Digit_Display hex_digit_display_5 (.value(LedData[19:16]));  // open: dp
  ROM #(.addrWidth(10), .dataWidth(32), .Select("high")) rom_1 (.addr(IF_PC[11:2]), .data(IF_IR));
  Hex_Digit_Display hex_digit_display_6 (.value(LedData[7:4]));  // open: dp
  Hex_Digit_Display hex_digit_display_7 (.value(LedData[11:8]));  // open: dp
  Clock #(.highDuration(1), .lowDuration(1)) clock_1 (.out(clock_1_out));
  // Probe on EX_PC[19:0]
  // Mips_Probe mips_probe_3: pin names not known; wires that end beside it: clock_1_out, EX_IR, CLK
  IF_ID if_id_1 (
    .CTK(CLK), .RST(RST), .in_4(IF_IR), .in_5(IF_PC), .out_9(ID_IR), .out_10(ID_PC), .Enable(Enable));  // open: 同步置0, in_6, out_11, in_7, out_12
  Hex_Digit_Display hex_digit_display_8 (.value(LedData[3:0]));  // open: dp
  // Probe on \总周期数 
  // Probe on M_PC[19:0]
  // Mips_Probe mips_probe_4: pin names not known; wires that end beside it: mips_probe_4_p1, MEM_IR
  \单周期硬布线控制器  \u_单周期硬布线控制器_1  (
    .Func(ID_IR[5:0]), .OP(ID_IR[31:26]), .ALU_OP(\单周期硬布线控制器_1_alu_op ), .MemToReg(\单周期硬布线控制器_1_memtoreg ),
    .MemWrite(\单周期硬布线控制器_1_memwrite ), .ALU_SRC(\单周期硬布线控制器_1_alu_src ), .SysCALL(Syscall),
    .SignedExt(SignedExt), .RegDst(\单周期硬布线控制器_1_regdst ), .Beq(mips_probe_4_p1), .SLLV(SLLV), .LB(LB),
    .BLTZ(BLTZ), .RegWrite(\单周期硬布线控制器_1_regwrite ));  // open: JR, JMP, JAL, Bne, out_20, out_21, ERET, Func_2, MFC0, MTC0
  Multiplexer #(.select(1), .width(5), .disabled("Z"), .enable("false")) multiplexer_1 (
    .in0(ID_IR[25:21]), .in1(5'b00010), .out(multiplexer_1_out), .sel(Syscall));
  Multiplexer #(.select(1), .width(5), .disabled("Z"), .enable("false")) multiplexer_2 (
    .in0(ID_IR[20:16]), .in1(5'b00100), .out(multiplexer_2_out), .sel(Syscall));
  Multiplexer #(.select(1), .width(5), .disabled("Z"), .enable("false")) multiplexer_3 (
    .in0(WB_IR[20:16]), .in1(WB_IR[15:11]), .out(multiplexer_3_out), .sel(RegDst));
  Multiplexer #(.select(1), .width(5), .disabled("Z"), .enable("false")) multiplexer_4 (
    .in0(ID_IR[10:6]), .in1(R1[4:0]), .sel(SLLV));  // open: out
  assign bit_extender_1_out = {{16{1'b0}}, ID_IR[15:0]};  // Bit_Extender bit_extender_1
  assign bit_extender_2_out = {{16{ID_IR[15]}}, ID_IR[15:0]};  // Bit_Extender bit_extender_2
  Comparator #(.width(32), .mode("twosComplement")) comparator_1 (
    .a(R1), .b(32'h22), .eq(comparator_1_eq));  // open: gt, lt
  // Probe on \总周期数 
  // Probe on \无条件分支数 
  // Probe on \条件分支成功数 
  // Probe on \插入气泡数 
  // Probe on \LoadUse次数 
  Multiplexer #(.select(1), .width(32), .disabled("Z"), .enable("false")) multiplexer_5 (
    .in0(bit_extender_1_out), .in1(bit_extender_2_out), .out(multiplexer_5_out), .sel(SignedExt));
  and and_1 (Led, Syscall, comparator_1_eq);
  and and_2 (halt, Syscall, ~comparator_1_eq);  // AND_Gate
  // Probe on IF_PC[11:0]
  // Probe on WB_PC[19:0]
  // Mips_Probe mips_probe_5: pin names not known; wires that end beside it: WB_IR
  MIPS_Regifile mips_regifile_1 (
    .Din(RDin), .Clk(CLK), .R1(R1), .R2(mips_regifile_1_r2), .WE(RegWrite), .WAdr(multiplexer_3_out),
    .R1Adr(multiplexer_1_out), .R2Adr(multiplexer_2_out));
  // Probe on ID_PC[11:0]
  // Probe on EX_PC[11:0]
  // Probe on M_PC[11:0]
  D_Flip_Flop #(.trigger("high"), .Pre_Clr_Positions("LEGACY"), .NegatePresetClear("false"), .enable("true"), .NewFFLayout("false")) d_ff_1 (.Q(d_ff_1_q));  // open: clk, D, Qn, preset, en, reset
  // Probe on 13'hc
  ID_EX id_ex_1 (
    .CTK(CLK), .RST(RST), .Enable(Enable), .\指令 (ID_IR), .PC(ID_PC), .out_30(EX_IR), .out_31(EX_PC),
    .\寄存器1 (R1), .out_32(id_ex_1_out_32), .\寄存器2 (mips_regifile_1_r2), .out_33(id_ex_1_out_33),
    .MenToReg(\单周期硬布线控制器_1_memtoreg ), .out_34(id_ex_1_out_34), .MenWrite(\单周期硬布线控制器_1_memwrite ),
    .out_35(id_ex_1_out_35), .RegWrite(\单周期硬布线控制器_1_regwrite ), .out_38(id_ex_1_out_38), .sllv(Led),
    .out_39(id_ex_1_out_39), .halt(halt), .out_40(id_ex_1_out_40), .lb(LB), .out_41(id_ex_1_out_41),
    .RegDst(\单周期硬布线控制器_1_regdst ), .out_43(id_ex_1_out_43), .imm(multiplexer_5_out),
    .out_42({id_ex_1_out_42[31:11], id_ex_1_out_42_2, id_ex_1_out_42[5:0]}), .ALU_OP(\单周期硬布线控制器_1_alu_op ),
    .out_36(id_ex_1_out_36), .ALU_src(\单周期硬布线控制器_1_alu_src ), .out_37(id_ex_1_out_37));  // open: JR, out_44, JMP, out_45, JAL, out_46, BNE, out_47, BEQ, out_48, BLTZ, out_49, 同步置0, Signext, out_50, in_26, out_51, out_52, in_27, in_28, out_53, in_29, out_54
  // Probe on WB_PC[11:0]
  Comparator #(.width(13), .mode("twosComplement")) comparator_2 (
    .a(CNT_num), .b(13'hc), .eq(comparator_2_eq), .lt(comparator_2_lt));  // open: gt
  Clock #(.highDuration(1), .lowDuration(1)) clock_2 (.out(clock_2_out));
  nand nand_1 (nand_1_out, d_ff_1_q, comparator_2_eq);
  Counter #(.width(13), .max('h1fff), .ongoal("stay"), .trigger("rising"), .behavior("old")) counter_2 (
    .count(comparator_2_lt), .Q(CNT_num), .clk(clock_2_out));  // open: load, D, carry, clr, preset
  Multiplexer #(.select(1), .width(32), .disabled("Z"), .enable("false")) multiplexer_6 (
    .in0(id_ex_1_out_33), .in1({id_ex_1_out_42[31:11], id_ex_1_out_42_2, id_ex_1_out_42[5:0]}),
    .out(multiplexer_6_out), .sel(id_ex_1_out_37));
  assign CLK = nand_1_out ? clock_2_out : 1'bz;  // Controlled_Buffer controlled_buffer_1
  // Probe on id_ex_1_out_33
  MIPS_ALU mips_alu_1 (
    .X(id_ex_1_out_32), .Y(multiplexer_6_out), .AluOP(id_ex_1_out_36), .Result(mips_alu_1_result),
    .shamt(id_ex_1_out_42_2));  // open: Equal, Result_2
  // Probe on mips_alu_1_result
  Pull_Resistor #(.pull(1)) pull_resistor_1 (.node(CLK));
  EX_MEM ex_mem_1 (
    .CTK(CLK), .RST(RST), .Enable(Enable), .\指令 (EX_IR), .PC(EX_PC), .\寄存器1 (id_ex_1_out_33),
    .\寄存器2 (mips_alu_1_result), .MenToReg(id_ex_1_out_34), .MenWrite(id_ex_1_out_35),
    .RegDst(id_ex_1_out_38), .led(id_ex_1_out_39), .halt(id_ex_1_out_40), .lb(id_ex_1_out_41),
    .RegDst_2(id_ex_1_out_43), .out_17(MEM_IR), .out_18(M_PC), .out_19(MDin), .out_20(ex_mem_1_out_20),
    .out_21(ex_mem_1_out_21), .out_22(MemWrite), .out_23(ex_mem_1_out_23), .out_24(ex_mem_1_out_24),
    .out_25(ex_mem_1_out_25), .out_26(ex_mem_1_out_26), .out_28(ex_mem_1_out_28));  // open: PC_4, out_29, JAL, out_27
  // Probe on MDin
  // Probe on MDin
  Register #(.width(32), .trigger("rising"), .Select("low")) register_1 (
    .D(MDin), .en(ex_mem_1_out_24), .Q(LedData), .clk(CLK));  // open: clr
  // Probe on ex_mem_1_out_20
  RAM #(.addrWidth(10), .dataWidth(32), .bus("separate"), .Select("high")) ram_1 (
    .addr(ex_mem_1_out_20[11:2]), .din(MDin), .data(ram_1_data), .str(MemWrite), .clk(CLK), .clr(RST));  // open: sel, ld
  // Probe on ram_1_data
  MEM_WB mem_wb_1 (
    .CTK(CLK), .RST(RST), .Enable(Enable), .\指令 (MEM_IR), .PC(M_PC), .\运算器结果 (ex_mem_1_out_20),
    .\存储器结果 (ram_1_data), .MenToReg(ex_mem_1_out_21), .RegWrite(ex_mem_1_out_23), .halt(ex_mem_1_out_25),
    .lb(ex_mem_1_out_28), .RegDst(ex_mem_1_out_26), .out_15(WB_IR), .out_16(WB_PC), .out_17(mem_wb_1_out_17),
    .out_18(mem_wb_1_out_18), .out_19(RegDst), .out_20(RegWrite), .out_21(mem_wb_1_out_21), .out_22(RegDst),
    .out_23(lb_t));  // open: PC_2, out_25, JAL, out_24
  Multiplexer #(.select(1), .width(32), .disabled("Z"), .enable("false")) multiplexer_7 (
    .in0(mem_wb_1_out_17), .in1(mem_wb_1_out_18), .out(multiplexer_7_out), .sel(RegDst));
  or or_1 (Enable, ~mem_wb_1_out_21, Go);  // OR_Gate
  Multiplexer #(.select(2), .width(8), .disabled("Z"), .enable("false")) multiplexer_8 (
    .in0(mem_wb_1_out_18[7:0]), .in1(mem_wb_1_out_18[15:8]), .in2(mem_wb_1_out_18[23:16]),
    .in3(mem_wb_1_out_18[31:24]), .out(multiplexer_8_out), .sel(mem_wb_1_out_17[1:0]));
  Multiplexer #(.select(1), .width(32), .disabled("Z"), .enable("false")) multiplexer_9 (
    .in0(multiplexer_7_out), .in1(bit_extender_3_out), .out(RDin), .sel(lb_t));
  assign bit_extender_3_out = {{24{multiplexer_8_out[7]}}, multiplexer_8_out};  // Bit_Extender bit_extender_3

  // Other names for the same wires on the sheet: MEM_PC[31:0] = M_PC

  // Notes on the sheet:
  //   中断源
  //   时空图监测，可删除
  //   中断等待指示
  //   数码管输出
  //   contents of rom_1 (hex, n*v repeats v):
  //   20110001 8100005 20110001 20120002 20130003 8100009 20110001 20120002 20130003 810000d 20110001
  //   20120002 20130003 8100011 20110001 20120002 20130003 c1000b8 20100001 20110001 118fc0 112020
  //   20020022 c 118882 12200001 8100015 112020 20020022 c 20110001 118880 112020 20020022 c 12200001
  //   810001f 20110001 118fc0 112020 20020022 c 1188c3 112020 20020022 c 118903 112020 20020022 c 118903
  //   112020 20020022 c 118903 112020 20020022 c 118903 112020 20020022 c 118903 112020 20020022 c 118903
  //   112020 20020022 c 118903 112020 20020022 c 20100001 109fc0 139fc3 8021 2012000c 24160003 26100001
  //   3210000f 20080008 20090001 139900 2709825 132020 20020022 c 1094022 1500fff9 22100001 2018000f
  //   2188024 108700 20080008 20090001 139902 2709825 132021 20020022 c 1094022 1500fff9 108702 2c9b022
  //   12c00001 8100050 4020 1084027 84400 3508ffff 82021 20020022 c 2010ffff 20110000 ae300000 22100001
  //   22310004 ae300000 22100001 22310004 ae300000 22100001 22310004 ae300000 22100001 22310004 ae300000
  //   22100001 22310004 ae300000 22100001 22310004 ae300000 22100001 22310004 ae300000 22100001 22310004
  //   ae300000 22100001 22310004 ae300000 22100001 22310004 ae300000 22100001 22310004 ae300000 22100001
  //   22310004 ae300000 22100001 22310004 ae300000 22100001 22310004 ae300000 22100001 22310004 ae300000
  //   22100001 22310004 22100001 8020 2011003c 8e130000 8e340000 274402a 11000002 ae330000 ae140000
  //   2231fffc 1611fff8 102020 20020022 c 22100004 2011003c 1611fff2 20020032 c 20100000 22100001 102020
  //   20020022 c 22100002 102020 20020022 c 22100003 102020 20020022 c 22100004 102020 20020022 c 22100005
  //   102020 20020022 c 22100006 102020 20020022 c 22100007 102020 20020022 c 22100008 102020 20020022
  //   20020022 c 2011fff1 112020 20020022 c 22310001 620fffb 2002000a c 20090000 200b0010 34118483
  //   20120404 118c00 129400 36318281 22520404 ad310000 2328820 21290004 216bffff 1560fffb 200b0020
  //   20090000 81310000 112020 20020022 c 21290001 216bffff 1560fff9 2002000a c 20080001 20090003 20110876
  //   112020 20020022 c 200b0008 1118804 1318804 112020 20020022 c 216bffff 1560fff9 2002000a c 2008ffff
  //   20117777 112020 20020022 c 200b0010 3a31ffff 112020 20020022 c 216bffff 1560fffa 2002000a c 3e00008
  //   OP
  //   rs
  //   rt
  //   rd
  //   JMP
  //   JR
  //   Func
  //   shamt
  //   imm16
  //   imm26
  //   Beq
  //   Bne
  //   MemToReg
  //   MemWrite
  //   AluOP
  //   AluSrcB
  //   RegWrite
  //   JAL
  //   Syscall
  //   控制位
  //   流水调试日志用
  //   暂停节拍，不能为0
  //   戳工具置1进入计数暂停模式，ctrl+k时钟自动运行到对应节拍暂停
  //   ctrl+k关闭时钟连续运行，将控制位置零，进入单步调试模式调试
  //   用这个时钟源需要去掉电路中的其他时钟源
  //   可计数暂停的时钟源
  //   为方便自动评测，需要输出流水线各段保存的PC值，注意是PC不是PC+4，另外ID段寄存器写入信息，Mem段内存写入信息也要输出
endmodule

module \气泡流水线  (
  output RegWrite,
  output MemWrite,
  output [31:0] IF_PC,
  output [31:0] ID_PC,
  output [31:0] EX_PC,
  output [31:0] M_PC,
  output [31:0] WB_PC,
  output [31:0] RDin,
  output [31:0] MDin,
  output [31:0] LedData
);

  wire and_1_out, and_2_out, and_5_out, and_6_out, and_7_out, BEQ, BLTZ, bltz_out_34, bltz_out_35,
       bltz_out_37, bltz_out_38, bltz_out_39, bltz_out_41, bltz_out_43, bltz_out_50, bltz_t, BNE, Branch,
       Bubble, CLK, clock_2_out, comparator_1_eq, comparator_2_eq, comparator_2_lt, controlled_buffer_1_out,
       d_ff_1_q, Enable, ex_mem_1_out_21, ex_mem_1_out_23, ex_mem_1_out_24, ex_mem_1_out_25, ex_mem_1_out_26,
       ex_mem_1_out_27, ex_mem_1_out_28, Go, halt, IR1, IR2, IR3, J, JAL, JMP, JR, LB, lb_t, Led,
       mem_wb_1_out_21, mips_alu_1_equal, nand_1_out, not_1_out, or_1_out, R, RegDst, RST, SignedExt, SLLV,
       Syscall, W1, W2, W3, \冲突 , \单周期硬布线控制器_1_alu_src , \单周期硬布线控制器_1_beq , \单周期硬布线控制器_1_bne ,
       \单周期硬布线控制器_1_jal , \单周期硬布线控制器_1_jmp , \单周期硬布线控制器_1_jr , \单周期硬布线控制器_1_memtoreg ,
       \单周期硬布线控制器_1_memwrite , \单周期硬布线控制器_1_out_20 , \单周期硬布线控制器_1_out_21 , \单周期硬布线控制器_1_regdst ,
       \单周期硬布线控制器_1_regwrite ;
  wire [3:0] bltz_out_36, bltz_out_51, bltz_out_51_2, bltz_out_51_3, bltz_out_51_4, bltz_out_51_5,
       bltz_out_51_6, bltz_out_51_7, \单周期硬布线控制器_1_alu_op ;
  wire [4:0] multiplexer_4_out, multiplexer_6_out, multiplexer_7_out, multiplexer_10_out, R1_num, R2_num;
  wire [7:0] multiplexer_12_out;
  wire [12:0] CNT_num;
  wire [15:0] \LoadUse次数 , \总周期数 , \插入气泡数 , \无条件分支数 , \条件分支成功数 ;
  wire [30:0] mips_alu_1_result;
  wire [31:0] adder_1_out, bit_extender_1_out, bit_extender_2_out, bit_extender_3_out, bit_extender_4_out,
       bltz_out_33, Branch_PC, EX_IR, ex_mem_1_out_20, ex_mem_1_out_29, ID_IR, if_id_1_out_11, IF_IR, JR_PC,
       MEM_IR, mem_wb_1_out_17, mem_wb_1_out_18, mem_wb_1_out_25, mips_regifile_1_r2, multiplexer_1_out,
       multiplexer_8_out, multiplexer_9_out, multiplexer_11_out, multiplexer_13_out, R1, ram_1_data,
       shifter_1_out, WB_IR;
  wire [31:2] JMP_PC;
  wire [31:26] bltz_out_42;

  Button \u_总复位  (.out(RST));
  Button _1 (.out(IR1));
  Button _2 (.out(IR2));
  Button _3 (.out(IR3));
  // Probe on \总周期数 
  // Probe on \总周期数 
  Button \u_继续运行  (.out(Go));
  LED #(.active("true")) led_1 (.in(W1));
  LED #(.active("true")) led_2 (.in(W2));
  LED #(.active("true")) led_3 (.in(W3));
  and and_1 (and_1_out, Enable, ~\冲突 );  // AND_Gate
  Hex_Digit_Display hex_digit_display_1 (.value(LedData[31:28]));  // open: dp
  // Probe on IF_PC[19:0]
  // Mips_Probe mips_probe_1: pin names not known; wires that end beside it: IF_IR
  // Probe on multiplexer_1_out
  Multiplexer #(.select(3), .width(32), .disabled("Z"), .enable("false")) multiplexer_1 (
    .in0(adder_1_out), .in1(Branch_PC), .in2({JMP_PC, 2'b00}), .in6(JR_PC), .out(multiplexer_1_out),
    .sel({JR, JMP, Branch}));  // open: in3, in4, in5, in7
  Register #(.width(32), .trigger("rising"), .Select("low")) PC (
    .D(multiplexer_1_out), .en(and_1_out), .Q(IF_PC), .clk(CLK), .clr(RST));
  Hex_Digit_Display hex_digit_display_2 (.value(LedData[27:24]));  // open: dp
  Hex_Digit_Display hex_digit_display_3 (.value(LedData[23:20]));  // open: dp
  // Probe on ID_PC[19:0]
  // Mips_Probe mips_probe_2: pin names not known; wires that end beside it: ID_IR
  Counter #(.width(16), .max('hffff), .ongoal("wrap"), .trigger("rising"), .behavior("old")) counter_1 (
    .count(not_1_out), .Q(\总周期数 ), .clk(CLK), .clr(RST));  // open: load, D, carry, preset
  not not_1 (not_1_out, halt);
  Adder #(.width(32)) adder_1 (.a(IF_PC), .b(32'h4), .out(adder_1_out));  // open: cin, cout
  Hex_Digit_Display hex_digit_display_4 (.value(LedData[19:16]));  // open: dp
  Hex_Digit_Display hex_digit_display_5 (.value(LedData[15:12]));  // open: dp
  Hex_Digit_Display hex_digit_display_6 (.value(LedData[7:4]));  // open: dp
  Hex_Digit_Display hex_digit_display_7 (.value(LedData[11:8]));  // open: dp
  Clock #(.highDuration(1), .lowDuration(1)) clock_1 (.out(CLK));
  // Probe on EX_PC[19:0]
  // Mips_Probe mips_probe_3: pin names not known; wires that end beside it: EX_IR
  ROM #(.addrWidth(10), .dataWidth(32), .Select("high")) rom_1 (.addr(IF_PC[11:2]), .data(IF_IR));
  and and_2 (and_2_out, Enable, ~\冲突 );  // AND_Gate
  Hex_Digit_Display hex_digit_display_8 (.value(LedData[3:0]));  // open: dp
  \数据冲突检测电路  \u_数据冲突检测电路_1  (
    .\R1使用情况 (\单周期硬布线控制器_1_out_20 ), .\EX段写入信号 (bltz_out_38), .\MEM段写入信号 (ex_mem_1_out_23),
    .\EX段写入编号 (multiplexer_7_out), .\MEM段写入编号 (multiplexer_10_out), .\R1编号 (R1_num), .\R2编号 (R2_num),
    .\R2使用情况 (\单周期硬布线控制器_1_out_21 ), .\冲突 (\冲突 ));  // open: R1, R2
  IF_ID if_id_1 (
    .CTK(CLK), .RST(RST), .in_4(IF_IR), .in_5(IF_PC), .out_9(ID_IR), .out_10(ID_PC), .Enable(and_2_out),
    .\同步置0 (Bubble), .in_6(adder_1_out), .out_11(if_id_1_out_11));  // open: in_7, out_12
  // Probe on \总周期数 
  // Probe on M_PC[19:0]
  // Mips_Probe mips_probe_4: pin names not known; wires that end beside it: MEM_IR
  // Probe on \总周期数 
  // Probe on \无条件分支数 
  // Probe on \条件分支成功数 
  // Probe on \插入气泡数 
  // Probe on \LoadUse次数 
  \单周期硬布线控制器  \u_单周期硬布线控制器_1  (
    .Func(ID_IR[5:0]), .OP(ID_IR[31:26]), .ALU_OP(\单周期硬布线控制器_1_alu_op ), .MemToReg(\单周期硬布线控制器_1_memtoreg ),
    .MemWrite(\单周期硬布线控制器_1_memwrite ), .ALU_SRC(\单周期硬布线控制器_1_alu_src ), .SysCALL(Syscall),
    .SignedExt(SignedExt), .RegDst(\单周期硬布线控制器_1_regdst ), .JR(\单周期硬布线控制器_1_jr ), .JMP(\单周期硬布线控制器_1_jmp ),
    .Beq(\单周期硬布线控制器_1_beq ), .JAL(\单周期硬布线控制器_1_jal ), .Bne(\单周期硬布线控制器_1_bne ), .SLLV(SLLV), .LB(LB),
    .BLTZ(BLTZ), .out_20(\单周期硬布线控制器_1_out_20 ), .out_21(\单周期硬布线控制器_1_out_21 ),
    .RegWrite(\单周期硬布线控制器_1_regwrite ));  // open: ERET, Func_2, MFC0, MTC0
  Multiplexer #(.select(1), .width(5), .disabled("Z"), .enable("false")) multiplexer_2 (
    .in0(ID_IR[25:21]), .in1(5'b00010), .out(R1_num), .sel(Syscall));
  Multiplexer #(.select(1), .width(5), .disabled("Z"), .enable("false")) multiplexer_3 (
    .in0(ID_IR[20:16]), .in1(5'b00100), .out(R2_num), .sel(Syscall));
  Multiplexer #(.select(1), .width(5), .disabled("Z"), .enable("false")) multiplexer_4 (
    .in0(WB_IR[20:16]), .in1(WB_IR[15:11]), .out(multiplexer_4_out), .sel(RegDst));
  Multiplexer #(.select(1), .width(5), .disabled("Z"), .enable("false")) multiplexer_5 (
    .in0(ID_IR[10:6]), .in1(R1[4:0]), .sel(SLLV));  // open: out
  assign bit_extender_1_out = {{6{1'b0}}, ID_IR[25:0]};  // Bit_Extender bit_extender_1
  Comparator #(.width(32), .mode("twosComplement")) comparator_1 (
    .a(R1), .b(32'h22), .eq(comparator_1_eq));  // open: gt, lt
  // Probe on IF_PC[11:0]
  // Probe on WB_PC[19:0]
  // Mips_Probe mips_probe_5: pin names not known; wires that end beside it: WB_IR
  Multiplexer #(.select(1), .width(5), .disabled("Z"), .enable("false")) multiplexer_6 (
    .in0(multiplexer_4_out), .in1({5{1'b1}}), .out(multiplexer_6_out), .sel(J));
  and and_3 (Led, Syscall, comparator_1_eq);
  and and_4 (halt, Syscall, ~comparator_1_eq);  // AND_Gate
  // Probe on ID_PC[11:0]
  // Probe on EX_PC[11:0]
  MIPS_Regifile mips_regifile_1 (
    .Din(RDin), .Clk(CLK), .R1(R1), .R2(mips_regifile_1_r2), .WE(RegWrite), .WAdr(multiplexer_6_out),
    .R1Adr(R1_num), .R2Adr(R2_num));
  // Probe on M_PC[11:0]
  D_Flip_Flop #(.trigger("high"), .Pre_Clr_Positions("LEGACY"), .NegatePresetClear("false"), .enable("true"), .NewFFLayout("false")) d_ff_1 (.Q(d_ff_1_q));  // open: clk, D, Qn, preset, en, reset
  // Probe on 13'hc
  // Probe on R1
  // Probe on WB_PC[11:0]
  Comparator #(.width(13), .mode("twosComplement")) comparator_2 (
    .a(CNT_num), .b(13'hc), .eq(comparator_2_eq), .lt(comparator_2_lt));  // open: gt
  Clock #(.highDuration(1), .lowDuration(1)) clock_2 (.out(clock_2_out));
  ID_EX u_bltz (
    .CTK(CLK), .RST(RST), .Enable(Enable), .\指令 (ID_IR), .PC(ID_PC), .out_30(EX_IR), .out_31(EX_PC),
    .\寄存器1 (R1), .out_32(JR_PC), .\寄存器2 (mips_regifile_1_r2), .out_33(bltz_out_33),
    .MenToReg(\单周期硬布线控制器_1_memtoreg ), .out_34(bltz_out_34), .MenWrite(\单周期硬布线控制器_1_memwrite ),
    .out_35(bltz_out_35), .RegWrite(\单周期硬布线控制器_1_regwrite ), .out_38(bltz_out_38), .sllv(Led),
    .out_39(bltz_out_39), .halt(halt), .lb(LB), .out_41(bltz_out_41), .RegDst(\单周期硬布线控制器_1_regdst ),
    .out_43(bltz_out_43), .imm(bit_extender_1_out), .out_42({bltz_out_42, JMP_PC[27:2]}),
    .ALU_OP(\单周期硬布线控制器_1_alu_op ), .out_36(bltz_out_36), .ALU_src(\单周期硬布线控制器_1_alu_src ),
    .out_37(bltz_out_37), .JR(\单周期硬布线控制器_1_jr ), .out_44(JR), .JMP(\单周期硬布线控制器_1_jmp ), .out_45(JMP),
    .JAL(\单周期硬布线控制器_1_jal ), .out_46(JAL), .BNE(\单周期硬布线控制器_1_bne ), .out_47(BNE), .BEQ(\单周期硬布线控制器_1_beq ),
    .out_48(BEQ), .BLTZ(BLTZ), .out_49(bltz_t), .\同步置0 (or_1_out), .Signext(SignedExt), .out_50(bltz_out_50),
    .in_26(if_id_1_out_11),
    .out_51({JMP_PC[31:28], bltz_out_51_7, bltz_out_51_6, bltz_out_51_5, bltz_out_51_4, bltz_out_51_3, bltz_out_51_2, bltz_out_51}));  // open: out_40, out_52, in_27, in_28, out_53, in_29, out_54
  nand nand_1 (nand_1_out, d_ff_1_q, comparator_2_eq);
  Counter #(.width(13), .max('h1fff), .ongoal("stay"), .trigger("rising"), .behavior("old")) counter_2 (
    .count(comparator_2_lt), .Q(CNT_num), .clk(clock_2_out));  // open: load, D, carry, clr, preset
  // Probe on JR_PC
  or or_1 (or_1_out, \冲突 , Bubble);
  assign controlled_buffer_1_out = nand_1_out ? clock_2_out : 1'bz;  // Controlled_Buffer controlled_buffer_1
  Multiplexer #(.select(1), .width(5), .disabled("Z"), .enable("false")) multiplexer_7 (
    .in0(EX_IR[20:16]), .in1(EX_IR[15:11]), .out(multiplexer_7_out), .sel(bltz_out_43));
  Multiplexer #(.select(1), .width(32), .disabled("Z"), .enable("false")) multiplexer_8 (
    .in0(bltz_out_33), .in1(multiplexer_9_out), .out(multiplexer_8_out), .sel(bltz_out_37));
  assign bit_extender_2_out = {{16{1'b0}}, JMP_PC[17:2]};  // Bit_Extender bit_extender_2
  assign bit_extender_3_out = {{16{JMP_PC[17]}}, JMP_PC[17:2]};  // Bit_Extender bit_extender_3
  Clock #(.highDuration(1), .lowDuration(1)) clock_3 (.out(controlled_buffer_1_out));
  Pull_Resistor #(.pull(1)) pull_resistor_1 (.node(controlled_buffer_1_out));
  MIPS_ALU mips_alu_1 (
    .X(JR_PC), .Y(multiplexer_8_out), .AluOP(bltz_out_36), .Equal(mips_alu_1_equal),
    .Result({R, mips_alu_1_result}), .shamt(JMP_PC[12:8]));  // open: Result_2
  Multiplexer #(.select(1), .width(32), .disabled("Z"), .enable("false")) multiplexer_9 (
    .in0(bit_extender_2_out), .in1(bit_extender_3_out), .out(multiplexer_9_out), .sel(bltz_out_50));
  Shifter #(.width(32), .shift("ll")) shifter_1 (.in(bit_extender_3_out), .\dist (5'b00010), .out(shifter_1_out));
  and and_5 (and_5_out, mips_alu_1_equal, BEQ);
  and and_6 (and_6_out, ~mips_alu_1_equal, BNE);  // AND_Gate
  or or_2 (Branch, and_5_out, and_6_out, and_7_out);
  and and_7 (and_7_out, R, bltz_t);
  // Probe on bltz_out_33
  // Probe on {R, mips_alu_1_result}
  Adder #(.width(32)) adder_2 (
    .a(shifter_1_out),
    .b({JMP_PC[31:28], bltz_out_51_7, bltz_out_51_6, bltz_out_51_5, bltz_out_51_4, bltz_out_51_3, bltz_out_51_2, bltz_out_51}),
    .out(Branch_PC));  // open: cin, cout
  or or_3 (Bubble, Branch, JMP);
  EX_MEM ex_mem_1 (
    .CTK(CLK), .RST(RST), .Enable(Enable), .\指令 (EX_IR), .PC(EX_PC), .\寄存器1 (bltz_out_33),
    .\寄存器2 ({R, mips_alu_1_result}), .MenToReg(bltz_out_34), .MenWrite(bltz_out_35), .RegDst(bltz_out_38),
    .led(bltz_out_39), .halt(halt), .lb(bltz_out_41), .RegDst_2(bltz_out_43), .out_17(MEM_IR), .out_18(M_PC),
    .out_19(MDin), .out_20(ex_mem_1_out_20), .out_21(ex_mem_1_out_21), .out_22(MemWrite),
    .out_23(ex_mem_1_out_23), .out_24(ex_mem_1_out_24), .out_25(ex_mem_1_out_25), .out_26(ex_mem_1_out_26),
    .out_28(ex_mem_1_out_28),
    .PC_4({JMP_PC[31:28], bltz_out_51_7, bltz_out_51_6, bltz_out_51_5, bltz_out_51_4, bltz_out_51_3, bltz_out_51_2, bltz_out_51}),
    .out_29(ex_mem_1_out_29), .JAL(JAL), .out_27(ex_mem_1_out_27));
  // Probe on MDin
  // Probe on MDin
  Register #(.width(32), .trigger("rising"), .Select("low")) register_1 (
    .D(bltz_out_33), .en(Led), .Q(LedData), .clk(CLK));  // open: clr
  // Probe on ex_mem_1_out_20
  Multiplexer #(.select(1), .width(5), .disabled("Z"), .enable("false")) multiplexer_10 (
    .in0(MEM_IR[20:16]), .in1(MEM_IR[15:11]), .out(multiplexer_10_out), .sel(ex_mem_1_out_28));
  RAM #(.addrWidth(10), .dataWidth(32), .bus("separate"), .Select("high")) ram_1 (
    .addr(ex_mem_1_out_20[11:2]), .din(MDin), .data(ram_1_data), .str(MemWrite), .clk(CLK), .clr(RST));  // open: sel, ld
  // Probe on ram_1_data
  MEM_WB mem_wb_1 (
    .CTK(CLK), .RST(RST), .Enable(Enable), .\指令 (MEM_IR), .PC(M_PC), .\运算器结果 (ex_mem_1_out_20),
    .\存储器结果 (ram_1_data), .MenToReg(ex_mem_1_out_21), .RegWrite(ex_mem_1_out_23), .halt(ex_mem_1_out_25),
    .lb(ex_mem_1_out_28), .RegDst(ex_mem_1_out_26), .out_15(WB_IR), .out_16(WB_PC), .out_17(mem_wb_1_out_17),
    .out_18(mem_wb_1_out_18), .out_19(RegDst), .out_20(RegWrite), .out_21(mem_wb_1_out_21), .out_22(RegDst),
    .out_23(lb_t), .PC_2(ex_mem_1_out_29), .out_25(mem_wb_1_out_25), .JAL(ex_mem_1_out_27), .out_24(J));
  // Probe on mem_wb_1_out_17
  Multiplexer #(.select(1), .width(32), .disabled("Z"), .enable("false")) multiplexer_11 (
    .in0(mem_wb_1_out_17), .in1(mem_wb_1_out_18), .out(multiplexer_11_out), .sel(RegDst));
  // Probe on mem_wb_1_out_18
  or or_4 (Enable, ~mem_wb_1_out_21, Go);  // OR_Gate
  Multiplexer #(.select(2), .width(8), .disabled("Z"), .enable("false")) multiplexer_12 (
    .in0(mem_wb_1_out_18[7:0]), .in1(mem_wb_1_out_18[15:8]), .in2(mem_wb_1_out_18[23:16]),
    .in3(mem_wb_1_out_18[31:24]), .out(multiplexer_12_out), .sel(mem_wb_1_out_17[1:0]));
  Multiplexer #(.select(1), .width(32), .disabled("Z"), .enable("false")) multiplexer_13 (
    .in0(multiplexer_11_out), .in1(bit_extender_4_out), .out(multiplexer_13_out), .sel(lb_t));
  assign bit_extender_4_out = {{24{multiplexer_12_out[7]}}, multiplexer_12_out};  // Bit_Extender bit_extender_4
  Multiplexer #(.select(1), .width(32), .disabled("Z"), .enable("false")) multiplexer_14 (
    .in0(multiplexer_13_out), .in1(mem_wb_1_out_25), .out(RDin), .sel(J));

  // Other names for the same wires on the sheet: MEM_PC[31:0] = M_PC

  // Notes on the sheet:
  //   中断源
  //   时空图监测，可删除
  //   中断等待指示
  //   数码管输出
  //   contents of rom_1 (hex, n*v repeats v):
  //   2011fff1 112020 20020022 c 22310001 620fffb 2002000a c 20090000 200b0010 34118483 20120404 118c00
  //   129400 36318281 22520404 ad310000 2328820 21290004 216bffff 1560fffb 200b0020 20090000 81310000
  //   112020 20020022 c 21290001 216bffff 1560fff9 2002000a c 20080001 20090003 20110876 112020 20020022 c
  //   200b0008 1118804 1318804 112020 20020022 c 216bffff 1560fff9 2002000a c 2008ffff 20117777 112020
  //   20020022 c 200b0010 3a31ffff 112020 20020022 c 216bffff 1560fffa 2002000a c
  //   JMP
  //   JR
  //   OP
  //   Func
  //   rs
  //   rt
  //   rd
  //   shamt
  //   imm16
  //   imm26
  //   Beq
  //   Bne
  //   MemToReg
  //   MemWrite
  //   AluOP
  //   AluSrcB
  //   RegWrite
  //   JAL
  //   Syscall
  //   控制位
  //   流水调试日志用
  //   暂停节拍，不能为0
  //   戳工具置1进入计数暂停模式，ctrl+k时钟自动运行到对应节拍暂停
  //   ctrl+k关闭时钟连续运行，将控制位置零，进入单步调试模式调试
  //   可计数暂停的时钟源
  //   为方便自动评测，需要输出流水线各段保存的PC值，注意是PC不是PC+4，另外ID段寄存器写入信息，Mem段内存写入信息也要输出
endmodule

module \重定向流水线  (
  output RegWrite,
  output MemWrite,
  output [31:0] IF_PC,
  output [31:0] ID_PC,
  output [31:0] EX_PC,
  output [31:0] M_PC,
  output [31:0] WB_PC,
  output [31:0] RDin,
  output [31:0] MDin,
  output [31:0] LedData
);

  wire ALU_src, and_1_out, and_2_out, and_5_out, and_6_out, and_7_out, and_8_out, and_9_out, and_10_out,
       and_11_out, and_12_out, BEQ, BLTZ, bltz_t, BNE, Branch, Bubble, CLK, clock_1_out, clock_2_out,
       comparator_1_eq, comparator_2_eq, comparator_2_lt, d_ff_1_q, Enable, ex_mem_1_out_21, ex_mem_1_out_23,
       ex_mem_1_out_24, ex_mem_1_out_25, ex_mem_1_out_26, ex_mem_1_out_27, ex_mem_1_out_28, Go, halt,
       id_ex_1_out_34, id_ex_1_out_35, id_ex_1_out_38, id_ex_1_out_39, id_ex_1_out_41, id_ex_1_out_43,
       id_ex_1_out_50, IR1, IR2, IR3, J, JAL, JMP, JR, LB, lb_t, Led, load_use, mem_wb_1_out_21, MemToReg,
       mips_alu_1_equal, multiplexer_15_out, multiplexer_17_out, multiplexer_19_out, multiplexer_23_out,
       nand_1_out, not_1_out, not_2_out, not_3_out, not_4_out, not_5_out, not_6_out, not_7_out, not_8_out,
       or_1_out, R, RegDst, RST, SignedExt, SLLV, Syscall, undriven, W1, W2, W3, \冲突 , \单周期硬布线控制器_1_alu_src ,
       \单周期硬布线控制器_1_beq , \单周期硬布线控制器_1_bne , \单周期硬布线控制器_1_jal , \单周期硬布线控制器_1_jmp , \单周期硬布线控制器_1_jr ,
       \单周期硬布线控制器_1_memtoreg , \单周期硬布线控制器_1_memwrite , \单周期硬布线控制器_1_out_20 , \单周期硬布线控制器_1_out_21 ,
       \单周期硬布线控制器_1_regdst , \单周期硬布线控制器_1_regwrite , \单周期硬布线控制器_1_syscall ;
  wire [1:0] multiplexer_7_out, multiplexer_8_out, R1_Re, R2_Re, \数据冲突检测电路_1_r1 , \数据冲突检测电路_1_r2 ;
  wire [3:0] id_ex_1_out_36, id_ex_1_out_51, id_ex_1_out_51_2, id_ex_1_out_51_3, id_ex_1_out_51_4,
       id_ex_1_out_51_5, id_ex_1_out_51_6, id_ex_1_out_51_7, \单周期硬布线控制器_1_alu_op ;
  wire [4:0] multiplexer_4_out, multiplexer_6_out, multiplexer_9_out, multiplexer_10_out, multiplexer_16_out,
       R1_num, R2_num;
  wire [7:0] multiplexer_20_out;
  wire [12:0] CNT_num;
  wire [15:0] adder_3_out, \LoadUse次数 , multiplier_1_out, \总周期数 , \插入气泡数 , \无条件分支数 , \条件分支成功数 ;
  wire [31:0] adder_1_out, bit_extender_1_out, bit_extender_2_out, bit_extender_3_out, bit_extender_4_out,
       Branch_PC, EX_IR, ex_mem_1_out_29, ID_IR, if_id_1_out_11, IF_IR, JR_PC, Mem_ALU, MEM_IR,
       mem_wb_1_out_17, mem_wb_1_out_18, mem_wb_1_out_25, mips_regifile_1_r2, multiplexer_1_out,
       multiplexer_11_out, multiplexer_18_out, multiplexer_21_out, R1, \R1_原 , R2_233, R2_in, \R2_原 ,
       ram_1_data, shifter_1_out, WB_IR;
  wire [31:1] mips_alu_1_result;
  wire [31:2] JMP_PC;
  wire [31:26] id_ex_1_out_42;

  Button \u_总复位  (.out(RST));
  Button _1 (.out(IR1));
  Button _2 (.out(IR2));
  Button _3 (.out(IR3));
  // Probe on \总周期数 
  // Probe on \总周期数 
  Button \u_继续运行  (.out(Go));
  LED #(.active("true")) led_1 (.in(W1));
  LED #(.active("true")) led_2 (.in(W2));
  LED #(.active("true")) led_3 (.in(W3));
  and and_1 (and_1_out, Enable, ~load_use);  // AND_Gate
  Hex_Digit_Display hex_digit_display_1 (.value(LedData[31:28]));  // open: dp
  // Probe on IF_PC[19:0]
  // Mips_Probe mips_probe_1: pin names not known; wires that end beside it: IF_IR
  // Probe on multiplexer_1_out
  Register #(.width(32), .trigger("rising"), .Select("low")) PC (
    .D(multiplexer_1_out), .en(and_1_out), .Q(IF_PC), .clk(CLK), .clr(RST));
  Multiplexer #(.select(3), .width(32), .disabled("Z"), .enable("false")) multiplexer_1 (
    .in0(adder_1_out), .in1(Branch_PC), .in2({JMP_PC, 2'b00}), .in6(JR_PC), .out(multiplexer_1_out),
    .sel({JR, JMP, Branch}));  // open: in3, in4, in5, in7
  Hex_Digit_Display hex_digit_display_2 (.value(LedData[23:20]));  // open: dp
  Hex_Digit_Display hex_digit_display_3 (.value(LedData[27:24]));  // open: dp
  // Probe on ID_PC[19:0]
  // Mips_Probe mips_probe_2: pin names not known; wires that end beside it: ID_IR
  Adder #(.width(32)) adder_1 (.a(IF_PC), .b(32'h4), .out(adder_1_out));  // open: cin, cout
  Hex_Digit_Display hex_digit_display_4 (.value(LedData[19:16]));  // open: dp
  Hex_Digit_Display hex_digit_display_5 (.value(LedData[15:12]));  // open: dp
  Hex_Digit_Display hex_digit_display_6 (.value(LedData[11:8]));  // open: dp
  Hex_Digit_Display hex_digit_display_7 (.value(LedData[7:4]));  // open: dp
  Clock #(.highDuration(1), .lowDuration(1)) clock_1 (.out(clock_1_out));
  // Probe on EX_PC[19:0]
  // Mips_Probe mips_probe_3: pin names not known; wires that end beside it: clock_1_out, EX_IR, CLK
  ROM #(.addrWidth(10), .dataWidth(32), .Select("high")) rom_1 (.addr(IF_PC[11:2]), .data(IF_IR));
  and and_2 (and_2_out, Enable, ~load_use);  // AND_Gate
  Hex_Digit_Display hex_digit_display_8 (.value(LedData[3:0]));  // open: dp
  \数据冲突检测电路  \u_数据冲突检测电路_1  (
    .\R1使用情况 (\单周期硬布线控制器_1_out_20 ), .\EX段写入信号 (id_ex_1_out_38), .\MEM段写入信号 (ex_mem_1_out_23),
    .\EX段写入编号 (multiplexer_9_out), .\MEM段写入编号 (multiplexer_16_out), .\R1编号 (R1_num), .\R2编号 (R2_num),
    .\R2使用情况 (\单周期硬布线控制器_1_out_21 ), .R1(\数据冲突检测电路_1_r1 ), .\冲突 (\冲突 ), .R2(\数据冲突检测电路_1_r2 ));
  \Load_Use检测  \load_use检测_1  (
    .\R1使用情况 (\单周期硬布线控制器_1_out_20 ), .\EX段写入信号 (id_ex_1_out_34), .\EX段写入编号 (multiplexer_9_out),
    .\R1编号 (R1_num), .\R2编号 (R2_num), .\R2使用情况 (\单周期硬布线控制器_1_out_21 ), .out_7(load_use));
  IF_ID if_id_1 (
    .CTK(CLK), .RST(RST), .in_4(IF_IR), .in_5(IF_PC), .out_9(ID_IR), .out_10(ID_PC), .Enable(and_2_out),
    .\同步置0 (Bubble), .in_6(adder_1_out), .out_11(if_id_1_out_11));  // open: in_7, out_12
  // Probe on \总周期数 
  // Probe on M_PC[19:0]
  // Mips_Probe mips_probe_4: pin names not known; wires that end beside it: MEM_IR
  // Probe on \总周期数 
  // Probe on \无条件分支数 
  // Probe on \条件分支成功数 
  // Probe on \插入气泡数 
  // Probe on \LoadUse次数 
  \单周期硬布线控制器  \u_单周期硬布线控制器_1  (
    .Func(ID_IR[5:0]), .OP(ID_IR[31:26]), .ALU_OP(\单周期硬布线控制器_1_alu_op ), .MemToReg(\单周期硬布线控制器_1_memtoreg ),
    .MemWrite(\单周期硬布线控制器_1_memwrite ), .ALU_SRC(\单周期硬布线控制器_1_alu_src ), .SysCALL(\单周期硬布线控制器_1_syscall ),
    .SignedExt(SignedExt), .RegDst(\单周期硬布线控制器_1_regdst ), .JR(\单周期硬布线控制器_1_jr ), .JMP(\单周期硬布线控制器_1_jmp ),
    .Beq(\单周期硬布线控制器_1_beq ), .JAL(\单周期硬布线控制器_1_jal ), .Bne(\单周期硬布线控制器_1_bne ), .SLLV(SLLV), .LB(LB),
    .BLTZ(BLTZ), .out_20(\单周期硬布线控制器_1_out_20 ), .out_21(\单周期硬布线控制器_1_out_21 ),
    .RegWrite(\单周期硬布线控制器_1_regwrite ));  // open: ERET, Func_2, MFC0, MTC0
  Multiplexer #(.select(1), .width(5), .disabled("Z"), .enable("false")) multiplexer_2 (
    .in0(ID_IR[25:21]), .in1(5'b00010), .out(R1_num), .sel(\单周期硬布线控制器_1_syscall ));
  Multiplexer #(.select(1), .width(5), .disabled("Z"), .enable("false")) multiplexer_3 (
    .in0(ID_IR[20:16]), .in1(5'b00100), .out(R2_num), .sel(\单周期硬布线控制器_1_syscall ));
  Multiplexer #(.select(1), .width(5), .disabled("Z"), .enable("false")) multiplexer_4 (
    .in0(WB_IR[20:16]), .in1(WB_IR[15:11]), .out(multiplexer_4_out), .sel(RegDst));
  Multiplexer #(.select(1), .width(5), .disabled("Z"), .enable("false")) multiplexer_5 (
    .in0(ID_IR[10:6]), .in1(R1[4:0]), .sel(SLLV));  // open: out
  assign bit_extender_1_out = {{6{1'b0}}, ID_IR[25:0]};  // Bit_Extender bit_extender_1
  Comparator #(.width(32), .mode("twosComplement")) comparator_1 (
    .a(JR_PC), .b(32'h22), .eq(comparator_1_eq));  // open: gt, lt
  // Probe on IF_PC[11:0]
  // Probe on WB_PC[19:0]
  // Mips_Probe mips_probe_5: pin names not known; wires that end beside it: WB_IR
  Multiplexer #(.select(1), .width(5), .disabled("Z"), .enable("false")) multiplexer_6 (
    .in0(multiplexer_4_out), .in1({5{1'b1}}), .out(multiplexer_6_out), .sel(J));
  and and_3 (Led, Syscall, comparator_1_eq);
  and and_4 (halt, Syscall, ~comparator_1_eq);  // AND_Gate
  // Probe on EX_PC[11:0]
  // Probe on ID_PC[11:0]
  MIPS_Regifile mips_regifile_1 (
    .Din(RDin), .Clk(CLK), .R1(R1), .R2(mips_regifile_1_r2), .WE(RegWrite), .WAdr(multiplexer_6_out),
    .R1Adr(R1_num), .R2Adr(R2_num));
  // Probe on M_PC[11:0]
  D_Flip_Flop #(.trigger("high"), .Pre_Clr_Positions("LEGACY"), .NegatePresetClear("false"), .enable("true"), .NewFFLayout("false")) d_ff_1 (.Q(d_ff_1_q));  // open: clk, D, Qn, preset, en, reset
  // Probe on 13'hc
  Multiplexer #(.select(1), .width(2), .disabled("Z"), .enable("false")) multiplexer_7 (
    .in0(\数据冲突检测电路_1_r1 ), .in1(2'b00), .out(multiplexer_7_out), .sel(load_use));
  Multiplexer #(.select(1), .width(2), .disabled("Z"), .enable("false")) multiplexer_8 (
    .in0(\数据冲突检测电路_1_r2 ), .in1(2'b00), .out(multiplexer_8_out), .sel(load_use));
  // Probe on R1
  // Probe on WB_PC[11:0]
  Comparator #(.width(13), .mode("twosComplement")) comparator_2 (
    .a(CNT_num), .b(13'hc), .eq(comparator_2_eq), .lt(comparator_2_lt));  // open: gt
  Clock #(.highDuration(1), .lowDuration(1)) clock_2 (.out(clock_2_out));
  ID_EX id_ex_1 (
    .CTK(CLK), .RST(RST), .Enable(Enable), .\指令 (ID_IR), .PC(ID_PC), .out_30(EX_IR), .out_31(EX_PC),
    .\寄存器1 (R1), .out_32(\R1_原 ), .\寄存器2 (mips_regifile_1_r2), .out_33(\R2_原 ),
    .MenToReg(\单周期硬布线控制器_1_memtoreg ), .out_34(id_ex_1_out_34), .MenWrite(\单周期硬布线控制器_1_memwrite ),
    .out_35(id_ex_1_out_35), .RegWrite(\单周期硬布线控制器_1_regwrite ), .out_38(id_ex_1_out_38), .sllv(SLLV),
    .out_39(id_ex_1_out_39), .halt(\单周期硬布线控制器_1_syscall ), .out_40(Syscall), .lb(LB),
    .out_41(id_ex_1_out_41), .RegDst(\单周期硬布线控制器_1_regdst ), .out_43(id_ex_1_out_43),
    .imm(bit_extender_1_out), .out_42({id_ex_1_out_42, JMP_PC[27:2]}), .ALU_OP(\单周期硬布线控制器_1_alu_op ),
    .out_36(id_ex_1_out_36), .ALU_src(\单周期硬布线控制器_1_alu_src ), .out_37(ALU_src), .JR(\单周期硬布线控制器_1_jr ),
    .out_44(JR), .JMP(\单周期硬布线控制器_1_jmp ), .out_45(JMP), .JAL(\单周期硬布线控制器_1_jal ), .out_46(JAL),
    .BNE(\单周期硬布线控制器_1_bne ), .out_47(BNE), .BEQ(\单周期硬布线控制器_1_beq ), .out_48(BEQ), .BLTZ(BLTZ),
    .out_49(bltz_t), .\同步置0 (or_1_out), .Signext(SignedExt), .out_50(id_ex_1_out_50), .in_26(if_id_1_out_11),
    .out_51({JMP_PC[31:28], id_ex_1_out_51_7, id_ex_1_out_51_6, id_ex_1_out_51_5, id_ex_1_out_51_4, id_ex_1_out_51_3, id_ex_1_out_51_2, id_ex_1_out_51}),
    .out_52(R1_Re), .in_27(multiplexer_7_out), .in_28(multiplexer_8_out), .out_53(R2_Re));  // open: in_29, out_54
  nand nand_1 (nand_1_out, d_ff_1_q, comparator_2_eq);
  Counter #(.width(13), .max('h1fff), .ongoal("stay"), .trigger("rising"), .behavior("old")) counter_1 (
    .count(comparator_2_lt), .Q(CNT_num), .clk(clock_2_out));  // open: load, D, carry, clr, preset
  // Probe on \R1_原 
  or or_1 (or_1_out, load_use, Bubble);
  assign CLK = nand_1_out ? clock_2_out : 1'bz;  // Controlled_Buffer controlled_buffer_1
  Multiplexer #(.select(1), .width(5), .disabled("Z"), .enable("false")) multiplexer_9 (
    .in0(EX_IR[20:16]), .in1(EX_IR[15:11]), .out(multiplexer_9_out), .sel(id_ex_1_out_43));
  Multiplexer #(.select(1), .width(5), .disabled("Z"), .enable("false")) multiplexer_10 (
    .in0(JMP_PC[12:8]), .in1(JR_PC[4:0]), .out(multiplexer_10_out), .sel(id_ex_1_out_39));
  assign bit_extender_2_out = {{16{1'b0}}, JMP_PC[17:2]};  // Bit_Extender bit_extender_2
  assign bit_extender_3_out = {{16{JMP_PC[17]}}, JMP_PC[17:2]};  // Bit_Extender bit_extender_3
  Pull_Resistor #(.pull(1)) pull_resistor_1 (.node(CLK));
  MIPS_ALU mips_alu_1 (
    .X(JR_PC), .Y(R2_in), .AluOP(id_ex_1_out_36), .Equal(mips_alu_1_equal), .Result({mips_alu_1_result, R}),
    .shamt(multiplexer_10_out));  // open: Result_2
  Multiplexer #(.select(1), .width(32), .disabled("Z"), .enable("false")) multiplexer_11 (
    .in0(bit_extender_2_out), .in1(bit_extender_3_out), .out(multiplexer_11_out), .sel(id_ex_1_out_50));
  Shifter #(.width(32), .shift("ll")) shifter_1 (.in(bit_extender_3_out), .\dist (5'b00010), .out(shifter_1_out));
  and and_5 (and_5_out, mips_alu_1_equal, BEQ);
  or or_2 (Branch, and_5_out, and_6_out, and_7_out);
  and and_6 (and_6_out, ~mips_alu_1_equal, BNE);  // AND_Gate
  and and_7 (and_7_out, R, bltz_t);
  // Probe on R2_233
  // Probe on {mips_alu_1_result, R}
  Adder #(.width(32)) adder_2 (
    .a(shifter_1_out),
    .b({JMP_PC[31:28], id_ex_1_out_51_7, id_ex_1_out_51_6, id_ex_1_out_51_5, id_ex_1_out_51_4, id_ex_1_out_51_3, id_ex_1_out_51_2, id_ex_1_out_51}),
    .out(Branch_PC));  // open: cin, cout
  or or_3 (Bubble, Branch, JMP);
  EX_MEM ex_mem_1 (
    .CTK(CLK), .RST(RST), .Enable(Enable), .\指令 (EX_IR), .PC(EX_PC), .\寄存器1 (R2_233),
    .\寄存器2 ({mips_alu_1_result, R}), .MenToReg(id_ex_1_out_34), .MenWrite(id_ex_1_out_35),
    .RegDst(id_ex_1_out_38), .led(undriven), .halt(halt), .lb(id_ex_1_out_41), .RegDst_2(id_ex_1_out_43),
    .out_17(MEM_IR), .out_18(M_PC), .out_19(MDin), .out_20(Mem_ALU), .out_21(ex_mem_1_out_21),
    .out_22(MemWrite), .out_23(ex_mem_1_out_23), .out_24(ex_mem_1_out_24), .out_25(ex_mem_1_out_25),
    .out_26(ex_mem_1_out_26), .out_28(ex_mem_1_out_28),
    .PC_4({JMP_PC[31:28], id_ex_1_out_51_7, id_ex_1_out_51_6, id_ex_1_out_51_5, id_ex_1_out_51_4, id_ex_1_out_51_3, id_ex_1_out_51_2, id_ex_1_out_51}),
    .out_29(ex_mem_1_out_29), .JAL(JAL), .out_27(ex_mem_1_out_27));
  // Probe on MDin
  // Probe on MDin
  // Probe on JR_PC
  Multiplexer #(.select(2), .width(32), .disabled("Z"), .enable("false")) multiplexer_12 (
    .in0(\R1_原 ), .in1(RDin), .in2(Mem_ALU), .in3(Mem_ALU), .out(JR_PC), .sel(R1_Re));
  Multiplexer #(.select(2), .width(32), .disabled("Z"), .enable("false")) multiplexer_13 (
    .in0(\R2_原 ), .in1(RDin), .in2(Mem_ALU), .in3(Mem_ALU), .out(R2_233), .sel(R2_Re));
  // Probe on Mem_ALU
  // Probe on R2_Re
  Multiplexer #(.select(1), .width(32), .disabled("Z"), .enable("false")) multiplexer_14 (
    .in0(R2_233), .in1(multiplexer_11_out), .out(R2_in), .sel(ALU_src));
  Counter #(.width(16), .max('hffff), .ongoal("wrap"), .trigger("rising"), .behavior("old")) counter_2 (
    .count(1'b1), .Q(\无条件分支数 ), .clk(multiplexer_15_out), .clr(RST));  // open: load, D, carry, preset
  Multiplexer #(.select(1), .width(1), .disabled("Z"), .enable("false")) multiplexer_15 (
    .in0(and_8_out), .in1(1'b0), .out(multiplexer_15_out), .sel(not_1_out));
  not not_1 (not_1_out, not_2_out);
  and and_8 (and_8_out, JMP, CLK);
  Multiplexer #(.select(1), .width(5), .disabled("Z"), .enable("false")) multiplexer_16 (
    .in0(MEM_IR[20:16]), .in1(MEM_IR[15:11]), .out(multiplexer_16_out), .sel(ex_mem_1_out_28));
  Register #(.width(32), .trigger("rising"), .Select("low")) register_1 (
    .D(R2_233), .en(Led), .Q(LedData), .clk(CLK));  // open: clr
  // Probe on R1_Re
  not not_2 (not_2_out, CLK);
  RAM #(.addrWidth(10), .dataWidth(32), .bus("separate"), .Select("high")) ram_1 (
    .addr(Mem_ALU[11:2]), .din(MDin), .data(ram_1_data), .str(MemWrite), .clk(CLK), .clr(RST));  // open: sel, ld
  // Probe on ram_1_data
  Multiplexer #(.select(1), .width(1), .disabled("Z"), .enable("false")) multiplexer_17 (
    .in0(and_9_out), .in1(1'b0), .out(multiplexer_17_out), .sel(not_4_out));
  and and_9 (and_9_out, Branch, CLK);
  MEM_WB mem_wb_1 (
    .CTK(CLK), .RST(RST), .Enable(Enable), .\指令 (MEM_IR), .PC(M_PC), .\运算器结果 (Mem_ALU), .\存储器结果 (ram_1_data),
    .MenToReg(ex_mem_1_out_21), .RegWrite(ex_mem_1_out_23), .halt(ex_mem_1_out_25), .lb(ex_mem_1_out_28),
    .RegDst(ex_mem_1_out_26), .out_15(WB_IR), .out_16(WB_PC), .out_17(mem_wb_1_out_17),
    .out_18(mem_wb_1_out_18), .out_19(MemToReg), .out_20(RegWrite), .out_21(mem_wb_1_out_21),
    .out_22(RegDst), .out_23(lb_t), .PC_2(ex_mem_1_out_29), .out_25(mem_wb_1_out_25), .JAL(ex_mem_1_out_27),
    .out_24(J));
  // Probe on mem_wb_1_out_17
  Counter #(.width(16), .max('hffff), .ongoal("wrap"), .trigger("rising"), .behavior("old")) counter_3 (
    .count(1'b1), .Q(\条件分支成功数 ), .clk(multiplexer_17_out), .clr(RST));  // open: load, D, carry, preset
  not not_3 (not_3_out, CLK);
  not not_4 (not_4_out, not_3_out);
  Multiplexer #(.select(1), .width(32), .disabled("Z"), .enable("false")) multiplexer_18 (
    .in0(mem_wb_1_out_17), .in1(mem_wb_1_out_18), .out(multiplexer_18_out), .sel(MemToReg));
  // Probe on mem_wb_1_out_18
  Counter #(.width(16), .max('hffff), .ongoal("wrap"), .trigger("rising"), .behavior("old")) counter_4 (
    .count(1'b1), .Q(\总周期数 ), .clk(multiplexer_19_out), .clr(RST));  // open: load, D, carry, preset
  Multiplexer #(.select(1), .width(1), .disabled("Z"), .enable("false")) multiplexer_19 (
    .in0(and_10_out), .in1(1'b0), .out(multiplexer_19_out), .sel(not_5_out));
  and and_10 (and_10_out, Enable, CLK);
  or or_4 (Enable, ~mem_wb_1_out_21, Go);  // OR_Gate
  Multiplexer #(.select(2), .width(8), .disabled("Z"), .enable("false")) multiplexer_20 (
    .in0(mem_wb_1_out_18[7:0]), .in1(mem_wb_1_out_18[15:8]), .in2(mem_wb_1_out_18[23:16]),
    .in3(mem_wb_1_out_18[31:24]), .out(multiplexer_20_out), .sel(mem_wb_1_out_17[1:0]));
  not not_5 (not_5_out, not_6_out);
  not not_6 (not_6_out, CLK);
  Multiplexer #(.select(1), .width(32), .disabled("Z"), .enable("false")) multiplexer_21 (
    .in0(multiplexer_18_out), .in1(bit_extender_4_out), .out(multiplexer_21_out), .sel(lb_t));
  assign bit_extender_4_out = {{24{multiplexer_20_out[7]}}, multiplexer_20_out};  // Bit_Extender bit_extender_4
  Multiplexer #(.select(1), .width(32), .disabled("Z"), .enable("false")) multiplexer_22 (
    .in0(multiplexer_21_out), .in1(mem_wb_1_out_25), .out(RDin), .sel(J));
  and and_11 (and_11_out, load_use, Enable);
  Adder #(.width(16)) adder_3 (.a(\无条件分支数 ), .b(\条件分支成功数 ), .out(adder_3_out));  // open: cin, cout
  Counter #(.width(16), .max('hffff), .ongoal("wrap"), .trigger("rising"), .behavior("old")) counter_5 (
    .count(1'b1), .Q(\LoadUse次数 ), .clk(multiplexer_23_out), .clr(RST));  // open: load, D, carry, preset
  Multiplexer #(.select(1), .width(1), .disabled("Z"), .enable("false")) multiplexer_23 (
    .in0(and_12_out), .in1(1'b0), .out(multiplexer_23_out), .sel(not_8_out));
  not not_7 (not_7_out, CLK);
  not not_8 (not_8_out, not_7_out);
  and and_12 (and_12_out, and_11_out, CLK);
  Multiplier #(.width(16)) multiplier_1 (.a(adder_3_out), .b(16'h2), .out(multiplier_1_out));  // open: cin, cout
  Adder #(.width(16)) adder_4 (.a(multiplier_1_out), .b(\LoadUse次数 ), .out(\插入气泡数 ));  // open: cin, cout

  // Other names for the same wires on the sheet: shamt1[4:0] = JMP_PC[12:8]; MEM_PC[31:0] = M_PC; R1_in[31:0] = JR_PC;
  //   shamt2[4:0] = JR_PC[4:0]; WB_in[31:0] = RDin

  // Notes on the sheet:
  //   中断源
  //   时空图监测，可删除
  //   中断等待指示
  //   数码管输出
  //   contents of rom_1 (hex, n*v repeats v):
  //   20110001 8100005 20110001 20120002 20130003 8100009 20110001 20120002 20130003 810000d 20110001
  //   20120002 20130003 8100011 20110001 20120002 20130003 c1000f8 20100001 20110001 118fc0 112020
  //   20020022 c 118882 12200001 8100015 112020 20020022 c 20110001 118880 112020 20020022 c 12200001
  //   810001f 20110001 118fc0 112020 20020022 c 1188c3 112020 20020022 c 118903 112020 20020022 c 118903
  //   112020 20020022 c 118903 112020 20020022 c 118903 112020 20020022 c 118903 112020 20020022 c 118903
  //   112020 20020022 c 118903 112020 20020022 c 20100001 109fc0 139fc3 8021 2012000c 24160003 26100001
  //   3210000f 20080008 20090001 139900 2709825 132020 20020022 c 1094022 1500fff9 22100001 2018000f
  //   2188024 108700 20080008 20090001 139902 2709825 132021 20020022 c 1094022 1500fff9 108702 2c9b022
  //   12c00001 8100050 4020 1084027 84400 3508ffff 82021 20020022 c 2010ffff 20110000 ae300000 22100001
  //   22310004 ae300000 22100001 22310004 ae300000 22100001 22310004 ae300000 22100001 22310004 ae300000
  //   22100001 22310004 ae300000 22100001 22310004 ae300000 22100001 22310004 ae300000 22100001 22310004
  //   ae300000 22100001 22310004 ae300000 22100001 22310004 ae300000 22100001 22310004 ae300000 22100001
  //   22310004 ae300000 22100001 22310004 ae300000 22100001 22310004 ae300000 22100001 22310004 ae300000
  //   22100001 22310004 22100001 8020 2011003c 8e130000 8e340000 274402a 11000002 ae330000 ae140000
  //   2231fffc 1611fff8 102020 20020022 c 22100004 2011003c 1611fff2 20020032 c 2008ffff 20117777 112020
  //   20020022 c 200b0010 3a31ffff 112020 20020022 c 216bffff 1560fffa 2002000a c 20080001 20090003
  //   20110876 112020 20020022 c 200b0008 1118804 1318804 112020 20020022 c 216bffff 1560fff9 2002000a c
  //   20090000 200b0010 34118483 20120404 118c00 129400 36318281 22520404 ad310000 2328820 21290004
  //   216bffff 1560fffb 200b0020 20090000 81310000 112020 20020022 c 21290001 216bffff 1560fff9 2002000a c
  //   2011fff1 112020 20020022 c 22310001 620fffb 2002000a c 2002000a c 20100000 22100001 102020 20020022
  //   c 22100002 102020 20020022 c 22100003 102020 20020022 c 22100004 102020 20020022 c 22100005 102020
  //   20020022 c 22100006 102020 20020022 c 22100007 102020 20020022 c 22100008 102020 20020022 20020022 c
  //   3e00008
  //   JMP
  //   JR
  //   OP
  //   Func
  //   rs
  //   rt
  //   rd
  //   shamt
  //   imm16
  //   imm26
  //   Beq
  //   Bne
  //   MemToReg
  //   MemWrite
  //   AluOP
  //   AluSrcB
  //   RegWrite
  //   JAL
  //   Syscall
  //   控制位
  //   流水调试日志用
  //   暂停节拍，不能为0
  //   戳工具置1进入计数暂停模式，ctrl+k时钟自动运行到对应节拍暂停
  //   ctrl+k关闭时钟连续运行，将控制位置零，进入单步调试模式调试
  //   可计数暂停的时钟源
  //   为方便自动评测，需要输出流水线各段保存的PC值，注意是PC不是PC+4，另外ID段寄存器写入信息，Mem段内存写入信息也要输出
endmodule

module \中断按键参考电路  (
  input  \同步清零信号 ,
  output \与中断屏蔽位与 
);

  wire \_1号中断_out , and_1_out, clock_1_out, d_ff_1_q, or_1_out, or_2_out;

  Clock #(.highDuration(1), .lowDuration(1)) clock_1 (.out(clock_1_out));
  Button \_1号中断  (.out(\_1号中断_out ));
  LED #(.active("true")) \_1号中断等待指示灯  (.in(or_1_out));
  or or_1 (or_1_out, \与中断屏蔽位与 , d_ff_1_q);
  D_Flip_Flop #(.trigger("rising"), .Pre_Clr_Positions("LEGACY"), .NegatePresetClear("false"), .enable("true"), .NewFFLayout("false")) d_ff_1 (
    .clk(\_1号中断_out ), .D(1'b1), .Q(d_ff_1_q), .reset(\与中断屏蔽位与 ));  // open: Qn, preset, en
  or or_2 (or_2_out, d_ff_1_q, \与中断屏蔽位与 );
  and and_1 (and_1_out, or_2_out, ~\同步清零信号 );  // AND_Gate
  D_Flip_Flop #(.trigger("rising"), .Pre_Clr_Positions("LEGACY"), .NegatePresetClear("false"), .enable("true"), .NewFFLayout("false")) IR1 (
    .clk(clock_1_out), .D(and_1_out), .Q(\与中断屏蔽位与 ));  // open: Qn, preset, en, reset

  // Notes on the sheet:
  //   中断信号采样参考电路
  //   Reset 
endmodule
module \单周期MIPS_单级中断  (
  input  IR1,
  input  IR2,
  input  IR3,
  output RegWrite,
  output MemWrite,
  output [31:0] PC,
  output [31:0] IR,
  output [31:0] RDin,
  output [31:0] MDin,
  output [31:0] LedData
);

  wire and_1_out, and_2_out, and_3_out, and_6_out, and_7_out, and_8_out, and_9_out, and_10_out, and_11_out,
       and_12_out, and_13_out, BLTZ, CLK, clock_2_out, comparator_1_eq, comparator_2_eq, comparator_3_eq,
       comparator_4_eq, comparator_5_eq, comparator_5_lt, comparator_6_eq, comparator_7_eq, d_ff_1_q,
       d_ff_2_q, d_ff_3_q, d_ff_4_q, ERET, Go, halt, IR1_q, IR1_t, IR2_q, IR2_t, IR3_q, IR3_t, IRA, IRB, IRC,
       LB, Led, MemToReg, mips_alu_1_equal, mips_probe_1_p2, multiplexer_16_out, nand_1_out, not_1_out,
       not_2_out, or_1_out, or_2_out, or_6_out, or_10_out, or_11_out, or_12_out, or_13_out,
       priority_encoder_1_gs, RST, SignedExt, SLLV, W1, W2, W3, \中断状态_q , \单周期硬布线控制器_1_alu_src ,
       \单周期硬布线控制器_1_beq , \单周期硬布线控制器_1_bne , \单周期硬布线控制器_1_jal , \单周期硬布线控制器_1_jmp , \单周期硬布线控制器_1_jr ,
       \单周期硬布线控制器_1_regdst ;
  wire [1:0] IR_now, priority_encoder_1_out;
  wire [3:0] \单周期硬布线控制器_1_alu_op ;
  wire [4:0] multiplexer_4_out, multiplexer_5_out, multiplexer_6_out, multiplexer_7_out, multiplexer_8_out;
  wire [7:0] multiplexer_12_out, ram_1_data, ram_1_data_2, ram_1_data_3, ram_1_data_4;
  wire [12:0] CNT_num;
  wire [15:0] \总周期数 ;
  wire [31:0] adder_2_out, Addr, bit_extender_1_out, bit_extender_2_out, bit_extender_3_out,
       multiplexer_1_out, multiplexer_2_out, multiplexer_9_out, multiplexer_10_out, multiplexer_11_out,
       multiplexer_13_out, multiplexer_15_out, multiplexer_17_out, multiplexer_18_out, nextPC, PC_2_q, PC_4,
       PCout, R1, shifter_1_out;

  Clock #(.highDuration(1), .lowDuration(1)) clock_1 ();  // open: out
  Button _1 ();  // open: out
  Button _2 ();  // open: out
  Button _3 ();  // open: out
  Button \u_继续运行  (.out(Go));
  LED #(.active("true")) led_1 (.in(W1));
  LED #(.active("true")) led_2 (.in(W2));
  LED #(.active("true")) led_3 (.in(W3));
  Hex_Digit_Display hex_digit_display_1 (.value(LedData[31:28]));  // open: dp
  Comparator #(.width(16), .mode("twosComplement")) comparator_1 (
    .a(16'h23b), .b(\总周期数 ), .eq(comparator_1_eq));  // open: gt, lt
  Comparator #(.width(16), .mode("twosComplement")) comparator_2 (
    .a(\总周期数 ), .b(16'h1), .eq(comparator_2_eq));  // open: gt, lt
  Comparator #(.width(16), .mode("twosComplement")) comparator_3 (
    .a(\总周期数 ), .b(16'h4), .eq(comparator_3_eq));  // open: gt, lt
  Comparator #(.width(16), .mode("twosComplement")) comparator_4 (
    .a(\总周期数 ), .b(16'h7), .eq(comparator_4_eq));  // open: gt, lt
  Multiplexer #(.select(1), .width(32), .disabled("Z"), .enable("false")) multiplexer_1 (
    .in0(PC_4), .in1(adder_2_out), .out(multiplexer_1_out), .sel(or_6_out));
  Hex_Digit_Display hex_digit_display_2 (.value(LedData[27:24]));  // open: dp
  Hex_Digit_Display hex_digit_display_3 (.value(LedData[23:20]));  // open: dp
  or or_1 (or_1_out, comparator_1_eq, comparator_2_eq);
  assign IRA = or_1_out ? ~CLK : 1'bz;  // Controlled_Inverter controlled_inverter_1
  assign IRB = comparator_3_eq ? ~CLK : 1'bz;  // Controlled_Inverter controlled_inverter_2
  assign IRC = comparator_4_eq ? ~CLK : 1'bz;  // Controlled_Inverter controlled_inverter_3
  Multiplexer #(.select(1), .width(32), .disabled("Z"), .enable("false")) multiplexer_2 (
    .in0(multiplexer_1_out), .in1({PC[31:28], IR[25:0], 2'b00}), .out(multiplexer_2_out),
    .sel(\单周期硬布线控制器_1_jmp ));
  Multiplexer #(.select(1), .width(32), .disabled("Z"), .enable("false")) multiplexer_3 (
    .in0(multiplexer_2_out), .in1(R1), .out(nextPC), .sel(\单周期硬布线控制器_1_jr ));
  or or_2 (or_2_out, not_1_out, Go);
  not not_1 (not_1_out, halt);
  Hex_Digit_Display hex_digit_display_4 (.value(LedData[19:16]));  // open: dp
  Hex_Digit_Display hex_digit_display_5 (.value(LedData[15:12]));  // open: dp
  Pull_Resistor #(.pull(0)) pull_resistor_1 (.node(IRA));
  Pull_Resistor #(.pull(0)) pull_resistor_2 (.node(IRB));
  Pull_Resistor #(.pull(0)) pull_resistor_3 (.node(IRC));
  Register #(.width(32), .trigger("rising"), .Select("low")) u_PC (
    .D(PCout), .en(or_2_out), .Q(PC), .clk(CLK), .clr(RST));
  Hex_Digit_Display hex_digit_display_6 (.value(LedData[11:8]));  // open: dp
  Hex_Digit_Display hex_digit_display_7 (.value(LedData[7:4]));  // open: dp
  // Probe on \总周期数 
  Adder #(.width(32)) adder_1 (.a(PC), .b(32'h4), .out(PC_4));  // open: cin, cout
  Hex_Digit_Display hex_digit_display_8 (.value(LedData[3:0]));  // open: dp
  Button button_1 (.out(RST));
  // Mips_Probe mips_probe_1: pin names not known; wires that end beside it: IR, mips_probe_1_p2
  ROM #(.addrWidth(10), .dataWidth(32), .Select("high")) rom_1 (.addr(PC[11:2]), .data(IR));
  or or_3 (IR1_t, IR1, IRA);
  D_Flip_Flop #(.trigger("high"), .Pre_Clr_Positions("LEGACY"), .NegatePresetClear("false"), .enable("true"), .NewFFLayout("false")) d_ff_1 (.Q(d_ff_1_q));  // open: clk, D, Qn, preset, en, reset
  // Probe on 13'hba
  \单周期硬布线控制器  \u_单周期硬布线控制器_1  (
    .Func(IR[5:0]), .OP(IR[31:26]), .ALU_OP(\单周期硬布线控制器_1_alu_op ), .MemToReg(MemToReg), .MemWrite(MemWrite),
    .ALU_SRC(\单周期硬布线控制器_1_alu_src ), .SysCALL(mips_probe_1_p2), .SignedExt(SignedExt),
    .RegDst(\单周期硬布线控制器_1_regdst ), .JR(\单周期硬布线控制器_1_jr ), .JMP(\单周期硬布线控制器_1_jmp ), .Beq(\单周期硬布线控制器_1_beq ),
    .JAL(\单周期硬布线控制器_1_jal ), .Bne(\单周期硬布线控制器_1_bne ), .SLLV(SLLV), .LB(LB), .BLTZ(BLTZ), .ERET(ERET),
    .RegWrite(RegWrite));  // open: out_20, out_21, Func_2, MFC0, MTC0
  Multiplexer #(.select(1), .width(5), .disabled("Z"), .enable("false")) multiplexer_4 (
    .in0(IR[25:21]), .in1(5'b00010), .out(multiplexer_4_out), .sel(mips_probe_1_p2));
  Multiplexer #(.select(1), .width(5), .disabled("Z"), .enable("false")) multiplexer_5 (
    .in0(IR[20:16]), .in1(5'b00100), .out(multiplexer_5_out), .sel(mips_probe_1_p2));
  Multiplexer #(.select(1), .width(5), .disabled("Z"), .enable("false")) multiplexer_6 (
    .in0(IR[20:16]), .in1(IR[15:11]), .out(multiplexer_6_out), .sel(\单周期硬布线控制器_1_regdst ));
  or or_4 (IR2_t, IR2, IRB);
  Clock #(.highDuration(1), .lowDuration(1)) clock_2 (.out(clock_2_out));
  Multiplexer #(.select(1), .width(5), .disabled("Z"), .enable("false")) multiplexer_7 (
    .in0(multiplexer_6_out), .in1({5{1'b1}}), .out(multiplexer_7_out), .sel(\单周期硬布线控制器_1_jal ));
  Multiplexer #(.select(1), .width(5), .disabled("Z"), .enable("false")) multiplexer_8 (
    .in0(IR[10:6]), .in1(R1[4:0]), .out(multiplexer_8_out), .sel(SLLV));
  assign bit_extender_1_out = {{16{1'b0}}, IR[15:0]};  // Bit_Extender bit_extender_1
  assign bit_extender_2_out = {{16{IR[15]}}, IR[15:0]};  // Bit_Extender bit_extender_2
  Comparator #(.width(13), .mode("twosComplement")) comparator_5 (
    .a(CNT_num), .b(13'hba), .eq(comparator_5_eq), .lt(comparator_5_lt));  // open: gt
  Multiplexer #(.select(1), .width(32), .disabled("Z"), .enable("false")) multiplexer_9 (
    .in0(bit_extender_1_out), .in1(bit_extender_2_out), .out(multiplexer_9_out), .sel(SignedExt));
  // Probe on multiplexer_9_out
  or or_5 (IR3_t, IR3, IRC);
  nand nand_1 (nand_1_out, d_ff_1_q, comparator_5_eq);
  Counter #(.width(13), .max('h1fff), .ongoal("stay"), .trigger("rising"), .behavior("old")) counter_1 (
    .count(comparator_5_lt), .Q(CNT_num), .clk(clock_2_out));  // open: load, D, carry, clr, preset
  MIPS_Regifile mips_regifile_1 (
    .Din(RDin), .Clk(CLK), .R1(R1), .R2(MDin), .WE(RegWrite), .WAdr(multiplexer_7_out),
    .R1Adr(multiplexer_4_out), .R2Adr(multiplexer_5_out));
  Shifter #(.width(32), .shift("ll")) shifter_1 (.in(bit_extender_2_out), .\dist (5'b00010), .out(shifter_1_out));
  assign CLK = nand_1_out ? clock_2_out : 1'bz;  // Controlled_Buffer controlled_buffer_1
  Pull_Resistor #(.pull(1)) pull_resistor_4 (.node(CLK));
  Multiplexer #(.select(1), .width(32), .disabled("Z"), .enable("false")) multiplexer_10 (
    .in0(MDin), .in1(multiplexer_9_out), .out(multiplexer_10_out), .sel(\单周期硬布线控制器_1_alu_src ));
  Multiplexer #(.select(1), .width(32), .disabled("Z"), .enable("false")) multiplexer_11 (
    .in0(multiplexer_10_out), .in1({32{1'b0}}), .out(multiplexer_11_out), .sel(BLTZ));
  Adder #(.width(32)) adder_2 (.a(shifter_1_out), .b(PC_4), .out(adder_2_out));  // open: cin, cout
  and and_1 (and_1_out, Addr[31], BLTZ);
  and and_2 (and_2_out, \单周期硬布线控制器_1_beq , mips_alu_1_equal);
  and and_3 (and_3_out, \单周期硬布线控制器_1_bne , ~mips_alu_1_equal);  // AND_Gate
  // Probe on R1
  MIPS_ALU mips_alu_1 (
    .X(R1), .Y(multiplexer_11_out), .AluOP(\单周期硬布线控制器_1_alu_op ), .Equal(mips_alu_1_equal), .Result(Addr),
    .shamt(multiplexer_8_out));  // open: Result_2
  // Probe on multiplexer_10_out
  or or_6 (or_6_out, and_2_out, and_1_out, and_3_out);
  Register #(.width(32), .trigger("rising"), .Select("low")) register_1 (
    .D(MDin), .en(Led), .Q(LedData), .clk(CLK));  // open: clr
  Comparator #(.width(32), .mode("twosComplement")) comparator_6 (
    .a(R1), .b(32'h22), .eq(comparator_6_eq));  // open: gt, lt
  and and_4 (Led, mips_probe_1_p2, comparator_6_eq);
  and and_5 (halt, mips_probe_1_p2, ~comparator_6_eq);  // AND_Gate
  RAM #(.addrWidth(10), .dataWidth(32), .bus("separate"), .Select("high")) ram_1 (
    .addr(Addr[11:2]), .din(MDin), .data({ram_1_data_4, ram_1_data_3, ram_1_data_2, ram_1_data}),
    .str(MemWrite), .clk(CLK), .clr(RST));  // open: sel, ld
  Multiplexer #(.select(2), .width(8), .disabled("Z"), .enable("false")) multiplexer_12 (
    .in0(ram_1_data), .in1(ram_1_data_2), .in2(ram_1_data_3), .in3(ram_1_data_4), .out(multiplexer_12_out),
    .sel(Addr[1:0]));
  // Probe on Addr
  Multiplexer #(.select(1), .width(32), .disabled("Z"), .enable("false")) multiplexer_13 (
    .in0(Addr), .in1(multiplexer_15_out), .out(multiplexer_13_out), .sel(MemToReg));
  assign bit_extender_3_out = {{24{multiplexer_12_out[7]}}, multiplexer_12_out};  // Bit_Extender bit_extender_3
  or or_7 (W1, IR1_q, d_ff_2_q);
  or or_8 (W2, IR2_q, d_ff_3_q);
  or or_9 (W3, IR3_q, d_ff_4_q);
  Multiplexer #(.select(1), .width(32), .disabled("Z"), .enable("false")) multiplexer_14 (
    .in0(multiplexer_13_out), .in1(PC_4), .out(RDin), .sel(\单周期硬布线控制器_1_jal ));
  D_Flip_Flop #(.trigger("rising"), .Pre_Clr_Positions("LEGACY"), .NegatePresetClear("false"), .enable("true"), .NewFFLayout("false")) d_ff_2 (
    .clk(IRA), .D(1'b1), .Q(d_ff_2_q), .reset(IR1_q));  // open: Qn, preset, en
  D_Flip_Flop #(.trigger("rising"), .Pre_Clr_Positions("LEGACY"), .NegatePresetClear("false"), .enable("true"), .NewFFLayout("false")) d_ff_3 (
    .clk(IRB), .D(1'b1), .Q(d_ff_3_q), .reset(IR2_q));  // open: Qn, preset, en
  D_Flip_Flop #(.trigger("rising"), .Pre_Clr_Positions("LEGACY"), .NegatePresetClear("false"), .enable("true"), .NewFFLayout("false")) d_ff_4 (
    .clk(IRC), .D(1'b1), .Q(d_ff_4_q), .reset(IR3_q));  // open: Qn, preset, en
  not not_2 (not_2_out, halt);
  Multiplexer #(.select(1), .width(32), .disabled("Z"), .enable("false")) multiplexer_15 (
    .in0({ram_1_data_4, ram_1_data_3, ram_1_data_2, ram_1_data}), .in1(bit_extender_3_out),
    .out(multiplexer_15_out), .sel(LB));
  or or_10 (or_10_out, d_ff_2_q, IR1_q);
  or or_11 (or_11_out, d_ff_3_q, IR2_q);
  or or_12 (or_12_out, d_ff_4_q, IR3_q);
  Counter #(.width(16), .max('hffff), .ongoal("wrap"), .trigger("rising"), .behavior("old")) counter_2 (
    .count(not_2_out), .Q(\总周期数 ), .clk(CLK), .clr(RST));  // open: load, D, carry, preset
  and and_6 (and_6_out, ERET, IR_now[0], ~IR_now[1]);  // AND_Gate
  and and_7 (and_7_out, ERET, ~IR_now[0], IR_now[1]);  // AND_Gate
  and and_8 (and_8_out, ERET, IR_now[0], IR_now[1]);
  and and_9 (and_9_out, or_10_out, ~and_6_out);  // AND_Gate
  and and_10 (and_10_out, or_11_out, ~and_7_out);  // AND_Gate
  and and_11 (and_11_out, or_12_out, ~and_8_out);  // AND_Gate
  D_Flip_Flop #(.trigger("rising"), .Pre_Clr_Positions("LEGACY"), .NegatePresetClear("false"), .enable("true"), .NewFFLayout("false")) u_IR1 (
    .clk(CLK), .D(and_9_out), .Q(IR1_q));  // open: Qn, preset, en, reset
  D_Flip_Flop #(.trigger("rising"), .Pre_Clr_Positions("LEGACY"), .NegatePresetClear("false"), .enable("true"), .NewFFLayout("false")) u_IR2 (
    .clk(CLK), .D(and_10_out), .Q(IR2_q));  // open: Qn, preset, en, reset
  D_Flip_Flop #(.trigger("rising"), .Pre_Clr_Positions("LEGACY"), .NegatePresetClear("false"), .enable("true"), .NewFFLayout("false")) u_IR3 (
    .clk(CLK), .D(and_11_out), .Q(IR3_q));  // open: Qn, preset, en, reset
  Priority_Encoder #(.select(2), .disabled("Z")) priority_encoder_1 (
    .in0(1'b1), .in1(IR1_q), .in2(IR2_q), .in3(IR3_q), .out(priority_encoder_1_out),
    .gs(priority_encoder_1_gs));  // open: en_out, en_in
  // Probe on priority_encoder_1_out
  Multiplexer #(.select(2), .width(1), .disabled("Z"), .enable("false")) multiplexer_16 (
    .in0(1'b0), .in1(priority_encoder_1_gs), .in2(priority_encoder_1_gs), .in3(priority_encoder_1_gs),
    .out(multiplexer_16_out), .sel(priority_encoder_1_out));
  Register #(.width(2), .trigger("rising"), .Select("low")) macause (
    .D(priority_encoder_1_out), .en(and_12_out), .Q(IR_now), .clk(CLK), .clr(comparator_7_eq));
  and and_12 (and_12_out, and_13_out, ~ERET);  // AND_Gate
  and and_13 (and_13_out, multiplexer_16_out, ~\中断状态_q );  // AND_Gate
  or or_13 (or_13_out, and_13_out, \中断状态_q );
  Multiplexer #(.select(1), .width(32), .disabled("Z"), .enable("false")) multiplexer_17 (
    .in0(nextPC), .in1(multiplexer_18_out), .out(multiplexer_17_out), .sel(and_13_out));
  Multiplexer #(.select(2), .width(32), .disabled("Z"), .enable("false")) multiplexer_18 (
    .in0(nextPC), .in1(32'h30ac), .in2(32'h3150), .in3(32'h31f4), .out(multiplexer_18_out),
    .sel(priority_encoder_1_out));
  Register #(.width(1), .trigger("rising"), .Select("low")) \u_中断状态  (
    .D(or_13_out), .Q(\中断状态_q ), .clk(CLK), .clr(ERET));  // open: en
  Register #(.width(32), .trigger("rising"), .Select("low")) PC_2 (
    .D(nextPC), .en(and_13_out), .Q(PC_2_q), .clk(CLK));  // open: clr
  Comparator #(.width(2), .mode("twosComplement")) comparator_7 (
    .a(priority_encoder_1_out), .b(2'b00), .eq(comparator_7_eq));  // open: gt, lt
  // Probe on PCout
  Multiplexer #(.select(1), .width(32), .disabled("Z"), .enable("false")) multiplexer_19 (
    .in0(multiplexer_17_out), .in1(PC_2_q), .out(PCout), .sel(ERET));

  // Notes on the sheet:
  //   中断源
  //   中断等待指示
  //   总复位信号应将除ROM以外所有存储组件全部清零
  //   单级中断测试信号模拟器
  //   总复位信号应将除ROM以外所有存储组件全部清零
  //   数码管输出
  //   数码管输出应该用寄存器锁存，否则显示数据只能一闪而过
  //   指令存储器
  //   contents of rom_1 (hex, n*v repeats v):
  //   201d07d0 20100001 109fc0 139fc3 8021 2012000c 24160008 26100001 3210000f 20080008 20090001 139900
  //   2709825 132020 20020022 c 1094022 1500fff9 22100001 2018000f 2188024 108700 20080008 20090001 139902
  //   2709825 132021 20020022 c 1094022 1500fff9 108702 2c9b022 12c00001 8000c07 4020 1084027 84400
  //   3508ffff 82021 20020022 c 8000c01 afa20000 23bd0004 afa40000 23bd0004 afb00000 23bd0004 afb30000
  //   23bd0004 afb40000 23bd0004 afb50000 23bd0004 afb60000 23bd0004 20160001 20140003 20150001 168020
  //   108100 2149825 132020 20020022 c 1600fffa 295a022 1680fff7 23bdfffc 8fb60000 23bdfffc 8fb50000
  //   23bdfffc 8fb40000 23bdfffc 8fb30000 23bdfffc 8fb00000 23bdfffc 8fa40000 23bdfffc 8fa20000 42000018
  //   afa20000 23bd0004 afa40000 23bd0004 afb00000 23bd0004 afb30000 23bd0004 afb40000 23bd0004 afb50000
  //   23bd0004 afb60000 23bd0004 20160002 20140003 20150001 168020 108100 2149825 132020 20020022 c
  //   1600fffa 295a022 1680fff7 23bdfffc 8fb60000 23bdfffc 8fb50000 23bdfffc 8fb40000 23bdfffc 8fb30000
  //   23bdfffc 8fb00000 23bdfffc 8fa40000 23bdfffc 8fa20000 42000018 afa20000 23bd0004 afa40000 23bd0004
  //   afb00000 23bd0004 afb30000 23bd0004 afb40000 23bd0004 afb50000 23bd0004 afb60000 23bd0004 20160003
  //   20140003 20150001 168020 108100 2149825 132020 20020022 c 1600fffa 295a022 1680fff7 23bdfffc
  //   8fb60000 23bdfffc 8fb50000 23bdfffc 8fb40000 23bdfffc 8fb30000 23bdfffc 8fb00000 23bdfffc 8fa40000
  //   23bdfffc 8fa20000 42000018
  //   数码管输出应该用寄存器锁存，否则显示数据只能一闪而过
  //   OP
  //   rs
  //   指令字
  //   rt
  //   rd
  //   shamt
  //   imm16
  //   imm26
  //   控制位
  //   暂停节拍，不能为0
  //   JMP
  //   JR
  //   Func
  //   Syscall
  //   Beq
  //   Bne
  //   MemToReg
  //   MemWrite
  //   AluOP
  //   AluSrcB
  //   RegWrite
  //   JAL
  //   RegDst
  //   可计数暂停的时钟源
  //   为方便自动评测，需要输出PC，IR，寄存器堆写如数据RDin
  //   RAM写使能MemWrite、RAM写入数据MDin等信号
  //   戳工具置1进入计数暂停模式，ctrl+k时钟自动运行到对应节拍暂停
  //   ctrl+k关闭时钟连续运行，将控制位置零，进入单步调试模式调试
  //   用这个时钟源需要去掉电路中的其他时钟源
  //   Reset 
  //   Reset 
  //   Reset 
endmodule

module \单周期MIPS_多级中断  (
  input  IR1,
  input  IR2,
  input  IR3,
  output RegWrite,
  output MemWrite,
  output [31:0] PC,
  output [31:0] IR,
  output [31:0] RDin,
  output [31:0] MDin,
  output [31:0] LedData
);

  wire and_1_out, and_2_out, and_3_out, and_6_out, and_8_out, and_9_out, and_10_out, and_11_out, and_12_out,
       and_13_out, and_15_out, BLTZ, CLK, clock_2_out, comparator_1_eq, comparator_2_eq, comparator_2_lt,
       comparator_3_eq, comparator_4_eq, comparator_5_gt, d_ff_1_q, d_ff_2_q, d_ff_3_q, d_ff_4_q, d_ff_5_q,
       d_ff_5_qn, ERET, Go, halt, INT, IR1_q, IR1_t, IR2_q, IR2_t, IR3_q, IR3_t, IRA, IRB, IRC, LB, Led,
       MemToReg, MFC0, mips_alu_1_equal, mips_probe_1_p2, MTC0, multiplexer_17_out, nand_1_out, not_1_out,
       not_2_out, or_1_out, or_5_out, or_9_out, or_10_out, or_11_out, or_12_out, or_13_out,
       priority_encoder_1_gs, RST, SignedExt, SLLV, W1, W2, W3, \单周期硬布线控制器_1_alu_src , \单周期硬布线控制器_1_beq ,
       \单周期硬布线控制器_1_bne , \单周期硬布线控制器_1_jal , \单周期硬布线控制器_1_jmp , \单周期硬布线控制器_1_jr , \单周期硬布线控制器_1_regdst ;
  wire [1:0] IR_now, priority_encoder_1_out;
  wire [1:1] and_7_out;
  wire [3:0] \单周期硬布线控制器_1_alu_op ;
  wire [4:0] multiplexer_4_out, multiplexer_5_out, multiplexer_6_out, multiplexer_7_out, multiplexer_8_out;
  wire [7:0] multiplexer_13_out;
  wire [12:0] CNT_num;
  wire [15:0] \总周期数 ;
  wire [31:0] adder_2_out, Addr, bit_extender_1_out, bit_extender_2_out, bit_extender_3_out,
       bit_extender_4_out, DATA, demultiplexer_1_out0, demultiplexer_1_out1, EPC_q, multiplexer_1_out,
       multiplexer_2_out, multiplexer_9_out, multiplexer_10_out, multiplexer_11_out, multiplexer_14_out,
       multiplexer_15_out, multiplexer_16_out, multiplexer_18_out, multiplexer_19_out, multiplexer_20_out,
       nextPC, PC_4, PCout, R1, ram_1_data, shifter_1_out;

  Clock #(.highDuration(1), .lowDuration(1)) clock_1 ();  // open: out
  Button _1 (.out(IRA));
  Button _2 (.out(IRB));
  Button _3 (.out(IRC));
  Button \u_继续运行  (.out(Go));
  LED #(.active("true")) led_1 (.in(W1));
  LED #(.active("true")) led_2 (.in(W2));
  LED #(.active("true")) led_3 (.in(W3));
  Multiplexer #(.select(1), .width(32), .disabled("Z"), .enable("false")) multiplexer_1 (
    .in0(PC_4), .in1(adder_2_out), .out(multiplexer_1_out), .sel(or_5_out));
  Hex_Digit_Display hex_digit_display_1 (.value(LedData[31:28]));  // open: dp
  Multiplexer #(.select(1), .width(32), .disabled("Z"), .enable("false")) multiplexer_2 (
    .in0(multiplexer_1_out), .in1({PC[31:28], IR[25:0], 2'b00}), .out(multiplexer_2_out),
    .sel(\单周期硬布线控制器_1_jmp ));
  Multiplexer #(.select(1), .width(32), .disabled("Z"), .enable("false")) multiplexer_3 (
    .in0(multiplexer_2_out), .in1(R1), .out(nextPC), .sel(\单周期硬布线控制器_1_jr ));
  not not_1 (not_1_out, halt);
  Hex_Digit_Display hex_digit_display_2 (.value(LedData[23:20]));  // open: dp
  Hex_Digit_Display hex_digit_display_3 (.value(LedData[27:24]));  // open: dp
  Register #(.width(32), .trigger("rising"), .Select("low")) u_PC (
    .D(PCout), .en(or_1_out), .Q(PC), .clk(CLK), .clr(RST));
  or or_1 (or_1_out, not_1_out, Go);
  Hex_Digit_Display hex_digit_display_4 (.value(LedData[15:12]));  // open: dp
  Hex_Digit_Display hex_digit_display_5 (.value(LedData[19:16]));  // open: dp
  // Probe on PC
  Adder #(.width(32)) adder_1 (.a(PC), .b(32'h4), .out(PC_4));  // open: cin, cout
  Hex_Digit_Display hex_digit_display_6 (.value(LedData[7:4]));  // open: dp
  Hex_Digit_Display hex_digit_display_7 (.value(LedData[11:8]));  // open: dp
  // Probe on \总周期数 
  // Mips_Probe mips_probe_1: pin names not known; wires that end beside it: IR, mips_probe_1_p2
  Hex_Digit_Display hex_digit_display_8 (.value(LedData[3:0]));  // open: dp
  ROM #(.addrWidth(10), .dataWidth(32), .Select("high")) rom_1 (.addr(PC[11:2]), .data(IR));
  or or_2 (IR1_t, IR1, IRA);
  \单周期硬布线控制器  \u_单周期硬布线控制器_1  (
    .Func(IR[5:0]), .OP(IR[31:26]), .ALU_OP(\单周期硬布线控制器_1_alu_op ), .MemToReg(MemToReg), .MemWrite(MemWrite),
    .ALU_SRC(\单周期硬布线控制器_1_alu_src ), .SysCALL(mips_probe_1_p2), .SignedExt(SignedExt),
    .RegDst(\单周期硬布线控制器_1_regdst ), .JR(\单周期硬布线控制器_1_jr ), .JMP(\单周期硬布线控制器_1_jmp ), .Beq(\单周期硬布线控制器_1_beq ),
    .JAL(\单周期硬布线控制器_1_jal ), .Bne(\单周期硬布线控制器_1_bne ), .SLLV(SLLV), .LB(LB), .BLTZ(BLTZ), .ERET(ERET),
    .Func_2(IR[25:21]), .MFC0(MFC0), .MTC0(MTC0), .RegWrite(RegWrite));  // open: out_20, out_21
  Multiplexer #(.select(1), .width(5), .disabled("Z"), .enable("false")) multiplexer_4 (
    .in0(IR[25:21]), .in1(5'b00010), .out(multiplexer_4_out), .sel(mips_probe_1_p2));
  Multiplexer #(.select(1), .width(5), .disabled("Z"), .enable("false")) multiplexer_5 (
    .in0(IR[20:16]), .in1(5'b00100), .out(multiplexer_5_out), .sel(mips_probe_1_p2));
  Multiplexer #(.select(1), .width(5), .disabled("Z"), .enable("false")) multiplexer_6 (
    .in0(IR[20:16]), .in1(IR[15:11]), .out(multiplexer_6_out), .sel(\单周期硬布线控制器_1_regdst ));
  Multiplexer #(.select(1), .width(5), .disabled("Z"), .enable("false")) multiplexer_7 (
    .in0(multiplexer_6_out), .in1({5{1'b1}}), .out(multiplexer_7_out), .sel(\单周期硬布线控制器_1_jal ));
  Multiplexer #(.select(1), .width(5), .disabled("Z"), .enable("false")) multiplexer_8 (
    .in0(IR[10:6]), .in1(R1[4:0]), .out(multiplexer_8_out), .sel(SLLV));
  assign bit_extender_1_out = {{16{1'b0}}, IR[15:0]};  // Bit_Extender bit_extender_1
  assign bit_extender_2_out = {{16{IR[15]}}, IR[15:0]};  // Bit_Extender bit_extender_2
  or or_3 (IR2_t, IR2, IRB);
  Multiplexer #(.select(1), .width(32), .disabled("Z"), .enable("false")) multiplexer_9 (
    .in0(bit_extender_1_out), .in1(bit_extender_2_out), .out(multiplexer_9_out), .sel(SignedExt));
  MIPS_Regifile mips_regifile_1 (
    .Din(RDin), .Clk(CLK), .R1(R1), .R2(MDin), .WE(RegWrite), .WAdr(multiplexer_7_out),
    .R1Adr(multiplexer_4_out), .R2Adr(multiplexer_5_out));
  Shifter #(.width(32), .shift("ll")) shifter_1 (.in(bit_extender_2_out), .\dist (5'b00010), .out(shifter_1_out));
  or or_4 (IR3_t, IR3, IRC);
  Multiplexer #(.select(1), .width(32), .disabled("Z"), .enable("false")) multiplexer_10 (
    .in0(MDin), .in1(multiplexer_9_out), .out(multiplexer_10_out), .sel(\单周期硬布线控制器_1_alu_src ));
  Multiplexer #(.select(1), .width(32), .disabled("Z"), .enable("false")) multiplexer_11 (
    .in0(multiplexer_10_out), .in1({32{1'b0}}), .out(multiplexer_11_out), .sel(BLTZ));
  Adder #(.width(32)) adder_2 (.a(shifter_1_out), .b(PC_4), .out(adder_2_out));  // open: cin, cout
  MIPS_ALU mips_alu_1 (
    .X(R1), .Y(multiplexer_11_out), .AluOP(\单周期硬布线控制器_1_alu_op ), .Equal(mips_alu_1_equal), .Result(Addr),
    .shamt(multiplexer_8_out));  // open: Result_2
  and and_1 (and_1_out, Addr[31], BLTZ);
  and and_2 (and_2_out, \单周期硬布线控制器_1_beq , mips_alu_1_equal);
  and and_3 (and_3_out, \单周期硬布线控制器_1_bne , ~mips_alu_1_equal);  // AND_Gate
  Register #(.width(32), .trigger("rising"), .Select("low")) register_1 (
    .D(MDin), .en(Led), .Q(LedData), .clk(CLK));  // open: clr
  or or_5 (or_5_out, and_2_out, and_1_out, and_3_out);
  Comparator #(.width(32), .mode("twosComplement")) comparator_1 (
    .a(R1), .b(32'h22), .eq(comparator_1_eq));  // open: gt, lt
  and and_4 (Led, mips_probe_1_p2, comparator_1_eq);
  and and_5 (halt, mips_probe_1_p2, ~comparator_1_eq);  // AND_Gate
  RAM #(.addrWidth(10), .dataWidth(32), .bus("separate"), .Select("high")) ram_1 (
    .addr(Addr[11:2]), .din(MDin), .data(ram_1_data), .str(MemWrite), .clk(CLK), .clr(RST));  // open: sel, ld
  Multiplexer #(.select(1), .width(32), .disabled("Z"), .enable("false")) multiplexer_12 (
    .in0(multiplexer_15_out), .in1(DATA), .out(RDin), .sel(MFC0));
  Multiplexer #(.select(2), .width(8), .disabled("Z"), .enable("false")) multiplexer_13 (
    .in0(ram_1_data[7:0]), .in1(ram_1_data[15:8]), .in2(ram_1_data[23:16]), .in3(ram_1_data[31:24]),
    .out(multiplexer_13_out), .sel(Addr[1:0]));
  assign bit_extender_3_out = {{24{multiplexer_13_out[7]}}, multiplexer_13_out};  // Bit_Extender bit_extender_3
  Multiplexer #(.select(1), .width(32), .disabled("Z"), .enable("false")) multiplexer_14 (
    .in0(Addr), .in1(multiplexer_16_out), .out(multiplexer_14_out), .sel(MemToReg));
  Multiplexer #(.select(1), .width(32), .disabled("Z"), .enable("false")) multiplexer_15 (
    .in0(multiplexer_14_out), .in1(PC_4), .out(multiplexer_15_out), .sel(\单周期硬布线控制器_1_jal ));
  D_Flip_Flop #(.trigger("high"), .Pre_Clr_Positions("LEGACY"), .NegatePresetClear("false"), .enable("true"), .NewFFLayout("false")) d_ff_1 (.Q(d_ff_1_q));  // open: clk, D, Qn, preset, en, reset
  not not_2 (not_2_out, halt);
  Multiplexer #(.select(1), .width(32), .disabled("Z"), .enable("false")) multiplexer_16 (
    .in0(ram_1_data), .in1(bit_extender_3_out), .out(multiplexer_16_out), .sel(LB));
  Button button_1 (.out(RST));
  // Probe on 13'hc
  Clock #(.highDuration(1), .lowDuration(1)) clock_2 (.out(clock_2_out));
  Counter #(.width(16), .max('hffff), .ongoal("wrap"), .trigger("rising"), .behavior("old")) counter_1 (
    .count(not_2_out), .Q(\总周期数 ), .clk(CLK), .clr(RST));  // open: load, D, carry, preset
  or or_6 (W1, IR1_q, d_ff_2_q);
  or or_7 (W2, IR2_q, d_ff_3_q);
  or or_8 (W3, IR3_q, d_ff_4_q);
  Comparator #(.width(13), .mode("twosComplement")) comparator_2 (
    .a(CNT_num), .b(13'hc), .eq(comparator_2_eq), .lt(comparator_2_lt));  // open: gt
  D_Flip_Flop #(.trigger("rising"), .Pre_Clr_Positions("LEGACY"), .NegatePresetClear("false"), .enable("true"), .NewFFLayout("false")) d_ff_2 (
    .clk(IRA), .D(1'b1), .Q(d_ff_2_q), .reset(IR1_q));  // open: Qn, preset, en
  D_Flip_Flop #(.trigger("rising"), .Pre_Clr_Positions("LEGACY"), .NegatePresetClear("false"), .enable("true"), .NewFFLayout("false")) d_ff_3 (
    .clk(IRB), .D(1'b1), .Q(d_ff_3_q), .reset(IR2_q));  // open: Qn, preset, en
  D_Flip_Flop #(.trigger("rising"), .Pre_Clr_Positions("LEGACY"), .NegatePresetClear("false"), .enable("true"), .NewFFLayout("false")) d_ff_4 (
    .clk(IRC), .D(1'b1), .Q(d_ff_4_q), .reset(IR3_q));  // open: Qn, preset, en
  Comparator #(.width(5), .mode("twosComplement")) comparator_3 (
    .a(IR[15:11]), .b(5'b01110), .eq(comparator_3_eq));  // open: gt, lt
  Comparator #(.width(5), .mode("twosComplement")) comparator_4 (
    .a(IR[15:11]), .b(5'b01100), .eq(comparator_4_eq));  // open: gt, lt
  nand nand_1 (nand_1_out, d_ff_1_q, comparator_2_eq);
  Counter #(.width(13), .max('h1fff), .ongoal("stay"), .trigger("rising"), .behavior("old")) counter_2 (
    .count(comparator_2_lt), .Q(CNT_num), .clk(clock_2_out));  // open: load, D, carry, clr, preset
  or or_9 (or_9_out, d_ff_2_q, IR1_q);
  or or_10 (or_10_out, d_ff_3_q, IR2_q);
  or or_11 (or_11_out, d_ff_4_q, IR3_q);
  and and_6 (and_6_out, comparator_3_eq, MTC0);
  and and_7 (and_7_out[1], comparator_4_eq, MTC0);
  assign CLK = nand_1_out ? clock_2_out : 1'bz;  // Controlled_Buffer controlled_buffer_1
  Pull_Resistor #(.pull(1)) pull_resistor_1 (.node(CLK));
  and and_8 (and_8_out, ERET, IR_now[0], ~IR_now[1]);  // AND_Gate
  and and_9 (and_9_out, ERET, ~IR_now[0], IR_now[1]);  // AND_Gate
  and and_10 (and_10_out, ERET, IR_now[0], IR_now[1]);
  and and_11 (and_11_out, or_9_out, ~and_8_out);  // AND_Gate
  and and_12 (and_12_out, or_10_out, ~and_9_out);  // AND_Gate
  and and_13 (and_13_out, or_11_out, ~and_10_out);  // AND_Gate
  D_Flip_Flop #(.trigger("rising"), .Pre_Clr_Positions("LEGACY"), .NegatePresetClear("false"), .enable("true"), .NewFFLayout("false")) u_IR1 (
    .clk(CLK), .D(and_11_out), .Q(IR1_q));  // open: Qn, preset, en, reset
  D_Flip_Flop #(.trigger("rising"), .Pre_Clr_Positions("LEGACY"), .NegatePresetClear("false"), .enable("true"), .NewFFLayout("false")) u_IR2 (
    .clk(CLK), .D(and_12_out), .Q(IR2_q));  // open: Qn, preset, en, reset
  D_Flip_Flop #(.trigger("rising"), .Pre_Clr_Positions("LEGACY"), .NegatePresetClear("false"), .enable("true"), .NewFFLayout("false")) u_IR3 (
    .clk(CLK), .D(and_13_out), .Q(IR3_q));  // open: Qn, preset, en, reset
  Priority_Encoder #(.select(2), .disabled("Z")) priority_encoder_1 (
    .in0(1'b1), .in1(IR1_q), .in2(IR2_q), .in3(IR3_q), .out(priority_encoder_1_out),
    .gs(priority_encoder_1_gs));  // open: en_out, en_in
  Multiplexer #(.select(2), .width(1), .disabled("Z"), .enable("false")) multiplexer_17 (
    .in0(1'b1), .in1(1'b0), .in2(demultiplexer_1_out1[0]), .out(multiplexer_17_out),
    .sel({and_7_out[1], ERET}));  // open: in3
  Demultiplexer #(.select(1), .width(32), .tristate("false"), .disabled("Z"), .enable("false")) demultiplexer_1 (
    .out0(demultiplexer_1_out0), .out1(demultiplexer_1_out1), .in(MDin), .sel(and_7_out[1]));
  // Probe on priority_encoder_1_out
  or or_12 (or_12_out, and_7_out[1], ERET, INT);
  \硬件堆栈  \u_硬件堆栈_1  (.\中断向量号 (priority_encoder_1_out), .\INT_新的中断 (INT), .ERET(ERET), .CLK(CLK), .out_5(IR_now));
  Multiplexer #(.select(2), .width(32), .disabled("Z"), .enable("false")) multiplexer_18 (
    .in0(nextPC), .in1(32'h30ac), .in2(32'h3174), .in3(32'h323c), .out(multiplexer_18_out),
    .sel(priority_encoder_1_out));
  Comparator #(.width(2), .mode("unsigned")) comparator_5 (
    .a(priority_encoder_1_out), .b(IR_now), .gt(comparator_5_gt));  // open: eq, lt
  // Probe on IR_now
  D_Flip_Flop #(.trigger("rising"), .Pre_Clr_Positions("LEGACY"), .NegatePresetClear("false"), .enable("true"), .NewFFLayout("false")) d_ff_5 (
    .clk(CLK), .D(multiplexer_17_out), .Q(d_ff_5_q), .Qn(d_ff_5_qn), .en(or_12_out));  // open: preset, reset
  Multiplexer #(.select(1), .width(32), .disabled("Z"), .enable("false")) multiplexer_19 (
    .in0(nextPC), .in1(demultiplexer_1_out0), .out(multiplexer_19_out), .sel(and_6_out));
  // Probe on multiplexer_20_out
  Multiplexer #(.select(1), .width(32), .disabled("Z"), .enable("false")) multiplexer_20 (
    .in0(nextPC), .in1(multiplexer_18_out), .out(multiplexer_20_out), .sel(INT));
  and and_14 (INT, comparator_5_gt, and_15_out);
  and and_15 (and_15_out, priority_encoder_1_gs, d_ff_5_qn);
  Register #(.width(32), .trigger("rising"), .Select("low")) EPC (
    .D(multiplexer_19_out), .en(or_13_out), .Q(EPC_q), .clk(CLK));  // open: clr
  or or_13 (or_13_out, and_6_out, INT);
  Multiplexer #(.select(1), .width(32), .disabled("Z"), .enable("false")) multiplexer_21 (
    .in0(multiplexer_20_out), .in1(EPC_q), .out(PCout), .sel(ERET));
  // Probe on EPC_q
  assign bit_extender_4_out = {{31{1'b0}}, d_ff_5_q};  // Bit_Extender bit_extender_4
  // Probe on PCout
  Multiplexer #(.select(1), .width(32), .disabled("Z"), .enable("false")) multiplexer_22 (
    .in0(bit_extender_4_out), .in1(EPC_q), .out(DATA), .sel(comparator_3_eq));

  // Other names for the same wires on the sheet: rd[4:0] = IR[15:11]; R2[31:0] = MDin

  // Notes on the sheet:
  //   中断源
  //   中断等待指示
  //   总复位信号应将除ROM以外所有存储组件全部清零
  //   数码管输出
  //   数码管输出应该用寄存器锁存，否则显示数据只能一闪而过
  //   指令存储器
  //   OP
  //   rs
  //   指令字
  //   contents of rom_1 (hex, n*v repeats v):
  //   201d07d0 20100001 109fc0 139fc3 8021 2012000c 24160008 26100001 3210000f 20080008 20090001 139900
  //   2709825 132020 20020022 c 1094022 1500fff9 22100001 2018000f 2188024 108700 20080008 20090001 139902
  //   2709825 132021 20020022 c 1094022 1500fff9 108702 2c9b022 12c00001 8000c07 4020 1084027 84400
  //   3508ffff 82021 20020022 c 8000c01 afa20000 23bd0004 afa40000 23bd0004 afb00000 23bd0004 afb30000
  //   23bd0004 afb40000 23bd0004 afb50000 23bd0004 afb60000 23bd0004 40167000 afb60000 23bd0004 40806000
  //   20160001 20140003 20150001 168020 108100 2149825 132020 20020022 c 1600fffa 295a022 1680fff7
  //   20160001 40966000 23bdfffc 8fb60000 40967000 23bdfffc 8fb60000 23bdfffc 8fb50000 23bdfffc 8fb40000
  //   23bdfffc 8fb30000 23bdfffc 8fb00000 23bdfffc 8fa40000 23bdfffc 8fa20000 42000018 afa20000 23bd0004
  //   afa40000 23bd0004 afb00000 23bd0004 afb30000 23bd0004 afb40000 23bd0004 afb50000 23bd0004 afb60000
  //   23bd0004 40167000 afb60000 23bd0004 40806000 20160002 20140003 20150001 168020 108100 2149825 132020
  //   20020022 c 1600fffa 295a022 1680fff7 20160001 40966000 23bdfffc 8fb60000 40967000 23bdfffc 8fb60000
  //   23bdfffc 8fb50000 23bdfffc 8fb40000 23bdfffc 8fb30000 23bdfffc 8fb00000 23bdfffc 8fa40000 23bdfffc
  //   8fa20000 42000018 afa20000 23bd0004 afa40000 23bd0004 afb00000 23bd0004 afb30000 23bd0004 afb40000
  //   23bd0004 afb50000 23bd0004 afb60000 23bd0004 40167000 afb60000 23bd0004 40806000 20160003 20140003
  //   20150001 168020 108100 2149825 132020 20020022 c 1600fffa 295a022 1680fff7 20160001 40966000
  //   23bdfffc 8fb60000 40967000 23bdfffc 8fb60000 23bdfffc 8fb50000 23bdfffc 8fb40000 23bdfffc 8fb30000
  //   23bdfffc 8fb00000 23bdfffc 8fa40000 23bdfffc 8fa20000 42000018
  //   rt
  //   rd
  //   JMP
  //   JR
  //   Func
  //   shamt
  //   imm16
  //   imm26
  //   Beq
  //   Bne
  //   MemToReg
  //   MemWrite
  //   AluOP
  //   AluSrcB
  //   RegWrite
  //   JAL
  //   RegDst
  //   Syscall
  //   为方便自动评测，需要输出PC，IR，寄存器堆写如数据RDin
  //   RAM写使能MemWrite、RAM写入数据MDin等信号
  //   控制位
  //   暂停节拍，不能为0
  //   用这个时钟源需要去掉电路中的其他时钟源
  //   戳工具置1进入计数暂停模式，ctrl+k时钟自动运行到对应节拍暂停
  //   ctrl+k关闭时钟连续运行，将控制位置零，进入单步调试模式调试
  //   可计数暂停的时钟源
  //   Reset 
  //   Reset 
  //   Reset 
endmodule

module \封装正确性测试  (
);

  wire IR1, IR2, IR3, MemW, RegW;
  wire [31:0] EX_PC, ID_PC, IF_PC, IR, LED, MDin, MDinr, MEM_PC, PC, RDin, RDinr, WB_PC;

  \单周期MIPS  \u_单周期mips_1  (.in_1(RegW), .in_2(MemW));
  \气泡流水线  \u_气泡流水线_1  (
    .RegWrite(RegW), .MemWrite(MemW), .IF_PC(IF_PC), .ID_PC(ID_PC), .EX_PC(EX_PC), .M_PC(MEM_PC),
    .WB_PC(WB_PC), .RDin(RDinr), .MDin(MDinr), .LedData(LED));
  \单周期MIPS_单级中断  \u_单周期mips_单级中断_1  (
    .IR1(IR1), .IR2(IR2), .IR3(IR3), .RegWrite(RegW), .MemWrite(MemW), .PC(PC), .IR(IR), .RDin(RDin),
    .MDin(MDin), .LedData(LED));
  \理想流水线  \u_理想流水线_1  (
    .RegWrite(RegW), .MemWrite(MemW), .IF_PC(IF_PC), .ID_PC(ID_PC), .EX_PC(EX_PC), .M_PC(MEM_PC),
    .WB_PC(WB_PC), .RDin(RDinr), .MDin(MDinr), .LedData(LED));
  \重定向流水线  \u_重定向流水线_1  (
    .RegWrite(RegW), .MemWrite(MemW), .IF_PC(IF_PC), .ID_PC(ID_PC), .EX_PC(EX_PC), .M_PC(MEM_PC),
    .WB_PC(WB_PC), .RDin(RDinr), .MDin(MDinr), .LedData(LED));
  \单周期MIPS_多级中断  \u_单周期mips_多级中断_1  (
    .IR1(IR1), .IR2(IR2), .IR3(IR3), .RegWrite(RegW), .MemWrite(MemW), .PC(PC), .IR(IR), .RDin(RDin),
    .MDin(MDin), .LedData(LED));

  // Notes on the sheet:
  //   单周期封装测试
  //   气泡流水封装测试
  //   单周期+单级中断封装测试
  //   请检查上面封装有无位宽不匹配，引脚标签是否和连接的标签相对应，否则无法在educoder平台上正确测试
  //   理想流水封装测试
  //   重定向流水封装测试
  //   单周期+多级中断封装测试
endmodule

module IF_ID (
  input  CTK,
  input  RST,
  input  Enable,
  input  [31:0] in_4,
  input  [31:0] in_5,
  input  [31:0] in_6,
  input  in_7,
  input  \同步置0 ,
  output [31:0] out_9,
  output [31:0] out_10,
  output [31:0] out_11,
  output out_12
);

  wire multiplexer_4_out;
  wire [31:0] multiplexer_1_out, multiplexer_2_out, multiplexer_3_out;

  // Probe on in_5
  Multiplexer #(.select(1), .width(32), .disabled("Z"), .enable("false")) multiplexer_1 (
    .in0(in_4), .in1({32{1'b0}}), .out(multiplexer_1_out), .sel(\同步置0 ));
  Multiplexer #(.select(1), .width(32), .disabled("Z"), .enable("false")) multiplexer_2 (
    .in0(in_5), .in1({32{1'b0}}), .out(multiplexer_2_out), .sel(\同步置0 ));
  Multiplexer #(.select(1), .width(32), .disabled("Z"), .enable("false")) multiplexer_3 (
    .in0(in_6), .in1({32{1'b0}}), .out(multiplexer_3_out), .sel(\同步置0 ));
  Multiplexer #(.select(1), .width(1), .disabled("Z"), .enable("false")) multiplexer_4 (
    .in0(in_7), .in1(1'b0), .out(multiplexer_4_out), .sel(\同步置0 ));
  Register #(.width(32), .trigger("rising"), .Select("low")) register_1 (
    .D(multiplexer_1_out), .en(Enable), .Q(out_9), .clk(CTK), .clr(RST));
  Register #(.width(32), .trigger("rising"), .Select("low")) register_2 (
    .D(multiplexer_2_out), .en(Enable), .Q(out_10), .clk(CTK), .clr(RST));
  Register #(.width(32), .trigger("rising"), .Select("low")) register_3 (
    .D(multiplexer_3_out), .en(Enable), .Q(out_11), .clk(CTK), .clr(RST));
  Register #(.width(1), .trigger("rising"), .Select("low")) register_4 (
    .D(multiplexer_4_out), .en(Enable), .Q(out_12), .clk(CTK), .clr(RST));
endmodule

module ID_EX (
  input  CTK,
  input  RST,
  input  Enable,
  input  [31:0] \指令 ,
  input  [31:0] PC,
  input  [31:0] \寄存器1 ,
  input  [31:0] \寄存器2 ,
  input  MenToReg,
  input  MenWrite,
  input  [3:0] ALU_OP,
  input  ALU_src,
  input  RegWrite,
  input  sllv,
  input  halt,
  input  lb,
  input  [31:0] imm,
  input  \同步置0 ,
  input  RegDst,
  input  JR,
  input  JMP,
  input  JAL,
  input  BNE,
  input  BEQ,
  input  BLTZ,
  input  Signext,
  input  [31:0] in_26,
  input  [1:0] in_27,
  input  [1:0] in_28,
  input  in_29,
  output [31:0] out_30,
  output [31:0] out_31,
  output [31:0] out_32,
  output [31:0] out_33,
  output out_34,
  output out_35,
  output [3:0] out_36,
  output out_37,
  output out_38,
  output out_39,
  output out_40,
  output out_41,
  output [31:0] out_42,
  output out_43,
  output out_44,
  output out_45,
  output out_46,
  output out_47,
  output out_48,
  output out_49,
  output out_50,
  output [31:0] out_51,
  output [1:0] out_52,
  output [1:0] out_53,
  output out_54
);

  wire multiplexer_5_out, multiplexer_6_out, multiplexer_8_out, multiplexer_9_out, multiplexer_10_out,
       multiplexer_11_out, multiplexer_12_out, multiplexer_14_out, multiplexer_15_out, multiplexer_16_out,
       multiplexer_17_out, multiplexer_18_out, multiplexer_19_out, multiplexer_20_out, multiplexer_21_out,
       multiplexer_25_out;
  wire [1:0] multiplexer_23_out, multiplexer_24_out;
  wire [3:0] multiplexer_7_out;
  wire [31:0] multiplexer_1_out, multiplexer_2_out, multiplexer_3_out, multiplexer_4_out, multiplexer_13_out,
       multiplexer_22_out;

  // Probe on multiplexer_2_out
  Multiplexer #(.select(1), .width(32), .disabled("Z"), .enable("false")) multiplexer_1 (
    .in0(\指令 ), .in1({32{1'b0}}), .out(multiplexer_1_out), .sel(\同步置0 ));
  Multiplexer #(.select(1), .width(32), .disabled("Z"), .enable("false")) multiplexer_2 (
    .in0(PC), .in1({32{1'b0}}), .out(multiplexer_2_out), .sel(\同步置0 ));
  Multiplexer #(.select(1), .width(32), .disabled("Z"), .enable("false")) multiplexer_3 (
    .in0(\寄存器1 ), .in1({32{1'b0}}), .out(multiplexer_3_out), .sel(\同步置0 ));
  Multiplexer #(.select(1), .width(32), .disabled("Z"), .enable("false")) multiplexer_4 (
    .in0(\寄存器2 ), .in1({32{1'b0}}), .out(multiplexer_4_out), .sel(\同步置0 ));
  Multiplexer #(.select(1), .width(1), .disabled("Z"), .enable("false")) multiplexer_5 (
    .in0(MenToReg), .in1(1'b0), .out(multiplexer_5_out), .sel(\同步置0 ));
  Multiplexer #(.select(1), .width(1), .disabled("Z"), .enable("false")) multiplexer_6 (
    .in0(MenWrite), .in1(1'b0), .out(multiplexer_6_out), .sel(\同步置0 ));
  Multiplexer #(.select(1), .width(4), .disabled("Z"), .enable("false")) multiplexer_7 (
    .in0(ALU_OP), .in1(4'b0000), .out(multiplexer_7_out), .sel(\同步置0 ));
  Multiplexer #(.select(1), .width(1), .disabled("Z"), .enable("false")) multiplexer_8 (
    .in0(ALU_src), .in1(1'b0), .out(multiplexer_8_out), .sel(\同步置0 ));
  Multiplexer #(.select(1), .width(1), .disabled("Z"), .enable("false")) multiplexer_9 (
    .in0(RegWrite), .in1(1'b0), .out(multiplexer_9_out), .sel(\同步置0 ));
  Multiplexer #(.select(1), .width(1), .disabled("Z"), .enable("false")) multiplexer_10 (
    .in0(sllv), .in1(1'b0), .out(multiplexer_10_out), .sel(\同步置0 ));
  Multiplexer #(.select(1), .width(1), .disabled("Z"), .enable("false")) multiplexer_11 (
    .in0(halt), .in1(1'b0), .out(multiplexer_11_out), .sel(\同步置0 ));
  Multiplexer #(.select(1), .width(1), .disabled("Z"), .enable("false")) multiplexer_12 (
    .in0(lb), .in1(1'b0), .out(multiplexer_12_out), .sel(\同步置0 ));
  Multiplexer #(.select(1), .width(32), .disabled("Z"), .enable("false")) multiplexer_13 (
    .in0(imm), .in1({32{1'b0}}), .out(multiplexer_13_out), .sel(\同步置0 ));
  Multiplexer #(.select(1), .width(1), .disabled("Z"), .enable("false")) multiplexer_14 (
    .in0(RegDst), .in1(1'b0), .out(multiplexer_14_out), .sel(\同步置0 ));
  Multiplexer #(.select(1), .width(1), .disabled("Z"), .enable("false")) multiplexer_15 (
    .in0(JR), .in1(1'b0), .out(multiplexer_15_out), .sel(\同步置0 ));
  Multiplexer #(.select(1), .width(1), .disabled("Z"), .enable("false")) multiplexer_16 (
    .in0(JMP), .in1(1'b0), .out(multiplexer_16_out), .sel(\同步置0 ));
  Multiplexer #(.select(1), .width(1), .disabled("Z"), .enable("false")) multiplexer_17 (
    .in0(JAL), .in1(1'b0), .out(multiplexer_17_out), .sel(\同步置0 ));
  Multiplexer #(.select(1), .width(1), .disabled("Z"), .enable("false")) multiplexer_18 (
    .in0(BNE), .in1(1'b0), .out(multiplexer_18_out), .sel(\同步置0 ));
  Multiplexer #(.select(1), .width(1), .disabled("Z"), .enable("false")) multiplexer_19 (
    .in0(BEQ), .in1(1'b0), .out(multiplexer_19_out), .sel(\同步置0 ));
  Multiplexer #(.select(1), .width(1), .disabled("Z"), .enable("false")) multiplexer_20 (
    .in0(BLTZ), .in1(1'b0), .out(multiplexer_20_out), .sel(\同步置0 ));
  Multiplexer #(.select(1), .width(1), .disabled("Z"), .enable("false")) multiplexer_21 (
    .in0(Signext), .in1(1'b0), .out(multiplexer_21_out), .sel(\同步置0 ));
  Multiplexer #(.select(1), .width(32), .disabled("Z"), .enable("false")) multiplexer_22 (
    .in0(in_26), .in1({32{1'b0}}), .out(multiplexer_22_out), .sel(\同步置0 ));
  Multiplexer #(.select(1), .width(2), .disabled("Z"), .enable("false")) multiplexer_23 (
    .in0(in_27), .in1(2'b00), .out(multiplexer_23_out), .sel(\同步置0 ));
  Multiplexer #(.select(1), .width(2), .disabled("Z"), .enable("false")) multiplexer_24 (
    .in0(in_28), .in1(2'b00), .out(multiplexer_24_out), .sel(\同步置0 ));
  Multiplexer #(.select(1), .width(1), .disabled("Z"), .enable("false")) multiplexer_25 (
    .in0(in_29), .in1(1'b0), .out(multiplexer_25_out), .sel(\同步置0 ));
  Register #(.width(32), .trigger("rising"), .Select("low")) register_1 (
    .D(multiplexer_1_out), .en(Enable), .Q(out_30), .clk(CTK), .clr(RST));
  Register #(.width(32), .trigger("rising"), .Select("low")) register_2 (
    .D(multiplexer_2_out), .en(Enable), .Q(out_31), .clk(CTK), .clr(RST));
  Register #(.width(32), .trigger("rising"), .Select("low")) register_3 (
    .D(multiplexer_3_out), .en(Enable), .Q(out_32), .clk(CTK), .clr(RST));
  Register #(.width(32), .trigger("rising"), .Select("low")) register_4 (
    .D(multiplexer_4_out), .en(Enable), .Q(out_33), .clk(CTK), .clr(RST));
  Register #(.width(1), .trigger("rising"), .Select("low")) register_5 (
    .D(multiplexer_5_out), .en(Enable), .Q(out_34), .clk(CTK), .clr(RST));
  Register #(.width(1), .trigger("rising"), .Select("low")) register_6 (
    .D(multiplexer_6_out), .en(Enable), .Q(out_35), .clk(CTK), .clr(RST));
  Register #(.width(4), .trigger("rising"), .Select("low")) register_7 (
    .D(multiplexer_7_out), .en(Enable), .Q(out_36), .clk(CTK), .clr(RST));
  Register #(.width(1), .trigger("rising"), .Select("low")) register_8 (
    .D(multiplexer_8_out), .en(Enable), .Q(out_37), .clk(CTK), .clr(RST));
  Register #(.width(1), .trigger("rising"), .Select("low")) register_9 (
    .D(multiplexer_9_out), .en(Enable), .Q(out_38), .clk(CTK), .clr(RST));
  Register #(.width(1), .trigger("rising"), .Select("low")) register_10 (
    .D(multiplexer_10_out), .en(Enable), .Q(out_39), .clk(CTK), .clr(RST));
  Register #(.width(1), .trigger("rising"), .Select("low")) register_11 (
    .D(multiplexer_11_out), .en(Enable), .Q(out_40), .clk(CTK), .clr(RST));
  Register #(.width(1), .trigger("rising"), .Select("low")) register_12 (
    .D(multiplexer_12_out), .en(Enable), .Q(out_41), .clk(CTK), .clr(RST));
  Register #(.width(32), .trigger("rising"), .Select("low")) register_13 (
    .D(multiplexer_13_out), .en(Enable), .Q(out_42), .clk(CTK), .clr(RST));
  Register #(.width(1), .trigger("rising"), .Select("low")) register_14 (
    .D(multiplexer_14_out), .en(Enable), .Q(out_43), .clk(CTK), .clr(RST));
  Register #(.width(1), .trigger("rising"), .Select("low")) register_15 (
    .D(multiplexer_15_out), .en(Enable), .Q(out_44), .clk(CTK), .clr(RST));
  Register #(.width(1), .trigger("rising"), .Select("low")) register_16 (
    .D(multiplexer_16_out), .en(Enable), .Q(out_45), .clk(CTK), .clr(RST));
  Register #(.width(1), .trigger("rising"), .Select("low")) register_17 (
    .D(multiplexer_17_out), .en(Enable), .Q(out_46), .clk(CTK), .clr(RST));
  Register #(.width(1), .trigger("rising"), .Select("low")) register_18 (
    .D(multiplexer_18_out), .en(Enable), .Q(out_47), .clk(CTK), .clr(RST));
  Register #(.width(1), .trigger("rising"), .Select("low")) register_19 (
    .D(multiplexer_19_out), .en(Enable), .Q(out_48), .clk(CTK), .clr(RST));
  Register #(.width(1), .trigger("rising"), .Select("low")) register_20 (
    .D(multiplexer_20_out), .en(Enable), .Q(out_49), .clk(CTK), .clr(RST));
  Register #(.width(1), .trigger("rising"), .Select("low")) register_21 (
    .D(multiplexer_21_out), .en(Enable), .Q(out_50), .clk(CTK), .clr(RST));
  Register #(.width(32), .trigger("rising"), .Select("low")) register_22 (
    .D(multiplexer_22_out), .en(Enable), .Q(out_51), .clk(CTK), .clr(RST));
  Register #(.width(2), .trigger("rising"), .Select("low")) register_23 (
    .D(multiplexer_23_out), .en(Enable), .Q(out_52), .clk(CTK), .clr(RST));
  Register #(.width(2), .trigger("rising"), .Select("low")) register_24 (
    .D(multiplexer_24_out), .en(Enable), .Q(out_53), .clk(CTK), .clr(RST));
  Register #(.width(1), .trigger("rising"), .Select("low")) register_25 (
    .D(multiplexer_25_out), .en(Enable), .Q(out_54), .clk(CTK), .clr(RST));
endmodule

module EX_MEM (
  input  CTK,
  input  RST,
  input  Enable,
  input  [31:0] \指令 ,
  input  [31:0] PC,
  input  [31:0] \寄存器1 ,
  input  [31:0] \寄存器2 ,
  input  MenToReg,
  input  MenWrite,
  input  RegDst,
  input  led,
  input  halt,
  input  lb,
  input  JAL,
  input  RegDst_2,
  input  [31:0] PC_4,
  output [31:0] out_17,
  output [31:0] out_18,
  output [31:0] out_19,
  output [31:0] out_20,
  output out_21,
  output out_22,
  output out_23,
  output out_24,
  output out_25,
  output out_26,
  output out_27,
  output out_28,
  output [31:0] out_29
);

  Register #(.width(32), .trigger("rising"), .Select("low")) register_1 (
    .D(\指令 ), .en(Enable), .Q(out_17), .clk(CTK), .clr(RST));
  Register #(.width(32), .trigger("rising"), .Select("low")) register_2 (
    .D(PC), .en(Enable), .Q(out_18), .clk(CTK), .clr(RST));
  Register #(.width(32), .trigger("rising"), .Select("low")) register_3 (
    .D(\寄存器1 ), .en(Enable), .Q(out_19), .clk(CTK), .clr(RST));
  Register #(.width(32), .trigger("rising"), .Select("low")) register_4 (
    .D(\寄存器2 ), .en(Enable), .Q(out_20), .clk(CTK), .clr(RST));
  Register #(.width(1), .trigger("rising"), .Select("low")) register_5 (
    .D(MenToReg), .en(Enable), .Q(out_21), .clk(CTK), .clr(RST));
  Register #(.width(1), .trigger("rising"), .Select("low")) register_6 (
    .D(MenWrite), .en(Enable), .Q(out_22), .clk(CTK), .clr(RST));
  Register #(.width(1), .trigger("rising"), .Select("low")) register_7 (
    .D(RegDst), .en(Enable), .Q(out_23), .clk(CTK), .clr(RST));
  Register #(.width(1), .trigger("rising"), .Select("low")) register_8 (
    .D(led), .en(Enable), .Q(out_24), .clk(CTK), .clr(RST));
  Register #(.width(1), .trigger("rising"), .Select("low")) register_9 (
    .D(halt), .en(Enable), .Q(out_25), .clk(CTK), .clr(RST));
  Register #(.width(1), .trigger("rising"), .Select("low")) register_10 (
    .D(lb), .en(Enable), .Q(out_26), .clk(CTK), .clr(RST));
  Register #(.width(1), .trigger("rising"), .Select("low")) register_11 (
    .D(JAL), .en(Enable), .Q(out_27), .clk(CTK), .clr(RST));
  Register #(.width(1), .trigger("rising"), .Select("low")) register_12 (
    .D(RegDst_2), .en(Enable), .Q(out_28), .clk(CTK), .clr(RST));
  Register #(.width(32), .trigger("rising"), .Select("low")) register_13 (
    .D(PC_4), .en(Enable), .Q(out_29), .clk(CTK), .clr(RST));
endmodule

module MEM_WB (
  input  CTK,
  input  RST,
  input  Enable,
  input  [31:0] \指令 ,
  input  [31:0] PC,
  input  [31:0] \运算器结果 ,
  input  [31:0] \存储器结果 ,
  input  MenToReg,
  input  RegWrite,
  input  halt,
  input  lb,
  input  RegDst,
  input  JAL,
  input  [31:0] PC_2,
  output [31:0] out_15,
  output [31:0] out_16,
  output [31:0] out_17,
  output [31:0] out_18,
  output out_19,
  output out_20,
  output out_21,
  output out_22,
  output out_23,
  output out_24,
  output [31:0] out_25
);

  Register #(.width(32), .trigger("rising"), .Select("low")) register_1 (
    .D(\指令 ), .en(Enable), .Q(out_15), .clk(CTK), .clr(RST));
  Register #(.width(32), .trigger("rising"), .Select("low")) register_2 (
    .D(PC), .en(Enable), .Q(out_16), .clk(CTK), .clr(RST));
  Register #(.width(32), .trigger("rising"), .Select("low")) register_3 (
    .D(\运算器结果 ), .en(Enable), .Q(out_17), .clk(CTK), .clr(RST));
  Register #(.width(32), .trigger("rising"), .Select("low")) register_4 (
    .D(\存储器结果 ), .en(Enable), .Q(out_18), .clk(CTK), .clr(RST));
  Register #(.width(1), .trigger("rising"), .Select("low")) register_5 (
    .D(MenToReg), .en(Enable), .Q(out_19), .clk(CTK), .clr(RST));
  Register #(.width(1), .trigger("rising"), .Select("low")) register_6 (
    .D(RegWrite), .en(Enable), .Q(out_20), .clk(CTK), .clr(RST));
  Register #(.width(1), .trigger("rising"), .Select("low")) register_7 (
    .D(halt), .en(Enable), .Q(out_21), .clk(CTK), .clr(RST));
  Register #(.width(1), .trigger("rising"), .Select("low")) register_8 (
    .D(lb), .en(Enable), .Q(out_22), .clk(CTK), .clr(RST));
  Register #(.width(1), .trigger("rising"), .Select("low")) register_9 (
    .D(RegDst), .en(Enable), .Q(out_23), .clk(CTK), .clr(RST));
  Register #(.width(1), .trigger("rising"), .Select("low")) register_10 (
    .D(JAL), .en(Enable), .Q(out_24), .clk(CTK), .clr(RST));
  Register #(.width(32), .trigger("rising"), .Select("low")) register_11 (
    .D(PC_2), .en(Enable), .Q(out_25), .clk(CTK), .clr(RST));
endmodule

module \寄存器使用情况电路  (
  input  OP0,
  input  OP1,
  input  OP2,
  input  OP3,
  input  OP4,
  input  OP5,
  input  F0,
  input  F1,
  input  F2,
  input  F3,
  input  F4,
  input  F5,
  output R1_USED,
  output R2_USED
);

  wire and_1_out, and_2_out, and_3_out, and_4_out, and_5_out, and_6_out, and_7_out, and_8_out, and_9_out,
       and_10_out, and_11_out, and_12_out, and_13_out, and_14_out, and_15_out, and_16_out, and_17_out,
       and_18_out, and_19_out, and_20_out, and_21_out, and_22_out, and_23_out, and_24_out, and_25_out,
       and_26_out, and_27_out, and_28_out, and_29_out, and_30_out, and_31_out, and_32_out, and_33_out,
       and_34_out, and_35_out, and_36_out, and_37_out, and_38_out, and_39_out, and_40_out, and_41_out,
       and_42_out, not_1_out, not_2_out, not_3_out, not_4_out, not_5_out, not_6_out, not_7_out, not_8_out,
       not_9_out, not_10_out, not_11_out, not_12_out, not_13_out, not_14_out, not_15_out, not_16_out,
       not_17_out, not_18_out, not_19_out, not_20_out, not_21_out, not_22_out, not_23_out, not_24_out,
       not_25_out, not_26_out, not_27_out, not_28_out, not_29_out, not_30_out, not_31_out, not_32_out,
       not_33_out, not_34_out, not_35_out, not_36_out, not_37_out, not_38_out, not_39_out, not_40_out,
       not_41_out, not_42_out, not_43_out, not_44_out, not_45_out, not_46_out, not_47_out, not_48_out,
       not_49_out, not_50_out, not_51_out, not_52_out, not_53_out, not_54_out, not_55_out, not_56_out,
       not_57_out, not_58_out, not_59_out, not_60_out, not_61_out, not_62_out, not_63_out, not_64_out,
       not_65_out, not_66_out, not_67_out, not_68_out, not_69_out, not_70_out, not_71_out, not_72_out,
       not_73_out, not_74_out, not_75_out, not_76_out, not_77_out, not_78_out, not_79_out, not_80_out,
       not_81_out, not_82_out, not_83_out, not_84_out, not_85_out, not_86_out, not_87_out, not_88_out,
       not_89_out, not_90_out, not_91_out, not_92_out, not_93_out, not_94_out, not_95_out, not_96_out,
       not_97_out, not_98_out, not_99_out, not_100_out, not_101_out, not_102_out, not_103_out, not_104_out,
       not_105_out, not_106_out, not_107_out, not_108_out, not_109_out, not_110_out, not_111_out,
       not_112_out, not_113_out, not_114_out, not_115_out, not_116_out, not_117_out, not_118_out,
       not_119_out, not_120_out, not_121_out, not_122_out, not_123_out, not_124_out, not_125_out,
       not_126_out, not_127_out, not_128_out, not_129_out, not_130_out, not_131_out, not_132_out,
       not_133_out, not_134_out, not_135_out, not_136_out, not_137_out, not_138_out, not_139_out,
       not_140_out, not_141_out, not_142_out, not_143_out, not_144_out, not_145_out, not_146_out,
       not_147_out, not_148_out, not_149_out, not_150_out, not_151_out, not_152_out, not_153_out,
       not_154_out, not_155_out, not_156_out, not_157_out, not_158_out, not_159_out, not_160_out,
       not_161_out, not_162_out, not_163_out, not_164_out, not_165_out, not_166_out, not_167_out,
       not_168_out, not_169_out, not_170_out, not_171_out, not_172_out, not_173_out, not_174_out,
       not_175_out, not_176_out, not_177_out, not_178_out, not_179_out, not_180_out, not_181_out,
       not_182_out, not_183_out, not_184_out, not_185_out, not_186_out, not_187_out, not_188_out,
       not_189_out, not_190_out, not_191_out, not_192_out, not_193_out, not_194_out, not_195_out,
       not_196_out, not_197_out, not_198_out, not_199_out, not_200_out, not_201_out, not_202_out,
       not_203_out, not_204_out, not_205_out, not_206_out, not_207_out, not_208_out, not_209_out,
       not_210_out, not_211_out, not_212_out, not_213_out, not_214_out, not_215_out, not_216_out,
       not_217_out, not_218_out, not_219_out, not_220_out, not_221_out, not_222_out, not_223_out,
       not_224_out, not_225_out, not_226_out, not_227_out, not_228_out, not_229_out, not_230_out,
       not_231_out, not_232_out, not_233_out, not_234_out, not_235_out, not_236_out, not_237_out,
       not_238_out, not_239_out, not_240_out, not_241_out, not_242_out, not_243_out, not_244_out,
       not_245_out, not_246_out, not_247_out, not_248_out, not_249_out, not_250_out, not_251_out,
       not_252_out, not_253_out, not_254_out, not_255_out, not_256_out, not_257_out, not_258_out,
       not_259_out, not_260_out, not_261_out, not_262_out, not_263_out, not_264_out, not_265_out,
       not_266_out, not_267_out, not_268_out, not_269_out, not_270_out, not_271_out, not_272_out,
       not_273_out, not_274_out, not_275_out, not_276_out, not_277_out, not_278_out, not_279_out,
       not_280_out, not_281_out, not_282_out, not_283_out, not_284_out, not_285_out, not_286_out,
       not_287_out, not_288_out, not_289_out, not_290_out, not_291_out, not_292_out, not_293_out,
       not_294_out, not_295_out, not_296_out, not_297_out, not_298_out, not_299_out, not_300_out,
       not_301_out, not_302_out, not_303_out, not_304_out;

  not not_1 (not_1_out, OP5);
  not not_2 (not_2_out, OP4);
  not not_3 (not_3_out, OP3);
  not not_4 (not_4_out, OP2);
  not not_5 (not_5_out, OP1);
  not not_6 (not_6_out, OP0);
  not not_7 (not_7_out, F4);
  not not_8 (not_8_out, F3);
  not not_9 (not_9_out, F2);
  not not_10 (not_10_out, F1);
  not not_11 (not_11_out, F0);
  not not_12 (not_12_out, OP5);
  not not_13 (not_13_out, OP4);
  not not_14 (not_14_out, OP3);
  not not_15 (not_15_out, OP2);
  not not_16 (not_16_out, OP1);
  not not_17 (not_17_out, OP0);
  not not_18 (not_18_out, F4);
  not not_19 (not_19_out, F3);
  not not_20 (not_20_out, F2);
  not not_21 (not_21_out, F1);
  not not_22 (not_22_out, OP5);
  not not_23 (not_23_out, OP4);
  not not_24 (not_24_out, OP3);
  not not_25 (not_25_out, OP2);
  not not_26 (not_26_out, OP1);
  not not_27 (not_27_out, OP0);
  not not_28 (not_28_out, F4);
  not not_29 (not_29_out, F3);
  not not_30 (not_30_out, F2);
  not not_31 (not_31_out, F0);
  not not_32 (not_32_out, OP5);
  not not_33 (not_33_out, OP4);
  not not_34 (not_34_out, OP3);
  not not_35 (not_35_out, OP2);
  not not_36 (not_36_out, OP1);
  not not_37 (not_37_out, OP0);
  not not_38 (not_38_out, F4);
  not not_39 (not_39_out, F3);
  not not_40 (not_40_out, F1);
  not not_41 (not_41_out, F0);
  not not_42 (not_42_out, OP5);
  not not_43 (not_43_out, OP4);
  not not_44 (not_44_out, OP3);
  not not_45 (not_45_out, OP2);
  not not_46 (not_46_out, OP1);
  not not_47 (not_47_out, OP0);
  not not_48 (not_48_out, F4);
  not not_49 (not_49_out, F3);
  not not_50 (not_50_out, F1);
  not not_51 (not_51_out, OP5);
  not not_52 (not_52_out, OP4);
  not not_53 (not_53_out, OP3);
  not not_54 (not_54_out, OP2);
  not not_55 (not_55_out, OP1);
  not not_56 (not_56_out, OP0);
  not not_57 (not_57_out, F4);
  not not_58 (not_58_out, F3);
  not not_59 (not_59_out, OP5);
  not not_60 (not_60_out, OP4);
  not not_61 (not_61_out, OP3);
  not not_62 (not_62_out, OP2);
  not not_63 (not_63_out, OP1);
  not not_64 (not_64_out, OP0);
  not not_65 (not_65_out, F4);
  not not_66 (not_66_out, F2);
  not not_67 (not_67_out, F0);
  not not_68 (not_68_out, OP5);
  not not_69 (not_69_out, OP4);
  not not_70 (not_70_out, OP3);
  not not_71 (not_71_out, OP2);
  not not_72 (not_72_out, OP1);
  not not_73 (not_73_out, OP0);
  not not_74 (not_74_out, F4);
  not not_75 (not_75_out, F2);
  not not_76 (not_76_out, OP5);
  not not_77 (not_77_out, OP4);
  not not_78 (not_78_out, OP3);
  not not_79 (not_79_out, OP2);
  not not_80 (not_80_out, OP1);
  not not_81 (not_81_out, OP0);
  not not_82 (not_82_out, F5);
  not not_83 (not_83_out, F4);
  not not_84 (not_84_out, F2);
  not not_85 (not_85_out, F1);
  not not_86 (not_86_out, F0);
  not not_87 (not_87_out, OP5);
  not not_88 (not_88_out, OP4);
  not not_89 (not_89_out, OP3);
  not not_90 (not_90_out, OP2);
  not not_91 (not_91_out, OP1);
  not not_92 (not_92_out, OP0);
  not not_93 (not_93_out, F5);
  not not_94 (not_94_out, F4);
  not not_95 (not_95_out, F1);
  not not_96 (not_96_out, F0);
  not not_97 (not_97_out, OP5);
  not not_98 (not_98_out, OP4);
  not not_99 (not_99_out, OP3);
  not not_100 (not_100_out, OP1);
  not not_101 (not_101_out, OP0);
  not not_102 (not_102_out, OP5);
  not not_103 (not_103_out, OP4);
  not not_104 (not_104_out, OP3);
  not not_105 (not_105_out, OP1);
  not not_106 (not_106_out, OP5);
  not not_107 (not_107_out, OP4);
  not not_108 (not_108_out, OP2);
  not not_109 (not_109_out, OP1);
  not not_110 (not_110_out, OP0);
  not not_111 (not_111_out, OP5);
  not not_112 (not_112_out, OP4);
  not not_113 (not_113_out, OP1);
  not not_114 (not_114_out, OP0);
  not not_115 (not_115_out, OP5);
  not not_116 (not_116_out, OP4);
  not not_117 (not_117_out, OP2);
  not not_118 (not_118_out, OP1);
  not not_119 (not_119_out, OP5);
  not not_120 (not_120_out, OP4);
  not not_121 (not_121_out, OP2);
  not not_122 (not_122_out, OP0);
  not not_123 (not_123_out, OP5);
  not not_124 (not_124_out, OP4);
  not not_125 (not_125_out, OP1);
  not not_126 (not_126_out, OP4);
  not not_127 (not_127_out, OP3);
  not not_128 (not_128_out, OP2);
  not not_129 (not_129_out, OP4);
  not not_130 (not_130_out, OP2);
  not not_131 (not_131_out, OP5);
  not not_132 (not_132_out, OP4);
  not not_133 (not_133_out, OP0);
  not not_134 (not_134_out, OP5);
  not not_135 (not_135_out, OP4);
  not not_136 (not_136_out, OP5);
  not not_137 (not_137_out, OP4);
  not not_138 (not_138_out, OP3);
  not not_139 (not_139_out, OP2);
  not not_140 (not_140_out, OP1);
  not not_141 (not_141_out, OP0);
  not not_142 (not_142_out, F5);
  not not_143 (not_143_out, F4);
  not not_144 (not_144_out, F3);
  not not_145 (not_145_out, F1);
  not not_146 (not_146_out, F0);
  not not_147 (not_147_out, OP4);
  not not_148 (not_148_out, OP3);
  not not_149 (not_149_out, OP2);
  not not_150 (not_150_out, OP1);
  not not_151 (not_151_out, OP0);
  not not_152 (not_152_out, OP5);
  not not_153 (not_153_out, OP4);
  not not_154 (not_154_out, OP3);
  not not_155 (not_155_out, OP2);
  not not_156 (not_156_out, OP1);
  not not_157 (not_157_out, OP5);
  not not_158 (not_158_out, OP4);
  not not_159 (not_159_out, OP3);
  not not_160 (not_160_out, OP2);
  not not_161 (not_161_out, OP1);
  not not_162 (not_162_out, OP0);
  not not_163 (not_163_out, F5);
  not not_164 (not_164_out, F4);
  not not_165 (not_165_out, F3);
  not not_166 (not_166_out, F2);
  not not_167 (not_167_out, F1);
  not not_168 (not_168_out, F0);
  not not_169 (not_169_out, OP5);
  not not_170 (not_170_out, OP4);
  not not_171 (not_171_out, OP3);
  not not_172 (not_172_out, OP2);
  not not_173 (not_173_out, OP1);
  not not_174 (not_174_out, OP0);
  not not_175 (not_175_out, F5);
  not not_176 (not_176_out, F4);
  not not_177 (not_177_out, F3);
  not not_178 (not_178_out, F2);
  not not_179 (not_179_out, OP5);
  not not_180 (not_180_out, OP4);
  not not_181 (not_181_out, OP3);
  not not_182 (not_182_out, OP2);
  not not_183 (not_183_out, OP1);
  not not_184 (not_184_out, OP0);
  not not_185 (not_185_out, F5);
  not not_186 (not_186_out, F4);
  not not_187 (not_187_out, F3);
  not not_188 (not_188_out, F2);
  not not_189 (not_189_out, F0);
  not not_190 (not_190_out, OP5);
  not not_191 (not_191_out, OP4);
  not not_192 (not_192_out, OP3);
  not not_193 (not_193_out, OP2);
  not not_194 (not_194_out, OP1);
  not not_195 (not_195_out, OP0);
  not not_196 (not_196_out, F4);
  not not_197 (not_197_out, F3);
  not not_198 (not_198_out, F2);
  not not_199 (not_199_out, F1);
  not not_200 (not_200_out, F0);
  not not_201 (not_201_out, OP5);
  not not_202 (not_202_out, OP4);
  not not_203 (not_203_out, OP3);
  not not_204 (not_204_out, OP2);
  not not_205 (not_205_out, OP1);
  not not_206 (not_206_out, OP0);
  not not_207 (not_207_out, F4);
  not not_208 (not_208_out, F3);
  not not_209 (not_209_out, F2);
  not not_210 (not_210_out, F1);
  not not_211 (not_211_out, OP5);
  not not_212 (not_212_out, OP4);
  not not_213 (not_213_out, OP3);
  not not_214 (not_214_out, OP2);
  not not_215 (not_215_out, OP1);
  not not_216 (not_216_out, OP0);
  not not_217 (not_217_out, F4);
  not not_218 (not_218_out, F3);
  not not_219 (not_219_out, F2);
  not not_220 (not_220_out, F0);
  not not_221 (not_221_out, OP5);
  not not_222 (not_222_out, OP4);
  not not_223 (not_223_out, OP3);
  not not_224 (not_224_out, OP2);
  not not_225 (not_225_out, OP1);
  not not_226 (not_226_out, OP0);
  not not_227 (not_227_out, F4);
  not not_228 (not_228_out, F3);
  not not_229 (not_229_out, F1);
  not not_230 (not_230_out, F0);
  not not_231 (not_231_out, OP5);
  not not_232 (not_232_out, OP4);
  not not_233 (not_233_out, OP3);
  not not_234 (not_234_out, OP2);
  not not_235 (not_235_out, OP1);
  not not_236 (not_236_out, OP0);
  not not_237 (not_237_out, F4);
  not not_238 (not_238_out, F3);
  not not_239 (not_239_out, F1);
  not not_240 (not_240_out, OP5);
  not not_241 (not_241_out, OP4);
  not not_242 (not_242_out, OP3);
  not not_243 (not_243_out, OP2);
  not not_244 (not_244_out, OP1);
  not not_245 (not_245_out, OP0);
  not not_246 (not_246_out, F4);
  not not_247 (not_247_out, F3);
  not not_248 (not_248_out, OP5);
  not not_249 (not_249_out, OP4);
  not not_250 (not_250_out, OP3);
  not not_251 (not_251_out, OP2);
  not not_252 (not_252_out, OP1);
  not not_253 (not_253_out, OP0);
  not not_254 (not_254_out, F4);
  not not_255 (not_255_out, F2);
  not not_256 (not_256_out, F0);
  not not_257 (not_257_out, OP5);
  not not_258 (not_258_out, OP4);
  not not_259 (not_259_out, OP3);
  not not_260 (not_260_out, OP2);
  not not_261 (not_261_out, OP1);
  not not_262 (not_262_out, OP0);
  not not_263 (not_263_out, F4);
  not not_264 (not_264_out, F2);
  not not_265 (not_265_out, OP5);
  not not_266 (not_266_out, OP4);
  not not_267 (not_267_out, OP3);
  not not_268 (not_268_out, OP2);
  not not_269 (not_269_out, OP1);
  not not_270 (not_270_out, OP0);
  not not_271 (not_271_out, F5);
  not not_272 (not_272_out, F4);
  not not_273 (not_273_out, F1);
  not not_274 (not_274_out, F0);
  not not_275 (not_275_out, OP5);
  not not_276 (not_276_out, OP4);
  not not_277 (not_277_out, OP3);
  not not_278 (not_278_out, OP1);
  not not_279 (not_279_out, OP0);
  not not_280 (not_280_out, OP5);
  not not_281 (not_281_out, OP4);
  not not_282 (not_282_out, OP3);
  not not_283 (not_283_out, OP1);
  not not_284 (not_284_out, OP4);
  not not_285 (not_285_out, OP3);
  not not_286 (not_286_out, OP2);
  not not_287 (not_287_out, OP4);
  not not_288 (not_288_out, OP2);
  not not_289 (not_289_out, OP5);
  not not_290 (not_290_out, OP4);
  not not_291 (not_291_out, OP3);
  not not_292 (not_292_out, OP2);
  not not_293 (not_293_out, OP1);
  not not_294 (not_294_out, OP0);
  not not_295 (not_295_out, F5);
  not not_296 (not_296_out, F4);
  not not_297 (not_297_out, F3);
  not not_298 (not_298_out, F1);
  not not_299 (not_299_out, F0);
  not not_300 (not_300_out, OP4);
  not not_301 (not_301_out, OP3);
  not not_302 (not_302_out, OP2);
  not not_303 (not_303_out, OP1);
  not not_304 (not_304_out, OP0);
  and and_1 (and_1_out, not_1_out, not_2_out, not_3_out, not_4_out, not_5_out, not_6_out, F5, not_7_out, not_8_out, not_9_out, not_10_out, not_11_out);
  and and_2 (and_2_out, not_12_out, not_13_out, not_14_out, not_15_out, not_16_out, not_17_out, F5, not_18_out, not_19_out, not_20_out, not_21_out, F0);
  and and_3 (and_3_out, not_22_out, not_23_out, not_24_out, not_25_out, not_26_out, not_27_out, F5, not_28_out, not_29_out, not_30_out, F1, not_31_out);
  and and_4 (and_4_out, not_32_out, not_33_out, not_34_out, not_35_out, not_36_out, not_37_out, F5, not_38_out, not_39_out, F2, not_40_out, not_41_out);
  and and_5 (and_5_out, not_42_out, not_43_out, not_44_out, not_45_out, not_46_out, not_47_out, F5, not_48_out, not_49_out, F2, not_50_out, F0);
  and and_6 (and_6_out, not_51_out, not_52_out, not_53_out, not_54_out, not_55_out, not_56_out, F5, not_57_out, not_58_out, F2, F1, F0);
  and and_7 (and_7_out, not_59_out, not_60_out, not_61_out, not_62_out, not_63_out, not_64_out, F5, not_65_out, F3, not_66_out, F1, not_67_out);
  and and_8 (and_8_out, not_68_out, not_69_out, not_70_out, not_71_out, not_72_out, not_73_out, F5, not_74_out, F3, not_75_out, F1, F0);
  and and_9 (and_9_out, not_76_out, not_77_out, not_78_out, not_79_out, not_80_out, not_81_out, not_82_out, not_83_out, F3, not_84_out, not_85_out, not_86_out);
  and and_10 (and_10_out, not_87_out, not_88_out, not_89_out, not_90_out, not_91_out, not_92_out, not_93_out, not_94_out, F3, F2, not_95_out, not_96_out);
  and and_11 (and_11_out, not_97_out, not_98_out, not_99_out, OP2, not_100_out, not_101_out);
  and and_12 (and_12_out, not_102_out, not_103_out, not_104_out, OP2, not_105_out, OP0);
  and and_13 (and_13_out, not_106_out, not_107_out, OP3, not_108_out, not_109_out, not_110_out);
  and and_14 (and_14_out, not_111_out, not_112_out, OP3, OP2, not_113_out, not_114_out);
  and and_15 (and_15_out, not_115_out, not_116_out, OP3, not_117_out, not_118_out, OP0);
  and and_16 (and_16_out, not_119_out, not_120_out, OP3, not_121_out, OP1, not_122_out);
  and and_17 (and_17_out, not_123_out, not_124_out, OP3, OP2, not_125_out, OP0);
  and and_18 (and_18_out, OP5, not_126_out, not_127_out, not_128_out, OP1, OP0);
  and and_19 (and_19_out, OP5, not_129_out, OP3, not_130_out, OP1, OP0);
  and and_20 (and_20_out, not_131_out, not_132_out, OP3, OP2, OP1, not_133_out);
  and and_21 (and_21_out, not_134_out, not_135_out, OP3, OP2, OP1, OP0);
  and and_22 (and_22_out, not_136_out, not_137_out, not_138_out, not_139_out, not_140_out, not_141_out, not_142_out, not_143_out, not_144_out, F2, not_145_out, not_146_out);
  and and_23 (and_23_out, OP5, not_147_out, not_148_out, not_149_out, not_150_out, not_151_out);
  and and_24 (and_24_out, not_152_out, not_153_out, not_154_out, not_155_out, not_156_out, OP0);
  and and_25 (and_25_out, not_157_out, not_158_out, not_159_out, not_160_out, not_161_out, not_162_out, not_163_out, not_164_out, not_165_out, not_166_out, not_167_out, not_168_out);
  and and_26 (and_26_out, not_169_out, not_170_out, not_171_out, not_172_out, not_173_out, not_174_out, not_175_out, not_176_out, not_177_out, not_178_out, F1, F0);
  and and_27 (and_27_out, not_179_out, not_180_out, not_181_out, not_182_out, not_183_out, not_184_out, not_185_out, not_186_out, not_187_out, not_188_out, F1, not_189_out);
  and and_28 (and_28_out, not_190_out, not_191_out, not_192_out, not_193_out, not_194_out, not_195_out, F5, not_196_out, not_197_out, not_198_out, not_199_out, not_200_out);
  and and_29 (and_29_out, not_201_out, not_202_out, not_203_out, not_204_out, not_205_out, not_206_out, F5, not_207_out, not_208_out, not_209_out, not_210_out, F0);
  and and_30 (and_30_out, not_211_out, not_212_out, not_213_out, not_214_out, not_215_out, not_216_out, F5, not_217_out, not_218_out, not_219_out, F1, not_220_out);
  and and_31 (and_31_out, not_221_out, not_222_out, not_223_out, not_224_out, not_225_out, not_226_out, F5, not_227_out, not_228_out, F2, not_229_out, not_230_out);
  and and_32 (and_32_out, not_231_out, not_232_out, not_233_out, not_234_out, not_235_out, not_236_out, F5, not_237_out, not_238_out, F2, not_239_out, F0);
  and and_33 (and_33_out, not_240_out, not_241_out, not_242_out, not_243_out, not_244_out, not_245_out, F5, not_246_out, not_247_out, F2, F1, F0);
  and and_34 (and_34_out, not_248_out, not_249_out, not_250_out, not_251_out, not_252_out, not_253_out, F5, not_254_out, F3, not_255_out, F1, not_256_out);
  and and_35 (and_35_out, not_257_out, not_258_out, not_259_out, not_260_out, not_261_out, not_262_out, F5, not_263_out, F3, not_264_out, F1, F0);
  and and_36 (and_36_out, not_265_out, not_266_out, not_267_out, not_268_out, not_269_out, not_270_out, not_271_out, not_272_out, F3, F2, not_273_out, not_274_out);
  and and_37 (and_37_out, not_275_out, not_276_out, not_277_out, OP2, not_278_out, not_279_out);
  and and_38 (and_38_out, not_280_out, not_281_out, not_282_out, OP2, not_283_out, OP0);
  and and_39 (and_39_out, OP5, not_284_out, not_285_out, not_286_out, OP1, OP0);
  and and_40 (and_40_out, OP5, not_287_out, OP3, not_288_out, OP1, OP0);
  and and_41 (and_41_out, not_289_out, not_290_out, not_291_out, not_292_out, not_293_out, not_294_out, not_295_out, not_296_out, not_297_out, F2, not_298_out, not_299_out);
  and and_42 (and_42_out, OP5, not_300_out, not_301_out, not_302_out, not_303_out, not_304_out);
  or or_1 (R1_USED, and_1_out, and_2_out, and_3_out, and_4_out, and_5_out, and_6_out, and_7_out, and_8_out, and_9_out, and_10_out, and_11_out, and_12_out, and_13_out, and_14_out, and_15_out, and_16_out, and_17_out, and_18_out, and_19_out, and_20_out, and_21_out, and_22_out, and_23_out, and_24_out);
  or or_2 (R2_USED, and_25_out, and_26_out, and_27_out, and_28_out, and_29_out, and_30_out, and_31_out, and_32_out, and_33_out, and_34_out, and_35_out, and_36_out, and_37_out, and_38_out, and_39_out, and_40_out, and_41_out, and_42_out);
endmodule

module \数据冲突检测电路  (
  input  \R1使用情况 ,
  input  \EX段写入信号 ,
  input  \MEM段写入信号 ,
  input  [4:0] \EX段写入编号 ,
  input  [4:0] \MEM段写入编号 ,
  input  [4:0] \R1编号 ,
  input  [4:0] \R2编号 ,
  input  \R2使用情况 ,
  output [1:0] R1,
  output \冲突 ,
  output [1:0] R2
);

  wire comparator_1_eq, comparator_2_eq, comparator_3_eq, comparator_4_eq, comparator_5_eq, comparator_6_eq;

  Comparator #(.width(5), .mode("twosComplement")) comparator_1 (
    .a(\EX段写入编号 ), .b(\R1编号 ), .eq(comparator_1_eq));  // open: gt, lt
  Comparator #(.width(5), .mode("twosComplement")) comparator_2 (
    .a(\MEM段写入编号 ), .b(\R1编号 ), .eq(comparator_2_eq));  // open: gt, lt
  Comparator #(.width(5), .mode("twosComplement")) comparator_3 (
    .a(\R1编号 ), .b({5{1'b0}}), .eq(comparator_3_eq));  // open: gt, lt
  Comparator #(.width(5), .mode("twosComplement")) comparator_4 (
    .a(\R2编号 ), .b({5{1'b0}}), .eq(comparator_4_eq));  // open: gt, lt
  Comparator #(.width(5), .mode("twosComplement")) comparator_5 (
    .a(\R2编号 ), .b(\EX段写入编号 ), .eq(comparator_5_eq));  // open: gt, lt
  Comparator #(.width(5), .mode("twosComplement")) comparator_6 (
    .a(\MEM段写入编号 ), .b(\R2编号 ), .eq(comparator_6_eq));  // open: gt, lt
  and and_1 (R1[1], \R1使用情况 , \EX段写入信号 , comparator_1_eq, ~comparator_3_eq);  // AND_Gate
  and and_2 (R1[0], \R1使用情况 , \MEM段写入信号 , comparator_2_eq, ~comparator_3_eq);  // AND_Gate
  and and_3 (R2[1], \EX段写入信号 , comparator_5_eq, \R2使用情况 , ~comparator_4_eq);  // AND_Gate
  and and_4 (R2[0], \MEM段写入信号 , comparator_6_eq, \R2使用情况 , ~comparator_4_eq);  // AND_Gate
  or or_1 (\冲突 , R1[1], R1[0], R2[1], R2[0]);

  // Notes on the sheet:
  //   R1 and EX
  //   R1 and MEM
  //   R1 and 0
  //   R2 and 0
  //   R2 and EX
  //   R2 and MEM
  //   R2 and EX
  //   R2 and MEM
  //   R1 and EX
  //   R1 and MEM
endmodule

module \Load_Use检测  (
  input  \R1使用情况 ,
  input  \EX段写入信号 ,
  input  [4:0] \EX段写入编号 ,
  input  [4:0] \R1编号 ,
  input  [4:0] \R2编号 ,
  input  \R2使用情况 ,
  output out_7
);

  wire and_1_out, and_2_out, comparator_1_eq, comparator_2_eq, comparator_3_eq, comparator_4_eq;

  Comparator #(.width(5), .mode("twosComplement")) comparator_1 (
    .a(\EX段写入编号 ), .b(\R1编号 ), .eq(comparator_1_eq));  // open: gt, lt
  Comparator #(.width(5), .mode("twosComplement")) comparator_2 (
    .a(\R1编号 ), .b({5{1'b0}}), .eq(comparator_2_eq));  // open: gt, lt
  Comparator #(.width(5), .mode("twosComplement")) comparator_3 (
    .a(\R2编号 ), .b({5{1'b0}}), .eq(comparator_3_eq));  // open: gt, lt
  Comparator #(.width(5), .mode("twosComplement")) comparator_4 (
    .a(\R2编号 ), .b(\EX段写入编号 ), .eq(comparator_4_eq));  // open: gt, lt
  and and_1 (and_1_out, \R1使用情况 , \EX段写入信号 , comparator_1_eq, ~comparator_2_eq);  // AND_Gate
  and and_2 (and_2_out, \EX段写入信号 , comparator_4_eq, \R2使用情况 , ~comparator_3_eq);  // AND_Gate
  or or_1 (out_7, and_1_out, and_2_out);

  // Notes on the sheet:
  //   R1 and EX
  //   R1 and MEM
  //   R1 and 0
  //   R2 and 0
  //   R2 and EX
  //   R2 and MEM
endmodule

module \硬件堆栈  (
  input  [1:0] \中断向量号 ,
  input  \INT_新的中断 ,
  input  ERET,
  input  CLK,
  output [1:0] out_5
);

  wire and_1_out, and_2_out, and_3_out, decoder_1_out0, decoder_1_out1, decoder_1_out2, or_1_out;
  wire [1:0] counter_1_q, demultiplexer_1_out0, demultiplexer_1_out1, demultiplexer_1_out2, register_1_q,
       register_2_q, register_3_q, subtractor_1_out;

  Demultiplexer #(.select(2), .width(2), .tristate("false"), .disabled("Z"), .enable("false")) demultiplexer_1 (
    .out0(demultiplexer_1_out0), .out1(demultiplexer_1_out1), .out2(demultiplexer_1_out2), .in(\中断向量号 ),
    .sel(counter_1_q));  // open: out3
  or or_1 (or_1_out, \INT_新的中断 , ERET);
  Counter #(.width(2), .max('h3), .ongoal("wrap"), .trigger("rising"), .behavior("new")) counter_1 (
    .count(or_1_out), .Q(counter_1_q), .clk(CLK), .down(ERET));  // open: load, D, carry, clr, preset
  Register #(.width(2), .trigger("rising"), .Select("low")) register_1 (
    .D(demultiplexer_1_out0), .en(and_1_out), .Q(register_1_q), .clk(CLK));  // open: clr
  and and_1 (and_1_out, decoder_1_out0, \INT_新的中断 );
  Decoder #(.select(2), .tristate("false"), .disabled("Z"), .enable("false")) decoder_1 (
    .out0(decoder_1_out0), .out1(decoder_1_out1), .out2(decoder_1_out2), .sel(counter_1_q));  // open: out3
  and and_2 (and_2_out, decoder_1_out1, \INT_新的中断 );
  Register #(.width(2), .trigger("rising"), .Select("low")) register_2 (
    .D(demultiplexer_1_out1), .en(and_2_out), .Q(register_2_q), .clk(CLK));  // open: clr
  and and_3 (and_3_out, decoder_1_out2, \INT_新的中断 );
  Register #(.width(2), .trigger("rising"), .Select("low")) register_3 (
    .D(demultiplexer_1_out2), .en(and_3_out), .Q(register_3_q), .clk(CLK));  // open: clr
  Multiplexer #(.select(2), .width(2), .disabled("Z"), .enable("false")) multiplexer_1 (
    .in0(register_1_q), .in1(register_2_q), .in2(register_3_q), .in3(2'b00), .out(out_5),
    .sel(subtractor_1_out));
  Subtractor #(.width(2)) subtractor_1 (.a(counter_1_q), .b(2'b01), .out(subtractor_1_out));  // open: bin, bout
endmodule
module \流水线中断  (
  output RegWrite,
  output MemWrite,
  output [31:0] IF_PC,
  output [31:0] ID_PC,
  output [31:0] EX_PC,
  output [31:0] M_PC,
  output [31:0] WB_PC,
  output [31:0] RDin,
  output [31:0] MDin,
  output [31:0] LedData
);

  wire ALU_src, and_1_out, and_2_out, and_3_out, and_4_out, and_5_out, and_8_out, and_9_out, and_10_out,
       and_11_out, and_13_out, and_14_out, and_15_out, and_16_out, and_17_out, and_18_out, and_19_out, BEQ,
       BLTZ, BNE, Branch, Bubble, \Bubble寄存1 , \Bubble寄存2 , CLK, clock_1_out, clock_2_out, comparator_1_eq,
       comparator_2_eq, comparator_2_lt, comparator_3_eq, comparator_4_eq, d_ff_1_q, d_ff_2_q, d_ff_3_q,
       d_ff_4_q, Enable, ERET, ex_mem_1_out_21, ex_mem_1_out_23, ex_mem_1_out_24, ex_mem_1_out_25,
       ex_mem_1_out_26, ex_mem_1_out_27, ex_mem_1_out_28, Go, halt, id_ex_1_out_34, id_ex_1_out_35,
       id_ex_1_out_38, id_ex_1_out_39, id_ex_1_out_41, id_ex_1_out_43, id_ex_1_out_50, INT, IR1, IR1_q, IR2,
       IR2_q, IR3, IR3_q, J, JAL, JMP, JR, LB, lb_t, Led, load_use, \load_use寄存 , mem_wb_1_out_21, MemToReg,
       mips_alu_1_equal, multiplexer_9_out, multiplexer_17_out, multiplexer_20_out, multiplexer_26_out,
       nand_1_out, not_1_out, not_2_out, not_3_out, not_4_out, not_5_out, not_6_out, not_7_out, or_4_out,
       or_5_out, or_6_out, or_7_out, or_8_out, or_9_out, priority_encoder_1_gs, R, RegDst, RST, SignedExt,
       SLLV, Syscall, W1, W2, W3, \中断状态_q , \冲突 , \单周期硬布线控制器_1_alu_src , \单周期硬布线控制器_1_beq ,
       \单周期硬布线控制器_1_bne , \单周期硬布线控制器_1_jal , \单周期硬布线控制器_1_jmp , \单周期硬布线控制器_1_jr , \单周期硬布线控制器_1_memtoreg ,
       \单周期硬布线控制器_1_memwrite , \单周期硬布线控制器_1_out_20 , \单周期硬布线控制器_1_out_21 , \单周期硬布线控制器_1_regdst ,
       \单周期硬布线控制器_1_regwrite , \单周期硬布线控制器_1_syscall ;
  wire [1:0] IR_now, multiplexer_7_out, multiplexer_8_out, priority_encoder_1_out, R1_Re, R2_Re,
       \数据冲突检测电路_1_r1 , \数据冲突检测电路_1_r2 ;
  wire [3:0] id_ex_1_out_36, \单周期硬布线控制器_1_alu_op ;
  wire [4:0] multiplexer_4_out, multiplexer_6_out, multiplexer_11_out, multiplexer_19_out, R1_num, R2_num;
  wire [7:0] multiplexer_23_out;
  wire [12:0] CNT_num;
  wire [15:0] adder_3_out, \LoadUse次数 , multiplier_1_out, \总周期数 , \插入气泡数 , \无条件分支数 , \条件分支成功数 ;
  wire [27:0] id_ex_1_out_51;
  wire [30:0] mips_alu_1_result;
  wire [31:0] adder_1_out, bit_extender_1_out, bit_extender_2_out, bit_extender_3_out, bit_extender_4_out,
       Branch_PC, EX_IR, ex_mem_1_out_29, ID_IR, if_id_1_out_11, IF_IR, JR_PC, Mem_ALU, MEM_IR,
       mem_wb_1_out_17, mem_wb_1_out_18, mem_wb_1_out_25, mips_regifile_1_r2, multiplexer_10_out,
       multiplexer_12_out, multiplexer_13_out, multiplexer_21_out, multiplexer_24_out, nextPC, PC_3_q, PCout,
       \PC寄存 , R1, \R1_原 , R2_233, R2_in, \R2_原 , ram_1_data, shifter_1_out, WB_in, WB_IR;
  wire [31:2] JMP_PC;
  wire [31:26] id_ex_1_out_42;

  Button \u_总复位  (.out(RST));
  Button _1 (.out(IR1));
  Button _2 (.out(IR2));
  Button _3 (.out(IR3));
  // Probe on \总周期数 
  // Probe on \总周期数 
  Button \u_继续运行  (.out(Go));
  LED #(.active("true")) led_1 (.in(W1));
  LED #(.active("true")) led_2 (.in(W2));
  LED #(.active("true")) led_3 (.in(W3));
  Hex_Digit_Display hex_digit_display_1 (.value(LedData[31:28]));  // open: dp
  // Probe on IF_PC[19:0]
  // Mips_Probe mips_probe_1: pin names not known; wires that end beside it: IF_IR
  and and_1 (and_1_out, Enable, ~load_use);  // AND_Gate
  Hex_Digit_Display hex_digit_display_2 (.value(LedData[27:24]));  // open: dp
  Hex_Digit_Display hex_digit_display_3 (.value(LedData[23:20]));  // open: dp
  // Probe on ID_PC[19:0]
  // Mips_Probe mips_probe_2: pin names not known; wires that end beside it: ID_IR
  Register #(.width(32), .trigger("rising"), .Select("low")) PC (.D(nextPC), .Q(\PC寄存 ));  // open: en, clk, clr
  // Probe on nextPC
  Multiplexer #(.select(3), .width(32), .disabled("Z"), .enable("false")) multiplexer_1 (
    .in0(adder_1_out), .in1(Branch_PC), .in2({JMP_PC, 2'b00}), .in6(JR_PC), .out(nextPC),
    .sel({JR, JMP, Branch}));  // open: in3, in4, in5, in7
  Register #(.width(32), .trigger("rising"), .Select("low")) PC_2 (
    .D(PCout), .en(and_1_out), .Q(IF_PC), .clk(CLK), .clr(RST));
  Hex_Digit_Display hex_digit_display_4 (.value(LedData[15:12]));  // open: dp
  Hex_Digit_Display hex_digit_display_5 (.value(LedData[19:16]));  // open: dp
  Adder #(.width(32)) adder_1 (.a(IF_PC), .b(32'h4), .out(adder_1_out));  // open: cin, cout
  Hex_Digit_Display hex_digit_display_6 (.value(LedData[11:8]));  // open: dp
  Hex_Digit_Display hex_digit_display_7 (.value(LedData[7:4]));  // open: dp
  Clock #(.highDuration(1), .lowDuration(1)) clock_1 (.out(clock_1_out));
  // Probe on EX_PC[19:0]
  // Mips_Probe mips_probe_3: pin names not known; wires that end beside it: clock_1_out, EX_IR, CLK
  Hex_Digit_Display hex_digit_display_8 (.value(LedData[3:0]));  // open: dp
  ROM #(.addrWidth(10), .dataWidth(32), .Select("high")) rom_1 (.addr(IF_PC[11:2]), .data(IF_IR));
  and and_2 (and_2_out, Enable, ~load_use);  // AND_Gate
  // Probe on \总周期数 
  // Probe on M_PC[19:0]
  // Mips_Probe mips_probe_4: pin names not known; wires that end beside it: MEM_IR
  or or_1 (W1, IR1_q, d_ff_1_q);
  or or_2 (W2, IR2_q, d_ff_2_q);
  or or_3 (W3, IR3_q, d_ff_3_q);
  \数据冲突检测电路  \u_数据冲突检测电路_1  (
    .\R1使用情况 (\单周期硬布线控制器_1_out_20 ), .\EX段写入信号 (id_ex_1_out_38), .\MEM段写入信号 (ex_mem_1_out_23),
    .\EX段写入编号 (multiplexer_11_out), .\MEM段写入编号 (multiplexer_19_out), .\R1编号 (R1_num), .\R2编号 (R2_num),
    .\R2使用情况 (\单周期硬布线控制器_1_out_21 ), .R1(\数据冲突检测电路_1_r1 ), .\冲突 (\冲突 ), .R2(\数据冲突检测电路_1_r2 ));
  \Load_Use检测  \load_use检测_1  (
    .\R1使用情况 (\单周期硬布线控制器_1_out_20 ), .\EX段写入信号 (id_ex_1_out_34), .\EX段写入编号 (multiplexer_11_out),
    .\R1编号 (R1_num), .\R2编号 (R2_num), .\R2使用情况 (\单周期硬布线控制器_1_out_21 ), .out_7(load_use));
  IF_ID if_id_1 (
    .CTK(CLK), .RST(RST), .in_4(IF_IR), .in_5(IF_PC), .out_9(ID_IR), .out_10(ID_PC), .Enable(and_2_out),
    .\同步置0 (or_4_out), .in_6(adder_1_out), .out_11(if_id_1_out_11));  // open: in_7, out_12
  // Probe on \总周期数 
  // Probe on \无条件分支数 
  // Probe on \条件分支成功数 
  // Probe on \插入气泡数 
  // Probe on \LoadUse次数 
  D_Flip_Flop #(.trigger("rising"), .Pre_Clr_Positions("LEGACY"), .NegatePresetClear("false"), .enable("true"), .NewFFLayout("false")) d_ff_1 (
    .clk(IR1), .D(1'b1), .Q(d_ff_1_q), .reset(IR1_q));  // open: Qn, preset, en
  D_Flip_Flop #(.trigger("rising"), .Pre_Clr_Positions("LEGACY"), .NegatePresetClear("false"), .enable("true"), .NewFFLayout("false")) d_ff_2 (
    .clk(IR2), .D(1'b1), .Q(d_ff_2_q), .reset(IR2_q));  // open: Qn, preset, en
  D_Flip_Flop #(.trigger("rising"), .Pre_Clr_Positions("LEGACY"), .NegatePresetClear("false"), .enable("true"), .NewFFLayout("false")) d_ff_3 (
    .clk(IR3), .D(1'b1), .Q(d_ff_3_q), .reset(IR3_q));  // open: Qn, preset, en
  or or_4 (or_4_out, ERET, INT, Bubble);
  // Probe on IF_PC[11:0]
  // Probe on WB_PC[19:0]
  // Mips_Probe mips_probe_5: pin names not known; wires that end beside it: WB_IR
  or or_5 (or_5_out, d_ff_1_q, IR1_q);
  or or_6 (or_6_out, d_ff_2_q, IR2_q);
  or or_7 (or_7_out, d_ff_3_q, IR3_q);
  \单周期硬布线控制器  \u_单周期硬布线控制器_1  (
    .Func(ID_IR[5:0]), .OP(ID_IR[31:26]), .ALU_OP(\单周期硬布线控制器_1_alu_op ), .MemToReg(\单周期硬布线控制器_1_memtoreg ),
    .MemWrite(\单周期硬布线控制器_1_memwrite ), .ALU_SRC(\单周期硬布线控制器_1_alu_src ), .SysCALL(\单周期硬布线控制器_1_syscall ),
    .SignedExt(SignedExt), .RegDst(\单周期硬布线控制器_1_regdst ), .JR(\单周期硬布线控制器_1_jr ), .JMP(\单周期硬布线控制器_1_jmp ),
    .Beq(\单周期硬布线控制器_1_beq ), .JAL(\单周期硬布线控制器_1_jal ), .Bne(\单周期硬布线控制器_1_bne ), .SLLV(SLLV), .LB(LB),
    .BLTZ(BLTZ), .out_20(\单周期硬布线控制器_1_out_20 ), .out_21(\单周期硬布线控制器_1_out_21 ), .ERET(ERET),
    .RegWrite(\单周期硬布线控制器_1_regwrite ));  // open: Func_2, MFC0, MTC0
  Multiplexer #(.select(1), .width(5), .disabled("Z"), .enable("false")) multiplexer_2 (
    .in0(ID_IR[25:21]), .in1(5'b00010), .out(R1_num), .sel(\单周期硬布线控制器_1_syscall ));
  Multiplexer #(.select(1), .width(5), .disabled("Z"), .enable("false")) multiplexer_3 (
    .in0(ID_IR[20:16]), .in1(5'b00100), .out(R2_num), .sel(\单周期硬布线控制器_1_syscall ));
  Multiplexer #(.select(1), .width(5), .disabled("Z"), .enable("false")) multiplexer_4 (
    .in0(WB_IR[20:16]), .in1(WB_IR[15:11]), .out(multiplexer_4_out), .sel(RegDst));
  Multiplexer #(.select(1), .width(5), .disabled("Z"), .enable("false")) multiplexer_5 (
    .in0(ID_IR[10:6]), .in1(R1[4:0]), .sel(SLLV));  // open: out
  assign bit_extender_1_out = {{6{1'b0}}, ID_IR[25:0]};  // Bit_Extender bit_extender_1
  Comparator #(.width(32), .mode("twosComplement")) comparator_1 (
    .a(JR_PC), .b(32'h22), .eq(comparator_1_eq));  // open: gt, lt
  // Probe on EX_PC[11:0]
  // Probe on ID_PC[11:0]
  and and_3 (and_3_out, ERET, IR_now[0], ~IR_now[1]);  // AND_Gate
  and and_4 (and_4_out, ERET, ~IR_now[0], IR_now[1]);  // AND_Gate
  and and_5 (and_5_out, ERET, IR_now[0], IR_now[1]);
  Multiplexer #(.select(1), .width(5), .disabled("Z"), .enable("false")) multiplexer_6 (
    .in0(multiplexer_4_out), .in1({5{1'b1}}), .out(multiplexer_6_out), .sel(J));
  and and_6 (Led, Syscall, comparator_1_eq);
  and and_7 (halt, Syscall, ~comparator_1_eq);  // AND_Gate
  // Probe on M_PC[11:0]
  D_Flip_Flop #(.trigger("high"), .Pre_Clr_Positions("LEGACY"), .NegatePresetClear("false"), .enable("true"), .NewFFLayout("false")) d_ff_4 (.Q(d_ff_4_q));  // open: clk, D, Qn, preset, en, reset
  // Probe on 13'hc
  and and_8 (and_8_out, or_5_out, ~and_3_out);  // AND_Gate
  and and_9 (and_9_out, or_6_out, ~and_4_out);  // AND_Gate
  and and_10 (and_10_out, or_7_out, ~and_5_out);  // AND_Gate
  MIPS_Regifile mips_regifile_1 (
    .Din(RDin), .Clk(CLK), .R1(R1), .R2(mips_regifile_1_r2), .WE(RegWrite), .WAdr(multiplexer_6_out),
    .R1Adr(R1_num), .R2Adr(R2_num));
  // Probe on WB_PC[11:0]
  Comparator #(.width(13), .mode("twosComplement")) comparator_2 (
    .a(CNT_num), .b(13'hc), .eq(comparator_2_eq), .lt(comparator_2_lt));  // open: gt
  Clock #(.highDuration(1), .lowDuration(1)) clock_2 (.out(clock_2_out));
  D_Flip_Flop #(.trigger("rising"), .Pre_Clr_Positions("LEGACY"), .NegatePresetClear("false"), .enable("true"), .NewFFLayout("false")) u_IR1 (
    .clk(CLK), .D(and_8_out), .Q(IR1_q));  // open: Qn, preset, en, reset
  D_Flip_Flop #(.trigger("rising"), .Pre_Clr_Positions("LEGACY"), .NegatePresetClear("false"), .enable("true"), .NewFFLayout("false")) u_IR2 (
    .clk(CLK), .D(and_9_out), .Q(IR2_q));  // open: Qn, preset, en, reset
  D_Flip_Flop #(.trigger("rising"), .Pre_Clr_Positions("LEGACY"), .NegatePresetClear("false"), .enable("true"), .NewFFLayout("false")) u_IR3 (
    .clk(CLK), .D(and_10_out), .Q(IR3_q));  // open: Qn, preset, en, reset
  Multiplexer #(.select(1), .width(2), .disabled("Z"), .enable("false")) multiplexer_7 (
    .in0(\数据冲突检测电路_1_r1 ), .in1(2'b00), .out(multiplexer_7_out), .sel(load_use));
  Multiplexer #(.select(1), .width(2), .disabled("Z"), .enable("false")) multiplexer_8 (
    .in0(\数据冲突检测电路_1_r2 ), .in1(2'b00), .out(multiplexer_8_out), .sel(load_use));
  // Probe on R1
  nand nand_1 (nand_1_out, d_ff_4_q, comparator_2_eq);
  Counter #(.width(13), .max('h1fff), .ongoal("stay"), .trigger("rising"), .behavior("old")) counter_1 (
    .count(comparator_2_lt), .Q(CNT_num), .clk(clock_2_out));  // open: load, D, carry, clr, preset
  // Probe on priority_encoder_1_out
  Priority_Encoder #(.select(2), .disabled("Z")) priority_encoder_1 (
    .in0(1'b1), .in1(IR1_q), .in2(IR2_q), .in3(IR3_q), .out(priority_encoder_1_out),
    .gs(priority_encoder_1_gs));  // open: en_out, en_in
  ID_EX id_ex_1 (
    .CTK(CLK), .RST(RST), .Enable(Enable), .\指令 (ID_IR), .PC(ID_PC), .out_30(EX_IR), .out_31(EX_PC),
    .\寄存器1 (R1), .out_32(\R1_原 ), .\寄存器2 (mips_regifile_1_r2), .out_33(\R2_原 ),
    .MenToReg(\单周期硬布线控制器_1_memtoreg ), .out_34(id_ex_1_out_34), .MenWrite(\单周期硬布线控制器_1_memwrite ),
    .out_35(id_ex_1_out_35), .RegWrite(\单周期硬布线控制器_1_regwrite ), .out_38(id_ex_1_out_38), .sllv(Led),
    .out_39(id_ex_1_out_39), .halt(\单周期硬布线控制器_1_syscall ), .out_40(Syscall), .lb(LB),
    .out_41(id_ex_1_out_41), .RegDst(\单周期硬布线控制器_1_regdst ), .out_43(id_ex_1_out_43),
    .imm(bit_extender_1_out), .out_42({id_ex_1_out_42, JMP_PC[27:2]}), .ALU_OP(\单周期硬布线控制器_1_alu_op ),
    .out_36(id_ex_1_out_36), .ALU_src(\单周期硬布线控制器_1_alu_src ), .out_37(ALU_src), .JR(\单周期硬布线控制器_1_jr ),
    .out_44(JR), .JMP(\单周期硬布线控制器_1_jmp ), .out_45(JMP), .JAL(\单周期硬布线控制器_1_jal ), .out_46(JAL),
    .BNE(\单周期硬布线控制器_1_bne ), .out_47(BNE), .BEQ(\单周期硬布线控制器_1_beq ), .out_48(BEQ), .BLTZ(BLTZ), .out_49(BLTZ),
    .\同步置0 (or_8_out), .Signext(SignedExt), .out_50(id_ex_1_out_50), .in_26(if_id_1_out_11),
    .out_51({JMP_PC[31:28], id_ex_1_out_51}), .out_52(R1_Re), .in_27(multiplexer_7_out),
    .in_28(multiplexer_8_out), .out_53(R2_Re));  // open: in_29, out_54
  assign CLK = nand_1_out ? clock_2_out : 1'bz;  // Controlled_Buffer controlled_buffer_1
  Multiplexer #(.select(2), .width(1), .disabled("Z"), .enable("false")) multiplexer_9 (
    .in0(1'b0), .in1(priority_encoder_1_gs), .in2(priority_encoder_1_gs), .in3(priority_encoder_1_gs),
    .out(multiplexer_9_out), .sel(priority_encoder_1_out));
  // Probe on \R1_原 
  or or_8 (or_8_out, load_use, INT, Bubble);
  Pull_Resistor #(.pull(1)) pull_resistor_1 (.node(CLK));
  Multiplexer #(.select(2), .width(32), .disabled("Z"), .enable("false")) multiplexer_10 (
    .in0(nextPC), .in1(32'h30ac), .in2(32'h3150), .in3(32'h31f4), .out(multiplexer_10_out),
    .sel(priority_encoder_1_out));
  Register #(.width(2), .trigger("rising"), .Select("low")) macause (
    .D(priority_encoder_1_out), .en(and_11_out), .Q(IR_now), .clk(CLK), .clr(comparator_3_eq));
  and and_11 (and_11_out, INT, ~ERET);  // AND_Gate
  and and_12 (INT, multiplexer_9_out, ~\中断状态_q );  // AND_Gate
  or or_9 (or_9_out, INT, \中断状态_q );
  Multiplexer #(.select(1), .width(5), .disabled("Z"), .enable("false")) multiplexer_11 (
    .in0(EX_IR[20:16]), .in1(EX_IR[15:11]), .out(multiplexer_11_out), .sel(id_ex_1_out_43));
  assign bit_extender_2_out = {{16{1'b0}}, JMP_PC[17:2]};  // Bit_Extender bit_extender_2
  assign bit_extender_3_out = {{16{JMP_PC[17]}}, JMP_PC[17:2]};  // Bit_Extender bit_extender_3
  not not_1 (not_1_out, halt);
  Multiplexer #(.select(1), .width(32), .disabled("Z"), .enable("false")) multiplexer_12 (
    .in0(nextPC), .in1(multiplexer_10_out), .out(multiplexer_12_out), .sel(INT));
  Register #(.width(1), .trigger("rising"), .Select("low")) \u_中断状态  (
    .D(or_9_out), .Q(\中断状态_q ), .clk(CLK), .clr(ERET));  // open: en
  MIPS_ALU mips_alu_1 (
    .X(JR_PC), .Y(R2_in), .AluOP(id_ex_1_out_36), .Equal(mips_alu_1_equal), .Result({R, mips_alu_1_result}),
    .shamt(JMP_PC[12:8]));  // open: Result_2
  Multiplexer #(.select(1), .width(32), .disabled("Z"), .enable("false")) multiplexer_13 (
    .in0(bit_extender_2_out), .in1(bit_extender_3_out), .out(multiplexer_13_out), .sel(id_ex_1_out_50));
  Shifter #(.width(32), .shift("ll")) shifter_1 (.in(bit_extender_3_out), .\dist (5'b00010), .out(shifter_1_out));
  Counter #(.width(16), .max('hffff), .ongoal("wrap"), .trigger("rising"), .behavior("old")) counter_2 (
    .count(not_1_out), .Q(\总周期数 ), .clk(CLK), .clr(RST));  // open: load, D, carry, preset
  // Probe on PC_3_q
  Multiplexer #(.select(1), .width(32), .disabled("Z"), .enable("false")) multiplexer_14 (
    .in0(multiplexer_12_out), .in1(PC_3_q), .out(PCout), .sel(ERET));
  Register #(.width(32), .trigger("rising"), .Select("low")) PC_3 (
    .D(multiplexer_21_out), .en(INT), .Q(PC_3_q), .clk(CLK));  // open: clr
  Comparator #(.width(2), .mode("twosComplement")) comparator_3 (
    .a(priority_encoder_1_out), .b(2'b00), .eq(comparator_3_eq));  // open: gt, lt
  and and_13 (and_13_out, mips_alu_1_equal, BEQ);
  and and_14 (and_14_out, ~mips_alu_1_equal, BNE);  // AND_Gate
  or or_10 (Branch, and_13_out, and_14_out, and_15_out);
  and and_15 (and_15_out, R, BLTZ);
  // Probe on R2_233
  // Probe on {R, mips_alu_1_result}
  Adder #(.width(32)) adder_2 (
    .a(shifter_1_out), .b({JMP_PC[31:28], id_ex_1_out_51}), .out(Branch_PC));  // open: cin, cout
  // Probe on PCout
  or or_11 (Bubble, Branch, JMP);
  EX_MEM ex_mem_1 (
    .CTK(CLK), .RST(RST), .Enable(Enable), .\指令 (EX_IR), .PC(EX_PC), .\寄存器1 (R2_233),
    .\寄存器2 ({R, mips_alu_1_result}), .MenToReg(id_ex_1_out_34), .MenWrite(id_ex_1_out_35),
    .RegDst(id_ex_1_out_38), .led(id_ex_1_out_39), .halt(halt), .lb(id_ex_1_out_41),
    .RegDst_2(id_ex_1_out_43), .out_17(MEM_IR), .out_18(M_PC), .out_19(MDin), .out_20(Mem_ALU),
    .out_21(ex_mem_1_out_21), .out_22(MemWrite), .out_23(ex_mem_1_out_23), .out_24(ex_mem_1_out_24),
    .out_25(ex_mem_1_out_25), .out_26(ex_mem_1_out_26), .out_28(ex_mem_1_out_28),
    .PC_4({JMP_PC[31:28], id_ex_1_out_51}), .out_29(ex_mem_1_out_29), .JAL(JAL), .out_27(ex_mem_1_out_27));
  // Probe on MDin
  // Probe on MDin
  // Probe on JR_PC
  Multiplexer #(.select(2), .width(32), .disabled("Z"), .enable("false")) multiplexer_15 (
    .in0(\R1_原 ), .in1(WB_in), .in2(Mem_ALU), .in3(Mem_ALU), .out(JR_PC), .sel(R1_Re));
  Multiplexer #(.select(2), .width(32), .disabled("Z"), .enable("false")) multiplexer_16 (
    .in0(\R2_原 ), .in1(WB_in), .in2(Mem_ALU), .in3(Mem_ALU), .out(R2_233), .sel(R2_Re));
  Counter #(.width(16), .max('hffff), .ongoal("wrap"), .trigger("rising"), .behavior("old")) counter_3 (
    .count(1'b1), .Q(\无条件分支数 ), .clk(multiplexer_17_out), .clr(RST));  // open: load, D, carry, preset
  Multiplexer #(.select(1), .width(1), .disabled("Z"), .enable("false")) multiplexer_17 (
    .in0(and_16_out), .in1(1'b0), .out(multiplexer_17_out), .sel(not_2_out));
  not not_2 (not_2_out, not_3_out);
  not not_3 (not_3_out, CLK);
  and and_16 (and_16_out, JMP, CLK);
  // Probe on Mem_ALU
  // Probe on R2_Re
  Multiplexer #(.select(1), .width(32), .disabled("Z"), .enable("false")) multiplexer_18 (
    .in0(R2_233), .in1(multiplexer_13_out), .out(R2_in), .sel(ALU_src));
  Multiplexer #(.select(1), .width(5), .disabled("Z"), .enable("false")) multiplexer_19 (
    .in0(MEM_IR[20:16]), .in1(MEM_IR[15:11]), .out(multiplexer_19_out), .sel(ex_mem_1_out_28));
  Register #(.width(32), .trigger("rising"), .Select("low")) register_1 (
    .D(R2_233), .en(Led), .Q(LedData), .clk(CLK));  // open: clr
  // Probe on R1_Re
  Register #(.width(1), .trigger("rising"), .Select("low")) register_2 (
    .D(load_use), .Q(\load_use寄存 ), .clk(CLK), .clr(RST));  // open: en
  RAM #(.addrWidth(10), .dataWidth(32), .bus("separate"), .Select("high")) ram_1 (
    .addr(Mem_ALU[11:2]), .din(MDin), .data(ram_1_data), .str(MemWrite), .clk(CLK), .clr(RST));  // open: sel, ld
  // Probe on ram_1_data
  Counter #(.width(16), .max('hffff), .ongoal("wrap"), .trigger("rising"), .behavior("old")) counter_4 (
    .count(1'b1), .Q(\条件分支成功数 ), .clk(multiplexer_20_out), .clr(RST));  // open: load, D, carry, preset
  Multiplexer #(.select(1), .width(1), .disabled("Z"), .enable("false")) multiplexer_20 (
    .in0(and_17_out), .in1(1'b0), .out(multiplexer_20_out), .sel(not_5_out));
  and and_17 (and_17_out, Branch, CLK);
  Register #(.width(1), .trigger("rising"), .Select("low")) register_3 (
    .D(Bubble), .Q(\Bubble寄存1 ), .clk(CLK), .clr(RST));  // open: en
  not not_4 (not_4_out, CLK);
  not not_5 (not_5_out, not_4_out);
  Register #(.width(1), .trigger("rising"), .Select("low")) register_4 (
    .D(\Bubble寄存1 ), .Q(\Bubble寄存2 ), .clk(CLK), .clr(RST));  // open: en
  Multiplexer #(.select(3), .width(32), .disabled("Z"), .enable("false")) multiplexer_21 (
    .in0(ID_PC), .in1(ID_PC), .in2(\PC寄存 ), .in4(ID_PC), .out(multiplexer_21_out),
    .sel({\Bubble寄存2 , \Bubble寄存1 , \load_use寄存 }));  // open: in3, in5, in6, in7
  MEM_WB mem_wb_1 (
    .CTK(CLK), .RST(RST), .Enable(Enable), .\指令 (MEM_IR), .PC(M_PC), .\运算器结果 (Mem_ALU), .\存储器结果 (ram_1_data),
    .MenToReg(ex_mem_1_out_21), .RegWrite(ex_mem_1_out_23), .halt(ex_mem_1_out_25), .lb(ex_mem_1_out_28),
    .RegDst(ex_mem_1_out_26), .out_15(WB_IR), .out_16(WB_PC), .out_17(mem_wb_1_out_17),
    .out_18(mem_wb_1_out_18), .out_19(MemToReg), .out_20(RegWrite), .out_21(mem_wb_1_out_21),
    .out_22(RegDst), .out_23(lb_t), .PC_2(ex_mem_1_out_29), .out_25(mem_wb_1_out_25), .JAL(ex_mem_1_out_27),
    .out_24(J));
  // Probe on mem_wb_1_out_17
  Multiplexer #(.select(1), .width(32), .disabled("Z"), .enable("false")) multiplexer_22 (
    .in0(mem_wb_1_out_17), .in1(mem_wb_1_out_18), .out(WB_in), .sel(MemToReg));
  // Probe on mem_wb_1_out_18
  Comparator #(.width(32), .mode("twosComplement")) comparator_4 (
    .a(ID_PC), .b({32{1'b0}}), .eq(comparator_4_eq));  // open: gt, lt
  or or_12 (Enable, ~mem_wb_1_out_21, Go);  // OR_Gate
  Multiplexer #(.select(2), .width(8), .disabled("Z"), .enable("false")) multiplexer_23 (
    .in0(mem_wb_1_out_18[7:0]), .in1(mem_wb_1_out_18[15:8]), .in2(mem_wb_1_out_18[23:16]),
    .in3(mem_wb_1_out_18[31:24]), .out(multiplexer_23_out), .sel(mem_wb_1_out_17[1:0]));
  Multiplexer #(.select(1), .width(32), .disabled("Z"), .enable("false")) multiplexer_24 (
    .in0(WB_in), .in1(bit_extender_4_out), .out(multiplexer_24_out), .sel(lb_t));
  assign bit_extender_4_out = {{24{multiplexer_23_out[7]}}, multiplexer_23_out};  // Bit_Extender bit_extender_4
  and and_18 (and_18_out, and_19_out, CLK);
  and and_19 (and_19_out, load_use, Enable);
  Adder #(.width(16)) adder_3 (.a(\无条件分支数 ), .b(\条件分支成功数 ), .out(adder_3_out));  // open: cin, cout
  Multiplexer #(.select(1), .width(32), .disabled("Z"), .enable("false")) multiplexer_25 (
    .in0(multiplexer_24_out), .in1(mem_wb_1_out_25), .out(RDin), .sel(J));
  Counter #(.width(16), .max('hffff), .ongoal("wrap"), .trigger("rising"), .behavior("old")) counter_5 (
    .count(1'b1), .Q(\LoadUse次数 ), .clk(multiplexer_26_out), .clr(RST));  // open: load, D, carry, preset
  Multiplexer #(.select(1), .width(1), .disabled("Z"), .enable("false")) multiplexer_26 (
    .in0(and_18_out), .in1(1'b0), .out(multiplexer_26_out), .sel(not_7_out));
  not not_6 (not_6_out, CLK);
  not not_7 (not_7_out, not_6_out);
  Multiplier #(.width(16)) multiplier_1 (.a(adder_3_out), .b(16'h2), .out(multiplier_1_out));  // open: cin, cout
  Adder #(.width(16)) adder_4 (.a(multiplier_1_out), .b(\LoadUse次数 ), .out(\插入气泡数 ));  // open: cin, cout

  // Other names for the same wires on the sheet: MEM_PC[31:0] = M_PC; R1_in[31:0] = JR_PC

  // Notes on the sheet:
  //   中断源
  //   时空图监测，可删除
  //   中断等待指示
  //   数码管输出
  //   contents of rom_1 (hex, n*v repeats v):
  //   201d07d0 20100001 109fc0 139fc3 8021 2012000c 24160008 26100001 3210000f 20080008 20090001 139900
  //   2709825 132020 20020022 c 1094022 1500fff9 22100001 2018000f 2188024 108700 20080008 20090001 139902
  //   2709825 132021 20020022 c 1094022 1500fff9 108702 2c9b022 12c00001 8000c07 4020 1084027 84400
  //   3508ffff 82021 20020022 c 8000c01 afa20000 23bd0004 afa40000 23bd0004 afb00000 23bd0004 afb30000
  //   23bd0004 afb40000 23bd0004 afb50000 23bd0004 afb60000 23bd0004 20160001 20140003 20150001 168020
  //   108100 2149825 132020 20020022 c 1600fffa 295a022 1680fff7 23bdfffc 8fb60000 23bdfffc 8fb50000
  //   23bdfffc 8fb40000 23bdfffc 8fb30000 23bdfffc 8fb00000 23bdfffc 8fa40000 23bdfffc 8fa20000 42000018
  //   afa20000 23bd0004 afa40000 23bd0004 afb00000 23bd0004 afb30000 23bd0004 afb40000 23bd0004 afb50000
  //   23bd0004 afb60000 23bd0004 20160002 20140003 20150001 168020 108100 2149825 132020 20020022 c
  //   1600fffa 295a022 1680fff7 23bdfffc 8fb60000 23bdfffc 8fb50000 23bdfffc 8fb40000 23bdfffc 8fb30000
  //   23bdfffc 8fb00000 23bdfffc 8fa40000 23bdfffc 8fa20000 42000018 afa20000 23bd0004 afa40000 23bd0004
  //   afb00000 23bd0004 afb30000 23bd0004 afb40000 23bd0004 afb50000 23bd0004 afb60000 23bd0004 20160003
  //   20140003 20150001 168020 108100 2149825 132020 20020022 c 1600fffa 295a022 1680fff7 23bdfffc
  //   8fb60000 23bdfffc 8fb50000 23bdfffc 8fb40000 23bdfffc 8fb30000 23bdfffc 8fb00000 23bdfffc 8fa40000
  //   23bdfffc 8fa20000 42000018
  //   JMP
  //   JR
  //   OP
  //   Func
  //   rs
  //   rt
  //   rd
  //   shamt
  //   imm16
  //   imm26
  //   Beq
  //   Bne
  //   MemToReg
  //   MemWrite
  //   AluOP
  //   AluSrcB
  //   RegWrite
  //   JAL
  //   Syscall
  //   控制位
  //   流水调试日志用
  //   暂停节拍，不能为0
  //   Reset 
  //   Reset 
  //   Reset 
  //   戳工具置1进入计数暂停模式，ctrl+k时钟自动运行到对应节拍暂停
  //   ctrl+k关闭时钟连续运行，将控制位置零，进入单步调试模式调试
  //   可计数暂停的时钟源
  //   为方便自动评测，需要输出流水线各段保存的PC值，注意是PC不是PC+4，另外ID段寄存器写入信息，Mem段内存写入信息也要输出
endmodule

module \分支预测  (
  output MemWrite,
  output RegWrite,
  output [31:0] IF_PC,
  output [31:0] ID_PC,
  output [31:0] EX_PC,
  output [31:0] M_PC,
  output [31:0] WB_PC,
  output [31:0] RDin,
  output [31:0] MDin,
  output [31:0] LedData
);

  wire ALU_src, and_1_out, and_2_out, and_3_out, and_6_out, and_7_out, and_8_out, and_9_out, and_10_out,
       and_11_out, and_12_out, and_13_out, BEQ, BLTZ, bltz_t, BNE, Branch, btb_1_predictjump, Bubble, CLK,
       clock_1_out, clock_2_out, comparator_1_eq, comparator_2_eq, comparator_2_lt, d_ff_1_q, Enable,
       EX_Branch, ex_mem_1_out_21, ex_mem_1_out_23, ex_mem_1_out_24, ex_mem_1_out_25, ex_mem_1_out_26,
       ex_mem_1_out_27, ex_mem_1_out_28, Go, halt, id_ex_1_out_34, id_ex_1_out_35, id_ex_1_out_38,
       id_ex_1_out_39, id_ex_1_out_41, id_ex_1_out_43, id_ex_1_out_50, if_id_1_out_12, IR1, IR2, IR3, J, JAL,
       JMP, JR, LB, lb_t, Led, load_use, mem_wb_1_out_21, MemToReg, mips_alu_1_equal, multiplexer_1_out,
       multiplexer_19_out, multiplexer_21_out, multiplexer_26_out, multiplexer_27_out, nand_1_out, not_1_out,
       not_2_out, not_3_out, not_4_out, not_5_out, not_6_out, not_7_out, not_8_out, not_9_out, not_10_out,
       or_1_out, predictJump, R, RegDst, RST, SignedExt, SLLV, Syscall, W1, W2, W3, Wrong, \冲突 ,
       \单周期硬布线控制器_1_alu_src , \单周期硬布线控制器_1_beq , \单周期硬布线控制器_1_bne , \单周期硬布线控制器_1_jal , \单周期硬布线控制器_1_jmp ,
       \单周期硬布线控制器_1_jr , \单周期硬布线控制器_1_memtoreg , \单周期硬布线控制器_1_memwrite , \单周期硬布线控制器_1_out_20 ,
       \单周期硬布线控制器_1_out_21 , \单周期硬布线控制器_1_regdst , \单周期硬布线控制器_1_regwrite , \单周期硬布线控制器_1_syscall ;
  wire [1:0] multiplexer_11_out, multiplexer_12_out, R1_Re, R2_Re, \数据冲突检测电路_1_r1 , \数据冲突检测电路_1_r2 ;
  wire [3:0] id_ex_1_out_36, id_ex_1_out_51, id_ex_1_out_51_2, id_ex_1_out_51_3, id_ex_1_out_51_4,
       id_ex_1_out_51_5, id_ex_1_out_51_6, id_ex_1_out_51_7, \单周期硬布线控制器_1_alu_op ;
  wire [4:0] multiplexer_8_out, multiplexer_10_out, multiplexer_13_out, multiplexer_14_out,
       multiplexer_20_out, R1_num, R2_num;
  wire [7:0] multiplexer_23_out;
  wire [12:0] CNT_num;
  wire [15:0] \LoadUse次数 , multiplier_1_out, \判断出错 , \总周期数 , \插入气泡数 , \无条件分支数 , \条件分支成功数 ;
  wire [31:0] adder_1_out, bit_extender_1_out, bit_extender_2_out, bit_extender_3_out, bit_extender_4_out,
       Branch_PC, EX_branchAddress, EX_IR, ex_mem_1_out_29, EX_PC_4, ID_IR, if_id_1_out_11, IF_IR, JR_PC,
       JumpAddress, Mem_ALU, MEM_IR, mem_wb_1_out_17, mem_wb_1_out_18, mem_wb_1_out_25, mips_regifile_1_r2,
       multiplexer_2_out, multiplexer_3_out, multiplexer_5_out, multiplexer_15_out, multiplexer_22_out,
       multiplexer_24_out, R1, \R1_原 , R2_233, R2_in, \R2_原 , ram_1_data, shifter_1_out, WB_IR;
  wire [31:1] mips_alu_1_result;
  wire [31:2] JMP_PC;
  wire [31:26] id_ex_1_out_42;

  Button \u_总复位  (.out(RST));
  Button _1 (.out(IR1));
  Button _2 (.out(IR2));
  Button _3 (.out(IR3));
  // Probe on \总周期数 
  // Probe on \总周期数 
  Button \u_继续运行  (.out(Go));
  LED #(.active("true")) led_1 (.in(W1));
  LED #(.active("true")) led_2 (.in(W2));
  LED #(.active("true")) led_3 (.in(W3));
  and and_1 (and_1_out, Enable, ~load_use);  // AND_Gate
  Hex_Digit_Display hex_digit_display_1 (.value(LedData[31:28]));  // open: dp
  // Probe on IF_PC[19:0]
  // Mips_Probe mips_probe_1: pin names not known; wires that end beside it: IF_IR
  Counter #(.width(16), .max('hffff), .ongoal("wrap"), .trigger("rising"), .behavior("old")) counter_1 (
    .count(1'b1), .Q(\总周期数 ), .clk(multiplexer_1_out), .clr(RST));  // open: load, D, carry, preset
  Multiplexer #(.select(1), .width(1), .disabled("Z"), .enable("false")) multiplexer_1 (
    .in0(and_2_out), .in1(1'b0), .out(multiplexer_1_out), .sel(not_2_out));
  and and_2 (and_2_out, Enable, CLK);
  Multiplexer #(.select(1), .width(32), .disabled("Z"), .enable("false")) multiplexer_2 (
    .in0(adder_1_out), .in1(JumpAddress), .out(multiplexer_2_out), .sel(btb_1_predictjump));
  Multiplexer #(.select(1), .width(32), .disabled("Z"), .enable("false")) multiplexer_3 (
    .in0(EX_PC_4), .in1(EX_branchAddress), .out(multiplexer_3_out), .sel(Bubble));
  Multiplexer #(.select(3), .width(32), .disabled("Z"), .enable("false")) multiplexer_4 (
    .in0(adder_1_out), .in1(Branch_PC), .in2({JMP_PC, 2'b00}), .in6(JR_PC), .out(EX_branchAddress),
    .sel({JR, JMP, Branch}));  // open: in3, in4, in5, in7
  Register #(.width(32), .trigger("rising"), .Select("low")) PC (
    .D(multiplexer_5_out), .en(and_1_out), .Q(IF_PC), .clk(CLK), .clr(RST));
  Hex_Digit_Display hex_digit_display_2 (.value(LedData[27:24]));  // open: dp
  Hex_Digit_Display hex_digit_display_3 (.value(LedData[23:20]));  // open: dp
  // Probe on ID_PC[19:0]
  // Mips_Probe mips_probe_2: pin names not known; wires that end beside it: ID_IR
  not not_1 (not_1_out, CLK);
  not not_2 (not_2_out, not_1_out);
  Multiplexer #(.select(1), .width(32), .disabled("Z"), .enable("false")) multiplexer_5 (
    .in0(multiplexer_2_out), .in1(multiplexer_3_out), .out(multiplexer_5_out), .sel(Wrong));
  Adder #(.width(32)) adder_1 (.a(IF_PC), .b(32'h4), .out(adder_1_out));  // open: cin, cout
  Hex_Digit_Display hex_digit_display_4 (.value(LedData[19:16]));  // open: dp
  Hex_Digit_Display hex_digit_display_5 (.value(LedData[15:12]));  // open: dp
  BTB btb_1 (
    .IF_PC(IF_PC), .EX_branchAddress(EX_branchAddress), .EX_PC(EX_PC), .EX_branchtaken(EX_Branch),
    .EX_branch(Bubble), .CLK(CLK), .predictJump(btb_1_predictjump), .JumpAddress(JumpAddress));
  Hex_Digit_Display hex_digit_display_6 (.value(LedData[7:4]));  // open: dp
  Hex_Digit_Display hex_digit_display_7 (.value(LedData[11:8]));  // open: dp
  Clock #(.highDuration(1), .lowDuration(1)) clock_1 (.out(clock_1_out));
  // Probe on EX_PC[19:0]
  // Mips_Probe mips_probe_3: pin names not known; wires that end beside it: clock_1_out, EX_IR, CLK
  ROM #(.addrWidth(10), .dataWidth(32), .Select("high")) rom_1 (.addr(IF_PC[11:2]), .data(IF_IR));
  and and_3 (and_3_out, Enable, ~load_use);  // AND_Gate
  Hex_Digit_Display hex_digit_display_8 (.value(LedData[3:0]));  // open: dp
  \数据冲突检测电路  \u_数据冲突检测电路_1  (
    .\R1使用情况 (\单周期硬布线控制器_1_out_20 ), .\EX段写入信号 (id_ex_1_out_38), .\MEM段写入信号 (ex_mem_1_out_23),
    .\EX段写入编号 (multiplexer_13_out), .\MEM段写入编号 (multiplexer_20_out), .\R1编号 (R1_num), .\R2编号 (R2_num),
    .\R2使用情况 (\单周期硬布线控制器_1_out_21 ), .R1(\数据冲突检测电路_1_r1 ), .\冲突 (\冲突 ), .R2(\数据冲突检测电路_1_r2 ));
  \Load_Use检测  \load_use检测_1  (
    .\R1使用情况 (\单周期硬布线控制器_1_out_20 ), .\EX段写入信号 (id_ex_1_out_34), .\EX段写入编号 (multiplexer_13_out),
    .\R1编号 (R1_num), .\R2编号 (R2_num), .\R2使用情况 (\单周期硬布线控制器_1_out_21 ), .out_7(load_use));
  IF_ID if_id_1 (
    .CTK(CLK), .RST(RST), .in_4(IF_IR), .in_5(IF_PC), .out_9(ID_IR), .out_10(ID_PC), .Enable(and_3_out),
    .\同步置0 (Wrong), .in_6(adder_1_out), .out_11(if_id_1_out_11), .in_7(btb_1_predictjump),
    .out_12(if_id_1_out_12));
  // Probe on \总周期数 
  // Probe on M_PC[19:0]
  // Mips_Probe mips_probe_4: pin names not known; wires that end beside it: MEM_IR
  // Probe on \总周期数 
  // Probe on \无条件分支数 
  // Probe on \条件分支成功数 
  // Probe on \插入气泡数 
  // Probe on \LoadUse次数 
  \单周期硬布线控制器  \u_单周期硬布线控制器_1  (
    .Func(ID_IR[5:0]), .OP(ID_IR[31:26]), .ALU_OP(\单周期硬布线控制器_1_alu_op ), .MemToReg(\单周期硬布线控制器_1_memtoreg ),
    .MemWrite(\单周期硬布线控制器_1_memwrite ), .ALU_SRC(\单周期硬布线控制器_1_alu_src ), .SysCALL(\单周期硬布线控制器_1_syscall ),
    .SignedExt(SignedExt), .RegDst(\单周期硬布线控制器_1_regdst ), .JR(\单周期硬布线控制器_1_jr ), .JMP(\单周期硬布线控制器_1_jmp ),
    .Beq(\单周期硬布线控制器_1_beq ), .JAL(\单周期硬布线控制器_1_jal ), .Bne(\单周期硬布线控制器_1_bne ), .SLLV(SLLV), .LB(LB),
    .BLTZ(bltz_t), .out_20(\单周期硬布线控制器_1_out_20 ), .out_21(\单周期硬布线控制器_1_out_21 ),
    .RegWrite(\单周期硬布线控制器_1_regwrite ));  // open: ERET, Func_2, MFC0, MTC0
  Multiplexer #(.select(1), .width(5), .disabled("Z"), .enable("false")) multiplexer_6 (
    .in0(ID_IR[25:21]), .in1(5'b00010), .out(R1_num), .sel(\单周期硬布线控制器_1_syscall ));
  Multiplexer #(.select(1), .width(5), .disabled("Z"), .enable("false")) multiplexer_7 (
    .in0(ID_IR[20:16]), .in1(5'b00100), .out(R2_num), .sel(\单周期硬布线控制器_1_syscall ));
  Multiplexer #(.select(1), .width(5), .disabled("Z"), .enable("false")) multiplexer_8 (
    .in0(WB_IR[20:16]), .in1(WB_IR[15:11]), .out(multiplexer_8_out), .sel(RegDst));
  Multiplexer #(.select(1), .width(5), .disabled("Z"), .enable("false")) multiplexer_9 (
    .in0(ID_IR[10:6]), .in1(R1[4:0]), .sel(SLLV));  // open: out
  assign bit_extender_1_out = {{6{1'b0}}, ID_IR[25:0]};  // Bit_Extender bit_extender_1
  Comparator #(.width(32), .mode("twosComplement")) comparator_1 (
    .a(JR_PC), .b(32'h22), .eq(comparator_1_eq));  // open: gt, lt
  // Probe on IF_PC[11:0]
  // Probe on WB_PC[19:0]
  // Mips_Probe mips_probe_5: pin names not known; wires that end beside it: WB_IR
  Multiplexer #(.select(1), .width(5), .disabled("Z"), .enable("false")) multiplexer_10 (
    .in0(multiplexer_8_out), .in1({5{1'b1}}), .out(multiplexer_10_out), .sel(J));
  and and_4 (Led, Syscall, comparator_1_eq);
  and and_5 (halt, Syscall, ~comparator_1_eq);  // AND_Gate
  // Probe on ID_PC[11:0]
  // Probe on EX_PC[11:0]
  MIPS_Regifile mips_regifile_1 (
    .Din(RDin), .Clk(CLK), .R1(R1), .R2(mips_regifile_1_r2), .WE(RegWrite), .WAdr(multiplexer_10_out),
    .R1Adr(R1_num), .R2Adr(R2_num));
  // Probe on M_PC[11:0]
  D_Flip_Flop #(.trigger("high"), .Pre_Clr_Positions("LEGACY"), .NegatePresetClear("false"), .enable("true"), .NewFFLayout("false")) d_ff_1 (.Q(d_ff_1_q));  // open: clk, D, Qn, preset, en, reset
  // Probe on 13'hc
  Multiplexer #(.select(1), .width(2), .disabled("Z"), .enable("false")) multiplexer_11 (
    .in0(\数据冲突检测电路_1_r1 ), .in1(2'b00), .out(multiplexer_11_out), .sel(load_use));
  Multiplexer #(.select(1), .width(2), .disabled("Z"), .enable("false")) multiplexer_12 (
    .in0(\数据冲突检测电路_1_r2 ), .in1(2'b00), .out(multiplexer_12_out), .sel(load_use));
  // Probe on R1
  // Probe on WB_PC[11:0]
  Comparator #(.width(13), .mode("twosComplement")) comparator_2 (
    .a(CNT_num), .b(13'hc), .eq(comparator_2_eq), .lt(comparator_2_lt));  // open: gt
  Clock #(.highDuration(1), .lowDuration(1)) clock_2 (.out(clock_2_out));
  ID_EX id_ex_1 (
    .CTK(CLK), .RST(RST), .Enable(Enable), .\指令 (ID_IR), .PC(ID_PC), .out_30(EX_IR), .out_31(EX_PC),
    .\寄存器1 (R1), .out_32(\R1_原 ), .\寄存器2 (mips_regifile_1_r2), .out_33(\R2_原 ),
    .MenToReg(\单周期硬布线控制器_1_memtoreg ), .out_34(id_ex_1_out_34), .MenWrite(\单周期硬布线控制器_1_memwrite ),
    .out_35(id_ex_1_out_35), .RegWrite(\单周期硬布线控制器_1_regwrite ), .out_38(id_ex_1_out_38), .sllv(SLLV),
    .out_39(id_ex_1_out_39), .halt(\单周期硬布线控制器_1_syscall ), .out_40(Syscall), .lb(LB),
    .out_41(id_ex_1_out_41), .RegDst(\单周期硬布线控制器_1_regdst ), .out_43(id_ex_1_out_43),
    .imm(bit_extender_1_out), .out_42({id_ex_1_out_42, JMP_PC[27:2]}), .ALU_OP(\单周期硬布线控制器_1_alu_op ),
    .out_36(id_ex_1_out_36), .ALU_src(\单周期硬布线控制器_1_alu_src ), .out_37(ALU_src), .JR(\单周期硬布线控制器_1_jr ),
    .out_44(JR), .JMP(\单周期硬布线控制器_1_jmp ), .out_45(JMP), .JAL(\单周期硬布线控制器_1_jal ), .out_46(JAL),
    .BNE(\单周期硬布线控制器_1_bne ), .out_47(BNE), .BEQ(\单周期硬布线控制器_1_beq ), .out_48(BEQ), .BLTZ(bltz_t),
    .out_49(BLTZ), .\同步置0 (or_1_out), .Signext(SignedExt), .out_50(id_ex_1_out_50), .in_26(if_id_1_out_11),
    .out_51({JMP_PC[31:28], id_ex_1_out_51_7, id_ex_1_out_51_6, id_ex_1_out_51_5, id_ex_1_out_51_4, id_ex_1_out_51_3, id_ex_1_out_51_2, id_ex_1_out_51}),
    .out_52(R1_Re), .in_27(multiplexer_11_out), .in_28(multiplexer_12_out), .out_53(R2_Re),
    .in_29(if_id_1_out_12), .out_54(predictJump));
  nand nand_1 (nand_1_out, d_ff_1_q, comparator_2_eq);
  Counter #(.width(13), .max('h1fff), .ongoal("stay"), .trigger("rising"), .behavior("old")) counter_2 (
    .count(comparator_2_lt), .Q(CNT_num), .clk(clock_2_out));  // open: load, D, carry, clr, preset
  // Probe on \R1_原 
  or or_1 (or_1_out, load_use, Wrong);
  assign CLK = nand_1_out ? clock_2_out : 1'bz;  // Controlled_Buffer controlled_buffer_1
  Multiplexer #(.select(1), .width(5), .disabled("Z"), .enable("false")) multiplexer_13 (
    .in0(EX_IR[20:16]), .in1(EX_IR[15:11]), .out(multiplexer_13_out), .sel(id_ex_1_out_43));
  Multiplexer #(.select(1), .width(5), .disabled("Z"), .enable("false")) multiplexer_14 (
    .in0(JMP_PC[12:8]), .in1(JR_PC[4:0]), .out(multiplexer_14_out), .sel(id_ex_1_out_39));
  assign bit_extender_2_out = {{16{1'b0}}, JMP_PC[17:2]};  // Bit_Extender bit_extender_2
  assign bit_extender_3_out = {{16{JMP_PC[17]}}, JMP_PC[17:2]};  // Bit_Extender bit_extender_3
  Pull_Resistor #(.pull(1)) pull_resistor_1 (.node(CLK));
  MIPS_ALU mips_alu_1 (
    .X(JR_PC), .Y(R2_in), .AluOP(id_ex_1_out_36), .Equal(mips_alu_1_equal), .Result({mips_alu_1_result, R}),
    .shamt(multiplexer_14_out));  // open: Result_2
  Multiplexer #(.select(1), .width(32), .disabled("Z"), .enable("false")) multiplexer_15 (
    .in0(bit_extender_2_out), .in1(bit_extender_3_out), .out(multiplexer_15_out), .sel(id_ex_1_out_50));
  Shifter #(.width(32), .shift("ll")) shifter_1 (.in(bit_extender_3_out), .\dist (5'b00010), .out(shifter_1_out));
  and and_6 (and_6_out, mips_alu_1_equal, BEQ);
  and and_7 (and_7_out, ~mips_alu_1_equal, BNE);  // AND_Gate
  or or_2 (Branch, and_6_out, and_7_out, and_8_out);
  and and_8 (and_8_out, R, BLTZ);
  Adder #(.width(32)) adder_2 (.a(EX_PC), .b(32'h4), .out(EX_PC_4));  // open: cin, cout
  // Probe on R2_233
  // Probe on {mips_alu_1_result, R}
  Adder #(.width(32)) adder_3 (
    .a(shifter_1_out),
    .b({JMP_PC[31:28], id_ex_1_out_51_7, id_ex_1_out_51_6, id_ex_1_out_51_5, id_ex_1_out_51_4, id_ex_1_out_51_3, id_ex_1_out_51_2, id_ex_1_out_51}),
    .out(Branch_PC));  // open: cin, cout
  or or_3 (Bubble, Branch, JMP);
  EX_MEM ex_mem_1 (
    .CTK(CLK), .RST(RST), .Enable(Enable), .\指令 (EX_IR), .PC(EX_PC), .\寄存器1 (R2_233),
    .\寄存器2 ({mips_alu_1_result, R}), .MenToReg(id_ex_1_out_34), .MenWrite(id_ex_1_out_35),
    .RegDst(id_ex_1_out_38), .led(Led), .halt(halt), .lb(id_ex_1_out_41), .RegDst_2(id_ex_1_out_43),
    .out_17(MEM_IR), .out_18(M_PC), .out_19(MDin), .out_20(Mem_ALU), .out_21(ex_mem_1_out_21),
    .out_22(MemWrite), .out_23(ex_mem_1_out_23), .out_24(ex_mem_1_out_24), .out_25(ex_mem_1_out_25),
    .out_26(ex_mem_1_out_26), .out_28(ex_mem_1_out_28),
    .PC_4({JMP_PC[31:28], id_ex_1_out_51_7, id_ex_1_out_51_6, id_ex_1_out_51_5, id_ex_1_out_51_4, id_ex_1_out_51_3, id_ex_1_out_51_2, id_ex_1_out_51}),
    .out_29(ex_mem_1_out_29), .JAL(JAL), .out_27(ex_mem_1_out_27));
  // Probe on MDin
  // Probe on MDin
  // Probe on JR_PC
  Multiplexer #(.select(2), .width(32), .disabled("Z"), .enable("false")) multiplexer_16 (
    .in0(\R1_原 ), .in1(RDin), .in2(Mem_ALU), .in3(Mem_ALU), .out(JR_PC), .sel(R1_Re));
  Multiplexer #(.select(2), .width(32), .disabled("Z"), .enable("false")) multiplexer_17 (
    .in0(\R2_原 ), .in1(RDin), .in2(Mem_ALU), .in3(Mem_ALU), .out(R2_233), .sel(R2_Re));
  or or_4 (EX_Branch, BEQ, BNE, BLTZ, JMP, JR);
  // Probe on Mem_ALU
  // Probe on R2_Re
  Multiplexer #(.select(1), .width(32), .disabled("Z"), .enable("false")) multiplexer_18 (
    .in0(R2_233), .in1(multiplexer_15_out), .out(R2_in), .sel(ALU_src));
  Counter #(.width(16), .max('hffff), .ongoal("wrap"), .trigger("rising"), .behavior("old")) counter_3 (
    .count(1'b1), .Q(\无条件分支数 ), .clk(multiplexer_19_out), .clr(RST));  // open: load, D, carry, preset
  Multiplexer #(.select(1), .width(1), .disabled("Z"), .enable("false")) multiplexer_19 (
    .in0(and_9_out), .in1(1'b0), .out(multiplexer_19_out), .sel(not_3_out));
  not not_3 (not_3_out, not_4_out);
  and and_9 (and_9_out, JMP, CLK);
  Multiplexer #(.select(1), .width(5), .disabled("Z"), .enable("false")) multiplexer_20 (
    .in0(MEM_IR[20:16]), .in1(MEM_IR[15:11]), .out(multiplexer_20_out), .sel(ex_mem_1_out_28));
  Register #(.width(32), .trigger("rising"), .Select("low")) register_1 (
    .D(R2_in), .en(Led), .Q(LedData), .clk(CLK));  // open: clr
  // Probe on R1_Re
  not not_4 (not_4_out, CLK);
  RAM #(.addrWidth(10), .dataWidth(32), .bus("separate"), .Select("high")) ram_1 (
    .addr(Mem_ALU[11:2]), .din(MDin), .data(ram_1_data), .str(MemWrite), .clk(CLK), .clr(RST));  // open: sel, ld
  // Probe on ram_1_data
  Multiplexer #(.select(1), .width(1), .disabled("Z"), .enable("false")) multiplexer_21 (
    .in0(and_10_out), .in1(1'b0), .out(multiplexer_21_out), .sel(not_6_out));
  and and_10 (and_10_out, Branch, CLK);
  xor xor_1 (Wrong, Bubble, predictJump);
  MEM_WB mem_wb_1 (
    .CTK(CLK), .RST(RST), .Enable(Enable), .\指令 (MEM_IR), .PC(M_PC), .\运算器结果 (Mem_ALU), .\存储器结果 (ram_1_data),
    .MenToReg(ex_mem_1_out_21), .RegWrite(ex_mem_1_out_23), .halt(ex_mem_1_out_25), .lb(ex_mem_1_out_28),
    .RegDst(ex_mem_1_out_26), .out_15(WB_IR), .out_16(WB_PC), .out_17(mem_wb_1_out_17),
    .out_18(mem_wb_1_out_18), .out_19(MemToReg), .out_20(RegWrite), .out_21(mem_wb_1_out_21),
    .out_22(RegDst), .out_23(lb_t), .PC_2(ex_mem_1_out_29), .out_25(mem_wb_1_out_25), .JAL(ex_mem_1_out_27),
    .out_24(J));
  // Probe on mem_wb_1_out_17
  Counter #(.width(16), .max('hffff), .ongoal("wrap"), .trigger("rising"), .behavior("old")) counter_4 (
    .count(1'b1), .Q(\条件分支成功数 ), .clk(multiplexer_21_out), .clr(RST));  // open: load, D, carry, preset
  not not_5 (not_5_out, CLK);
  not not_6 (not_6_out, not_5_out);
  Multiplexer #(.select(1), .width(32), .disabled("Z"), .enable("false")) multiplexer_22 (
    .in0(mem_wb_1_out_17), .in1(mem_wb_1_out_18), .out(multiplexer_22_out), .sel(MemToReg));
  // Probe on mem_wb_1_out_18
  or or_5 (Enable, ~mem_wb_1_out_21, Go);  // OR_Gate
  Multiplexer #(.select(2), .width(8), .disabled("Z"), .enable("false")) multiplexer_23 (
    .in0(mem_wb_1_out_18[7:0]), .in1(mem_wb_1_out_18[15:8]), .in2(mem_wb_1_out_18[23:16]),
    .in3(mem_wb_1_out_18[31:24]), .out(multiplexer_23_out), .sel(mem_wb_1_out_17[1:0]));
  Multiplexer #(.select(1), .width(32), .disabled("Z"), .enable("false")) multiplexer_24 (
    .in0(multiplexer_22_out), .in1(bit_extender_4_out), .out(multiplexer_24_out), .sel(lb_t));
  assign bit_extender_4_out = {{24{multiplexer_23_out[7]}}, multiplexer_23_out};  // Bit_Extender bit_extender_4
  Multiplexer #(.select(1), .width(32), .disabled("Z"), .enable("false")) multiplexer_25 (
    .in0(multiplexer_24_out), .in1(mem_wb_1_out_25), .out(RDin), .sel(J));
  and and_11 (and_11_out, load_use, Enable);
  Counter #(.width(16), .max('hffff), .ongoal("wrap"), .trigger("rising"), .behavior("old")) counter_5 (
    .count(1'b1), .Q(\判断出错 ), .clk(multiplexer_26_out), .clr(RST));  // open: load, D, carry, preset
  Multiplexer #(.select(1), .width(1), .disabled("Z"), .enable("false")) multiplexer_26 (
    .in0(and_12_out), .in1(1'b0), .out(multiplexer_26_out), .sel(not_9_out));
  and and_12 (and_12_out, Wrong, CLK);
  Counter #(.width(16), .max('hffff), .ongoal("wrap"), .trigger("rising"), .behavior("old")) counter_6 (
    .count(1'b1), .Q(\LoadUse次数 ), .clk(multiplexer_27_out), .clr(RST));  // open: load, D, carry, preset
  Multiplexer #(.select(1), .width(1), .disabled("Z"), .enable("false")) multiplexer_27 (
    .in0(and_13_out), .in1(1'b0), .out(multiplexer_27_out), .sel(not_7_out));
  not not_7 (not_7_out, not_8_out);
  not not_8 (not_8_out, CLK);
  and and_13 (and_13_out, and_11_out, CLK);
  Multiplier #(.width(16)) multiplier_1 (.a(\判断出错 ), .b(16'h1), .out(multiplier_1_out));  // open: cin, cout
  not not_9 (not_9_out, not_10_out);
  not not_10 (not_10_out, CLK);
  Adder #(.width(16)) adder_4 (.a(multiplier_1_out), .b(\LoadUse次数 ), .out(\插入气泡数 ));  // open: cin, cout

  // Other names for the same wires on the sheet: shamt1[4:0] = JMP_PC[12:8]; MEM_PC[31:0] = M_PC; R1_in[31:0] = JR_PC;
  //   shamt2[4:0] = JR_PC[4:0]; WB_in[31:0] = RDin

  // Notes on the sheet:
  //   中断源
  //   时空图监测，可删除
  //   中断等待指示
  //   数码管输出
  //   contents of rom_1 (hex, n*v repeats v):
  //   20110001 8100005 20110001 20120002 20130003 8100009 20110001 20120002 20130003 810000d 20110001
  //   20120002 20130003 8100011 20110001 20120002 20130003 c1000f8 20100001 20110001 118fc0 112020
  //   20020022 c 118882 12200001 8100015 112020 20020022 c 20110001 118880 112020 20020022 c 12200001
  //   810001f 20110001 118fc0 112020 20020022 c 1188c3 112020 20020022 c 118903 112020 20020022 c 118903
  //   112020 20020022 c 118903 112020 20020022 c 118903 112020 20020022 c 118903 112020 20020022 c 118903
  //   112020 20020022 c 118903 112020 20020022 c 20100001 109fc0 139fc3 8021 2012000c 24160003 26100001
  //   3210000f 20080008 20090001 139900 2709825 132020 20020022 c 1094022 1500fff9 22100001 2018000f
  //   2188024 108700 20080008 20090001 139902 2709825 132021 20020022 c 1094022 1500fff9 108702 2c9b022
  //   12c00001 8100050 4020 1084027 84400 3508ffff 82021 20020022 c 2010ffff 20110000 ae300000 22100001
  //   22310004 ae300000 22100001 22310004 ae300000 22100001 22310004 ae300000 22100001 22310004 ae300000
  //   22100001 22310004 ae300000 22100001 22310004 ae300000 22100001 22310004 ae300000 22100001 22310004
  //   ae300000 22100001 22310004 ae300000 22100001 22310004 ae300000 22100001 22310004 ae300000 22100001
  //   22310004 ae300000 22100001 22310004 ae300000 22100001 22310004 ae300000 22100001 22310004 ae300000
  //   22100001 22310004 22100001 8020 2011003c 8e130000 8e340000 274402a 11000002 ae330000 ae140000
  //   2231fffc 1611fff8 102020 20020022 c 22100004 2011003c 1611fff2 20020032 c 2008ffff 20117777 112020
  //   20020022 c 200b0010 3a31ffff 112020 20020022 c 216bffff 1560fffa 2002000a c 20080001 20090003
  //   20110876 112020 20020022 c 200b0008 1118804 1318804 112020 20020022 c 216bffff 1560fff9 2002000a c
  //   20090000 200b0010 34118483 20120404 118c00 129400 36318281 22520404 ad310000 2328820 21290004
  //   216bffff 1560fffb 200b0020 20090000 81310000 112020 20020022 c 21290001 216bffff 1560fff9 2002000a c
  //   2011fff1 112020 20020022 c 22310001 620fffb 2002000a c 2002000a c 20100000 22100001 102020 20020022
  //   c 22100002 102020 20020022 c 22100003 102020 20020022 c 22100004 102020 20020022 c 22100005 102020
  //   20020022 c 22100006 102020 20020022 c 22100007 102020 20020022 c 22100008 102020 20020022 20020022 c
  //   3e00008
  //   JMP
  //   JR
  //   OP
  //   Func
  //   rs
  //   rt
  //   rd
  //   shamt
  //   imm16
  //   imm26
  //   Beq
  //   Bne
  //   MemToReg
  //   MemWrite
  //   AluOP
  //   AluSrcB
  //   RegWrite
  //   JAL
  //   Syscall
  //   控制位
  //   流水调试日志用
  //   暂停节拍，不能为0
  //   戳工具置1进入计数暂停模式，ctrl+k时钟自动运行到对应节拍暂停
  //   ctrl+k关闭时钟连续运行，将控制位置零，进入单步调试模式调试
  //   可计数暂停的时钟源
  //   为方便自动评测，需要输出流水线各段保存的PC值，注意是PC不是PC+4，另外ID段寄存器写入信息，Mem段内存写入信息也要输出
endmodule

module BTB (
  input  [31:0] IF_PC,
  input  [31:0] EX_branchAddress,
  input  [31:0] EX_PC,
  input  EX_branchtaken,
  input  EX_branch,
  input  CLK,
  output predictJump,
  output [31:0] JumpAddress
);

  wire and_17_out, comparator_1_eq, comparator_2_eq, comparator_3_eq, comparator_4_eq, comparator_5_eq,
       comparator_6_eq, comparator_7_eq, comparator_8_eq, comparator_9_eq, comparator_10_eq,
       comparator_11_eq, comparator_12_eq, comparator_13_eq, comparator_14_eq, comparator_15_eq,
       comparator_16_eq, EX_Hit, EX_Miss, IF_Hit, IF_Miss, L0, L1, L2, L3, L4, L5, L6, L7, not_3_out,
       not_4_out, not_5_out, not_6_out, not_7_out, not_8_out, not_9_out, not_10_out, P0, P1, P2, P3, P4, P5,
       P6, P7, U0, U1, U2, U3, U4, U5, U6, U7, V0, V1, V2, V3, V4, V5, V6, V7, W0, W1, W2, W3, W4, W5, W6,
       W7, \槽满 ;
  wire [1:0] Pa0, Pa1, Pa2, Pa3, Pa4, Pa5, Pa6, Pa7, \预测状态有限状态机_1_f0 , \预测状态有限状态机_2_f0 , \预测状态有限状态机_3_f0 ,
       \预测状态有限状态机_4_f0 , \预测状态有限状态机_5_f0 , \预测状态有限状态机_6_f0 , \预测状态有限状态机_7_f0 , \预测状态有限状态机_8_f0 ;
  wire [2:0] max2_1_max_num, max2_2_max_num, max2_3_max_num, max2_4_max_num, max2_5_max_num, max2_6_max_num,
       multiplexer_1_out, \槽号 , \淘汰槽号 ;
  wire [15:0] C0, C1, C2, C3, C4, C5, C6, C7, max2_1_max, max2_2_max, max2_3_max, max2_4_max, max2_5_max,
       max2_6_max;
  wire [31:0] tag0, tag1, tag2, tag3, tag4, tag5, tag6, tag7, \数据副本_2_q , \数据副本_3_q , \数据副本_4_q , \数据副本_5_q ,
       \数据副本_6_q , \数据副本_7_q , \数据副本_8_q , \数据副本_q ;

  Register #(.width(1), .trigger("rising"), .Select("low")) valid (.D(1'b1), .en(W0), .Q(V0), .clk(CLK));  // open: clr
  Register #(.width(1), .trigger("rising"), .Select("low")) valid_2 (
    .D(1'b1), .en(W1), .Q(V1), .clk(CLK));  // open: clr
  Register #(.width(1), .trigger("rising"), .Select("low")) valid_3 (
    .D(1'b1), .en(W2), .Q(V2), .clk(CLK));  // open: clr
  Register #(.width(1), .trigger("rising"), .Select("low")) valid_4 (
    .D(1'b1), .en(W3), .Q(V3), .clk(CLK));  // open: clr
  Register #(.width(1), .trigger("rising"), .Select("low")) valid_5 (
    .D(1'b1), .en(W4), .Q(V4), .clk(CLK));  // open: clr
  Register #(.width(1), .trigger("rising"), .Select("low")) valid_6 (
    .D(1'b1), .en(W5), .Q(V5), .clk(CLK));  // open: clr
  Register #(.width(1), .trigger("rising"), .Select("low")) valid_7 (
    .D(1'b1), .en(W6), .Q(V6), .clk(CLK));  // open: clr
  Register #(.width(1), .trigger("rising"), .Select("low")) valid_8 (
    .D(1'b1), .en(W7), .Q(V7), .clk(CLK));  // open: clr
  Register #(.width(32), .trigger("rising"), .Select("low")) \TAG副本  (
    .D(EX_PC), .en(W0), .Q(tag0), .clk(CLK));  // open: clr
  Register #(.width(32), .trigger("rising"), .Select("low")) \TAG副本_2  (
    .D(EX_PC), .en(W1), .Q(tag1), .clk(CLK));  // open: clr
  Register #(.width(32), .trigger("rising"), .Select("low")) \TAG副本_3  (
    .D(EX_PC), .en(W2), .Q(tag2), .clk(CLK));  // open: clr
  Register #(.width(32), .trigger("rising"), .Select("low")) \TAG副本_4  (
    .D(EX_PC), .en(W3), .Q(tag3), .clk(CLK));  // open: clr
  Register #(.width(32), .trigger("rising"), .Select("low")) \TAG副本_5  (
    .D(EX_PC), .en(W4), .Q(tag4), .clk(CLK));  // open: clr
  Register #(.width(32), .trigger("rising"), .Select("low")) \TAG副本_6  (
    .D(EX_PC), .en(W5), .Q(tag5), .clk(CLK));  // open: clr
  Register #(.width(32), .trigger("rising"), .Select("low")) \TAG副本_7  (
    .D(EX_PC), .en(W6), .Q(tag6), .clk(CLK));  // open: clr
  Register #(.width(32), .trigger("rising"), .Select("low")) \TAG副本_8  (
    .D(EX_PC), .en(W7), .Q(tag7), .clk(CLK));  // open: clr
  Counter #(.width(16), .max('hffff), .ongoal("wrap"), .trigger("rising"), .behavior("new")) \u_淘汰计数  (
    .D({16{1'b0}}), .Q(C0), .clk(CLK), .clr(L0));  // open: load, count, carry, preset, down
  Counter #(.width(16), .max('hffff), .ongoal("wrap"), .trigger("rising"), .behavior("new")) \u_淘汰计数_2  (
    .D({16{1'b0}}), .Q(C1), .clk(CLK), .clr(L1));  // open: load, count, carry, preset, down
  Counter #(.width(16), .max('hffff), .ongoal("wrap"), .trigger("rising"), .behavior("new")) \u_淘汰计数_3  (
    .D({16{1'b0}}), .Q(C2), .clk(CLK), .clr(L2));  // open: load, count, carry, preset, down
  Counter #(.width(16), .max('hffff), .ongoal("wrap"), .trigger("rising"), .behavior("new")) \u_淘汰计数_4  (
    .D({16{1'b0}}), .Q(C3), .clk(CLK), .clr(L3));  // open: load, count, carry, preset, down
  Counter #(.width(16), .max('hffff), .ongoal("wrap"), .trigger("rising"), .behavior("new")) \u_淘汰计数_5  (
    .D({16{1'b0}}), .Q(C4), .clk(CLK), .clr(L4));  // open: load, count, carry, preset, down
  Counter #(.width(16), .max('hffff), .ongoal("wrap"), .trigger("rising"), .behavior("new")) \u_淘汰计数_6  (
    .D({16{1'b0}}), .Q(C5), .clk(CLK), .clr(L5));  // open: load, count, carry, preset, down
  Counter #(.width(16), .max('hffff), .ongoal("wrap"), .trigger("rising"), .behavior("new")) \u_淘汰计数_7  (
    .D({16{1'b0}}), .Q(C6), .clk(CLK), .clr(L6));  // open: load, count, carry, preset, down
  Counter #(.width(16), .max('hffff), .ongoal("wrap"), .trigger("rising"), .behavior("new")) \u_淘汰计数_8  (
    .D({16{1'b0}}), .Q(C7), .clk(CLK), .clr(L7));  // open: load, count, carry, preset, down
  Register #(.width(32), .trigger("rising"), .Select("low")) \u_数据副本  (
    .D(EX_branchAddress), .en(W0), .Q(\数据副本_q ), .clk(CLK));  // open: clr
  Register #(.width(32), .trigger("rising"), .Select("low")) \u_数据副本_2  (
    .D(EX_branchAddress), .en(W1), .Q(\数据副本_2_q ), .clk(CLK));  // open: clr
  Register #(.width(32), .trigger("rising"), .Select("low")) \u_数据副本_3  (
    .D(EX_branchAddress), .en(W2), .Q(\数据副本_3_q ), .clk(CLK));  // open: clr
  Register #(.width(32), .trigger("rising"), .Select("low")) \u_数据副本_4  (
    .D(EX_branchAddress), .en(W3), .Q(\数据副本_4_q ), .clk(CLK));  // open: clr
  Register #(.width(32), .trigger("rising"), .Select("low")) \u_数据副本_5  (
    .D(EX_branchAddress), .en(W4), .Q(\数据副本_5_q ), .clk(CLK));  // open: clr
  Register #(.width(32), .trigger("rising"), .Select("low")) \u_数据副本_6  (
    .D(EX_branchAddress), .en(W5), .Q(\数据副本_6_q ), .clk(CLK));  // open: clr
  Register #(.width(32), .trigger("rising"), .Select("low")) \u_数据副本_7  (
    .D(EX_branchAddress), .en(W6), .Q(\数据副本_7_q ), .clk(CLK));  // open: clr
  Register #(.width(32), .trigger("rising"), .Select("low")) \u_数据副本_8  (
    .D(EX_branchAddress), .en(W7), .Q(\数据副本_8_q ), .clk(CLK));  // open: clr
  assign JumpAddress = L0 ? \数据副本_q  : 32'bz;  // Controlled_Buffer controlled_buffer_1
  assign JumpAddress = L1 ? \数据副本_2_q  : 32'bz;  // Controlled_Buffer controlled_buffer_2
  assign JumpAddress = L2 ? \数据副本_3_q  : 32'bz;  // Controlled_Buffer controlled_buffer_3
  assign JumpAddress = L3 ? \数据副本_4_q  : 32'bz;  // Controlled_Buffer controlled_buffer_4
  assign JumpAddress = L4 ? \数据副本_5_q  : 32'bz;  // Controlled_Buffer controlled_buffer_5
  assign JumpAddress = L5 ? \数据副本_6_q  : 32'bz;  // Controlled_Buffer controlled_buffer_6
  assign JumpAddress = L6 ? \数据副本_7_q  : 32'bz;  // Controlled_Buffer controlled_buffer_7
  assign JumpAddress = L7 ? \数据副本_8_q  : 32'bz;  // Controlled_Buffer controlled_buffer_8
  Comparator #(.width(32), .mode("twosComplement")) comparator_1 (
    .a(IF_PC), .b(tag0), .eq(comparator_1_eq));  // open: gt, lt
  Comparator #(.width(32), .mode("twosComplement")) comparator_2 (
    .a(IF_PC), .b(tag1), .eq(comparator_2_eq));  // open: gt, lt
  Comparator #(.width(32), .mode("twosComplement")) comparator_3 (
    .a(IF_PC), .b(tag2), .eq(comparator_3_eq));  // open: gt, lt
  Comparator #(.width(32), .mode("twosComplement")) comparator_4 (
    .a(IF_PC), .b(tag3), .eq(comparator_4_eq));  // open: gt, lt
  Comparator #(.width(32), .mode("twosComplement")) comparator_5 (
    .a(IF_PC), .b(tag4), .eq(comparator_5_eq));  // open: gt, lt
  Comparator #(.width(32), .mode("twosComplement")) comparator_6 (
    .a(IF_PC), .b(tag5), .eq(comparator_6_eq));  // open: gt, lt
  Comparator #(.width(32), .mode("twosComplement")) comparator_7 (
    .a(IF_PC), .b(tag6), .eq(comparator_7_eq));  // open: gt, lt
  Comparator #(.width(32), .mode("twosComplement")) comparator_8 (
    .a(IF_PC), .b(tag7), .eq(comparator_8_eq));  // open: gt, lt
  Comparator #(.width(32), .mode("twosComplement")) comparator_9 (
    .a(EX_PC), .b(tag0), .eq(comparator_9_eq));  // open: gt, lt
  Comparator #(.width(32), .mode("twosComplement")) comparator_10 (
    .a(EX_PC), .b(tag1), .eq(comparator_10_eq));  // open: gt, lt
  Comparator #(.width(32), .mode("twosComplement")) comparator_11 (
    .a(EX_PC), .b(tag2), .eq(comparator_11_eq));  // open: gt, lt
  Comparator #(.width(32), .mode("twosComplement")) comparator_12 (
    .a(EX_PC), .b(tag3), .eq(comparator_12_eq));  // open: gt, lt
  Comparator #(.width(32), .mode("twosComplement")) comparator_13 (
    .a(EX_PC), .b(tag4), .eq(comparator_13_eq));  // open: gt, lt
  Comparator #(.width(32), .mode("twosComplement")) comparator_14 (
    .a(EX_PC), .b(tag5), .eq(comparator_14_eq));  // open: gt, lt
  Comparator #(.width(32), .mode("twosComplement")) comparator_15 (
    .a(EX_PC), .b(tag6), .eq(comparator_15_eq));  // open: gt, lt
  Comparator #(.width(32), .mode("twosComplement")) comparator_16 (
    .a(EX_PC), .b(tag7), .eq(comparator_16_eq));  // open: gt, lt
  and and_1 (L0, comparator_1_eq, V0);
  and and_2 (L1, comparator_2_eq, V1);
  and and_3 (L2, comparator_3_eq, V2);
  and and_4 (L3, comparator_4_eq, V3);
  and and_5 (L4, comparator_5_eq, V4);
  and and_6 (L5, comparator_6_eq, V5);
  and and_7 (L6, comparator_7_eq, V6);
  and and_8 (L7, comparator_8_eq, V7);
  and and_9 (U0, comparator_9_eq, V0);
  and and_10 (U1, comparator_10_eq, V1);
  and and_11 (U2, comparator_11_eq, V2);
  and and_12 (U3, comparator_12_eq, V3);
  and and_13 (U4, comparator_13_eq, V4);
  and and_14 (U5, comparator_14_eq, V5);
  and and_15 (U6, comparator_15_eq, V6);
  and and_16 (U7, comparator_16_eq, V7);
  not not_1 (IF_Miss, IF_Hit);
  not not_2 (EX_Miss, EX_Hit);
  or or_1 (IF_Hit, L0, L1, L2, L3, L4, L5, L6, L7);
  or or_2 (EX_Hit, U0, U1, U2, U3, U4, U5, U6, U7);
  Multiplexer #(.select(1), .width(3), .disabled("Z"), .enable("false")) multiplexer_1 (
    .in0(\槽号 ), .in1(\淘汰槽号 ), .out(multiplexer_1_out), .sel(\槽满 ));
  not not_3 (not_3_out, V0);
  not not_4 (not_4_out, V1);
  not not_5 (not_5_out, V2);
  not not_6 (not_6_out, V3);
  not not_7 (not_7_out, V4);
  not not_8 (not_8_out, V5);
  not not_9 (not_9_out, V6);
  not not_10 (not_10_out, V7);
  and and_17 (and_17_out, EX_branch, EX_Miss);
  Demultiplexer #(.select(3), .width(1), .tristate("false"), .disabled("Z"), .enable("false")) demultiplexer_1 (
    .out0(W0), .out1(W1), .out2(W2), .out3(W3), .out4(W4), .out5(W5), .out6(W6), .out7(W7), .in(and_17_out),
    .sel(multiplexer_1_out));
  Max2 max2_1 (.Y(C0), .X(C1), .Y_num(3'b000), .X_num(3'b001), .MAX(max2_1_max), .MAX_num(max2_1_max_num));
  Max2 max2_2 (.Y(C2), .X(C3), .Y_num(3'b010), .X_num(3'b011), .MAX(max2_2_max), .MAX_num(max2_2_max_num));
  Max2 max2_3 (.Y(C4), .X(C5), .Y_num(3'b100), .X_num(3'b101), .MAX(max2_3_max), .MAX_num(max2_3_max_num));
  Max2 max2_4 (.Y(C6), .X(C7), .Y_num(3'b110), .X_num(3'b111), .MAX(max2_4_max), .MAX_num(max2_4_max_num));
  Priority_Encoder #(.select(3), .disabled("Z")) priority_encoder_1 (
    .in0(not_3_out), .in1(not_4_out), .in2(not_5_out), .in3(not_6_out), .in4(not_7_out), .in5(not_8_out),
    .in6(not_9_out), .in7(not_10_out), .out(\槽号 ), .en_out(\槽满 ));  // open: gs, en_in
  Max2 max2_5 (
    .Y(max2_1_max), .X(max2_2_max), .Y_num(max2_1_max_num), .X_num(max2_2_max_num), .MAX(max2_5_max),
    .MAX_num(max2_5_max_num));
  Max2 max2_6 (
    .Y(max2_3_max), .X(max2_4_max), .Y_num(max2_3_max_num), .X_num(max2_4_max_num), .MAX(max2_6_max),
    .MAX_num(max2_6_max_num));
  Max2 max2_7 (
    .Y(max2_5_max), .X(max2_6_max), .Y_num(max2_5_max_num), .X_num(max2_6_max_num), .MAX_num(\淘汰槽号 ));  // open: MAX
  \预测状态有限状态机  \u_预测状态有限状态机_1  (
    .S1(Pa0[1]), .F1(\预测状态有限状态机_1_f0 [1]), .S0(Pa0[0]), .EXBranchTaken(EX_branchtaken),
    .F0(\预测状态有限状态机_1_f0 [0]), .PredictJump(P0));
  \预测状态有限状态机  \u_预测状态有限状态机_2  (
    .S1(Pa1[1]), .F1(\预测状态有限状态机_2_f0 [1]), .S0(Pa1[0]), .EXBranchTaken(EX_branchtaken),
    .F0(\预测状态有限状态机_2_f0 [0]), .PredictJump(P1));
  \预测状态有限状态机  \u_预测状态有限状态机_3  (
    .S1(Pa2[1]), .F1(\预测状态有限状态机_3_f0 [1]), .S0(Pa2[0]), .EXBranchTaken(EX_branchtaken),
    .F0(\预测状态有限状态机_3_f0 [0]), .PredictJump(P2));
  \预测状态有限状态机  \u_预测状态有限状态机_4  (
    .S1(Pa3[1]), .F1(\预测状态有限状态机_4_f0 [1]), .S0(Pa3[0]), .EXBranchTaken(EX_branchtaken),
    .F0(\预测状态有限状态机_4_f0 [0]), .PredictJump(P3));
  \预测状态有限状态机  \u_预测状态有限状态机_5  (
    .S1(Pa4[1]), .F1(\预测状态有限状态机_5_f0 [1]), .S0(Pa4[0]), .EXBranchTaken(EX_branchtaken),
    .F0(\预测状态有限状态机_5_f0 [0]), .PredictJump(P4));
  \预测状态有限状态机  \u_预测状态有限状态机_6  (
    .S1(Pa5[1]), .F1(\预测状态有限状态机_6_f0 [1]), .S0(Pa5[0]), .EXBranchTaken(EX_branchtaken),
    .F0(\预测状态有限状态机_6_f0 [0]), .PredictJump(P5));
  \预测状态有限状态机  \u_预测状态有限状态机_7  (
    .S1(Pa6[1]), .F1(\预测状态有限状态机_7_f0 [1]), .S0(Pa6[0]), .EXBranchTaken(EX_branchtaken),
    .F0(\预测状态有限状态机_7_f0 [0]), .PredictJump(P6));
  \预测状态有限状态机  \u_预测状态有限状态机_8  (
    .S1(Pa7[1]), .F1(\预测状态有限状态机_8_f0 [1]), .S0(Pa7[0]), .EXBranchTaken(EX_branchtaken),
    .F0(\预测状态有限状态机_8_f0 [0]), .PredictJump(P7));
  Register #(.width(2), .trigger("rising"), .Select("low")) register_1 (
    .D(\预测状态有限状态机_1_f0 ), .en(U0), .Q(Pa0), .clk(CLK));  // open: clr
  Register #(.width(2), .trigger("rising"), .Select("low")) register_2 (
    .D(\预测状态有限状态机_2_f0 ), .en(U1), .Q(Pa1), .clk(CLK));  // open: clr
  Register #(.width(2), .trigger("rising"), .Select("low")) register_3 (
    .D(\预测状态有限状态机_3_f0 ), .en(U2), .Q(Pa2), .clk(CLK));  // open: clr
  Register #(.width(2), .trigger("rising"), .Select("low")) register_4 (
    .D(\预测状态有限状态机_4_f0 ), .en(U3), .Q(Pa3), .clk(CLK));  // open: clr
  Register #(.width(2), .trigger("rising"), .Select("low")) register_5 (
    .D(\预测状态有限状态机_5_f0 ), .en(U4), .Q(Pa4), .clk(CLK));  // open: clr
  Register #(.width(2), .trigger("rising"), .Select("low")) register_6 (
    .D(\预测状态有限状态机_6_f0 ), .en(U5), .Q(Pa5), .clk(CLK));  // open: clr
  Register #(.width(2), .trigger("rising"), .Select("low")) register_7 (
    .D(\预测状态有限状态机_7_f0 ), .en(U6), .Q(Pa6), .clk(CLK));  // open: clr
  Register #(.width(2), .trigger("rising"), .Select("low")) register_8 (
    .D(\预测状态有限状态机_8_f0 ), .en(U7), .Q(Pa7), .clk(CLK));  // open: clr
  assign predictJump = L0 ? P0 : 1'bz;  // Controlled_Buffer controlled_buffer_9
  assign predictJump = L1 ? P1 : 1'bz;  // Controlled_Buffer controlled_buffer_10
  assign predictJump = L2 ? P2 : 1'bz;  // Controlled_Buffer controlled_buffer_11
  assign predictJump = L3 ? P3 : 1'bz;  // Controlled_Buffer controlled_buffer_12
  assign predictJump = L4 ? P4 : 1'bz;  // Controlled_Buffer controlled_buffer_13
  assign predictJump = L5 ? P5 : 1'bz;  // Controlled_Buffer controlled_buffer_14
  assign predictJump = L6 ? P6 : 1'bz;  // Controlled_Buffer controlled_buffer_15
  assign predictJump = L7 ? P7 : 1'bz;  // Controlled_Buffer controlled_buffer_16
  Pull_Resistor #(.pull(0)) pull_resistor_1 (.node(predictJump));

  // Other names for the same wires on the sheet: tag[31:0] = EX_PC

  // Notes on the sheet:
  //   输入引脚区
  //   请勿增改引脚，请勿修改子电路封装
  //   电路功能：利用上面给定的隧道构建8行的Cache，cache映射方式自选
  //   请在下方利用上方输入输出引脚的隧道信号构建电路，ctrl+d复制选择部件
endmodule

module Max2 (
  input  [15:0] Y,
  input  [15:0] X,
  input  [2:0] Y_num,
  input  [2:0] X_num,
  output [15:0] MAX,
  output [2:0] MAX_num
);

  wire comparator_1_eq, comparator_1_gt, or_1_out;

  Multiplexer #(.select(1), .width(16), .disabled("Z"), .enable("true")) multiplexer_1 (
    .in0(Y), .in1(X), .out(MAX), .sel(or_1_out), .en(1'b1));
  Comparator #(.width(16), .mode("unsigned")) comparator_1 (
    .a(X), .b(Y), .gt(comparator_1_gt), .eq(comparator_1_eq));  // open: lt
  or or_1 (or_1_out, comparator_1_gt, comparator_1_eq);
  Multiplexer #(.select(1), .width(3), .disabled("Z"), .enable("false")) multiplexer_2 (
    .in0(Y_num), .in1(X_num), .out(MAX_num), .sel(or_1_out));

  // Notes on the sheet:
  //   输出两个输入中的较大值，并输出较大值的2位编号
endmodule

module \预测状态有限状态机  (
  input  S1,
  input  S0,
  input  EXBranchTaken,
  output F1,
  output F0,
  output PredictJump
);

  wire nand_1_out, nand_2_out, nand_3_out, nand_4_out, nand_5_out, nand_6_out, nand_7_out, nand_8_out,
       nand_10_out, nand_11_out, nand_12_out, nand_13_out, nand_14_out;

  nand nand_1 (nand_1_out, S0, S0);
  nand nand_2 (nand_2_out, S1, S1);
  nand nand_3 (nand_3_out, S0, S0);
  nand nand_4 (nand_4_out, S0, S0);
  nand nand_5 (nand_5_out, S0, EXBranchTaken);
  nand nand_6 (nand_6_out, S1, nand_1_out);
  nand nand_7 (nand_7_out, nand_2_out, nand_3_out);
  nand nand_8 (nand_8_out, S1, nand_4_out);
  nand nand_9 (F1, nand_5_out, nand_6_out);
  nand nand_10 (nand_10_out, nand_7_out, nand_7_out);
  nand nand_11 (nand_11_out, nand_8_out, nand_8_out);
  nand nand_12 (nand_12_out, EXBranchTaken, EXBranchTaken);
  nand nand_13 (nand_13_out, nand_10_out, EXBranchTaken);
  nand nand_14 (nand_14_out, nand_11_out, nand_12_out);
  nand nand_15 (F0, nand_13_out, nand_14_out);

  assign PredictJump = S1;
endmodule

module \团队任务  (
);

  wire clock_1_out, keyboard_1_avail;
  wire [6:0] keyboard_1_data;

  Clock #(.highDuration(1), .lowDuration(1)) clock_1 (.out(clock_1_out));
  Keyboard #(.Char_bit_width(7), .buflen(32), .trigger("rising")) keyboard_1 (
    .clk(clock_1_out), .avail(keyboard_1_avail), .data(keyboard_1_data));  // open: re, clr
  TTY #(.Char_bit_width(7), .rows(8), .cols(32), .trigger("rising")) tty_1 (
    .data(keyboard_1_data), .clk(clock_1_out));  // open: we, clr
endmodule
